// Logisim project RegPC_Color.circ as structural Verilog: 19 circuits, main circuit Main
module Clock (
  input  Reset,
  input  Slow_Fast,
  input  Osc_Man,
  input  Tick,
  output CLK_PH,
  output nCLK_PH
);

  wire and_1_out, and_2_out, buffer_1_out, buffer_2_out, clock_1_out, clock_2_out, d_flip_flop_1_q,
       d_flip_flop_1_r, d_flip_flop_2_q, d_flip_flop_2_r, d_flip_flop_3_q, d_flip_flop_4_q, d_flip_flop_5_r,
       d_flip_flop_6_r, nand_1_out, nand_2_out, not_1_out, not_2_out, not_3_out, or_1_out, or_2_out, or_3_out;

  Button u_Reset (.out(Reset));
  Button button_1 ();  // open: out
  Clock_part clock_1 (.out(clock_1_out));
  Button button_2 ();  // open: out
  Clock_part #(.highDuration(3), .lowDuration(3)) clock_2 (.out(clock_2_out));
  Button u_Tick ();  // open: out
  buf buffer_1 (buffer_1_out, Slow_Fast);
  buf buffer_2 (buffer_2_out, Osc_Man);
  not not_1 (not_1_out, Slow_Fast);
  not not_2 (not_2_out, Osc_Man);
  not not_3 (not_3_out, Tick);
  D_Flip_Flop d_flip_flop_1 (
    .Q(d_flip_flop_1_q), .R(d_flip_flop_1_r), .D(d_flip_flop_1_r), .CLK(clock_1_out));  // open: SET, CLR
  D_Flip_Flop d_flip_flop_2 (
    .Q(d_flip_flop_2_q), .R(d_flip_flop_2_r), .D(d_flip_flop_2_r), .CLK(clock_2_out));  // open: SET, CLR
  and and_1 (and_1_out, not_1_out, buffer_2_out, d_flip_flop_6_r);
  and and_2 (and_2_out, buffer_1_out, buffer_2_out, d_flip_flop_5_r);
  nand nand_1 (nand_1_out, d_flip_flop_5_r, d_flip_flop_6_r, not_2_out);
  D_Flip_Flop d_flip_flop_3 (.Q(d_flip_flop_3_q), .D(and_1_out), .CLK(d_flip_flop_1_q));  // open: R, SET, CLR
  D_Flip_Flop d_flip_flop_4 (.Q(d_flip_flop_4_q), .D(and_2_out), .CLK(d_flip_flop_2_q));  // open: R, SET, CLR
  D_Flip_Flop d_flip_flop_5 (
    .R(d_flip_flop_5_r), .CLR(Reset), .D(d_flip_flop_3_q), .CLK(d_flip_flop_1_r));  // open: Q, SET
  D_Flip_Flop d_flip_flop_6 (
    .R(d_flip_flop_6_r), .CLR(Reset), .D(d_flip_flop_4_q), .CLK(d_flip_flop_2_r));  // open: Q, SET
  or or_1 (or_1_out, d_flip_flop_5_r, d_flip_flop_1_r);
  or or_2 (or_2_out, d_flip_flop_6_r, d_flip_flop_2_r);
  or or_3 (or_3_out, nand_1_out, not_3_out);
  nand nand_2 (nand_2_out, or_1_out, or_2_out, or_3_out);
  buf buffer_3 (CLK_PH, nand_2_out);
  not not_4 (nCLK_PH, nand_2_out);

  // Other names for the same wires on the sheet: RST = Reset
endmodule

module Main (
  input  SLOW,
  input  AUTO
);

  wire alu_1_alu_c, alu_1_alu_t, alu_1_alu_z, CLK, CTRL_CMP, CTRL_K_B, CTRL_RD_A, CTRL_RN_B, CTRL_RS_A,
       CTRL_SEL, CTRL_SHR, CTRL_WRRD, CTRL_WRSR, nCLK, SR_C, SR_T, SR_Z, TICK_out;
  wire [1:0] CTRL_GS;
  wire [2:0] CTRL_CS, IR_CC, IR_RN, IR_RS;
  wire [3:0] CTRL_PS;
  wire [15:0] alu_1_q, immdecoder_1_imm_out, registers_1_reg_a, rom_1_p1;
  wire [15:9] regir_1_ir_out;

  // ROM #(.addrWidth(16), .dataWidth(16), .line("dual")) rom_1: pin names not known; wires that end beside it: rom_1_p1
  RegIR regir_1 (.IR_OUT({regir_1_ir_out, IR_RN, IR_RS, IR_CC}), .CLK(CLK), .IN(rom_1_p1));  // open: nWR_IR
  InstDecoder instdecoder_1 (
    .CTRL_SEL(CTRL_SEL), .CTRL_PS0(CTRL_PS[0]), .CTRL_PS1(CTRL_PS[1]), .CTRL_PS2(CTRL_PS[2]),
    .CTRL_PS3(CTRL_PS[3]), .CTRL_CS0(CTRL_CS[0]), .CTRL_CS1(CTRL_CS[1]), .CTRL_CS2(CTRL_CS[2]),
    .CTRL_GS0(CTRL_GS[0]), .CTRL_GS1(CTRL_GS[1]), .CTRL_SHR(CTRL_SHR), .CTRL_CMP(CTRL_CMP),
    .CTRL_RD_A(CTRL_RD_A), .CTRL_RS_B(CTRL_RS_A), .CTRL_RN_B(CTRL_RN_B), .CTRL_K_A(CTRL_WRSR),
    .CTRL_WRRD(CTRL_K_B), .CTRL_WRSR(CTRL_WRRD), .IRin({regir_1_ir_out, IR_RN, IR_RS, IR_CC}));  // open: CLK, RESET
  Button TICK (.out(TICK_out));
  Clock clock_1 (.CLK_PH(CLK), .nCLK_PH(nCLK), .Slow_Fast(SLOW), .Osc_Man(AUTO), .Tick(TICK_out));  // open: Reset
  RegPC regpc_1 ();  // open: PC_OUT, IN, CLK, RESET, nWR_PC, nWR_PMAR, BR
  ImmDecoder immdecoder_1 (
    .IMM_OUT(immdecoder_1_imm_out), .nOE(CTRL_K_B), .IR({regir_1_ir_out, IR_RN, IR_RS, IR_CC}));  // open: CLK, RESET
  Registers registers_1 (
    .REG_A(registers_1_reg_a), .REG_B(immdecoder_1_imm_out), .CLK(CLK), .nWR_RD(CTRL_WRRD),
    .nRD_TO_A(CTRL_RD_A), .nRS_TO_A(CTRL_RS_A), .nRN_TO_B(CTRL_RN_B), .IN(alu_1_q), .RD(IR_CC), .RS(IR_RS),
    .RN(IR_RN));
  ALU alu_1 (
    .Q(alu_1_q), .ALU_Z(alu_1_alu_z), .ALU_C(alu_1_alu_c), .ALU_T(alu_1_alu_t), .C(SR_C), .T(SR_T),
    .CC(IR_CC), .CMP(CTRL_CMP), .GS0(CTRL_GS[0]), .GS1(CTRL_GS[1]), .SHR(CTRL_SHR), .A(registers_1_reg_a),
    .B(immdecoder_1_imm_out), .PSFunc(CTRL_SEL), .PS0(CTRL_PS[0]), .PS1(CTRL_PS[1]), .PS2(CTRL_PS[2]),
    .PS3(CTRL_PS[3]), .CS0(CTRL_CS[0]), .CS1(CTRL_CS[1]), .CS2(CTRL_CS[2]), .Z(SR_Z));
  RegSR regsr_1 (
    .SR_Z(SR_Z), .SR_C(SR_C), .SR_T(SR_T), .CLK(CLK), .nWR_SR(CTRL_WRSR), .Zin(alu_1_alu_z),
    .Cin(alu_1_alu_c), .Tin(alu_1_alu_t));

  // Other names for the same wires on the sheet: IR_RD[2:0] = IR_CC
endmodule

module ALU (
  input  PSFunc,
  input  PS0,
  input  PS1,
  input  PS2,
  input  PS3,
  input  CS0,
  input  CS1,
  input  CS2,
  input  Z,
  input  GS0,
  input  GS1,
  input  SHR,
  input  [15:0] A,
  input  [15:0] B,
  input  C,
  input  T,
  input  [2:0] CC,
  input  CMP,
  output [15:0] Q,
  output ALU_Z,
  output ALU_C,
  output ALU_T
);

  wire A15, alucore_1_c, alucore_1_cx, and_1_out, and_2_out, buffer_4_out, buffer_6_out, C_t, CS_Select_a, F,
       nA15, nand_1_out, not_1_out, not_5_out, not_6_out, T_t, xnor_1_out, xor_1_out, Zero_Detect_2_y1,
       Zero_Detect_2_y2, Zero_Detect_2_y3, Zero_Detect_3_y, Zero_Detect_y1, Zero_Detect_y2, Zero_Detect_y3;
  wire [2:0] ic_74x257_1_y1;
  wire [3:0] PS_Select_a1;

  not not_1 (not_1_out, Z);
  buf buffer_1 (A15, A[15]);
  not not_2 (nA15, A[15]);
  buf buffer_2 (C_t, C);
  buf buffer_3 (T_t, T);
  not not_3 (F, T);
  IC_74x3253 PS_Select (
    .A1(PS_Select_a1[0]), .A2(PS_Select_a1[1]), .B1_1(1'b0), .B1_2(1'b0), .B1_3(1'b0), .B1_4(1'b0),
    .B2_1(1'b0), .B2_2(T_t), .B2_3(F), .B2_4(T_t), .S0(PS0), .S1(PS1), .nOE1(1'b0), .nOE2(PSFunc));
  IC_74x3251 CS_Select (
    .A(CS_Select_a), .B1(1'b0), .B2(1'b1), .B3(F), .B4(T_t), .B5(nA15), .B6(A15), .B7(C_t), .B8(C_t),
    .S0(CS0), .S1(CS1), .S2(CS2), .nOE(1'b0));
  nand nand_1 (nand_1_out, CS1, CS2, not_1_out);
  IC_74x3253 PS_Select_2 (
    .A1(PS_Select_a1[2]), .A2(PS_Select_a1[3]), .B1_1(1'b0), .B1_2(1'b0), .B1_3(1'b0), .B1_4(F), .B2_1(1'b0),
    .B2_2(T_t), .B2_3(F), .B2_4(1'b1), .S0(PS0), .S1(PS1), .nOE1(1'b0), .nOE2(PSFunc));
  IC_74x3345 PS_ByPass (
    .A5(PS_Select_a1[0]), .A6(PS_Select_a1[1]), .A7(PS_Select_a1[2]), .A8(PS_Select_a1[3]), .B3(1'b0),
    .B4(1'b0), .B5(PS0), .B6(PS1), .B7(PS2), .B8(PS3), .OE(PSFunc), .nOE(1'b0), .B1(1'b0), .B2(1'b0));  // open: A3, A4, A1, A2
  ALUCore alucore_1 (
    .Q(Q), .Cx(alucore_1_cx), .C(alucore_1_c), .A(A), .B(B), .PS(PS_Select_a1), .GS({GS1, GS0}), .SHR(SHR),
    .CS(CS_Select_a));
  xor xor_1 (xor_1_out, alucore_1_c, alucore_1_cx);
  xnor xnor_1 (xnor_1_out, Q[15], xor_1_out);
  IC_74x27 Zero_Detect (
    .Y2(Zero_Detect_y2), .Y3(Zero_Detect_y3), .Y1(Zero_Detect_y1), .A2(Q[3]), .B2(Q[4]), .C2(Q[5]),
    .A3(Q[6]), .B3(Q[7]), .C3(Q[8]), .A1(Q[0]), .B1(Q[1]), .C1(Q[2]));
  IC_74x27 Zero_Detect_2 (
    .Y2(Zero_Detect_2_y2), .Y3(Zero_Detect_2_y3), .Y1(Zero_Detect_2_y1), .A2(Q[12]), .B2(Q[13]), .C2(Q[14]),
    .A3(Q[15]), .B3(1'b0), .C3(1'b0), .A1(Q[9]), .B1(Q[10]), .C1(Q[11]));
  IC_74x257 ic_74x257_1 (
    .Y1(ic_74x257_1_y1[0]), .Y2(ic_74x257_1_y1[1]), .Y3(ic_74x257_1_y1[2]), .I1_0(1'b0), .I2_0(CC[0]),
    .I1_1(1'b0), .I2_1(CC[1]), .I1_2(1'b0), .I2_2(CC[2]), .I1_3(1'b0), .I2_3(1'b0), .nA_B(CMP), .nOE(1'b0));  // open: Y4
  IC_74x30 Zero_Detect_3 (
    .Y(Zero_Detect_3_y), .C(Zero_Detect_y2), .D(Zero_Detect_y3), .E(Zero_Detect_2_y1), .F(Zero_Detect_2_y2),
    .G(Zero_Detect_2_y3), .A(nand_1_out), .H(1'b1), .B(Zero_Detect_y1));
  not not_4 (ALU_Z, Zero_Detect_3_y);
  buf buffer_4 (buffer_4_out, Zero_Detect_3_y);
  buf buffer_5 (ALU_C, alucore_1_c);
  not not_5 (not_5_out, alucore_1_c);
  buf buffer_6 (buffer_6_out, xnor_1_out);
  not not_6 (not_6_out, xnor_1_out);
  and and_1 (and_1_out, alucore_1_c, Zero_Detect_3_y);
  and and_2 (and_2_out, xnor_1_out, Zero_Detect_3_y);
  IC_74x3251 CondCode (
    .A(ALU_T), .B1(ALU_Z), .B2(buffer_4_out), .B3(ALU_C), .B4(not_5_out), .B5(buffer_6_out), .B6(not_6_out),
    .B7(and_1_out), .B8(and_2_out), .S0(ic_74x257_1_y1[0]), .S1(ic_74x257_1_y1[1]), .S2(ic_74x257_1_y1[2]),
    .nOE(1'b0));

  // Notes on the sheet:
  //   CS Select
  //   (GSSel)
  //   --------
  //   000
  //   001
  //   010
  //   011
  //   100
  //   101
  //   11x
  //   Efective
  //   CS
  //   -------
  //   0
  //   1
  //   /T
  //   T
  //   /A15
  //   A15
  //   Cy
  //   PSFunc
  //   ----------
  //   0  PSSelect
  //   1  PSByPass
  //   PSSelect 
  //   (PSFunc=0)
  //   ----------------
  //   xx00 Q = ZERO
  //   xx10 Q = SELt(A, 0)
  //   xx01 Q = SELf(A, 0)
  //   xx11 Q = SELt(A, B)
  //   PSSelect
  //   (PSFunc=1)
  //   -------------
  //   xxxx Q = bypas
  //   Efective 
  //   PS
  //   -------
  //   xxxx
  //   Efective 
  //   PS
  //   -------
  //   0000
  //   T0T0
  //   F0F0
  //   1FT0
  //   Conditon 
  //   Code (CC)
  //   ---------
  //   000 (EQ)
  //   001 (NE)
  //   010 (UGE)
  //   011 (ULT)
  //   100 (GE)
  //   101 (LT)
  //   110 (UGT)
  //   111 (GT)
  //   Logic 
  //   Function (T)
  //   ------------
  //   Z
  //   /Z
  //   C
  //   /C
  //   S == V
  //   S != V
  //   C AND /Z
  //   (S==V) AND /Z
endmodule

// ALU CORE
module ALUCore (
  input  [15:0] A,
  input  [15:0] B,
  input  [3:0] PS,
  input  [1:0] GS,
  input  SHR,
  input  CS,
  output C,
  output [15:0] Q,
  output Cx
);

  wire carrylookahead_1_c4, carrylookahead_2_c1, carrylookahead_2_c2, carrylookahead_2_c3,
       carrylookahead_3_c1, carrylookahead_3_c2, carrylookahead_3_c3, carrylookahead_4_c1,
       carrylookahead_4_c2, carrylookahead_4_c3, carrylookahead_5_c1, carrylookahead_5_c2, gC4, gC8, gC12,
       SHR_y1;
  wire [3:0] gG, gP, ic_74153_1_y1, ic_74153_1_y2, ic_74153_2_y1, ic_74153_2_y2, ic_74153_3_y1,
       ic_74153_3_y2, ic_74153_4_y1, ic_74153_4_y2, SHR_2_y1, SHR_3_y1, SHR_4_y1, SHR_5_y1;

  IC_74153 ic_74153_1 (
    .Y1(ic_74153_1_y1[0]), .Y2(ic_74153_1_y2[0]), .C1(PS[2]), .D1(PS[3]), .A2(1'b0), .A1(PS[0]), .B2(GS[0]),
    .C2(1'b0), .D2(GS[1]), .S0(A[0]), .S1(B[0]), .OE1(1'b0), .OE2(1'b0), .B1(PS[1]));
  IC_74153 ic_74153_2 (
    .Y1(ic_74153_2_y1[0]), .Y2(ic_74153_2_y2[0]), .C1(PS[2]), .D1(PS[3]), .A2(1'b0), .A1(PS[0]), .B2(GS[0]),
    .C2(1'b0), .D2(GS[1]), .S0(A[4]), .S1(B[4]), .OE1(1'b0), .OE2(1'b0), .B1(PS[1]));
  IC_74153 ic_74153_3 (
    .Y1(ic_74153_3_y1[0]), .Y2(ic_74153_3_y2[0]), .C1(PS[2]), .D1(PS[3]), .A2(1'b0), .A1(PS[0]), .B2(GS[0]),
    .C2(1'b0), .D2(GS[1]), .S0(A[8]), .S1(B[8]), .OE1(1'b0), .OE2(1'b0), .B1(PS[1]));
  IC_74153 ic_74153_4 (
    .Y1(ic_74153_4_y1[0]), .Y2(ic_74153_4_y2[0]), .C1(PS[2]), .D1(PS[3]), .A2(1'b0), .A1(PS[0]), .B2(GS[0]),
    .C2(1'b0), .D2(GS[1]), .S0(A[12]), .S1(B[12]), .OE1(1'b0), .OE2(1'b0), .B1(PS[1]));
  IC_74153 ic_74153_5 (
    .Y1(ic_74153_1_y1[1]), .Y2(ic_74153_1_y2[1]), .C1(PS[2]), .D1(PS[3]), .A2(1'b0), .A1(PS[0]), .B2(GS[0]),
    .C2(1'b0), .D2(GS[1]), .S0(A[1]), .S1(B[1]), .OE1(1'b0), .OE2(1'b0), .B1(PS[1]));
  IC_74153 ic_74153_6 (
    .Y1(ic_74153_2_y1[1]), .Y2(ic_74153_2_y2[1]), .C1(PS[2]), .D1(PS[3]), .A2(1'b0), .A1(PS[0]), .B2(GS[0]),
    .C2(1'b0), .D2(GS[1]), .S0(A[5]), .S1(B[5]), .OE1(1'b0), .OE2(1'b0), .B1(PS[1]));
  IC_74153 ic_74153_7 (
    .Y1(ic_74153_3_y1[1]), .Y2(ic_74153_3_y2[1]), .C1(PS[2]), .D1(PS[3]), .A2(1'b0), .A1(PS[0]), .B2(GS[0]),
    .C2(1'b0), .D2(GS[1]), .S0(A[9]), .S1(B[9]), .OE1(1'b0), .OE2(1'b0), .B1(PS[1]));
  IC_74153 ic_74153_8 (
    .Y1(ic_74153_4_y1[1]), .Y2(ic_74153_4_y2[1]), .C1(PS[2]), .D1(PS[3]), .A2(1'b0), .A1(PS[0]), .B2(GS[0]),
    .C2(1'b0), .D2(GS[1]), .S0(A[13]), .S1(B[13]), .OE1(1'b0), .OE2(1'b0), .B1(PS[1]));
  IC_74153 ic_74153_9 (
    .Y1(ic_74153_1_y1[2]), .Y2(ic_74153_1_y2[2]), .C1(PS[2]), .D1(PS[3]), .A2(1'b0), .A1(PS[0]), .B2(GS[0]),
    .C2(1'b0), .D2(GS[1]), .S0(A[2]), .S1(B[2]), .OE1(1'b0), .OE2(1'b0), .B1(PS[1]));
  IC_74153 ic_74153_10 (
    .Y1(ic_74153_2_y1[2]), .Y2(ic_74153_2_y2[2]), .C1(PS[2]), .D1(PS[3]), .A2(1'b0), .A1(PS[0]), .B2(GS[0]),
    .C2(1'b0), .D2(GS[1]), .S0(A[6]), .S1(B[6]), .OE1(1'b0), .OE2(1'b0), .B1(PS[1]));
  IC_74153 ic_74153_11 (
    .Y1(ic_74153_3_y1[2]), .Y2(ic_74153_3_y2[2]), .C1(PS[2]), .D1(PS[3]), .A2(1'b0), .A1(PS[0]), .B2(GS[0]),
    .C2(1'b0), .D2(GS[1]), .S0(A[10]), .S1(B[10]), .OE1(1'b0), .OE2(1'b0), .B1(PS[1]));
  IC_74153 ic_74153_12 (
    .Y1(ic_74153_4_y1[2]), .Y2(ic_74153_4_y2[2]), .C1(PS[2]), .D1(PS[3]), .A2(1'b0), .A1(PS[0]), .B2(GS[0]),
    .C2(1'b0), .D2(GS[1]), .S0(A[14]), .S1(B[14]), .OE1(1'b0), .OE2(1'b0), .B1(PS[1]));
  IC_74153 ic_74153_13 (
    .Y1(ic_74153_1_y1[3]), .Y2(ic_74153_1_y2[3]), .C1(PS[2]), .D1(PS[3]), .A2(1'b0), .A1(PS[0]), .B2(GS[0]),
    .C2(1'b0), .D2(GS[1]), .S0(A[3]), .S1(B[3]), .OE1(1'b0), .OE2(1'b0), .B1(PS[1]));
  IC_74153 ic_74153_14 (
    .Y1(ic_74153_2_y1[3]), .Y2(ic_74153_2_y2[3]), .C1(PS[2]), .D1(PS[3]), .A2(1'b0), .A1(PS[0]), .B2(GS[0]),
    .C2(1'b0), .D2(GS[1]), .S0(A[7]), .S1(B[7]), .OE1(1'b0), .OE2(1'b0), .B1(PS[1]));
  IC_74153 ic_74153_15 (
    .Y1(ic_74153_3_y1[3]), .Y2(ic_74153_3_y2[3]), .C1(PS[2]), .D1(PS[3]), .A2(1'b0), .A1(PS[0]), .B2(GS[0]),
    .C2(1'b0), .D2(GS[1]), .S0(A[11]), .S1(B[11]), .OE1(1'b0), .OE2(1'b0), .B1(PS[1]));
  IC_74153 ic_74153_16 (
    .Y1(ic_74153_4_y1[3]), .Y2(ic_74153_4_y2[3]), .C1(PS[2]), .D1(PS[3]), .A2(1'b0), .A1(PS[0]), .B2(GS[0]),
    .C2(1'b0), .D2(GS[1]), .S0(A[15]), .S1(B[15]), .OE1(1'b0), .OE2(1'b0), .B1(PS[1]));
  IC_74x257 u_SHR (
    .Y1(SHR_y1), .Y2(C), .I1_0(CS), .I2_0(1'b0), .I1_1(carrylookahead_1_c4), .I2_1(ic_74153_1_y1[0]),
    .nA_B(SHR), .nOE(1'b0));  // open: Y3, Y4, I1_2, I2_2, I1_3, I2_3
  IC_74x257 SHR_2 (
    .Y1(SHR_2_y1[0]), .Y2(SHR_2_y1[1]), .Y3(SHR_2_y1[2]), .Y4(SHR_2_y1[3]), .I1_0(ic_74153_1_y1[0]),
    .I2_0(ic_74153_1_y1[1]), .I1_1(ic_74153_1_y1[1]), .I2_1(ic_74153_1_y1[2]), .I1_2(ic_74153_1_y1[2]),
    .I2_2(ic_74153_1_y1[3]), .I1_3(ic_74153_1_y1[3]), .I2_3(ic_74153_2_y1[0]), .nA_B(SHR), .nOE(1'b0));
  IC_74x257 SHR_3 (
    .Y1(SHR_3_y1[0]), .Y2(SHR_3_y1[1]), .Y3(SHR_3_y1[2]), .Y4(SHR_3_y1[3]), .I1_0(ic_74153_2_y1[0]),
    .I2_0(ic_74153_2_y1[1]), .I1_1(ic_74153_2_y1[1]), .I2_1(ic_74153_2_y1[2]), .I1_2(ic_74153_2_y1[2]),
    .I2_2(ic_74153_2_y1[3]), .I1_3(ic_74153_2_y1[3]), .I2_3(ic_74153_3_y1[0]), .nA_B(SHR), .nOE(1'b0));
  IC_74x257 SHR_4 (
    .Y1(SHR_4_y1[0]), .Y2(SHR_4_y1[1]), .Y3(SHR_4_y1[2]), .Y4(SHR_4_y1[3]), .I1_0(ic_74153_3_y1[0]),
    .I2_0(ic_74153_3_y1[1]), .I1_1(ic_74153_3_y1[1]), .I2_1(ic_74153_3_y1[2]), .I1_2(ic_74153_3_y1[2]),
    .I2_2(ic_74153_3_y1[3]), .I1_3(ic_74153_3_y1[3]), .I2_3(ic_74153_4_y1[0]), .nA_B(SHR), .nOE(1'b0));
  IC_74x257 SHR_5 (
    .Y1(SHR_5_y1[0]), .Y2(SHR_5_y1[1]), .Y3(SHR_5_y1[2]), .Y4(SHR_5_y1[3]), .I1_0(ic_74153_4_y1[0]),
    .I2_0(ic_74153_4_y1[1]), .I1_1(ic_74153_4_y1[1]), .I2_1(ic_74153_4_y1[2]), .I1_2(ic_74153_4_y1[2]),
    .I2_2(ic_74153_4_y1[3]), .I1_3(ic_74153_4_y1[3]), .I2_3(CS), .nA_B(SHR), .nOE(1'b0));
  CarryLookAhead carrylookahead_1 (
    .C1(gC4), .C2(gC8), .C3(gC12), .C4(carrylookahead_1_c4), .C0in(CS), .P0(gP[0]), .G0(gG[0]), .P1(gP[1]),
    .G1(gG[1]), .P2(gP[2]), .G2(gG[2]), .P3(gP[3]), .G3(gG[3]));  // open: gP, gG
  CarryLookAhead carrylookahead_2 (
    .gP(gP[0]), .gG(gG[0]), .C1(carrylookahead_2_c1), .C2(carrylookahead_2_c2), .C3(carrylookahead_2_c3),
    .C0in(SHR_y1), .P0(ic_74153_1_y1[0]), .G0(ic_74153_1_y2[0]), .P1(ic_74153_1_y1[1]),
    .G1(ic_74153_1_y2[1]), .P2(ic_74153_1_y1[2]), .G2(ic_74153_1_y2[2]), .P3(ic_74153_1_y1[3]),
    .G3(ic_74153_1_y2[3]));  // open: C4
  CarryLookAhead carrylookahead_3 (
    .gP(gP[1]), .gG(gG[1]), .C1(carrylookahead_3_c1), .C2(carrylookahead_3_c2), .C3(carrylookahead_3_c3),
    .C0in(gC4), .P0(ic_74153_2_y1[0]), .G0(ic_74153_2_y2[0]), .P1(ic_74153_2_y1[1]), .G1(ic_74153_2_y2[1]),
    .P2(ic_74153_2_y1[2]), .G2(ic_74153_2_y2[2]), .P3(ic_74153_2_y1[3]), .G3(ic_74153_2_y2[3]));  // open: C4
  CarryLookAhead carrylookahead_4 (
    .gP(gP[2]), .gG(gG[2]), .C1(carrylookahead_4_c1), .C2(carrylookahead_4_c2), .C3(carrylookahead_4_c3),
    .C0in(gC8), .P0(ic_74153_3_y1[0]), .G0(ic_74153_3_y2[0]), .P1(ic_74153_3_y1[1]), .G1(ic_74153_3_y2[1]),
    .P2(ic_74153_3_y1[2]), .G2(ic_74153_3_y2[2]), .P3(ic_74153_3_y1[3]), .G3(ic_74153_3_y2[3]));  // open: C4
  CarryLookAhead carrylookahead_5 (
    .gP(gP[3]), .gG(gG[3]), .C1(carrylookahead_5_c1), .C2(carrylookahead_5_c2), .C3(Cx), .C0in(gC12),
    .P0(ic_74153_4_y1[0]), .G0(ic_74153_4_y2[0]), .P1(ic_74153_4_y1[1]), .G1(ic_74153_4_y2[1]),
    .P2(ic_74153_4_y1[2]), .G2(ic_74153_4_y2[2]), .P3(ic_74153_4_y1[3]), .G3(ic_74153_4_y2[3]));  // open: C4
  IC_7486 ic_7486_1 (
    .Y3(Q[2]), .Y4(Q[3]), .Y1(Q[0]), .Y2(Q[1]), .A3(carrylookahead_2_c2), .A4(carrylookahead_2_c3),
    .B1(SHR_2_y1[0]), .B2(SHR_2_y1[1]), .A1(SHR_y1), .B3(SHR_2_y1[2]), .B4(SHR_2_y1[3]),
    .A2(carrylookahead_2_c1));
  IC_7486 ic_7486_2 (
    .Y3(Q[6]), .Y4(Q[7]), .Y1(Q[4]), .Y2(Q[5]), .A3(carrylookahead_3_c2), .A4(carrylookahead_3_c3),
    .B1(SHR_3_y1[0]), .B2(SHR_3_y1[1]), .A1(gC4), .B3(SHR_3_y1[2]), .B4(SHR_3_y1[3]), .A2(carrylookahead_3_c1));
  IC_7486 ic_7486_3 (
    .Y3(Q[10]), .Y4(Q[11]), .Y1(Q[8]), .Y2(Q[9]), .A3(carrylookahead_4_c2), .A4(carrylookahead_4_c3),
    .B1(SHR_4_y1[0]), .B2(SHR_4_y1[1]), .A1(gC8), .B3(SHR_4_y1[2]), .B4(SHR_4_y1[3]), .A2(carrylookahead_4_c1));
  IC_7486 ic_7486_4 (
    .Y3(Q[14]), .Y4(Q[15]), .Y1(Q[12]), .Y2(Q[13]), .A3(carrylookahead_5_c2), .A4(Cx), .B1(SHR_5_y1[0]),
    .B2(SHR_5_y1[1]), .A1(gC12), .B3(SHR_5_y1[2]), .B4(SHR_5_y1[3]), .A2(carrylookahead_5_c1));

  // Other names for the same wires on the sheet: A0_3[3:0] = A[3:0]; A4_7[3:0] = A[7:4]; A8_11[3:0] = A[11:8];
  //   A12_15[3:0] = A[15:12]; B0_3[3:0] = B[3:0]; B4_7[3:0] = B[7:4]; B8_11[3:0] = B[11:8]; B12_15[3:0] = B[15:12];
  //   C0 = CS; sGS (some bits) = GS; sPS[3:0] = PS

  // Notes on the sheet:
  //   Function
  //   -----------
  //   SELECT 0
  //   SELECT 1
  //   SELECT A
  //   SELECT B
  //   OR A, B
  //   AND A, B
  //   XOR A, B
  //   NOT A
  //   ADD A, B
  //   ADDC A, B
  //   SUB A, B
  //   SUBC A, B
  //   NEG A
  //   SEXTW A
  //   LHR A
  //   LSRC A
  //   ASR A
  //   INC A (unused)
  //   DEC A (unused)
  //   (other functions are possible)
  //   PS
  //   -------------
  //   0000 (0x0)
  //   0000 (0x0)
  //   1010 (A)
  //   1100 (B)
  //   1110 (A OR B)
  //   1000 (A AND B)
  //   0110 (A XOR B)
  //   0101 (/A)
  //   0110 (A XOR B)
  //   0110 (A XOR B)
  //   1001 (A XOR /B)
  //   1001 (A XOR /B)
  //   0101 (/A)
  //   1111 (0xffff)
  //   1010 (A)
  //   1010 (A)
  //   1010 (A)
  //   1010 (A)
  //   0101 (/A)
  //   GS
  //   -----------
  //   00 (0x0)
  //   00 (0x0)
  //   00 (0x0)
  //   00 (0x0)
  //   00 (0x0)
  //   00 (0x0)
  //   00 (0x0)
  //   00 (0x0)
  //   10 (A AND B)
  //   10 (A AND B)
  //   01 (A AND /B)
  //   01 (A AND /B)
  //   00 (0x0)
  //   00 (0x0)
  //   00 (0x0)
  //   00 (0x0)
  //   00 (0x0)
  //   00 (0x0)
  //   11 (A)
  //   SHR
  //   ---
  //   0
  //   0
  //   0
  //   0
  //   0
  //   0
  //   0
  //   0
  //   0
  //   0
  //   0
  //   0
  //   0
  //   0
  //   1
  //   1
  //   1
  //   0
  //   0
  //   CS
  //   --------
  //   0
  //   1
  //   0
  //   0
  //   0
  //   0
  //   0
  //   0
  //   0
  //   Prev Carry
  //   1
  //   Prev Carry
  //   1
  //   /A15
  //   0
  //   Prev Carry
  //   A15
  //   1
  //   0
endmodule

// CY LOOK AHEAD
module CarryLookAhead (
  input  C0in,
  input  P0,
  input  G0,
  input  P1,
  input  G1,
  input  P2,
  input  G2,
  input  P3,
  input  G3,
  output C1,
  output C2,
  output C3,
  output C4,
  output gP,
  output gG
);

  wire and_1_out, and_2_out, and_3_out, and_4_out, and_5_out, and_6_out, and_7_out, and_8_out, and_9_out,
       and_10_out, and_12_out, and_13_out, and_14_out, buffer_1_out, buffer_2_out, buffer_3_out,
       buffer_4_out, buffer_5_out;

  buf buffer_1 (buffer_1_out, G0);
  and and_1 (and_1_out, C0in, P0);
  buf buffer_2 (buffer_2_out, G1);
  and and_2 (and_2_out, G0, P1);
  and and_3 (and_3_out, C0in, P0, P1);
  buf buffer_3 (buffer_3_out, G2);
  and and_4 (and_4_out, G1, P2);
  and and_5 (and_5_out, G0, P1, P2);
  and and_6 (and_6_out, C0in, P0, P1, P2);
  buf buffer_4 (buffer_4_out, G3);
  and and_7 (and_7_out, G2, P3);
  and and_8 (and_8_out, G1, P2, P3);
  and and_9 (and_9_out, G0, P1, P2, P3);
  and and_10 (and_10_out, C0in, P0, P1, P2, P3);
  and and_11 (gP, P0, P1, P2, P3);
  buf buffer_5 (buffer_5_out, G3);
  and and_12 (and_12_out, G2, P3);
  and and_13 (and_13_out, G1, P2, P3);
  and and_14 (and_14_out, G0, P1, P2, P3);
  or or_1 (C1, buffer_1_out, and_1_out);
  or or_2 (C2, buffer_2_out, and_2_out, and_3_out);
  or or_3 (C3, buffer_3_out, and_4_out, and_5_out, and_6_out);
  or or_4 (C4, buffer_4_out, and_7_out, and_8_out, and_9_out, and_10_out);
  or or_5 (gG, buffer_5_out, and_12_out, and_13_out, and_14_out);

  // Notes on the sheet:
  //   C0
  //   G0
  //   G1
  //   G2
  //   G3
  //   P0
  //   P1
  //   P2
  //   P3
  //   Logic Function
  //   -----------------------------------------------------------------
  //   C1 = (Cin . P0) + G0 
  //   C2 = (Cin . P1 . P0) + (G0 . P1) + G1
  //   C3 = (Cin . P2 . P1 . P0) + (G0 . P2 . P1) + (G1 . P2) + G2 
  //   C4 = (Cin . P3 . P2 . P1 . P0) + (G0 . P3 . P2 . P1) + (G1 . P3 . P2) + ( G2 . P3 ) + G3
  //   gP = (P3 . P2 . P1 . P0 )
  //   gG = (G0 . P3 . P2 . P1) + (G1 . P3 . P2) + (G2 . P3) + G3
endmodule

// Inst Decoder
module InstDecoder (
  input  RESET,
  input  CLK,
  input  [15:0] IRin,
  output CTRL_SEL,
  output CTRL_PS0,
  output CTRL_PS1,
  output CTRL_PS2,
  output CTRL_PS3,
  output CTRL_CS0,
  output CTRL_CS1,
  output CTRL_CS2,
  output CTRL_GS0,
  output CTRL_GS1,
  output CTRL_SHR,
  output CTRL_CMP,
  output CTRL_RD_A,
  output CTRL_RS_B,
  output CTRL_RN_B,
  output CTRL_K_A,
  output CTRL_WRRD,
  output CTRL_WRSR
);

  wire ic16v8b_3_1_q2, ic16v8b_3_1_q3, ic16v8b_3_1_q4, ic16v8b_3_1_q5, ic16v8b_3_1_q6, ic16v8b_3_1_q7,
       ic16v8b_4_1_q0, ic16v8b_4_1_q1, ic16v8b_4_1_q2, ic16v8b_4_1_q3, ic_74x74half_1_q1, ic_74x74half_1_r1,
       ic_74x151_1_y, ic_74x151_2_y, ic_74x151_3_y;
  wire [3:0] ic16v8b_4_1_q4;
  wire [6:0] Type_R2_q1;

  IC_74x151 ic_74x151_1 (
    .Y(ic_74x151_1_y), .D1(1'b1), .D2(1'b1), .D3(1'b1), .D4(1'b1), .D5(1'b1), .D6(1'b1), .D7(1'b1),
    .A(IRin[12]), .B(IRin[13]), .C(IRin[14]), .nG(1'b0), .D0(IRin[15]));  // open: W
  IC_74x151 ic_74x151_2 (
    .Y(ic_74x151_2_y), .D1(IRin[15]), .D2(IRin[15]), .D3(IRin[15]), .D4(1'b1), .D5(1'b1), .D6(1'b1),
    .D7(1'b1), .A(IRin[12]), .B(IRin[13]), .C(IRin[14]), .nG(1'b0), .D0(1'b1));  // open: W
  IC_74x151 ic_74x151_3 (
    .Y(ic_74x151_3_y), .D1(1'b0), .D2(1'b0), .D3(1'b0), .D4(1'b0), .D5(1'b0), .D6(1'b0), .D7(1'b0),
    .A(IRin[14]), .B(IRin[15]), .C(1'b0), .nG(1'b0), .D0(1'b1));  // open: W
  IC_74x74half ic_74x74half_1 (
    .R1(ic_74x74half_1_r1), .Q1(ic_74x74half_1_q1), .CLK1(CLK), .CLR1(RESET), .SET1(1'b1), .D1(ic16v8b_4_1_q3));
  IC_74x541 Type_R2 (
    .Q1(Type_R2_q1[0]), .Q2(Type_R2_q1[1]), .Q3(Type_R2_q1[2]), .Q4(Type_R2_q1[3]), .Q5(Type_R2_q1[4]),
    .Q6(Type_R2_q1[5]), .Q7(Type_R2_q1[6]), .I1(IRin[7]), .I2(IRin[8]), .I3(IRin[9]), .I4(IRin[10]),
    .I5(IRin[11]), .I6(1'b0), .I7(1'b0), .I8(1'b0), .nOE1(ic_74x151_1_y), .nOE2(ic_74x74half_1_q1));  // open: Q8
  IC_74x541 Type_J__R3 (
    .Q1(Type_R2_q1[0]), .Q2(Type_R2_q1[1]), .Q3(Type_R2_q1[2]), .Q4(Type_R2_q1[3]), .Q5(Type_R2_q1[4]),
    .Q6(Type_R2_q1[5]), .Q7(Type_R2_q1[6]), .I1(IRin[9]), .I2(IRin[10]), .I3(IRin[11]), .I4(IRin[12]),
    .I5(IRin[13]), .I6(1'b1), .I7(1'b0), .I8(1'b0), .nOE1(ic_74x151_2_y), .nOE2(ic_74x74half_1_q1));  // open: Q8
  IC_74x541 Type_I1__I2__P (
    .Q1(Type_R2_q1[0]), .Q2(Type_R2_q1[1]), .Q3(Type_R2_q1[2]), .Q4(Type_R2_q1[3]), .Q5(Type_R2_q1[4]),
    .Q6(Type_R2_q1[5]), .Q7(Type_R2_q1[6]), .I1(IRin[11]), .I2(IRin[12]), .I3(IRin[13]), .I4(IRin[14]),
    .I5(IRin[15]), .I6(1'b0), .I7(1'b1), .I8(1'b0), .nOE1(ic_74x151_3_y), .nOE2(ic_74x74half_1_q1));  // open: Q8
  IC_74x574 MIR_Reg (
    .Q2(Type_R2_q1[1]), .Q3(Type_R2_q1[2]), .Q4(Type_R2_q1[3]), .Q5(Type_R2_q1[4]), .Q6(Type_R2_q1[5]),
    .Q7(Type_R2_q1[6]), .Q1(Type_R2_q1[0]), .D2(ic16v8b_4_1_q4[1]), .D3(ic16v8b_4_1_q4[2]),
    .D4(ic16v8b_4_1_q4[3]), .D5(1'b0), .D6(1'b1), .D7(1'b1), .D8(1'b0), .CLK(CLK), .nOE(ic_74x74half_1_r1),
    .D1(ic16v8b_4_1_q4[0]));  // open: Probe, Q8
  IC16V8B_1 ic16v8b_1_1 (
    .Q0(CTRL_SEL), .Q1(CTRL_PS0), .Q2(CTRL_PS1), .Q3(CTRL_PS2), .Q4(CTRL_PS3), .Q5(CTRL_CS0), .Q6(CTRL_CS1),
    .Q7(CTRL_CS2), .I0(Type_R2_q1[0]), .I1(Type_R2_q1[1]), .I2(Type_R2_q1[2]), .I3(Type_R2_q1[3]),
    .I4(Type_R2_q1[4]), .I5(Type_R2_q1[5]), .I6(Type_R2_q1[6]), .I7(1'b0), .I8(1'b0), .I9(1'b0));
  IC16V8B_2 ic16v8b_2_1 (
    .Q0(CTRL_GS0), .Q1(CTRL_GS1), .Q2(CTRL_SHR), .Q3(CTRL_CMP), .Q4(CTRL_RD_A), .Q5(CTRL_RS_B),
    .Q6(CTRL_RN_B), .Q7(CTRL_K_A), .I0(Type_R2_q1[0]), .I1(Type_R2_q1[1]), .I2(Type_R2_q1[2]),
    .I3(Type_R2_q1[3]), .I4(Type_R2_q1[4]), .I5(Type_R2_q1[5]), .I6(Type_R2_q1[6]), .I7(1'b0), .I8(1'b0),
    .I9(1'b0));
  IC16V8B_3 ic16v8b_3_1 (
    .Q0(CTRL_WRRD), .Q1(CTRL_WRSR), .Q2(ic16v8b_3_1_q2), .Q3(ic16v8b_3_1_q3), .Q4(ic16v8b_3_1_q4),
    .Q5(ic16v8b_3_1_q5), .Q6(ic16v8b_3_1_q6), .Q7(ic16v8b_3_1_q7), .I0(Type_R2_q1[0]), .I1(Type_R2_q1[1]),
    .I2(Type_R2_q1[2]), .I3(Type_R2_q1[3]), .I4(Type_R2_q1[4]), .I5(Type_R2_q1[5]), .I6(Type_R2_q1[6]),
    .I7(1'b0), .I8(1'b0), .I9(1'b0));
  IC16V8B_4 ic16v8b_4_1 (
    .Q0(ic16v8b_4_1_q0), .Q1(ic16v8b_4_1_q1), .Q2(ic16v8b_4_1_q2), .Q3(ic16v8b_4_1_q3),
    .Q4(ic16v8b_4_1_q4[0]), .Q5(ic16v8b_4_1_q4[1]), .Q6(ic16v8b_4_1_q4[2]), .Q7(ic16v8b_4_1_q4[3]),
    .I0(Type_R2_q1[0]), .I1(Type_R2_q1[1]), .I2(Type_R2_q1[2]), .I3(Type_R2_q1[3]), .I4(Type_R2_q1[4]),
    .I5(Type_R2_q1[5]), .I6(Type_R2_q1[6]), .I7(1'b0), .I8(1'b0), .I9(1'b0));

  // Other names for the same wires on the sheet: CLR_n = RESET; IR7 = IRin[7]; IR8 = IRin[8]; IR9 = IRin[9];
  //   IR10 = IRin[10]; IR11 = IRin[11]; IR12 = IRin[12]; IR13 = IRin[13]; IR14 = IRin[14]; IR15 = IRin[15]
endmodule

// Imm
module ImmDecoder (
  input  RESET,
  input  CLK,
  input  nOE,
  input  [15:0] IR,
  output [15:0] IMM_OUT
);

  wire and_1_out, and_2_out, and_3_out, and_4_out, and_5_out, and_6_out, B0_n, B1_n, B2_n, B3_n, B4_n, B5_n,
       B6_n, B7, B7_n, C0, C3_n, IR12_n, not_1_out, PFIX_Reg_2_q4, PFIX_Reg_2_r4;
  wire [15:0] P_Imm_q1;
  wire [15:5] PFIX_Reg_y1;

  not not_1 (not_1_out, B2_n);
  and and_1 (and_1_out, B7, IR[11], IR[12]);
  and and_2 (and_2_out, B5_n, B6_n, B7_n);
  and and_3 (and_3_out, B7, IR[12]);
  and and_4 (and_4_out, B7, IR12_n, IR[10]);
  and and_5 (and_5_out, B2_n, B3_n, B4_n);
  and and_6 (and_6_out, not_1_out, C0, IR[10]);
  IC_74x541 P_Imm (
    .Q1(P_Imm_q1[0]), .Q2(P_Imm_q1[1]), .Q3(P_Imm_q1[2]), .Q4(P_Imm_q1[3]), .Q5(P_Imm_q1[4]),
    .Q6(P_Imm_q1[5]), .Q7(P_Imm_q1[6]), .Q8(P_Imm_q1[7]), .I1(IR[0]), .I2(IR[1]), .I3(IR[2]), .I4(IR[3]),
    .I5(IR[4]), .I6(IR[5]), .I7(IR[6]), .I8(IR[7]), .nOE1(B7_n), .nOE2(IR12_n));
  IC_74x541 P_Imm_2 (
    .Q1(P_Imm_q1[8]), .Q2(P_Imm_q1[9]), .Q3(P_Imm_q1[10]), .Q4(P_Imm_q1[11]), .Q5(P_Imm_q1[12]),
    .Q6(P_Imm_q1[13]), .Q7(P_Imm_q1[14]), .Q8(P_Imm_q1[15]), .I1(IR[8]), .I2(IR[9]), .I3(IR[10]), .I4(1'b0),
    .I5(1'b0), .I6(1'b0), .I7(1'b0), .I8(1'b0), .nOE1(B7_n), .nOE2(IR12_n));
  IC_74x541 I2_Imm (
    .Q1(P_Imm_q1[0]), .Q2(P_Imm_q1[1]), .Q3(P_Imm_q1[2]), .Q4(P_Imm_q1[3]), .Q5(P_Imm_q1[4]),
    .Q6(P_Imm_q1[5]), .Q7(P_Imm_q1[6]), .Q8(P_Imm_q1[7]), .I1(IR[6]), .I2(IR[7]), .I3(IR[8]), .I4(IR[9]),
    .I5(IR[10]), .I6(and_4_out), .I7(and_4_out), .I8(and_4_out), .nOE1(and_2_out), .nOE2(and_3_out));
  IC_74x541 I2_Imm_2 (
    .Q1(P_Imm_q1[8]), .Q2(P_Imm_q1[9]), .Q3(P_Imm_q1[10]), .Q4(P_Imm_q1[11]), .Q5(P_Imm_q1[12]),
    .Q6(P_Imm_q1[13]), .Q7(P_Imm_q1[14]), .Q8(P_Imm_q1[15]), .I1(and_4_out), .I2(and_4_out), .I3(and_4_out),
    .I4(and_4_out), .I5(and_4_out), .I6(and_4_out), .I7(and_4_out), .I8(and_4_out), .nOE1(and_2_out),
    .nOE2(and_3_out));
  IC_74x541 I1_Imm (
    .Q1(P_Imm_q1[0]), .Q2(P_Imm_q1[1]), .Q3(P_Imm_q1[2]), .Q4(P_Imm_q1[3]), .Q5(P_Imm_q1[4]),
    .Q6(P_Imm_q1[5]), .Q7(P_Imm_q1[6]), .Q8(P_Imm_q1[7]), .I1(IR[3]), .I2(IR[4]), .I3(IR[5]), .I4(IR[6]),
    .I5(IR[7]), .I6(IR[8]), .I7(IR[9]), .I8(IR[10]), .nOE1(and_5_out), .nOE2(and_5_out));
  IC_74x541 I1_Imm_2 (
    .Q1(P_Imm_q1[8]), .Q2(P_Imm_q1[9]), .Q3(P_Imm_q1[10]), .Q4(P_Imm_q1[11]), .Q5(P_Imm_q1[12]),
    .Q6(P_Imm_q1[13]), .Q7(P_Imm_q1[14]), .Q8(P_Imm_q1[15]), .I1(and_6_out), .I2(and_6_out), .I3(and_6_out),
    .I4(and_6_out), .I5(and_6_out), .I6(and_6_out), .I7(and_6_out), .I8(and_6_out), .nOE1(and_5_out),
    .nOE2(and_5_out));
  IC_74x541 J_Imm (
    .Q1(P_Imm_q1[0]), .Q2(P_Imm_q1[1]), .Q3(P_Imm_q1[2]), .Q4(P_Imm_q1[3]), .Q5(P_Imm_q1[4]),
    .Q6(P_Imm_q1[5]), .Q7(P_Imm_q1[6]), .Q8(P_Imm_q1[7]), .I1(IR[0]), .I2(IR[1]), .I3(IR[2]), .I4(IR[3]),
    .I5(IR[4]), .I6(IR[5]), .I7(IR[6]), .I8(IR[7]), .nOE1(B1_n), .nOE2(C3_n));
  IC_74x541 J_Imm_2 (
    .Q1(P_Imm_q1[8]), .Q2(P_Imm_q1[9]), .Q3(P_Imm_q1[10]), .Q4(P_Imm_q1[11]), .Q5(P_Imm_q1[12]),
    .Q6(P_Imm_q1[13]), .Q7(P_Imm_q1[14]), .Q8(P_Imm_q1[15]), .I1(IR[8]), .I2(IR[8]), .I3(IR[8]), .I4(IR[8]),
    .I5(IR[8]), .I6(IR[8]), .I7(IR[8]), .I8(IR[8]), .nOE1(B1_n), .nOE2(C3_n));
  Pull_Resistor pull_resistor_1 (.node(P_Imm_q1));
  IC_74273 PFIX_Reg (
    .Y2(PFIX_Reg_y1[6]), .Y3(PFIX_Reg_y1[7]), .Y1(PFIX_Reg_y1[5]), .Y4(PFIX_Reg_y1[8]), .Y5(PFIX_Reg_y1[9]),
    .Y6(PFIX_Reg_y1[10]), .Y7(PFIX_Reg_y1[11]), .Y8(PFIX_Reg_y1[12]), .D2(P_Imm_q1[1]), .D3(P_Imm_q1[2]),
    .D1(P_Imm_q1[0]), .D4(P_Imm_q1[3]), .D5(P_Imm_q1[4]), .D6(P_Imm_q1[5]), .D7(P_Imm_q1[6]),
    .D8(P_Imm_q1[7]), .CLK(CLK), .CLR(RESET));
  IC_74175 PFIX_Reg_2 (
    .Q2(PFIX_Reg_y1[14]), .Q3(PFIX_Reg_y1[15]), .Q1(PFIX_Reg_y1[13]), .Q4(PFIX_Reg_2_q4), .R4(PFIX_Reg_2_r4),
    .D2(P_Imm_q1[9]), .D3(P_Imm_q1[10]), .D1(P_Imm_q1[8]), .D4(and_1_out), .CLK(CLK), .CLR(RESET));  // open: R2, R3, R1
  nor nor_1 (C0, IR[11], IR[12]);
  nand nand_1 (C3_n, IR[11], IR[12]);
  not not_2 (IR12_n, IR[12]);
  IC_74138 ic_74138_1 (
    .Y0(B0_n), .Y1(B1_n), .Y2(B2_n), .Y3(B3_n), .Y4(B4_n), .Y5(B5_n), .Y6(B6_n), .Y7(B7_n), .A2(IR[15]),
    .A0(IR[13]), .OE1(1'b0), .OE2(1'b0), .OE3(1'b1), .A1(IR[14]));
  and and_7 (B7, IR[13], IR[14], IR[15]);
  IC_74x541 ic_74x541_1 (
    .Q1(IMM_OUT[0]), .Q2(IMM_OUT[1]), .Q3(IMM_OUT[2]), .Q4(IMM_OUT[3]), .Q5(IMM_OUT[4]), .Q6(IMM_OUT[5]),
    .Q7(IMM_OUT[6]), .Q8(IMM_OUT[7]), .I1(P_Imm_q1[0]), .I2(P_Imm_q1[1]), .I3(P_Imm_q1[2]), .I4(P_Imm_q1[3]),
    .I5(P_Imm_q1[4]), .I6(PFIX_Reg_y1[5]), .I7(PFIX_Reg_y1[6]), .I8(PFIX_Reg_y1[7]), .nOE1(PFIX_Reg_2_r4),
    .nOE2(nOE));
  IC_74x541 ic_74x541_2 (
    .Q1(IMM_OUT[8]), .Q2(IMM_OUT[9]), .Q3(IMM_OUT[10]), .Q4(IMM_OUT[11]), .Q5(IMM_OUT[12]), .Q6(IMM_OUT[13]),
    .Q7(IMM_OUT[14]), .Q8(IMM_OUT[15]), .I1(PFIX_Reg_y1[8]), .I2(PFIX_Reg_y1[9]), .I3(PFIX_Reg_y1[10]),
    .I4(PFIX_Reg_y1[11]), .I5(PFIX_Reg_y1[12]), .I6(PFIX_Reg_y1[13]), .I7(PFIX_Reg_y1[14]),
    .I8(PFIX_Reg_y1[15]), .nOE1(PFIX_Reg_2_r4), .nOE2(nOE));
  IC_74x541 ic_74x541_3 (
    .Q1(IMM_OUT[0]), .Q2(IMM_OUT[1]), .Q3(IMM_OUT[2]), .Q4(IMM_OUT[3]), .Q5(IMM_OUT[4]), .Q6(IMM_OUT[5]),
    .Q7(IMM_OUT[6]), .Q8(IMM_OUT[7]), .I1(P_Imm_q1[0]), .I2(P_Imm_q1[1]), .I3(P_Imm_q1[2]), .I4(P_Imm_q1[3]),
    .I5(P_Imm_q1[4]), .I6(P_Imm_q1[5]), .I7(P_Imm_q1[6]), .I8(P_Imm_q1[7]), .nOE1(PFIX_Reg_2_q4), .nOE2(nOE));
  IC_74x541 ic_74x541_4 (
    .Q1(IMM_OUT[8]), .Q2(IMM_OUT[9]), .Q3(IMM_OUT[10]), .Q4(IMM_OUT[11]), .Q5(IMM_OUT[12]), .Q6(IMM_OUT[13]),
    .Q7(IMM_OUT[14]), .Q8(IMM_OUT[15]), .I1(P_Imm_q1[8]), .I2(P_Imm_q1[9]), .I3(P_Imm_q1[10]),
    .I4(P_Imm_q1[11]), .I5(P_Imm_q1[12]), .I6(P_Imm_q1[13]), .I7(P_Imm_q1[14]), .I8(P_Imm_q1[15]),
    .nOE1(PFIX_Reg_2_q4), .nOE2(nOE));

  // Other names for the same wires on the sheet: CLR_n = RESET; OE_n = nOE
endmodule

// Register File
module Registers (
  input  CLK,
  input  nWR_RD,
  input  nRD_TO_A,
  input  nRS_TO_A,
  input  nRN_TO_B,
  input  [15:0] IN,
  input  [2:0] RD,
  input  [2:0] RS,
  input  [2:0] RN,
  output [15:0] REG_A,
  output [15:0] REG_B
);

  wire and_1_out, and_2_out, and_3_out, and_4_out, and_5_out, and_6_out, and_7_out, and_8_out,
       ic_74x138_1_y0, ic_74x138_1_y1, ic_74x138_1_y2, ic_74x138_1_y3, ic_74x138_1_y4, ic_74x138_1_y5,
       ic_74x138_1_y6, ic_74x138_1_y7, ic_74x138_2_y0, ic_74x138_2_y1, ic_74x138_2_y2, ic_74x138_2_y3,
       ic_74x138_2_y4, ic_74x138_2_y5, ic_74x138_2_y6, ic_74x138_2_y7, ic_74x138_3_y0, ic_74x138_3_y1,
       ic_74x138_3_y2, ic_74x138_3_y3, ic_74x138_3_y4, ic_74x138_3_y5, ic_74x138_3_y6, ic_74x138_3_y7,
       ic_74x138_5_y0, ic_74x138_5_y1, ic_74x138_5_y2, ic_74x138_5_y3, ic_74x138_5_y4, ic_74x138_5_y5,
       ic_74x138_5_y6, ic_74x138_5_y7, ic_74x563_1_q1, ic_74x563_1_q2, ic_74x563_1_q3, ic_74x563_1_q4,
       ic_74x563_1_q5, ic_74x563_1_q6, ic_74x563_1_q7, ic_74x563_1_q8, ic_74x573_1_q1, ic_74x573_1_q2,
       ic_74x573_1_q3, ic_74x573_1_q4, ic_74x573_1_q5, ic_74x573_1_q6, ic_74x573_1_q7, ic_74x573_1_q8, nCLK,
       not_2_out, sR0_A_n, sR0_B_n, sR1_A_n, sR1_B_n, sR2_A_n, sR2_B_n, sR3_A_n, sR3_B_n, sR4_A_n, sR4_B_n,
       sR5_A_n, sR5_B_n, sR6_A_n, sR6_B_n, sR7_A_n, sR7_B_n, WR_R0, WR_R1, WR_R2, WR_R3, WR_R4, WR_R5, WR_R6,
       WR_R7;

  not not_1 (nCLK, CLK);
  IC_74x574 R0_A (
    .Q2(REG_A[1]), .Q3(REG_A[2]), .Q4(REG_A[3]), .Q5(REG_A[4]), .Q6(REG_A[5]), .Q7(REG_A[6]), .Q8(REG_A[7]),
    .Q1(REG_A[0]), .D2(IN[1]), .D3(IN[2]), .D4(IN[3]), .D5(IN[4]), .D6(IN[5]), .D7(IN[6]), .D8(IN[7]),
    .CLK(WR_R0), .nOE(sR0_A_n), .D1(IN[0]));  // open: Probe
  IC_74x574 R0_A_2 (
    .Q2(REG_A[9]), .Q3(REG_A[10]), .Q4(REG_A[11]), .Q5(REG_A[12]), .Q6(REG_A[13]), .Q7(REG_A[14]),
    .Q8(REG_A[15]), .Q1(REG_A[8]), .D2(IN[9]), .D3(IN[10]), .D4(IN[11]), .D5(IN[12]), .D6(IN[13]),
    .D7(IN[14]), .D8(IN[15]), .CLK(WR_R0), .nOE(sR0_A_n), .D1(IN[8]));  // open: Probe
  IC_74x574 R1_A (
    .Q2(REG_A[1]), .Q3(REG_A[2]), .Q4(REG_A[3]), .Q5(REG_A[4]), .Q6(REG_A[5]), .Q7(REG_A[6]), .Q8(REG_A[7]),
    .Q1(REG_A[0]), .D2(IN[1]), .D3(IN[2]), .D4(IN[3]), .D5(IN[4]), .D6(IN[5]), .D7(IN[6]), .D8(IN[7]),
    .CLK(WR_R1), .nOE(sR1_A_n), .D1(IN[0]));  // open: Probe
  IC_74x574 R1_A_2 (
    .Q2(REG_A[9]), .Q3(REG_A[10]), .Q4(REG_A[11]), .Q5(REG_A[12]), .Q6(REG_A[13]), .Q7(REG_A[14]),
    .Q8(REG_A[15]), .Q1(REG_A[8]), .D2(IN[9]), .D3(IN[10]), .D4(IN[11]), .D5(IN[12]), .D6(IN[13]),
    .D7(IN[14]), .D8(IN[15]), .CLK(WR_R1), .nOE(sR1_A_n), .D1(IN[8]));  // open: Probe
  IC_74x574 R2_A (
    .Q2(REG_A[1]), .Q3(REG_A[2]), .Q4(REG_A[3]), .Q5(REG_A[4]), .Q6(REG_A[5]), .Q7(REG_A[6]), .Q8(REG_A[7]),
    .Q1(REG_A[0]), .D2(IN[1]), .D3(IN[2]), .D4(IN[3]), .D5(IN[4]), .D6(IN[5]), .D7(IN[6]), .D8(IN[7]),
    .CLK(WR_R2), .nOE(sR2_A_n), .D1(IN[0]));  // open: Probe
  IC_74x574 R2_A_2 (
    .Q2(REG_A[9]), .Q3(REG_A[10]), .Q4(REG_A[11]), .Q5(REG_A[12]), .Q6(REG_A[13]), .Q7(REG_A[14]),
    .Q8(REG_A[15]), .Q1(REG_A[8]), .D2(IN[9]), .D3(IN[10]), .D4(IN[11]), .D5(IN[12]), .D6(IN[13]),
    .D7(IN[14]), .D8(IN[15]), .CLK(WR_R2), .nOE(sR2_A_n), .D1(IN[8]));  // open: Probe
  IC_74x574 R3_A (
    .Q2(REG_A[1]), .Q3(REG_A[2]), .Q4(REG_A[3]), .Q5(REG_A[4]), .Q6(REG_A[5]), .Q7(REG_A[6]), .Q8(REG_A[7]),
    .Q1(REG_A[0]), .D2(IN[1]), .D3(IN[2]), .D4(IN[3]), .D5(IN[4]), .D6(IN[5]), .D7(IN[6]), .D8(IN[7]),
    .CLK(WR_R3), .nOE(sR3_A_n), .D1(IN[0]));  // open: Probe
  IC_74x574 R3_A_2 (
    .Q2(REG_A[9]), .Q3(REG_A[10]), .Q4(REG_A[11]), .Q5(REG_A[12]), .Q6(REG_A[13]), .Q7(REG_A[14]),
    .Q8(REG_A[15]), .Q1(REG_A[8]), .D2(IN[9]), .D3(IN[10]), .D4(IN[11]), .D5(IN[12]), .D6(IN[13]),
    .D7(IN[14]), .D8(IN[15]), .CLK(WR_R3), .nOE(sR3_A_n), .D1(IN[8]));  // open: Probe
  IC_74x138 ic_74x138_1 (
    .Y0(ic_74x138_1_y0), .Y1(ic_74x138_1_y1), .Y2(ic_74x138_1_y2), .Y3(ic_74x138_1_y3), .Y4(ic_74x138_1_y4),
    .Y5(ic_74x138_1_y5), .Y6(ic_74x138_1_y6), .Y7(ic_74x138_1_y7), .A(RD[0]), .B(RD[1]), .C(RD[2]),
    .nG2A(nWR_RD), .nG2B(1'b0), .G1(1'b1));
  IC_74x138 ic_74x138_2 (
    .Y0(ic_74x138_2_y0), .Y1(ic_74x138_2_y1), .Y2(ic_74x138_2_y2), .Y3(ic_74x138_2_y3), .Y4(ic_74x138_2_y4),
    .Y5(ic_74x138_2_y5), .Y6(ic_74x138_2_y6), .Y7(ic_74x138_2_y7), .A(RD[0]), .B(RD[1]), .C(RD[2]),
    .nG2A(nRD_TO_A), .nG2B(1'b0), .G1(1'b1));
  IC_74x138 ic_74x138_3 (
    .Y0(ic_74x138_3_y0), .Y1(ic_74x138_3_y1), .Y2(ic_74x138_3_y2), .Y3(ic_74x138_3_y3), .Y4(ic_74x138_3_y4),
    .Y5(ic_74x138_3_y5), .Y6(ic_74x138_3_y6), .Y7(ic_74x138_3_y7), .A(RS[0]), .B(RS[1]), .C(RS[2]),
    .nG2A(nRS_TO_A), .nG2B(1'b0), .G1(1'b1));
  IC_74x138 ic_74x138_4 (
    .Y0(sR0_B_n), .Y1(sR1_B_n), .Y2(sR2_B_n), .Y3(sR3_B_n), .Y4(sR4_B_n), .Y5(sR5_B_n), .Y6(sR6_B_n),
    .Y7(sR7_B_n), .A(RN[0]), .B(RN[1]), .C(RN[2]), .nG2A(nRN_TO_B), .nG2B(1'b0), .G1(1'b1));
  IC_74x574 RO_B (
    .Q2(REG_B[1]), .Q3(REG_B[2]), .Q4(REG_B[3]), .Q5(REG_B[4]), .Q6(REG_B[5]), .Q7(REG_B[6]), .Q8(REG_B[7]),
    .Q1(REG_B[0]), .D2(IN[1]), .D3(IN[2]), .D4(IN[3]), .D5(IN[4]), .D6(IN[5]), .D7(IN[6]), .D8(IN[7]),
    .CLK(WR_R0), .nOE(sR0_B_n), .D1(IN[0]));  // open: Probe
  IC_74x574 R0_B (
    .Q2(REG_B[9]), .Q3(REG_B[10]), .Q4(REG_B[11]), .Q5(REG_B[12]), .Q6(REG_B[13]), .Q7(REG_B[14]),
    .Q8(REG_B[15]), .Q1(REG_B[8]), .D2(IN[9]), .D3(IN[10]), .D4(IN[11]), .D5(IN[12]), .D6(IN[13]),
    .D7(IN[14]), .D8(IN[15]), .CLK(WR_R0), .nOE(sR0_B_n), .D1(IN[8]));  // open: Probe
  IC_74x574 R1_B (
    .Q2(REG_B[1]), .Q3(REG_B[2]), .Q4(REG_B[3]), .Q5(REG_B[4]), .Q6(REG_B[5]), .Q7(REG_B[6]), .Q8(REG_B[7]),
    .Q1(REG_B[0]), .D2(IN[1]), .D3(IN[2]), .D4(IN[3]), .D5(IN[4]), .D6(IN[5]), .D7(IN[6]), .D8(IN[7]),
    .CLK(WR_R1), .nOE(sR1_B_n), .D1(IN[0]));  // open: Probe
  IC_74x574 R1_B_2 (
    .Q2(REG_B[9]), .Q3(REG_B[10]), .Q4(REG_B[11]), .Q5(REG_B[12]), .Q6(REG_B[13]), .Q7(REG_B[14]),
    .Q8(REG_B[15]), .Q1(REG_B[8]), .D2(IN[9]), .D3(IN[10]), .D4(IN[11]), .D5(IN[12]), .D6(IN[13]),
    .D7(IN[14]), .D8(IN[15]), .CLK(WR_R1), .nOE(sR1_B_n), .D1(IN[8]));  // open: Probe
  IC_74x574 R2_B (
    .Q2(REG_B[1]), .Q3(REG_B[2]), .Q4(REG_B[3]), .Q5(REG_B[4]), .Q6(REG_B[5]), .Q7(REG_B[6]), .Q8(REG_B[7]),
    .Q1(REG_B[0]), .D2(IN[1]), .D3(IN[2]), .D4(IN[3]), .D5(IN[4]), .D6(IN[5]), .D7(IN[6]), .D8(IN[7]),
    .CLK(WR_R2), .nOE(sR2_B_n), .D1(IN[0]));  // open: Probe
  IC_74x574 R2_B_2 (
    .Q2(REG_B[9]), .Q3(REG_B[10]), .Q4(REG_B[11]), .Q5(REG_B[12]), .Q6(REG_B[13]), .Q7(REG_B[14]),
    .Q8(REG_B[15]), .Q1(REG_B[8]), .D2(IN[9]), .D3(IN[10]), .D4(IN[11]), .D5(IN[12]), .D6(IN[13]),
    .D7(IN[14]), .D8(IN[15]), .CLK(WR_R2), .nOE(sR2_B_n), .D1(IN[8]));  // open: Probe
  IC_74x574 R3_B (
    .Q2(REG_B[1]), .Q3(REG_B[2]), .Q4(REG_B[3]), .Q5(REG_B[4]), .Q6(REG_B[5]), .Q7(REG_B[6]), .Q8(REG_B[7]),
    .Q1(REG_B[0]), .D2(IN[1]), .D3(IN[2]), .D4(IN[3]), .D5(IN[4]), .D6(IN[5]), .D7(IN[6]), .D8(IN[7]),
    .CLK(WR_R3), .nOE(sR3_B_n), .D1(IN[0]));  // open: Probe
  IC_74x574 R3_B_2 (
    .Q2(REG_B[9]), .Q3(REG_B[10]), .Q4(REG_B[11]), .Q5(REG_B[12]), .Q6(REG_B[13]), .Q7(REG_B[14]),
    .Q8(REG_B[15]), .Q1(REG_B[8]), .D2(IN[9]), .D3(IN[10]), .D4(IN[11]), .D5(IN[12]), .D6(IN[13]),
    .D7(IN[14]), .D8(IN[15]), .CLK(WR_R3), .nOE(sR3_B_n), .D1(IN[8]));  // open: Probe
  IC_74x573 ic_74x573_1 (
    .Q2(ic_74x573_1_q2), .Q3(ic_74x573_1_q3), .Q4(ic_74x573_1_q4), .Q5(ic_74x573_1_q5), .Q6(ic_74x573_1_q6),
    .Q7(ic_74x573_1_q7), .Q8(ic_74x573_1_q8), .Q1(ic_74x573_1_q1), .D2(ic_74x138_1_y1), .D3(ic_74x138_1_y2),
    .D4(ic_74x138_1_y3), .D5(ic_74x138_1_y4), .D6(ic_74x138_1_y5), .D7(ic_74x138_1_y6), .D8(ic_74x138_1_y7),
    .LE(nCLK), .nOE(1'b0), .D1(ic_74x138_1_y0));  // open: Probe
  nor nor_1 (WR_R0, nCLK, ic_74x573_1_q1);
  nor nor_2 (WR_R1, nCLK, ic_74x573_1_q2);
  nor nor_3 (WR_R2, nCLK, ic_74x573_1_q3);
  nor nor_4 (WR_R3, nCLK, ic_74x573_1_q4);
  nor nor_5 (WR_R4, nCLK, ic_74x573_1_q5);
  nor nor_6 (WR_R5, nCLK, ic_74x573_1_q6);
  nor nor_7 (WR_R6, nCLK, ic_74x573_1_q7);
  nor nor_8 (WR_R7, nCLK, ic_74x573_1_q8);
  IC_74x3257 ic_74x3257_1 (
    .A1(sR0_A_n), .A2(sR1_A_n), .A3(sR2_A_n), .A4(sR3_A_n), .B2_1(ic_74x138_3_y0), .B1_2(ic_74x138_2_y1),
    .B2_2(ic_74x138_3_y1), .B1_3(ic_74x138_2_y2), .B2_3(ic_74x138_3_y2), .B1_4(ic_74x138_2_y3),
    .B2_4(ic_74x138_3_y3), .S(nRD_TO_A), .nOE(1'b0), .B1_1(ic_74x138_2_y0));
  IC_74x3257 ic_74x3257_2 (
    .A1(sR4_A_n), .A2(sR5_A_n), .A3(sR6_A_n), .A4(sR7_A_n), .B2_1(ic_74x138_3_y4), .B1_2(ic_74x138_2_y5),
    .B2_2(ic_74x138_3_y5), .B1_3(ic_74x138_2_y6), .B2_3(ic_74x138_3_y6), .B1_4(ic_74x138_2_y7),
    .B2_4(ic_74x138_3_y7), .S(nRD_TO_A), .nOE(1'b0), .B1_1(ic_74x138_2_y4));
  IC_74x574 R4_A (
    .Q2(REG_A[1]), .Q3(REG_A[2]), .Q4(REG_A[3]), .Q5(REG_A[4]), .Q6(REG_A[5]), .Q7(REG_A[6]), .Q8(REG_A[7]),
    .Q1(REG_A[0]), .D2(IN[1]), .D3(IN[2]), .D4(IN[3]), .D5(IN[4]), .D6(IN[5]), .D7(IN[6]), .D8(IN[7]),
    .CLK(WR_R4), .nOE(sR4_A_n), .D1(IN[0]));  // open: Probe
  IC_74x574 R4_A_2 (
    .Q2(REG_A[9]), .Q3(REG_A[10]), .Q4(REG_A[11]), .Q5(REG_A[12]), .Q6(REG_A[13]), .Q7(REG_A[14]),
    .Q8(REG_A[15]), .Q1(REG_A[8]), .D2(IN[9]), .D3(IN[10]), .D4(IN[11]), .D5(IN[12]), .D6(IN[13]),
    .D7(IN[14]), .D8(IN[15]), .CLK(WR_R4), .nOE(sR4_A_n), .D1(IN[8]));  // open: Probe
  IC_74x574 R5_A (
    .Q2(REG_A[1]), .Q3(REG_A[2]), .Q4(REG_A[3]), .Q5(REG_A[4]), .Q6(REG_A[5]), .Q7(REG_A[6]), .Q8(REG_A[7]),
    .Q1(REG_A[0]), .D2(IN[1]), .D3(IN[2]), .D4(IN[3]), .D5(IN[4]), .D6(IN[5]), .D7(IN[6]), .D8(IN[7]),
    .CLK(WR_R5), .nOE(sR5_A_n), .D1(IN[0]));  // open: Probe
  IC_74x574 R5_A_2 (
    .Q2(REG_A[9]), .Q3(REG_A[10]), .Q4(REG_A[11]), .Q5(REG_A[12]), .Q6(REG_A[13]), .Q7(REG_A[14]),
    .Q8(REG_A[15]), .Q1(REG_A[8]), .D2(IN[9]), .D3(IN[10]), .D4(IN[11]), .D5(IN[12]), .D6(IN[13]),
    .D7(IN[14]), .D8(IN[15]), .CLK(WR_R5), .nOE(sR5_A_n), .D1(IN[8]));  // open: Probe
  IC_74x574 R6_A (
    .Q2(REG_A[1]), .Q3(REG_A[2]), .Q4(REG_A[3]), .Q5(REG_A[4]), .Q6(REG_A[5]), .Q7(REG_A[6]), .Q8(REG_A[7]),
    .Q1(REG_A[0]), .D2(IN[1]), .D3(IN[2]), .D4(IN[3]), .D5(IN[4]), .D6(IN[5]), .D7(IN[6]), .D8(IN[7]),
    .CLK(WR_R6), .nOE(sR6_A_n), .D1(IN[0]));  // open: Probe
  IC_74x574 R6_A_2 (
    .Q2(REG_A[9]), .Q3(REG_A[10]), .Q4(REG_A[11]), .Q5(REG_A[12]), .Q6(REG_A[13]), .Q7(REG_A[14]),
    .Q8(REG_A[15]), .Q1(REG_A[8]), .D2(IN[9]), .D3(IN[10]), .D4(IN[11]), .D5(IN[12]), .D6(IN[13]),
    .D7(IN[14]), .D8(IN[15]), .CLK(WR_R6), .nOE(sR6_A_n), .D1(IN[8]));  // open: Probe
  IC_74x574 R7_A (
    .Q2(REG_A[1]), .Q3(REG_A[2]), .Q4(REG_A[3]), .Q5(REG_A[4]), .Q6(REG_A[5]), .Q7(REG_A[6]), .Q8(REG_A[7]),
    .Q1(REG_A[0]), .D2(IN[1]), .D3(IN[2]), .D4(IN[3]), .D5(IN[4]), .D6(IN[5]), .D7(IN[6]), .D8(IN[7]),
    .CLK(WR_R7), .nOE(sR7_A_n), .D1(IN[0]));  // open: Probe
  IC_74x574 R8_A (
    .Q2(REG_A[9]), .Q3(REG_A[10]), .Q4(REG_A[11]), .Q5(REG_A[12]), .Q6(REG_A[13]), .Q7(REG_A[14]),
    .Q8(REG_A[15]), .Q1(REG_A[8]), .D2(IN[9]), .D3(IN[10]), .D4(IN[11]), .D5(IN[12]), .D6(IN[13]),
    .D7(IN[14]), .D8(IN[15]), .CLK(WR_R7), .nOE(sR7_A_n), .D1(IN[8]));  // open: Probe
  IC_74x138 ic_74x138_5 (
    .Y0(ic_74x138_5_y0), .Y1(ic_74x138_5_y1), .Y2(ic_74x138_5_y2), .Y3(ic_74x138_5_y3), .Y4(ic_74x138_5_y4),
    .Y5(ic_74x138_5_y5), .Y6(ic_74x138_5_y6), .Y7(ic_74x138_5_y7), .A(RD[0]), .B(RD[1]), .C(RD[2]),
    .nG2A(nWR_RD), .nG2B(1'b0), .G1(1'b1));
  IC_74x574 R4_B (
    .Q2(REG_B[1]), .Q3(REG_B[2]), .Q4(REG_B[3]), .Q5(REG_B[4]), .Q6(REG_B[5]), .Q7(REG_B[6]), .Q8(REG_B[7]),
    .Q1(REG_B[0]), .D2(IN[1]), .D3(IN[2]), .D4(IN[3]), .D5(IN[4]), .D6(IN[5]), .D7(IN[6]), .D8(IN[7]),
    .CLK(WR_R4), .nOE(sR4_B_n), .D1(IN[0]));  // open: Probe
  IC_74x574 R4_B_2 (
    .Q2(REG_B[9]), .Q3(REG_B[10]), .Q4(REG_B[11]), .Q5(REG_B[12]), .Q6(REG_B[13]), .Q7(REG_B[14]),
    .Q8(REG_B[15]), .Q1(REG_B[8]), .D2(IN[9]), .D3(IN[10]), .D4(IN[11]), .D5(IN[12]), .D6(IN[13]),
    .D7(IN[14]), .D8(IN[15]), .CLK(WR_R4), .nOE(sR4_B_n), .D1(IN[8]));  // open: Probe
  IC_74x574 R5_B (
    .Q2(REG_B[1]), .Q3(REG_B[2]), .Q4(REG_B[3]), .Q5(REG_B[4]), .Q6(REG_B[5]), .Q7(REG_B[6]), .Q8(REG_B[7]),
    .Q1(REG_B[0]), .D2(IN[1]), .D3(IN[2]), .D4(IN[3]), .D5(IN[4]), .D6(IN[5]), .D7(IN[6]), .D8(IN[7]),
    .CLK(WR_R5), .nOE(sR5_B_n), .D1(IN[0]));  // open: Probe
  IC_74x574 R5_B_2 (
    .Q2(REG_B[9]), .Q3(REG_B[10]), .Q4(REG_B[11]), .Q5(REG_B[12]), .Q6(REG_B[13]), .Q7(REG_B[14]),
    .Q8(REG_B[15]), .Q1(REG_B[8]), .D2(IN[9]), .D3(IN[10]), .D4(IN[11]), .D5(IN[12]), .D6(IN[13]),
    .D7(IN[14]), .D8(IN[15]), .CLK(WR_R5), .nOE(sR5_B_n), .D1(IN[8]));  // open: Probe
  IC_74x574 R6_B (
    .Q2(REG_B[1]), .Q3(REG_B[2]), .Q4(REG_B[3]), .Q5(REG_B[4]), .Q6(REG_B[5]), .Q7(REG_B[6]), .Q8(REG_B[7]),
    .Q1(REG_B[0]), .D2(IN[1]), .D3(IN[2]), .D4(IN[3]), .D5(IN[4]), .D6(IN[5]), .D7(IN[6]), .D8(IN[7]),
    .CLK(WR_R6), .nOE(sR6_B_n), .D1(IN[0]));  // open: Probe
  IC_74x574 R6_B_2 (
    .Q2(REG_B[9]), .Q3(REG_B[10]), .Q4(REG_B[11]), .Q5(REG_B[12]), .Q6(REG_B[13]), .Q7(REG_B[14]),
    .Q8(REG_B[15]), .Q1(REG_B[8]), .D2(IN[9]), .D3(IN[10]), .D4(IN[11]), .D5(IN[12]), .D6(IN[13]),
    .D7(IN[14]), .D8(IN[15]), .CLK(WR_R6), .nOE(sR6_B_n), .D1(IN[8]));  // open: Probe
  IC_74x574 R7_B (
    .Q2(REG_B[1]), .Q3(REG_B[2]), .Q4(REG_B[3]), .Q5(REG_B[4]), .Q6(REG_B[5]), .Q7(REG_B[6]), .Q8(REG_B[7]),
    .Q1(REG_B[0]), .D2(IN[1]), .D3(IN[2]), .D4(IN[3]), .D5(IN[4]), .D6(IN[5]), .D7(IN[6]), .D8(IN[7]),
    .CLK(WR_R7), .nOE(sR7_B_n), .D1(IN[0]));  // open: Probe
  IC_74x574 R8_B (
    .Q2(REG_B[9]), .Q3(REG_B[10]), .Q4(REG_B[11]), .Q5(REG_B[12]), .Q6(REG_B[13]), .Q7(REG_B[14]),
    .Q8(REG_B[15]), .Q1(REG_B[8]), .D2(IN[9]), .D3(IN[10]), .D4(IN[11]), .D5(IN[12]), .D6(IN[13]),
    .D7(IN[14]), .D8(IN[15]), .CLK(WR_R7), .nOE(sR7_B_n), .D1(IN[8]));  // open: Probe
  not not_2 (not_2_out, CLK);
  IC_74x563 ic_74x563_1 (
    .Q2(ic_74x563_1_q2), .Q3(ic_74x563_1_q3), .Q4(ic_74x563_1_q4), .Q5(ic_74x563_1_q5), .Q6(ic_74x563_1_q6),
    .Q7(ic_74x563_1_q7), .Q8(ic_74x563_1_q8), .Q1(ic_74x563_1_q1), .D2(ic_74x138_5_y1), .D3(ic_74x138_5_y2),
    .D4(ic_74x138_5_y3), .D5(ic_74x138_5_y4), .D6(ic_74x138_5_y5), .D7(ic_74x138_5_y6), .D8(ic_74x138_5_y7),
    .LE(not_2_out), .nOE(1'b0), .D1(ic_74x138_5_y0));  // open: Probe
  and and_1 (and_1_out, CLK, ic_74x563_1_q1);
  and and_2 (and_2_out, CLK, ic_74x563_1_q2);
  and and_3 (and_3_out, CLK, ic_74x563_1_q3);
  and and_4 (and_4_out, CLK, ic_74x563_1_q4);
  and and_5 (and_5_out, CLK, ic_74x563_1_q5);
  and and_6 (and_6_out, CLK, ic_74x563_1_q6);
  and and_7 (and_7_out, CLK, ic_74x563_1_q7);
  and and_8 (and_8_out, CLK, ic_74x563_1_q8);

  // Other names for the same wires on the sheet: RD_A_n = nRD_TO_A; RN_B_n = nRN_TO_B; RS_A_n = nRS_TO_A
endmodule

// SR
module RegSR (
  input  CLK,
  input  nWR_SR,
  input  Zin,
  input  Cin,
  input  Tin,
  output SR_Z,
  output SR_C,
  output SR_T
);

  wire and_1_out, CLK_WR, d_latch_1_q, d_latch_2_q, nCLK, not_3_out, WR_SR;

  not not_1 (nCLK, CLK);
  not not_2 (WR_SR, nWR_SR);
  IC_74x574 SR (
    .Q2(SR_C), .Q3(SR_T), .Q1(SR_Z), .D2(Cin), .D3(Tin), .D4(1'b0), .D5(1'b0), .D6(1'b0), .D7(1'b0),
    .D8(1'b0), .CLK(CLK_WR), .nOE(1'b0), .D1(Zin));  // open: Probe, Q4, Q5, Q6, Q7, Q8
  D_Latch d_latch_1 (.Q(d_latch_1_q), .D(nWR_SR), .LE(nCLK));  // open: R, SET, CLR
  D_Latch d_latch_2 (.Q(d_latch_2_q), .D(WR_SR), .LE(not_3_out));  // open: R, SET, CLR
  not not_3 (not_3_out, CLK);
  nor nor_1 (CLK_WR, nCLK, d_latch_1_q);
  and and_1 (and_1_out, CLK, d_latch_2_q);
endmodule

// IR
module RegIR (
  input  CLK,
  input  nWR_IR,
  input  [15:0] IN,
  output [15:0] IR_OUT
);

  wire and_1_out, CLK_WR, d_latch_1_q, d_latch_2_q, nCLK, not_3_out, WR_IR;

  not not_1 (nCLK, CLK);
  not not_2 (WR_IR, nWR_IR);
  IC_74x574 IR (
    .Q2(IR_OUT[1]), .Q3(IR_OUT[2]), .Q4(IR_OUT[3]), .Q5(IR_OUT[4]), .Q6(IR_OUT[5]), .Q7(IR_OUT[6]),
    .Q8(IR_OUT[7]), .Q1(IR_OUT[0]), .D2(IN[1]), .D3(IN[2]), .D4(IN[3]), .D5(IN[4]), .D6(IN[5]), .D7(IN[6]),
    .D8(IN[7]), .CLK(CLK_WR), .nOE(1'b0), .D1(IN[0]));  // open: Probe
  IC_74x574 IR_2 (
    .Q2(IR_OUT[9]), .Q3(IR_OUT[10]), .Q4(IR_OUT[11]), .Q5(IR_OUT[12]), .Q6(IR_OUT[13]), .Q7(IR_OUT[14]),
    .Q8(IR_OUT[15]), .Q1(IR_OUT[8]), .D2(IN[9]), .D3(IN[10]), .D4(IN[11]), .D5(IN[12]), .D6(IN[13]),
    .D7(IN[14]), .D8(IN[15]), .CLK(CLK_WR), .nOE(1'b0), .D1(IN[8]));  // open: Probe
  D_Latch d_latch_1 (.Q(d_latch_1_q), .D(nWR_IR), .LE(nCLK));  // open: R, SET, CLR
  D_Latch d_latch_2 (.Q(d_latch_2_q), .D(WR_IR), .LE(not_3_out));  // open: R, SET, CLR
  not not_3 (not_3_out, CLK);
  nor nor_1 (CLK_WR, nCLK, d_latch_1_q);
  and and_1 (and_1_out, CLK, d_latch_2_q);
endmodule

module RegPC (
  input  CLK,
  input  RESET,
  input  nWR_PC,
  input  nWR_PMAR,
  input  BR,
  input  [15:0] IN,
  output [15:0] PC_OUT
);

  wire CLK_WRPC, CLK_WRPMAR, d_latch_1_q, d_latch_2_q, ic_74283_1_cout, ic_74283_2_cout, ic_74283_3_cout,
       nOE_PMAR, not_1_out;
  wire [3:0] ic_74283_1_y1;
  wire [7:4] ic_74283_2_y1;
  wire [11:8] ic_74283_3_y1;
  wire [15:0] ic_74x3257_1_a1, PC_q1;
  wire [15:12] ic_74283_4_y1;

  IC_74x273 PC (
    .Q1(PC_q1[0]), .Q2(PC_q1[1]), .Q3(PC_q1[2]), .Q4(PC_q1[3]), .Q5(PC_q1[4]), .Q6(PC_q1[5]), .Q7(PC_q1[6]),
    .Q8(PC_q1[7]), .D1(ic_74x3257_1_a1[0]), .D2(ic_74x3257_1_a1[1]), .D3(ic_74x3257_1_a1[2]),
    .D4(ic_74x3257_1_a1[3]), .D5(ic_74x3257_1_a1[4]), .D6(ic_74x3257_1_a1[5]), .D7(ic_74x3257_1_a1[6]),
    .D8(ic_74x3257_1_a1[7]), .CLK(CLK_WRPC), .nMR(RESET));  // open: Probe
  IC_74x273 PC_2 (
    .Q1(PC_q1[8]), .Q2(PC_q1[9]), .Q3(PC_q1[10]), .Q4(PC_q1[11]), .Q5(PC_q1[12]), .Q6(PC_q1[13]),
    .Q7(PC_q1[14]), .Q8(PC_q1[15]), .D1(ic_74x3257_1_a1[8]), .D2(ic_74x3257_1_a1[9]),
    .D3(ic_74x3257_1_a1[10]), .D4(ic_74x3257_1_a1[11]), .D5(ic_74x3257_1_a1[12]), .D6(ic_74x3257_1_a1[13]),
    .D7(ic_74x3257_1_a1[14]), .D8(ic_74x3257_1_a1[15]), .CLK(CLK_WRPC), .nMR(RESET));  // open: Probe
  IC_74x574 PMAR (
    .Q2(PC_OUT[1]), .Q3(PC_OUT[2]), .Q4(PC_OUT[3]), .Q5(PC_OUT[4]), .Q6(PC_OUT[5]), .Q7(PC_OUT[6]),
    .Q8(PC_OUT[7]), .Q1(PC_OUT[0]), .D2(IN[1]), .D3(IN[2]), .D4(IN[3]), .D5(IN[4]), .D6(IN[5]), .D7(IN[6]),
    .D8(IN[7]), .CLK(CLK_WRPMAR), .nOE(nOE_PMAR), .D1(IN[0]));  // open: Probe
  IC_74x574 PMAR_2 (
    .Q2(PC_OUT[9]), .Q3(PC_OUT[10]), .Q4(PC_OUT[11]), .Q5(PC_OUT[12]), .Q6(PC_OUT[13]), .Q7(PC_OUT[14]),
    .Q8(PC_OUT[15]), .Q1(PC_OUT[8]), .D2(IN[9]), .D3(IN[10]), .D4(IN[11]), .D5(IN[12]), .D6(IN[13]),
    .D7(IN[14]), .D8(IN[15]), .CLK(CLK_WRPMAR), .nOE(nOE_PMAR), .D1(IN[8]));  // open: Probe
  IC_74283 ic_74283_1 (
    .Y2(ic_74283_1_y1[1]), .Y3(ic_74283_1_y1[2]), .Y4(ic_74283_1_y1[3]), .Y1(ic_74283_1_y1[0]),
    .COUT(ic_74283_1_cout), .A3(PC_q1[2]), .A4(PC_q1[3]), .B1(1'b0), .B2(1'b0), .A1(PC_q1[0]), .B3(1'b0),
    .B4(1'b0), .CIN(1'b1), .A2(PC_q1[1]));
  IC_74283 ic_74283_2 (
    .Y2(ic_74283_2_y1[5]), .Y3(ic_74283_2_y1[6]), .Y4(ic_74283_2_y1[7]), .Y1(ic_74283_2_y1[4]),
    .COUT(ic_74283_2_cout), .A3(PC_q1[6]), .A4(PC_q1[7]), .B1(1'b0), .B2(1'b0), .A1(PC_q1[4]), .B3(1'b0),
    .B4(1'b0), .CIN(ic_74283_1_cout), .A2(PC_q1[5]));
  IC_74x3257 ic_74x3257_1 (
    .A1(ic_74x3257_1_a1[0]), .A2(ic_74x3257_1_a1[1]), .A3(ic_74x3257_1_a1[2]), .A4(ic_74x3257_1_a1[3]),
    .B2_1(IN[0]), .B1_2(ic_74283_1_y1[1]), .B2_2(IN[1]), .B1_3(ic_74283_1_y1[2]), .B2_3(IN[2]),
    .B1_4(ic_74283_1_y1[3]), .B2_4(IN[3]), .S(BR), .nOE(1'b0), .B1_1(ic_74283_1_y1[0]));
  not not_1 (not_1_out, CLK);
  IC_74283 ic_74283_3 (
    .Y2(ic_74283_3_y1[9]), .Y3(ic_74283_3_y1[10]), .Y4(ic_74283_3_y1[11]), .Y1(ic_74283_3_y1[8]),
    .COUT(ic_74283_3_cout), .A3(PC_q1[10]), .A4(PC_q1[11]), .B1(1'b0), .B2(1'b0), .A1(PC_q1[8]), .B3(1'b0),
    .B4(1'b0), .CIN(ic_74283_2_cout), .A2(PC_q1[9]));
  IC_74x3257 ic_74x3257_2 (
    .A1(ic_74x3257_1_a1[4]), .A2(ic_74x3257_1_a1[5]), .A3(ic_74x3257_1_a1[6]), .A4(ic_74x3257_1_a1[7]),
    .B2_1(IN[4]), .B1_2(ic_74283_2_y1[5]), .B2_2(IN[5]), .B1_3(ic_74283_2_y1[6]), .B2_3(IN[6]),
    .B1_4(ic_74283_2_y1[7]), .B2_4(IN[7]), .S(BR), .nOE(1'b0), .B1_1(ic_74283_2_y1[4]));
  D_Latch d_latch_1 (.Q(d_latch_1_q), .D(nWR_PC), .LE(not_1_out));  // open: R, SET, CLR
  D_Latch d_latch_2 (.Q(d_latch_2_q), .D(nWR_PMAR), .LE(not_1_out));  // open: R, SET, CLR
  D_Flip_Flop d_flip_flop_1 (.Q(nOE_PMAR), .D(nWR_PMAR), .CLK(CLK));  // open: R, SET, CLR
  nor nor_1 (CLK_WRPC, d_latch_1_q, not_1_out);
  nor nor_2 (CLK_WRPMAR, d_latch_2_q, not_1_out);
  IC_74283 ic_74283_4 (
    .Y2(ic_74283_4_y1[13]), .Y3(ic_74283_4_y1[14]), .Y4(ic_74283_4_y1[15]), .Y1(ic_74283_4_y1[12]),
    .A3(PC_q1[14]), .A4(PC_q1[15]), .B1(1'b0), .B2(1'b0), .A1(PC_q1[12]), .B3(1'b0), .B4(1'b0),
    .CIN(ic_74283_3_cout), .A2(PC_q1[13]));  // open: COUT
  IC_74x3257 ic_74x3257_3 (
    .A1(ic_74x3257_1_a1[8]), .A2(ic_74x3257_1_a1[9]), .A3(ic_74x3257_1_a1[10]), .A4(ic_74x3257_1_a1[11]),
    .B2_1(IN[8]), .B1_2(ic_74283_3_y1[9]), .B2_2(IN[9]), .B1_3(ic_74283_3_y1[10]), .B2_3(IN[10]),
    .B1_4(ic_74283_3_y1[11]), .B2_4(IN[11]), .S(BR), .nOE(1'b0), .B1_1(ic_74283_3_y1[8]));
  IC_74x3257 ic_74x3257_4 (
    .A1(ic_74x3257_1_a1[12]), .A2(ic_74x3257_1_a1[13]), .A3(ic_74x3257_1_a1[14]), .A4(ic_74x3257_1_a1[15]),
    .B2_1(IN[12]), .B1_2(ic_74283_4_y1[13]), .B2_2(IN[13]), .B1_3(ic_74283_4_y1[14]), .B2_3(IN[14]),
    .B1_4(ic_74283_4_y1[15]), .B2_4(IN[15]), .S(BR), .nOE(1'b0), .B1_1(ic_74283_4_y1[12]));
  IC_74x3345 ic_74x3345_1 (
    .A3(PC_OUT[2]), .A4(PC_OUT[3]), .A5(PC_OUT[4]), .A6(PC_OUT[5]), .A7(PC_OUT[6]), .A8(PC_OUT[7]),
    .A1(PC_OUT[0]), .A2(PC_OUT[1]), .B3(PC_q1[2]), .B4(PC_q1[3]), .B5(PC_q1[4]), .B6(PC_q1[5]),
    .B7(PC_q1[6]), .B8(PC_q1[7]), .OE(nOE_PMAR), .nOE(1'b1), .B1(PC_q1[0]), .B2(PC_q1[1]));
  IC_74x3345 ic_74x3345_2 (
    .A3(PC_OUT[10]), .A4(PC_OUT[11]), .A5(PC_OUT[12]), .A6(PC_OUT[13]), .A7(PC_OUT[14]), .A8(PC_OUT[15]),
    .A1(PC_OUT[8]), .A2(PC_OUT[9]), .B3(PC_q1[10]), .B4(PC_q1[11]), .B5(PC_q1[12]), .B6(PC_q1[13]),
    .B7(PC_q1[14]), .B8(PC_q1[15]), .OE(nOE_PMAR), .nOE(1'b1), .B1(PC_q1[8]), .B2(PC_q1[9]));

  // Other names for the same wires on the sheet: BRANCH = BR; CLR_n = RESET
endmodule

// 16V8B
module IC16V8B_1 (
  input  I0,
  input  I1,
  input  I2,
  input  I3,
  input  I4,
  input  I5,
  input  I6,
  input  I7,
  input  I8,
  input  I9,
  output Q0,
  output Q1,
  output Q2,
  output Q3,
  output Q4,
  output Q5,
  output Q6,
  output Q7
);

  PLA #(.in_width(10), .out_width(8), .\table ("0000000000 00000000")) pla_1 (
    .in({I9, I8, I7, I6, I5, I4, I3, I2, I1, I0}), .out({Q7, Q6, Q5, Q4, Q3, Q2, Q1, Q0}));
endmodule

// 16V8B
module IC16V8B_2 (
  input  I0,
  input  I1,
  input  I2,
  input  I3,
  input  I4,
  input  I5,
  input  I6,
  input  I7,
  input  I8,
  input  I9,
  output Q0,
  output Q1,
  output Q2,
  output Q3,
  output Q4,
  output Q5,
  output Q6,
  output Q7
);

  PLA #(.in_width(10), .out_width(8), .\table ("0000000000 00000000")) pla_1 (
    .in({I9, I8, I7, I6, I5, I4, I3, I2, I1, I0}), .out({Q7, Q6, Q5, Q4, Q3, Q2, Q1, Q0}));
endmodule

// 16V8B
module IC16V8B_3 (
  input  I0,
  input  I1,
  input  I2,
  input  I3,
  input  I4,
  input  I5,
  input  I6,
  input  I7,
  input  I8,
  input  I9,
  output Q0,
  output Q1,
  output Q2,
  output Q3,
  output Q4,
  output Q5,
  output Q6,
  output Q7
);

  PLA #(.in_width(10), .out_width(8), .\table ("0000000000 00000000")) pla_1 (
    .in({I9, I8, I7, I6, I5, I4, I3, I2, I1, I0}), .out({Q7, Q6, Q5, Q4, Q3, Q2, Q1, Q0}));
endmodule

// 16V8B
module IC16V8B_4 (
  input  I0,
  input  I1,
  input  I2,
  input  I3,
  input  I4,
  input  I5,
  input  I6,
  input  I7,
  input  I8,
  input  I9,
  output Q0,
  output Q1,
  output Q2,
  output Q3,
  output Q4,
  output Q5,
  output Q6,
  output Q7
);

  PLA #(.in_width(10), .out_width(8), .\table ("0000000000 00000000")) pla_1 (
    .in({I9, I8, I7, I6, I5, I4, I3, I2, I1, I0}), .out({Q7, Q6, Q5, Q4, Q3, Q2, Q1, Q0}));
endmodule

module VARIS_REFERENCIA (
);

  wire and_1_out, and_2_out, and_3_out, and_4_out, and_5_out, and_6_out, and_7_out, and_8_out, and_9_out,
       and_10_out, and_11_out, and_12_out, and_13_out, and_14_out, and_15_out, and_16_out, CLK,
       ic_74x138_1_y0, ic_74x138_2_y0, ic_74x138_3_y0, ic_74x138_4_y0, ic_74x138_5_y0, ic_74x138_5_y1,
       ic_74x138_5_y2, ic_74x138_5_y3, ic_74x138_5_y4, ic_74x138_5_y5, ic_74x138_5_y6, ic_74x138_5_y7,
       ic_74x138_6_y0, ic_74x138_6_y1, ic_74x138_6_y2, ic_74x138_6_y3, ic_74x138_6_y4, ic_74x138_6_y5,
       ic_74x138_6_y6, ic_74x138_6_y7, ic_74x138_7_y0, ic_74x138_7_y1, ic_74x138_7_y2, ic_74x138_7_y3,
       ic_74x138_7_y4, ic_74x138_7_y5, ic_74x138_7_y6, ic_74x138_7_y7, ic_74x238_1_y0, ic_74x238_1_y1,
       ic_74x238_1_y2, ic_74x238_1_y3, ic_74x238_1_y4, ic_74x238_1_y5, ic_74x238_1_y6, ic_74x238_1_y7,
       ic_74x563_1_q1, ic_74x563_1_q2, ic_74x563_1_q3, ic_74x563_1_q4, ic_74x563_1_q5, ic_74x563_1_q6,
       ic_74x563_1_q7, ic_74x563_1_q8, ic_7402_1_y1, ic_7402_1_y2, ic_7402_1_y3, ic_7402_1_y4, ic_7402_2_y1,
       ic_7402_2_y2, ic_7402_2_y3, ic_7402_2_y4, ic_7402_3_y1, ic_7402_3_y2, ic_7402_3_y3, ic_7402_3_y4,
       ic_7402_4_y1, ic_7402_4_y2, ic_7402_4_y3, ic_7402_4_y4, ic_7410_1_y1, ic_7411_1_p10, ic_7411_1_p11,
       ic_7411_1_p12, ic_7420_1_y1, ic_7420_1_y2, nand_1_out, nor_1_out, not_1_out, not_2_out, not_3_out,
       not_4_out, not_5_out, not_6_out, not_7_out, nQ_RD, nRD_A, nRS_A, pull_resistor_1_node, Q_RD_n,
       undriven_4, undriven_5, undriven_7, WR_R0, WR_R1, WR_R2, WR_R3, WR_R4, WR_R5, WR_R6, WR_R7;
  wire [2:0] RD, RS;
  wire [15:0] undriven, undriven_2, undriven_3, undriven_6;

  IC_74x138 ic_74x138_1 (
    .Y0(ic_74x138_1_y0), .A(undriven[0]), .B(undriven[1]), .C(undriven[2]), .nG2A(undriven[3]),
    .nG2B(undriven[4]), .G1(1'b1));  // open: Y1, Y2, Y3, Y4, Y5, Y6, Y7
  IC_74x138 ic_74x138_2 (
    .Y0(ic_74x138_2_y0), .A(undriven[5]), .B(undriven[6]), .C(undriven[7]), .nG2A(undriven[8]),
    .nG2B(undriven[9]), .G1(1'b1));  // open: Y1, Y2, Y3, Y4, Y5, Y6, Y7
  IC_74x138 ic_74x138_3 (
    .Y0(ic_74x138_3_y0), .A(undriven[10]), .B(undriven[11]), .C(undriven[12]), .nG2A(undriven[13]),
    .nG2B(undriven[14]), .G1(1'b1));  // open: Y1, Y2, Y3, Y4, Y5, Y6, Y7
  IC_7402 ic_7402_1 (
    .Y3(ic_7402_1_y3), .Y4(ic_7402_1_y4), .Y1(ic_7402_1_y1), .Y2(ic_7402_1_y2), .A3(undriven_2[2]),
    .A4(undriven_2[3]), .B1(undriven_2[4]), .B2(undriven_2[5]), .A1(undriven_2[0]), .B3(undriven_2[6]),
    .B4(undriven_2[7]), .A2(undriven_2[1]));
  IC_7402 ic_7402_2 (
    .Y3(ic_7402_2_y3), .Y4(ic_7402_2_y4), .Y1(ic_7402_2_y1), .Y2(ic_7402_2_y2), .A3(undriven_2[10]),
    .A4(undriven_2[11]), .B1(undriven_2[12]), .B2(undriven_2[13]), .A1(undriven_2[8]), .B3(undriven_2[14]),
    .B4(undriven_2[15]), .A2(undriven_2[9]));
  Pull_Resistor #(.pull(1)) pull_resistor_1 (.node(pull_resistor_1_node));
  IC_7405 ic_7405_1 (
    .Y3(pull_resistor_1_node), .Y4(pull_resistor_1_node), .Y5(pull_resistor_1_node),
    .Y6(pull_resistor_1_node), .Y1(pull_resistor_1_node), .Y2(pull_resistor_1_node), .A3(undriven_3[2]),
    .A4(undriven_3[3]), .A5(undriven_3[4]), .A6(undriven_3[5]), .A1(undriven_3[0]), .A2(undriven_3[1]));
  IC_7405 ic_7405_2 (
    .Y3(pull_resistor_1_node), .Y4(pull_resistor_1_node), .Y5(pull_resistor_1_node),
    .Y6(pull_resistor_1_node), .Y1(pull_resistor_1_node), .Y2(pull_resistor_1_node), .A3(undriven_3[8]),
    .A4(undriven_3[9]), .A5(undriven_3[10]), .A6(undriven_3[11]), .A1(undriven_3[6]), .A2(undriven_3[7]));
  IC_7405 ic_7405_3 (
    .Y3(pull_resistor_1_node), .Y4(pull_resistor_1_node), .Y1(pull_resistor_1_node),
    .Y2(pull_resistor_1_node), .A3(undriven_3[14]), .A4(undriven_3[15]), .A5(undriven_4), .A6(1'b0),
    .A1(undriven_3[12]), .A2(undriven_3[13]));  // open: Y5, Y6
  IC_7420 ic_7420_1 (
    .Y2(ic_7420_1_y2), .Y1(ic_7420_1_y1), .B1(ic_7402_1_y3), .B2(ic_7402_1_y4), .C1(ic_7402_2_y1),
    .A1(ic_7402_1_y1), .C2(ic_7402_2_y2), .D1(ic_7402_2_y3), .D2(ic_7402_2_y4), .A2(ic_7402_1_y2));
  IC_74x138 ic_74x138_4 (
    .Y0(ic_74x138_4_y0), .A(ic_74x138_1_y0), .B(ic_74x138_2_y0), .C(ic_74x138_3_y0), .nG2A(undriven[15]),
    .nG2B(undriven_5), .G1(1'b1));  // open: Y1, Y2, Y3, Y4, Y5, Y6, Y7
  nor nor_1 (nor_1_out, ic_7420_1_y1, ic_7420_1_y2);
  not not_1 (not_1_out, ic_74x138_4_y0);
  not not_2 (not_2_out, undriven_7);
  IC_7402 ic_7402_3 (
    .Y3(ic_7402_3_y3), .Y4(ic_7402_3_y4), .Y1(ic_7402_3_y1), .Y2(ic_7402_3_y2), .A3(undriven_6[2]),
    .A4(undriven_6[3]), .B1(undriven_6[4]), .B2(undriven_6[5]), .A1(undriven_6[0]), .B3(undriven_6[6]),
    .B4(undriven_6[7]), .A2(undriven_6[1]));
  IC_7402 ic_7402_4 (
    .Y3(ic_7402_4_y3), .Y4(ic_7402_4_y4), .Y1(ic_7402_4_y1), .Y2(ic_7402_4_y2), .A3(undriven_6[10]),
    .A4(undriven_6[11]), .B1(undriven_6[12]), .B2(undriven_6[13]), .A1(undriven_6[8]), .B3(undriven_6[14]),
    .B4(undriven_6[15]), .A2(undriven_6[9]));
  // IC_7411 ic_7411_1: pin names not known; wires that end beside it: not_2_out, ic_7402_3_y1, ic_7402_3_y2, ic_7402_3_y3, ic_7402_3_y4, ic_7402_4_y1, ic_7402_4_y2, ic_7402_4_y3, ic_7402_4_y4, ic_7411_1_p10, ic_7411_1_p11, ic_7411_1_p12
  IC_7410 ic_7410_1 (
    .Y1(ic_7410_1_y1), .A3(ic_7411_1_p12), .A1(ic_7411_1_p10), .A2(ic_7411_1_p11));  // open: Y3, Y2, B1, B2, B3, C1, C2, C3
  IC_74x138 ic_74x138_5 (
    .Y0(ic_74x138_5_y0), .Y1(ic_74x138_5_y1), .Y2(ic_74x138_5_y2), .Y3(ic_74x138_5_y3), .Y4(ic_74x138_5_y4),
    .Y5(ic_74x138_5_y5), .Y6(ic_74x138_5_y6), .Y7(ic_74x138_5_y7), .A(RD[0]), .B(RD[1]), .C(RD[2]),
    .nG2A(nQ_RD), .nG2B(1'b0), .G1(1'b1));
  IC_74x238 ic_74x238_1 (
    .Y0(ic_74x238_1_y0), .Y1(ic_74x238_1_y1), .Y2(ic_74x238_1_y2), .Y3(ic_74x238_1_y3), .Y4(ic_74x238_1_y4),
    .Y5(ic_74x238_1_y5), .Y6(ic_74x238_1_y6), .Y7(ic_74x238_1_y7), .A(RD[0]), .B(RD[1]), .C(RD[2]),
    .nG2A(Q_RD_n), .nG2B(1'b0), .G1(1'b1));
  not not_3 (not_3_out, CLK);
  IC_74x138 ic_74x138_6 (
    .Y0(ic_74x138_6_y0), .Y1(ic_74x138_6_y1), .Y2(ic_74x138_6_y2), .Y3(ic_74x138_6_y3), .Y4(ic_74x138_6_y4),
    .Y5(ic_74x138_6_y5), .Y6(ic_74x138_6_y6), .Y7(ic_74x138_6_y7), .A(RD[0]), .B(RD[1]), .C(RD[2]),
    .nG2A(nRD_A), .nG2B(1'b0), .G1(1'b1));
  IC_74x138 ic_74x138_7 (
    .Y0(ic_74x138_7_y0), .Y1(ic_74x138_7_y1), .Y2(ic_74x138_7_y2), .Y3(ic_74x138_7_y3), .Y4(ic_74x138_7_y4),
    .Y5(ic_74x138_7_y5), .Y6(ic_74x138_7_y6), .Y7(ic_74x138_7_y7), .A(RS[0]), .B(RS[1]), .C(RS[2]),
    .nG2A(nRS_A), .nG2B(1'b0), .G1(1'b1));
  not not_4 (not_4_out, CLK);
  not not_5 (not_5_out, not_3_out);
  not not_6 (not_6_out, not_5_out);
  IC_74x563 ic_74x563_1 (
    .Q2(ic_74x563_1_q2), .Q3(ic_74x563_1_q3), .Q4(ic_74x563_1_q4), .Q5(ic_74x563_1_q5), .Q6(ic_74x563_1_q6),
    .Q7(ic_74x563_1_q7), .Q8(ic_74x563_1_q8), .Q1(ic_74x563_1_q1), .D2(ic_74x138_5_y1), .D3(ic_74x138_5_y2),
    .D4(ic_74x138_5_y3), .D5(ic_74x138_5_y4), .D6(ic_74x138_5_y5), .D7(ic_74x138_5_y6), .D8(ic_74x138_5_y7),
    .LE(not_4_out), .nOE(1'b0), .D1(ic_74x138_5_y0));  // open: Probe
  nand nand_1 (nand_1_out, not_3_out, not_7_out);
  not not_7 (not_7_out, not_6_out);
  // IC_74273 ic_74273_1: pin names not known; wires that end beside it: ic_74x238_1_y0, ic_74x238_1_y1, ic_74x238_1_y2, ic_74x238_1_y3, ic_74x238_1_y4, ic_74x238_1_y5, ic_74x238_1_y6, ic_74x238_1_y7, CLK, nand_1_out, WR_R0, WR_R1, WR_R2, WR_R3, WR_R4, WR_R5, WR_R6, WR_R7
  and and_1 (and_1_out, ic_74x138_6_y0, ic_74x138_7_y0);
  and and_2 (and_2_out, ic_74x138_6_y1, ic_74x138_7_y1);
  and and_3 (and_3_out, ic_74x138_6_y2, ic_74x138_7_y2);
  and and_4 (and_4_out, ic_74x138_6_y3, ic_74x138_7_y3);
  and and_5 (and_5_out, ic_74x138_6_y4, ic_74x138_7_y4);
  and and_6 (and_6_out, ic_74x138_6_y5, ic_74x138_7_y5);
  and and_7 (and_7_out, ic_74x138_6_y6, ic_74x138_7_y6);
  and and_8 (and_8_out, ic_74x138_6_y7, ic_74x138_7_y7);
  and and_9 (and_9_out, CLK, ic_74x563_1_q1);
  and and_10 (and_10_out, CLK, ic_74x563_1_q2);
  and and_11 (and_11_out, CLK, ic_74x563_1_q3);
  and and_12 (and_12_out, CLK, ic_74x563_1_q4);
  and and_13 (and_13_out, CLK, ic_74x563_1_q5);
  and and_14 (and_14_out, CLK, ic_74x563_1_q6);
  and and_15 (and_15_out, CLK, ic_74x563_1_q7);
  and and_16 (and_16_out, CLK, ic_74x563_1_q8);
endmodule

module ALUFlags_obsolete (
  input  ALU_nZ,
  input  ALU_C,
  input  ALU_S,
  input  ALU_V,
  input  [2:0] IR_CC,
  input  CTRL_nENCC,
  output Z,
  output C,
  output T
);

  wire and_1_out, and_2_out, not_2_out, not_3_out, xnor_1_out;
  wire [2:0] PS_Bypass_z1;

  IC_74x241 PS_Bypass (
    .Y3(PS_Bypass_z1[2]), .Z1(PS_Bypass_z1[0]), .Z2(PS_Bypass_z1[1]), .Z3(PS_Bypass_z1[2]),
    .Y1(PS_Bypass_z1[0]), .Y2(PS_Bypass_z1[1]), .A3(IR_CC[2]), .A4(1'b0), .nOEA(CTRL_nENCC), .B1(1'b0),
    .B2(1'b0), .B3(1'b0), .B4(1'b0), .A1(IR_CC[0]), .OEB(CTRL_nENCC), .A2(IR_CC[1]));  // open: Y4, Z4
  xnor xnor_1 (xnor_1_out, ALU_S, ALU_V);
  not not_1 (Z, ALU_nZ);
  not not_2 (not_2_out, ALU_C);
  not not_3 (not_3_out, xnor_1_out);
  and and_1 (and_1_out, ALU_C, ALU_nZ);
  and and_2 (and_2_out, xnor_1_out, ALU_nZ);
  IC_74x151 ic_74x151_1 (
    .Y(T), .D1(ALU_nZ), .D2(ALU_C), .D3(not_2_out), .D4(xnor_1_out), .D5(not_3_out), .D6(and_1_out),
    .D7(and_2_out), .A(PS_Bypass_z1[0]), .B(PS_Bypass_z1[1]), .C(PS_Bypass_z1[2]), .nG(1'b0), .D0(Z));  // open: W

  assign C = ALU_C;

  // Notes on the sheet:
  //   Conditon 
  //   Codes
  //   000 (EQ)
  //   001 (NE)
  //   010 (UGE)
  //   011 (ULT)
  //   100 (GE)
  //   101 (LT)
  //   110 (UGT)
  //   111 (GT)
  //   Logic 
  //   Function
  //   Z
  //   /Z
  //   C
  //   /C
  //   S == V
  //   S != V
  //   C AND /Z
  //   (S==V) AND /Z
endmodule

// ALU Ctrl
module ALUControl_obsolete (
  input  Cy,
  input  T,
  input  nT,
  input  A15,
  input  nA15,
  input  PSFunc,
  input  [3:0] PSin,
  input  [2:0] CSSel,
  output [3:0] PS,
  output CS
);

  IC_74x253 PS_Select (
    .Y1(PS[0]), .Y2(PS[1]), .I_n_0(1'b0), .I1_1(1'b0), .I1_2(1'b0), .I1_3(1'b0), .I2_0(1'b0), .I2_1(T),
    .I2_2(T), .I2_3(nT), .S0(PSin[0]), .S1(PSin[1]), .nOE1(PSFunc), .nOE2(PSFunc));
  IC_74x151 CS_Select (
    .Y(CS), .D1(1'b1), .D2(Cy), .D3(1'b0), .D4(nT), .D5(T), .D6(nA15), .D7(A15), .A(CSSel[0]), .B(CSSel[1]),
    .C(CSSel[2]), .nG(1'b0), .D0(1'b0));  // open: W
  IC_74x253 PS_Select_2 (
    .Y1(PS[2]), .Y2(PS[3]), .I_n_0(1'b0), .I1_1(nT), .I1_2(1'b0), .I1_3(1'b0), .I2_0(1'b0), .I2_1(1'b1),
    .I2_2(T), .I2_3(nT), .S0(PSin[0]), .S1(PSin[1]), .nOE1(PSFunc), .nOE2(PSFunc));
  IC_74x241 PS_Bypass (
    .Z1(PS[0]), .Z2(PS[1]), .Z3(PS[2]), .Z4(PS[3]), .A3(1'b0), .A4(1'b0), .nOEA(1'b0), .B1(PSin[0]),
    .B2(PSin[1]), .B3(PSin[2]), .B4(PSin[3]), .A1(1'b0), .OEB(PSFunc), .A2(1'b0));  // open: Y3, Y4, Y1, Y2

  // Other names for the same wires on the sheet: F = nT

  // Notes on the sheet:
  //   PSFunc
  //   0  PSSelect
  //   1  PSByPass
  //   PSSelect (PSFunc=0)
  //   xx00 Q = ZERO
  //   xx10 Q = SELt(A, 0)
  //   xx01 Q = SELf(A, 0)
  //   xx11 Q = SELt(A, B)
  //   Efective PS
  //   0000
  //   1ft0
  //   t0t0
  //   f0f0
  //   CS Select
  //   000
  //   001
  //   010
  //   011
  //   100
  //   101
  //   110
  //   111
  //   Efective CS
  //   0
  //   1
  //   Cy
  //   (reserved)
  //   /T
  //   T
  //   /A15
  //   A15
endmodule

module MEM (
  input  CLK,
  input  CTRL_nWE
);

  wire ic_74x74half_1_q1, not_1_out, nWE;

  not not_1 (not_1_out, CTRL_nWE);
  IC_74x74half ic_74x74half_1 (
    .Q1(ic_74x74half_1_q1), .CLK1(CLK), .CLR1(not_1_out), .SET1(1'b1), .D1(1'b1));  // open: R1
  or or_1 (nWE, CTRL_nWE, ic_74x74half_1_q1);

  // Notes on the sheet:
  //   This prevents the /WE signal to last beyond the arribal of the CLK raising edge
  //   Therefore preventing corrupt memory writes shortly after the cycle has ended
endmodule
