// Logisim project CPU74V12.circ as structural Verilog
module Clock (
  input  Reset,
  input  Slow_Fast,
  input  Run,
  input  Tick,
  input  Halt,
  output CLK_PH,
  output nCLK_PH
);

  wire and_1_out, and_2_out, buffer_1_out, buffer_2_out, button_1_out, button_2_out, clock_1_out,
       clock_2_out, d_flip_flop_1_q, d_flip_flop_1_r, d_flip_flop_2_q, d_flip_flop_2_r, d_flip_flop_3_q,
       d_flip_flop_4_q, d_flip_flop_5_r, d_flip_flop_6_r, d_latch_1_q, nand_1_out, nand_2_out, nand_3_out,
       not_1_out, not_2_out, not_3_out, not_4_out, or_1_out, or_2_out, or_3_out, Tick_out;

  Button u_Reset ();  // open: out
  Button button_1 (.out(button_1_out));
  Clock_part clock_1 (.out(clock_1_out));
  Button button_2 (.out(button_2_out));
  Clock_part #(.highDuration(3), .lowDuration(3)) clock_2 (.out(clock_2_out));
  Button u_Tick (.out(Tick_out));
  buf buffer_1 (buffer_1_out, Slow_Fast);
  buf buffer_2 (buffer_2_out, Run);
  not not_1 (not_1_out, Slow_Fast);
  not not_2 (not_2_out, Run);
  not not_3 (not_3_out, Tick);
  D_Flip_Flop d_flip_flop_1 (
    .Q(d_flip_flop_1_q), .R(d_flip_flop_1_r), .D(d_flip_flop_1_r), .CLK(clock_1_out));  // open: SET, CLR
  D_Flip_Flop d_flip_flop_2 (
    .Q(d_flip_flop_2_q), .R(d_flip_flop_2_r), .D(d_flip_flop_2_r), .CLK(clock_2_out));  // open: SET, CLR
  and and_1 (and_1_out, not_1_out, buffer_2_out, d_flip_flop_6_r);
  and and_2 (and_2_out, buffer_1_out, buffer_2_out, d_flip_flop_5_r);
  nand nand_1 (nand_1_out, d_flip_flop_5_r, d_flip_flop_6_r, not_2_out);
  D_Flip_Flop d_flip_flop_3 (.Q(d_flip_flop_3_q), .D(and_1_out), .CLK(d_flip_flop_1_q));  // open: R, SET, CLR
  D_Flip_Flop d_flip_flop_4 (.Q(d_flip_flop_4_q), .D(and_2_out), .CLK(d_flip_flop_2_q));  // open: R, SET, CLR
  D_Flip_Flop d_flip_flop_5 (
    .R(d_flip_flop_5_r), .CLR(Reset), .D(d_flip_flop_3_q), .CLK(d_flip_flop_1_r));  // open: Q, SET
  D_Flip_Flop d_flip_flop_6 (
    .R(d_flip_flop_6_r), .CLR(Reset), .D(d_flip_flop_4_q), .CLK(d_flip_flop_2_r));  // open: Q, SET
  or or_1 (or_1_out, d_flip_flop_5_r, d_flip_flop_1_r);
  or or_2 (or_2_out, d_flip_flop_6_r, d_flip_flop_2_r);
  or or_3 (or_3_out, nand_1_out, not_3_out);
  nand nand_2 (nand_2_out, or_1_out, or_2_out, or_3_out);
  nand nand_3 (nand_3_out, not_3_out, Halt);
  not not_4 (not_4_out, nand_2_out);
  D_Latch d_latch_1 (.Q(d_latch_1_q), .D(nand_3_out), .LE(not_4_out));  // open: R, SET, CLR
  and and_3 (CLK_PH, nand_2_out, d_latch_1_q);

  // Other names for the same wires on the sheet: RST = Reset
endmodule

module Main (
  input  SLOW,
  input  RUN,
  input  RESET
);

  wire alu_1_alucore_c, alu_1_alucore_cx, and_1_out, and_2_out, and_3_out, and_4_out, BR, CE0_n, CE1_n,
       CLEAR_out, CLK, cpWR_MAR, cpWR_NEXT, cpWR_PMAR, cpWR_SP, cpWR_SR, CTRL_A_M, CTRL_ALU_Q, CTRL_CMP,
       CTRL_D_Q, CTRL_EXT, CTRL_HLT, CTRL_K_B, CTRL_M_Q, CTRL_P2, CTRL_PC_A, CTRL_R_A, CTRL_R_B, CTRL_SEXT,
       CTRL_SH1, CTRL_SHR, CTRL_SL8, CTRL_SP_A, CTRL_SR8, CTRL_WRMAR, CTRL_WRPMAR, CTRL_WRR, dbg_wscr,
       instdecoder1_1_ctrl_end, instdecoder1_1_ctrl_wrsp, instdecoder1_1_ctrl_wrsr, IR_A, marctrl_1_ishift,
       marctrl_1_nie_2, marctrl_1_noe_2, marctrl_1_noext, marctrl_1_oshift, marctrl_1_sext, MOE_n, MWE_n,
       ncpIR_CLR, nRST, or_1_out, or_2_out, regsr_1_sr_c, regsr_1_sr_f, regsr_1_sr_t, TICK_out;
  wire [1:0] CTRL_BR, CTRL_GS, CTRL_SL;
  wire [2:0] CTRL_CS, IR_RD, IR_RN, IR_RS;
  wire [3:0] CTRL_PS;
  wire [6:0] dbg_d, instdecoder1_1_mir;
  wire [7:0] Low_Byte_data;
  wire [7:7] High_Byte_data;
  wire [14:0] marctrl_1_addr;
  wire [15:0] alu_1_pipe, dbg_pmaddr, marctrl_1_addr_2, regir_1_d, regir_1_ir, regir_1_ir_2, registers_1_r0,
       registers_1_r1, registers_1_r2, registers_1_r3, registers_1_r4, registers_1_r5, registers_1_r6,
       registers_1_r7, registers_1_reg_a, registers_1_reg_b, regpc_1_pc, regsp_1_sp_2, rom_1_data, shl1_1_out;

  Button TICK (.out(TICK_out));
  ROM #(.addrWidth(16), .dataWidth(16)) rom_1 (.addr(dbg_pmaddr), .data(rom_1_data));
  Clock clock_1 (
    .CLK_PH(CLK), .Reset(RESET), .Slow_Fast(SLOW), .Run(RUN), .Tick(TICK_out), .Halt(CTRL_HLT));  // open: nCLK_PH
  not not_1 (nRST, RESET);
  Registers registers_1 (
    .R4(registers_1_r4), .R5(registers_1_r5), .R6(registers_1_r6), .R7(registers_1_r7),
    .REG_B(registers_1_reg_b), .REG_A(registers_1_reg_a), .R0(registers_1_r0), .R1(registers_1_r1),
    .R2(registers_1_r2), .R3(registers_1_r3), .CLK(CLK), .WR(CTRL_WRR), .nR_TO_A(CTRL_R_A),
    .nR_TO_B(CTRL_R_B), .IR_A(IR_A), .IN(regir_1_d), .RD(IR_RD), .RS(IR_RS), .RN(IR_RN));
  // Probe on regsp_1_sp_2
  RegSP regsp_1 (.SP_2(regsp_1_sp_2), .SP(registers_1_reg_a), .cpWR(cpWR_SP), .nOE(CTRL_SP_A), .IN(regir_1_d));
  // Probe on regpc_1_pc
  RegPC regpc_1 (
    .PC(regpc_1_pc), .MEM_ADDR(dbg_pmaddr), .PC_OUT(registers_1_reg_a), .CLK(CLK), .cpWRPC(cpWR_NEXT),
    .cpWRPMAR(cpWR_PMAR), .nRESET(nRST), .nOE_PC(CTRL_PC_A), .PMEM(CTRL_WRPMAR), .BR(BR), .IN(regir_1_d));
  // Probe on registers_1_r0
  // Probe on registers_1_r1
  // Probe on registers_1_r2
  // Probe on registers_1_r3
  // Probe on registers_1_r4
  // Probe on registers_1_r5
  // Probe on registers_1_r6
  // Probe on registers_1_r7
  // Probe on dbg_pmaddr
  RegIR regir_1 (
    .IR_2(regir_1_ir_2), .IR({regir_1_ir[15:11], IR_RD, IR_RS, IR_RN, regir_1_ir[1:0]}), .D(regir_1_d),
    .cpWR(cpWR_NEXT), .ncpRST(ncpIR_CLR), .nOE_D(CTRL_D_Q), .IN(rom_1_data));
  // Probe on regir_1_ir_2
  // FileViewer #(.cols(50), .lines(20), .select("address")) fileviewer_1: pin names not known; wires that end beside it: dbg_pmaddr
  // Probe on instdecoder1_1_mir
  ImmDecoder immdecoder_1 (
    .IMM_OUT(registers_1_reg_b), .cpPfix(cpWR_NEXT), .nOE(CTRL_K_B),
    .IR({regir_1_ir[15:11], IR_RD, IR_RS, IR_RN, regir_1_ir[1:0]}), .nRESET(nRST));  // open: PFix
  InstDecoder1 instdecoder1_1 (
    .CTRL_SHR(CTRL_SHR), .CTRL_CMP(CTRL_CMP), .CTRL_P2(CTRL_P2), .CTRL_SH1(CTRL_SH1), .CTRL_A_M(CTRL_A_M),
    .CTRL_SHL8(CTRL_SL8), .CTRL_SHR8(CTRL_SR8), .CTRL_EXT(CTRL_EXT), .CTRL_SEXT(CTRL_SEXT),
    .CTRL_R_A(CTRL_R_A), .CTRL_SP_A(CTRL_SP_A), .CTRL_PC_A(CTRL_PC_A), .CTRL_R_B(CTRL_R_B),
    .CTRL_K_B(CTRL_K_B), .CTRL_ALU_Q(CTRL_ALU_Q), .CTRL_M_Q(CTRL_M_Q), .CTRL_D_Q(CTRL_D_Q),
    .CTRL_WRRD(CTRL_WRR), .CTRL_WRSP(instdecoder1_1_ctrl_wrsp), .CTRL_WRSR(instdecoder1_1_ctrl_wrsr),
    .CTRL_WRMAR(CTRL_WRMAR), .CTRL_WRPMAR(CTRL_WRPMAR), .CTRL_HLT(CTRL_HLT),
    .CTRL_END(instdecoder1_1_ctrl_end), .CTRL_PS0(CTRL_PS[0]), .CTRL_PS1(CTRL_PS[1]), .CTRL_PS2(CTRL_PS[2]),
    .CTRL_PS3(CTRL_PS[3]), .CTRL_GS0(CTRL_GS[0]), .CTRL_GS1(CTRL_GS[1]), .CTRL_CS0(CTRL_CS[0]),
    .CTRL_CS1(CTRL_CS[1]), .CTRL_CS2(CTRL_CS[2]), .CTRL_SL0(CTRL_SL[0]), .CTRL_SL1(CTRL_SL[1]),
    .CTRL_BR0(CTRL_BR[0]), .CTRL_BR1(CTRL_BR[1]), .MIR(instdecoder1_1_mir), .IR_RA(IR_A), .CLK(CLK),
    .IRin({regir_1_ir[15:11], IR_RD, IR_RS, IR_RN, regir_1_ir[1:0]}), .nRESET(nRST));
  or or_1 (or_1_out, instdecoder1_1_ctrl_end, BR);
  RegSR regsr_1 (
    .SR_C(regsr_1_sr_c), .SR_T(regsr_1_sr_t), .SR_F(regsr_1_sr_f), .Cin(alu_1_alucore_c),
    .Cxin(alu_1_alucore_cx), .CC(IR_RD), .CMP(CTRL_CMP), .CS2(CTRL_CS[2]), .IN(alu_1_pipe), .cpWR(cpWR_SR));
  or or_2 (or_2_out, CTRL_WRPMAR, or_1_out);
  SHL1 shl1_1 (.Out(shl1_1_out), .B_BUS_IN(registers_1_reg_b), .ISw(CTRL_SH1));
  TTY #(.cols(40), .rows(20)) tty_1 (.data(dbg_d), .clk(dbg_wscr), .clr(CLEAR_out));  // open: we
  Button CLEAR (.out(CLEAR_out));
  // Probe on registers_1_reg_a
  // Probe on registers_1_reg_a
  // Probe on shl1_1_out
  // Probe on shl1_1_out
  // Probe on marctrl_1_addr_2
  WRSignals SYNC_SIGNALS (
    .CK0(cpWR_SP), .CK1(cpWR_SR), .CK2(cpWR_MAR), .CK3(cpWR_PMAR), .CK4(cpWR_NEXT), .CK7(ncpIR_CLR),
    .CLK(CLK), .WR0(instdecoder1_1_ctrl_wrsp), .WR1(instdecoder1_1_ctrl_wrsr), .WR2(CTRL_WRMAR),
    .WR3(or_2_out), .WR4(or_1_out), .WR7(BR));  // open: CK5, CK6, WR5, WR6
  Comparator #(.mode("unsigned"), .width(16)) comparator_1 (
    .a(marctrl_1_addr_2), .b({16{1'b1}}), .eq(dbg_wscr));  // open: gt, lt
  and and_1 (and_1_out, ~MOE_n, MWE_n, ~CE0_n);  // AND_Gate
  and and_2 (and_2_out, ~CE0_n, ~MWE_n);  // AND_Gate
  and and_3 (and_3_out, ~MOE_n, MWE_n, ~CE1_n);  // AND_Gate
  and and_4 (and_4_out, ~CE1_n, ~MWE_n);  // AND_Gate
  ALU alu_1 (
    .Pipe(alu_1_pipe), .ALUCore_C(alu_1_alucore_c), .ALUCore_Cx(alu_1_alucore_cx), .Q(regir_1_d),
    .ALU_BR(BR), .CS0(CTRL_CS[0]), .CS1(CTRL_CS[1]), .CS2(CTRL_CS[2]), .GS0(CTRL_GS[0]), .GS1(CTRL_GS[1]),
    .SHR(CTRL_SHR), .P2(CTRL_P2), .A(registers_1_reg_a), .B(shl1_1_out), .T(regsr_1_sr_t), .F(regsr_1_sr_f),
    .SL0(CTRL_SL[0]), .SL1(CTRL_SL[1]), .nOE(CTRL_ALU_Q), .BR0(CTRL_BR[0]), .BR1(CTRL_BR[1]),
    .PS0(CTRL_PS[0]), .PS1(CTRL_PS[1]), .PS2(CTRL_PS[2]), .PS3(CTRL_PS[3]), .C(regsr_1_sr_c));
  MARCTRL marctrl_1 (
    .Addr_2(marctrl_1_addr_2), .ADDR(marctrl_1_addr), .nOExt(marctrl_1_noext), .SExt(marctrl_1_sext),
    .IShift(marctrl_1_ishift), .OShift(marctrl_1_oshift), .nMWE(MWE_n), .nIE_2(marctrl_1_nie_2),
    .nOE_2(marctrl_1_noe_2), .nMOE(MOE_n), .nCE0(CE0_n), .nCE1(CE1_n), .cpWRMAR(cpWR_MAR),
    .Q_BUS_IN(regir_1_d), .nExt(CTRL_EXT), .SEx(CTRL_SEXT), .ISh(CTRL_SL8), .OSh(CTRL_SR8),
    .WRMAR(CTRL_WRMAR), .nIE(CTRL_A_M), .nOE(CTRL_M_Q), .RESET(nRST), .CLK(CLK));
  RAM #(.addrWidth(15), .databus("bidir"), .trigger("low")) Low_Byte (
    .addr(marctrl_1_addr), .data(Low_Byte_data));  // open: we, oe, clk
  RAM #(.addrWidth(15), .databus("bidir"), .trigger("low")) High_Byte (
    .addr(marctrl_1_addr), .data({High_Byte_data[7], dbg_d}));  // open: we, oe, clk
  // Probe on regir_1_d
  // Probe on regir_1_d
  // Probe on regir_1_d
  SHL8 shl8_1 (
    .D_LOW(Low_Byte_data), .D_HIGH({High_Byte_data[7], dbg_d}), .nIE(marctrl_1_nie_2),
    .A_BUS_IN(registers_1_reg_a), .ISh(marctrl_1_ishift));
  SHR8EXT shr8ext_1 (
    .Q_BUS_OUT(regir_1_d), .nOE(marctrl_1_noe_2), .OSh(marctrl_1_oshift), .SEx(marctrl_1_sext),
    .IN_LO(Low_Byte_data), .IN_HI({High_Byte_data[7], dbg_d}), .nExt(marctrl_1_noext));

  // Notes on the sheet:
  //   contents of rom_1 (hex, n*v repeats v):
  //   compressed eJyNWkmy3CoQ3HMK1l4xD8dBA/c/ws8EqVstwN+OFx2Sai6KpADXZA9pT51kTXaXVeEJf0Ep9f0i
  //   +pfyy2OU1Ao/tigrqlJZ6l2qLq0d2JShlJYFP4Jc8suFJ0++evHpruMgs5VzZrOLzmzgXDT4Zk+D
  //   V4snY90pbVKpiYnuifoTNti3RfuHNn4u9Gg79eOzzTV8X8Vls8XbA8Gr8QWu1kpzRkYlwp8tGy2N
  //   VkGGTI9+PQ+JhvJZ7xjc9g2YSg+pW4LsIkE+ffi1QOCaOU+MVL9taW0StWhSfwjmKfEcKkvCW0KA
  //   4FY2/MpGeKp62ogrG9ZsUxvGmjK1UZTR0ziKNnpqo5inxFOVNXpuw61s+JWNMCNQIi5soFDmNqJR
  //   cxvB4VvwKDytspunU5MwGzKT3XzI7FPiOWRupoo2/Mx4G/2VjbiyYXOcxmFsDvMhU7nOh0znOh8y
  //   Q8JsyOxT4mf0aWNG8E9VTxthZSMubERPSJgQwvEc/YeNin+g6rc+8aVGrxduqK0u4DQk8YEW2aAF
  //   SKp7rQFkdvz4XqdvbALSgKr93F3ADajGv2eeuDEHVOvnhQ7gAdUNsh2TgT6g+plsh6Bd6LCiRsoi
  //   T/M69QZzK3gzjdd4c0oTFvH+5E998yd6/mbW7vxN6+A3f0Pux/z9TN15/sQd5Sp/oudP9vzNcn/n
  //   b7UuVNHzN4n3k785HP7kTwTXYO5Tf6OEeNTfIn+i52+Kelf+5rn/yd+Q+zF/4rf+5KT+xG/9LZD1
  //   U3+TeCf195rOIqhYrk7BRnQbZCkq1rchLNMNMnZQnXoPMsQcx4O9H57K3d49WEJQFYR9QBUsTw1u
  //   1Dtrwemmr0H40C42MOp2lQo9hHp4g4jYtZVyyBDRemqy1coG0ZShsM+mw4Bo/ZBb6AbRvySvUjrd
  //   QrJ1ikHAgzRLBGwGOqrElMi3W+1QRqd9hfKsIsY/OnTHaRahtDgjhYaB0Wec+vjMvK59Lej5bq0+
  //   xgDVgjEwug9JoXY3YKN1hWL0KQzRNFmw5L+wUIGx4YANRxvRL1ig5YcvDoll+599+ObuocS6RCfy
  //   14mfrQKa1O7lnIHSNmTmwX19fDNAQ2OqT6afwS0vB380gHgO9vvgkriQ/jKMtn/Ko6xC7Ax3Pfir
  //   AL714Pi6w09AkGPpYosXCBKHPzk7Dxk5ve0BWMkOEWcP2YyykjmCkCINUVVR55DaFGgI6kE93Nur
  //   hHapmyyqDGiU3O1GUekYWq0MX3bdNqrYyE2orXsCCzbBYBmmSMqEJExVMcEOUuN6lqfcEWu/9i2/
  //   lQBqAx7dJtWQktyUjuibcsP1cZIHrHoywyFiOPaiWh98JZrHyCd7TXXsE/gKVbqnjv7ZPMTG/Wbd
  //   tjn2Jd2H7ERe7JD21NAv6w5T77zYA6tSMsndLG5gqdzHp8LZ3GFyzQLH96RbJuGLM+Mga+7MsfZy
  //   M7YjAxh21oNyMzwUV/3reyVKoAbLBewfZ8LhgpWHD0YeIWhxxKDkHsO0/vuY7iGs6h9e7R5aVvUv
  //   dxe6cTGr/z2H8F1p3ikENb6WGvFDfZfvo0BBnZZvn7OgTsuXBCuW5XtcDgXRyvegjVa+eHqWL16h
  //   Sgf0K6vyBRVFgfKdrnyg9vKl7DHkRYdH+b7zckSU724ie1S/v/PSUoKBv552E1hrPg1dT+Nz0d18
  //   eALf0Du1Pm4rIYHFqRULVNWPyRLY1djrnGjGe7KiLl5sVfYpL0AxQiCXad/UHBOwmrqLO12cWhVX
  //   ELCaP7z51+o7MTDtXqbFNCfaPVycJIZTKqphkK6FLnChi/LeBHcJ9p1JGtNmPDbWRqP1wHIp20Ff
  //   aS7nCjYKgC1K++G1mot0SG+DP6JXg00L0cRdmGJs57h6ZNvOIvPFVjj5jBLRRlRbYNbcsJRRXPyI
  //   24+4ag5e4kasxL/WxVeciYB3HwUOAGucg5I4TKqL6WgZeI8FLBielGHi53P/QC1HQMdZqyE/ACte
  //   AOtdidL7EqQPGHkfi5MulihWACtdAHND7RnAOl/8t8F4O+4c1P82GL+lWKTLAJJlP3+z1DXU3izH
  //   ul24WfYX6E5Yygt5xQ91G7sHccFvY/GXp1cLcX/bRQPi+3V7oPH9LUmni1tDMqh+DcmghjUkgxrX
  //   kAwPUBaxN1SHdEY1MN1HQNBGYpea+pPDiP4FKcl7In03b14iZQMa17aZC7gUN+REQk6+IId3LPfh
  //   R7vGsDxlAcrv7kRx75gN6Kw1d3XJvAd01g1gW27eQWNCjKcNzNXMih2OUFV538Zg+PaJ5XMJs/Ex
  //   ydvVDQO/8NOi0JaAthV3w5Inqm3Vy43lH0ovUhK04kVO/WiuTCkWZwu7v5q7V+3wvWkuzjSlod3S
  //   QKm+MZQHFiDwtKTqrs+a86vuefg3UXejW3ocaTQQC64WAFtzlE+aeWh+8+AQvQKWmmiIoBmrqdqO
  //   9S1B02dszDLyvNH4LV/Oe4+fI9CX85SRF3BGYzqGnWnxWxHFEyQOosx2+tE1lT/XTbW7hl5r4wnW
  //   +T+u8V6t69M2lodrxWGlLnv3qvaEa21hcte6ecWsw7W9JfEMn+p53ibWFFtOq2iXcHWrG48oKoHD
  //   dU+B47GfOPG6BGsHj84jTxQTB3VysFk4Dd8HCck+Ljp+5oN+965CJz+54eIEoH+UGM4pUtynh4Qt
  //   jolD4hN5D3BTs2Dacf8YTLsg2ID6i0u1Z0TiKeHnVwqfsGaGxHYdOo7ZuGMbeoO2HEyOq2fBNOyo
  //   ifsuzYHfUisB/SiB4HodVG7SCCBtk6ZZByzMpOeH44s68P+cNdRBnh7fLhOGOmgtRTuLnuZqQC/F
  //   um/FQFSqOwqpTVM+CYRfZTs/79PA63tChHYES7GI2WOm5fPMwfPwTdn5jeMsInPtdcaIxhyIS2KY
  //   C1fWFnOhI0OrAzTqe25da28oUl8eWvn6DFsbPfmyuKuzhpw9wJNdX4GvJRyJDGxvsXBwxx9sPxDy
  //   /QmIiPXZgLBtgdCJVq1b2mjpavE9LZh+LmV3oly6jgkYCavRnjS5d+C/j1/TJ9IgeS9+WPgaCcKx
  //   9QZtrKimEgyRBoPWBD+GymLbHVhZfr5i6x927LQKtxlKuAP7+Qg8lOFw4EUDH1sD4iP0e++A1tEC
  //   WEGE3H7JSW8hF7jRA93gmzMiYAcJn4JtTNhLfz8Eh6UQ3xxcgmCBW31S7uBwurUb3NbTKp0Wo4ZK
  //   D1xADBnbQBDqvzFZY+3tdQiMNiF8OAT/fUB/IyLPJWAaAslbMmU6QXl47XxoSUiMz1OxbYp7EO3/
  //   nDgqvEVFEy0tbwiS8YWwcTxoJGA7IJC3FjBS4iCFIKp0lcoDh8dz0KITWJpZhyAi2/CmxitD8Is7
  //   IXwrdGvJdiddMumC/sYr6Sxe/DjuqHu+vL+M6oaVFOIndzI3kQJ3MTAA+t6tmfgkXcnmiAhE5KRP
  //   rTpYX5WNJc82rhJwvMKKhJwT84Ap0+I/9vvjng==
  //   contents of fileviewer_1 (hex, n*v repeats v):
  //   Source: init 0000: 00000: (F83D) _pfix 1976  Program:+1976 0001: 00001: (3E18) jmp $setup
  //   Program:+1976  Source: TestUnits.c 0002: 00002: (F83C) _pfix 1944  Program:01944 0003: 00003: (F018)
  //   call printstr  Program:01944 0004: 00004: (0018) ret 0005: 00005: (6000) mov .L.str, r0  Data:00000
  //   0006: 00006: (F83C) _pfix 1944  Program:01944 0007: 00007: (F018) call printstr  Program:01944 0008:
  //   00008: (0018) ret 0009: 00009: (600A) mov .L.str.1, r0  Data:00010 000A: 00010: (F83C) _pfix 1944
  //   Program:01944 000B: 00011: (F018) call printstr  Program:01944 000C: 00012: (0018) ret 000D: 00013:
  //   (0020) mov r1, r0 000E: 00014: (1020) cmp eq, r1, r0 000F: 00015: (3A03) brcc 3 0010: 00016: (F009)
  //   call fail  Program:00009 0011: 00017: (001C) halt 0012: 00018: (0000) nop 0013: 00019: (0018) ret
  //   0014: 00020: (6014) mov .L.str.2, r0  Data:00020 0015: 00021: (F002) call test  Program:00002 0016:
  //   00022: (6001) mov 1, r0 0017: 00023: (A001) cmp eq, r0, 1 0018: 00024: (3A03) brcc 3 0019: 00025:
  //   (F009) call fail  Program:00009 001A: 00026: (001C) halt 001B: 00027: (0000) nop 001C: 00028: (F005)
  //   call pass  Program:00005 001D: 00029: (601F) mov .L.str.3, r0  Data:00031 001E: 00030: (F002) call
  //   test  Program:00002 001F: 00031: (6103) mov 3, r1 0020: 00032: (F00D) call function  Program:00013
  //   0021: 00033: (A003) cmp eq, r0, 3 0022: 00034: (3A03) brcc 3 0023: 00035: (F009) call fail
  //   Program:00009 0024: 00036: (001C) halt 0025: 00037: (0000) nop 0026: 00038: (F005) call pass
  //   Program:00005 0027: 00039: (602C) mov .L.str.4, r0  Data:00044 0028: 00040: (F002) call test
  //   Program:00002 0029: 00041: (6200) mov 0, r2 002A: 00042: (7205) add r2, 5, r2 002B: 00043: (3E22)
  //   jmp .Lpsb_test  Program:+34 002C: 00044: (6305) mov 5, r3 002D: 00045: (234E) add r2, r3, r3 002E:
  //   00046: (3808) brncc .Lpsb_forw  Program:+8 002F: 00047: (F009) call fail  Program:00009 0030: 00048:
  //   (001C) halt 0031: 00049: (0000) nop 0032: 00050: (6B01) sub r3, 1, r3 0033: 00051: (6B01) sub r3, 1,
  //   r3 0034: 00052: (6B01) sub r3, 1, r3 0035: 00053: (6B01) sub r3, 1, r3 0036: 00054: (6B01) sub r3,
  //   1, r3 0037: 00055: (6B01) sub r3, 1, r3 0038: 00056: (6B01) sub r3, 1, r3 0039: 00057: (6B01) sub
  //   r3, 1, r3 003A: 00058: (6B01) sub r3, 1, r3 003B: 00059: (6B01) sub r3, 1, r3 003C: 00060: (3A15)
  //   brcc .Lpsb_fwok  Program:+21 003D: 00061: (F009) call fail  Program:00009 003E: 00062: (001C) halt
  //   003F: 00063: (0000) nop 0040: 00064: (6A01) sub r2, 1, r2 0041: 00065: (6A01) sub r2, 1, r2 0042:
  //   00066: (6A01) sub r2, 1, r2 0043: 00067: (6A01) sub r2, 1, r2 0044: 00068: (6A01) sub r2, 1, r2
  //   0045: 00069: (6A01) sub r2, 1, r2 0046: 00070: (6A01) sub r2, 1, r2 0047: 00071: (6A01) sub r2, 1,
  //   r2 0048: 00072: (6A01) sub r2, 1, r2 0049: 00073: (6A01) sub r2, 1, r2 004A: 00074: (3BE1) brcc
  //   .Lpsb_bwok  Program:-31 004B: 00075: (F009) call fail  Program:00009 004C: 00076: (001C) halt 004D:
  //   00077: (0000) nop 004E: 00078: (39F6) brncc .Lpsb_back  Program:-10 004F: 00079: (F009) call fail
  //   Program:00009 0050: 00080: (001C) halt 0051: 00081: (0000) nop 0052: 00082: (F005) call pass
  //   Program:00005 0053: 00083: (603C) mov .L.str.5, r0  Data:00060 0054: 00084: (F002) call test
  //   Program:00002 0055: 00085: (6005) mov 5, r0 0056: 00086: (625A) mov .Lba0, r2  Program:00090 0057:
  //   00087: (61FF) mov -1, r1 0058: 00088: (2342) add r2, r0, r3 0059: 00089: (0070) jmp r3 005A: 00090:
  //   (B921) addx r1, 1, r1 005B: 00091: (B921) addx r1, 1, r1 005C: 00092: (B921) addx r1, 1, r1 005D:
  //   00093: (B921) addx r1, 1, r1 005E: 00094: (B921) addx r1, 1, r1 005F: 00095: (B921) addx r1, 1, r1
  //   0060: 00096: (2106) add r0, r1, r1 0061: 00097: (6905) sub r1, 5, r1 0062: 00098: (3A03) brcc
  //   .LbaNext  Program:+3 0063: 00099: (F009) call fail  Program:00009 0064: 00100: (001C) halt 0065:
  //   00101: (0000) nop 0066: 00102: (6801) sub r0, 1, r0 0067: 00103: (39EF) brncc .Lba_loop  Program:-17
  //   0068: 00104: (F005) call pass  Program:00005 0069: 00105: (604B) mov .L.str.6, r0  Data:00075 006A:
  //   00106: (F002) call test  Program:00002 006B: 00107: (6103) mov 3, r1 006C: 0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
endmodule

module Main1 (
  input  SLOW,
  input  RUN,
  input  HALT,
  input  RESET
);

  wire alu_1_alucore_c, alu_1_alucore_cx, and_1_out, and_2_out, and_3_out, and_4_out, BR, CE0_n, CE1_n, CLK,
       comparator_1_eq, cpWR_MAR, cpWR_NEXT, cpWR_PMAR, cpWR_SP, cpWR_SR, CTRL_A_M, CTRL_ALU_Q, CTRL_CMP,
       CTRL_D_Q, CTRL_EXT, CTRL_K_B, CTRL_M_Q, CTRL_P2, CTRL_PC_A, CTRL_R_A, CTRL_R_B, CTRL_SEXT, CTRL_SH1,
       CTRL_SHR, CTRL_SL8, CTRL_SP_A, CTRL_SR8, CTRL_WRMAR, CTRL_WRPMAR, CTRL_WRR, instdecoder_1_ctrl_end,
       instdecoder_1_ctrl_wrsp, instdecoder_1_ctrl_wrsr, IR_A, marctrl_1_ishift, marctrl_1_nie_2,
       marctrl_1_noe_2, marctrl_1_noext, marctrl_1_oshift, marctrl_1_sext, MOE_n, MWE_n, ncpIR_CLR, nRST,
       or_1_out, or_2_out, regsr_1_sr_c, regsr_1_sr_f, regsr_1_sr_t, TICK_out;
  wire [1:0] CTRL_BR, CTRL_GS, CTRL_SL;
  wire [2:0] CTRL_CS, IR_RD, IR_RN, IR_RS;
  wire [3:0] CTRL_PS;
  wire [6:0] instdecoder_1_mir;
  wire [7:0] High_Byte_data, Low_Byte_data;
  wire [14:0] marctrl_1_addr;
  wire [15:0] alu_1_pipe, dbg_maddr, immdecoder_1_pfix, regir_1_d, regir_1_ir_2, registers_1_r0,
       registers_1_r1, registers_1_r2, registers_1_r3, registers_1_r4, registers_1_r5, registers_1_r6,
       registers_1_r7, registers_1_reg_b, regpc_1_mem_addr, regpc_1_pc, regpc_1_pc_out, regsp_1_sp_2,
       rom_1_data, shl1_1_out;
  wire [15:9] regir_1_ir;

  // Probe on regpc_1_mem_addr
  ROM #(.addrWidth(16), .dataWidth(16)) rom_1 (.addr(regpc_1_mem_addr), .data(rom_1_data));
  Button TICK (.out(TICK_out));
  // Probe on regpc_1_pc
  RegPC regpc_1 (
    .PC(regpc_1_pc), .MEM_ADDR(regpc_1_mem_addr), .PC_OUT(regpc_1_pc_out), .CLK(CLK), .cpWRPC(cpWR_NEXT),
    .cpWRPMAR(cpWR_PMAR), .nRESET(nRST), .nOE_PC(CTRL_PC_A), .PMEM(CTRL_WRPMAR), .BR(BR), .IN(regir_1_d));
  not not_1 (nRST, RESET);
  Clock clock_1 (
    .CLK_PH(CLK), .Reset(RESET), .Slow_Fast(SLOW), .Run(RUN), .Tick(TICK_out), .Halt(HALT));  // open: nCLK_PH
  RegIR regir_1 (
    .IR_2(regir_1_ir_2), .IR({regir_1_ir, IR_RN, IR_RD, IR_RS}), .D(regir_1_d), .cpWR(cpWR_NEXT),
    .ncpRST(ncpIR_CLR), .nOE_D(CTRL_D_Q), .IN(rom_1_data));
  // Probe on regir_1_ir_2
  // Probe on {regir_1_ir, IR_RN, IR_RD, IR_RS}
  // Probe on instdecoder_1_mir
  InstDecoder instdecoder_1 (
    .MIR(instdecoder_1_mir), .CTRL_CS2(CTRL_CS[2]), .CTRL_GS0(CTRL_GS[0]), .CTRL_GS1(CTRL_GS[1]),
    .CTRL_SHR(CTRL_SHR), .CTRL_CMP(CTRL_CMP), .CTRL_P2(CTRL_P2), .CTRL_SH1(CTRL_SH1),
    .CTRL_ALU_Q(CTRL_ALU_Q), .CTRL_A_M(CTRL_A_M), .CTRL_M_Q(CTRL_M_Q), .CTRL_SHL8(CTRL_SL8),
    .CTRL_SHR8(CTRL_SR8), .CTRL_EXT(CTRL_EXT), .CTRL_SEXT(CTRL_SEXT), .CTRL_R_A(CTRL_R_A),
    .CTRL_SP_A(CTRL_SP_A), .CTRL_PC_A(CTRL_PC_A), .CTRL_R_B(CTRL_R_B), .CTRL_K_B(CTRL_K_B),
    .CTRL_D_Q(CTRL_D_Q), .CTRL_WRRD(CTRL_WRR), .CTRL_WRSP(instdecoder_1_ctrl_wrsp),
    .CTRL_WRSR(instdecoder_1_ctrl_wrsr), .CTRL_WRMAR(CTRL_WRMAR), .CTRL_WRPMAR(CTRL_WRPMAR),
    .CTRL_END(instdecoder_1_ctrl_end), .IR_RA(IR_A), .CTRL_PS0(CTRL_PS[0]), .CTRL_PS1(CTRL_PS[1]),
    .CTRL_PS2(CTRL_PS[2]), .CTRL_PS3(CTRL_PS[3]), .CTRL_SL0(CTRL_SL[0]), .CTRL_SL1(CTRL_SL[1]),
    .CTRL_BR0(CTRL_BR[0]), .CTRL_BR1(CTRL_BR[1]), .CTRL_CS0(CTRL_CS[0]), .CTRL_CS1(CTRL_CS[1]), .CLK(CLK),
    .IRin({regir_1_ir, IR_RN, IR_RD, IR_RS}), .nRESET(nRST));
  // Probe on regir_1_d
  // Probe on regir_1_d
  Registers registers_1 (
    .R4(registers_1_r4), .R5(registers_1_r5), .R6(registers_1_r6), .R7(registers_1_r7),
    .REG_B(registers_1_reg_b), .REG_A(regpc_1_pc_out), .R0(registers_1_r0), .R1(registers_1_r1),
    .R2(registers_1_r2), .R3(registers_1_r3), .CLK(CLK), .WR(CTRL_WRR), .nR_TO_A(CTRL_R_A),
    .nR_TO_B(CTRL_R_B), .IR_A(IR_A), .IN(regir_1_d), .RD(IR_RD), .RS(IR_RS), .RN(IR_RN));
  ImmDecoder immdecoder_1 (
    .PFix(immdecoder_1_pfix), .IMM_OUT(registers_1_reg_b), .cpPfix(CLK), .nOE(CTRL_K_B),
    .IR({regir_1_ir, IR_RN, IR_RD, IR_RS}), .nRESET(nRST));
  // Probe on immdecoder_1_pfix
  // Probe on registers_1_r0
  // Probe on registers_1_r1
  // Probe on registers_1_r2
  // Probe on registers_1_r3
  // Probe on registers_1_r4
  // Probe on registers_1_r5
  // Probe on registers_1_r6
  // Probe on registers_1_r7
  or or_1 (or_1_out, instdecoder_1_ctrl_end, BR);
  // Probe on regir_1_d
  or or_2 (or_2_out, CTRL_WRPMAR, or_1_out);
  // Probe on dbg_maddr
  and and_1 (and_1_out, ~MOE_n, MWE_n, ~CE0_n);  // AND_Gate
  and and_2 (and_2_out, ~CE0_n, ~MWE_n);  // AND_Gate
  and and_3 (and_3_out, ~MOE_n, MWE_n, ~CE1_n);  // AND_Gate
  and and_4 (and_4_out, ~CE1_n, ~MWE_n);  // AND_Gate
  WRSignals SYNC_SIGNALS (
    .CK0(cpWR_SP), .CK1(cpWR_SR), .CK2(cpWR_MAR), .CK3(cpWR_PMAR), .CK4(cpWR_NEXT), .CK7(ncpIR_CLR),
    .CLK(CLK), .WR0(instdecoder_1_ctrl_wrsp), .WR1(instdecoder_1_ctrl_wrsr), .WR2(CTRL_WRMAR),
    .WR3(or_2_out), .WR4(or_1_out), .WR7(BR));  // open: CK5, CK6, WR5, WR6
  RegSR regsr_1 (
    .SR_C(regsr_1_sr_c), .SR_T(regsr_1_sr_t), .SR_F(regsr_1_sr_f), .Cin(alu_1_alucore_c),
    .Cxin(alu_1_alucore_cx), .CC(IR_RD), .CMP(CTRL_CMP), .CS2(CTRL_CS[2]), .IN(alu_1_pipe), .cpWR(cpWR_SR));
  RegSP regsp_1 (.SP_2(regsp_1_sp_2), .SP(regpc_1_pc_out), .cpWR(cpWR_SP), .nOE(CTRL_SP_A), .IN(regir_1_d));
  MARCTRL marctrl_1 (
    .Addr_2(dbg_maddr), .ADDR(marctrl_1_addr), .nOExt(marctrl_1_noext), .SExt(marctrl_1_sext),
    .IShift(marctrl_1_ishift), .OShift(marctrl_1_oshift), .nMWE(MWE_n), .nIE_2(marctrl_1_nie_2),
    .nOE_2(marctrl_1_noe_2), .nMOE(MOE_n), .nCE0(CE0_n), .nCE1(CE1_n), .cpWRMAR(cpWR_MAR),
    .Q_BUS_IN(regir_1_d), .nExt(CTRL_EXT), .SEx(CTRL_SEXT), .ISh(CTRL_SL8), .OSh(CTRL_SR8),
    .WRMAR(CTRL_WRMAR), .nIE(CTRL_A_M), .nOE(CTRL_M_Q), .RESET(nRST), .CLK(CLK));
  // Probe on marctrl_1_addr
  RAM #(.addrWidth(15), .databus("bidir"), .trigger("low")) Low_Byte (
    .addr(marctrl_1_addr), .data(Low_Byte_data));  // open: we, oe, clk
  RAM #(.addrWidth(15), .databus("bidir"), .trigger("low")) High_Byte (
    .addr(marctrl_1_addr), .data(High_Byte_data));  // open: we, oe, clk
  // Probe on regsp_1_sp_2
  SHL1 shl1_1 (.Out(shl1_1_out), .B_BUS_IN(registers_1_reg_b), .ISw(CTRL_SH1));
  SHL8 shl8_1 (
    .D_LOW(Low_Byte_data), .D_HIGH(High_Byte_data), .nIE(marctrl_1_nie_2), .A_BUS_IN(regpc_1_pc_out),
    .ISh(marctrl_1_ishift));
  // Probe on regpc_1_pc_out
  // Probe on shl1_1_out
  // Probe on regpc_1_pc_out
  // Probe on shl1_1_out
  ALU alu_1 (
    .Pipe(alu_1_pipe), .ALUCore_C(alu_1_alucore_c), .ALUCore_Cx(alu_1_alucore_cx), .Q(regir_1_d),
    .ALU_BR(BR), .CS0(CTRL_CS[0]), .CS1(CTRL_CS[1]), .CS2(CTRL_CS[2]), .GS0(CTRL_GS[0]), .GS1(CTRL_GS[1]),
    .SHR(CTRL_SHR), .P2(CTRL_P2), .A(regpc_1_pc_out), .B(shl1_1_out), .T(regsr_1_sr_t), .F(regsr_1_sr_f),
    .SL0(CTRL_SL[0]), .SL1(CTRL_SL[1]), .nOE(CTRL_ALU_Q), .BR0(CTRL_BR[0]), .BR1(CTRL_BR[1]),
    .PS0(CTRL_PS[0]), .PS1(CTRL_PS[1]), .PS2(CTRL_PS[2]), .PS3(CTRL_PS[3]), .C(regsr_1_sr_c));
  SHR8EXT shr8ext_1 (
    .Q_BUS_OUT(regir_1_d), .nOE(marctrl_1_noe_2), .OSh(marctrl_1_oshift), .SEx(marctrl_1_sext),
    .IN_LO(Low_Byte_data), .IN_HI(High_Byte_data), .nExt(marctrl_1_noext));
  Comparator #(.mode("unsigned"), .width(16)) comparator_1 (
    .a(dbg_maddr), .b({16{1'b1}}), .eq(comparator_1_eq));  // open: gt, lt
  TTY #(.cols(40), .rows(20)) tty_1 (.data(High_Byte_data[6:0]), .clk(comparator_1_eq));  // open: we, clr

  // Notes on the sheet:
  //   contents of rom_1 (hex, n*v repeats v):
  //   fc7f 6000 80 658b 6010 6600 a000 3b10 599 d01a 7088 7110 6880 3c7f f001 e00 6000 f501 f898 6481 f302
  //   6500 ffff 5f81 6000 c00 c808 a001 3c10 b880 ffff 5f89 b890 c808 a001 2 3ccf c00 3f6f 9020 6008 6710
  //   2662 1118 601b 3a90 601b 1700 1110 b89b 3e5f ffff 5f99 b889 a281 394f 8020 3920 c00 6548 6c6c 206f
  //   6f77 6c72 2164 a 2710 3e8 64 a 1
endmodule

module WRSignals (
  input  CLK,
  input  WR0,
  input  WR1,
  input  WR2,
  input  WR3,
  input  WR4,
  input  WR5,
  input  WR6,
  input  WR7,
  output CK0,
  output CK1,
  output CK2,
  output CK3,
  output CK4,
  output CK5,
  output CK6,
  output CK7
);

  wire ic_74x573_1_q1, ic_74x573_1_q2, ic_74x573_1_q3, ic_74x573_1_q4, ic_74x573_1_q5, ic_74x573_1_q6,
       ic_74x573_1_q7, ic_74x573_1_q8, not_1_out;

  not not_1 (not_1_out, CLK);
  IC_74x573 ic_74x573_1 (
    .Q2(ic_74x573_1_q2), .Q3(ic_74x573_1_q3), .Q4(ic_74x573_1_q4), .Q5(ic_74x573_1_q5), .Q6(ic_74x573_1_q6),
    .Q7(ic_74x573_1_q7), .Q8(ic_74x573_1_q8), .Q1(ic_74x573_1_q1), .D2(WR1), .D3(WR2), .D4(WR3), .D5(WR4),
    .D6(WR5), .D7(WR6), .D8(WR7), .LE(not_1_out), .nOE(1'b0), .D1(WR0));  // open: Probe
  and and_1 (CK0, CLK, ic_74x573_1_q1);
  and and_2 (CK1, CLK, ic_74x573_1_q2);
  and and_3 (CK2, CLK, ic_74x573_1_q3);
  and and_4 (CK3, CLK, ic_74x573_1_q4);
  and and_5 (CK4, CLK, ic_74x573_1_q5);
  and and_6 (CK5, CLK, ic_74x573_1_q6);
  and and_7 (CK6, CLK, ic_74x573_1_q7);
  nand nand_1 (CK7, CLK, ic_74x573_1_q8);
endmodule

module PreDecoder (
  input  [15:0] IRin,
  output Type_R2,
  output Type_P,
  output PFix,
  output Type_JJ,
  output TypeR3,
  output Type_I2,
  output Type_J,
  output Type_I1,
  output TypeI1_I2_P
);

  wire Pfx_out;

  IC_74x3251 u_Type_R2 (
    .A(Type_R2), .B1(IRin[15]), .B2(1'b1), .B3(1'b1), .B4(1'b1), .B5(1'b1), .B6(1'b1), .B7(1'b1), .B8(1'b1),
    .S0(IRin[12]), .S1(IRin[13]), .S2(IRin[14]), .nOE(1'b0));
  IC_74x3251 Type_R3 (
    .A(TypeR3), .B1(1'b1), .B2(IRin[15]), .B3(IRin[15]), .B4(1'b1), .B5(1'b1), .B6(1'b1), .B7(1'b1),
    .B8(1'b1), .S0(IRin[12]), .S1(IRin[13]), .S2(IRin[14]), .nOE(1'b0));
  IC_74x3251 u_Type_J (
    .A(Type_J), .B1(1'b1), .B2(1'b1), .B3(1'b1), .B4(IRin[15]), .B5(1'b1), .B6(1'b1), .B7(1'b1), .B8(1'b1),
    .S0(IRin[12]), .S1(IRin[13]), .S2(IRin[14]), .nOE(1'b0));
  IC_74x3251 Type_I1__I2__P (
    .A(TypeI1_I2_P), .B1(1'b1), .B2(1'b0), .B3(1'b0), .B4(1'b0), .B5(1'b0), .B6(1'b0), .B7(1'b0), .B8(1'b0),
    .S0(IRin[14]), .S1(IRin[15]), .S2(1'b0), .nOE(1'b0));
  nand P (Type_P, IRin[13], IRin[14], IRin[15]);
  nand Pfx (Pfx_out, IRin[11], IRin[12], 1'b1);
  or J (Type_JJ, IRin[14], IRin[15]);
  or Pfx_2 (PFix, Type_P, Pfx_out);
  IC_74x3251 Type_I2_Sel (
    .A(Type_I2), .B1(1'b1), .B2(1'b1), .B3(1'b1), .B4(1'b1), .B5(1'b1), .B6(1'b0), .B7(1'b0), .B8(1'b1),
    .S0(IRin[13]), .S1(IRin[14]), .S2(IRin[15]), .nOE(1'b0));
  IC_74x3251 Type_I1_Sel (
    .A(Type_I1), .B1(1'b1), .B2(1'b1), .B3(1'b0), .B4(1'b0), .B5(1'b0), .B6(1'b1), .B7(1'b1), .B8(1'b1),
    .S0(IRin[13]), .S1(IRin[14]), .S2(IRin[15]), .nOE(1'b0));

  // Other names for the same wires on the sheet: IR4 = IRin[4]; IR5 = IRin[5]; IR7 = IRin[7]; IR8 = IRin[8];
  //   IR9 = IRin[9]; IR10 = IRin[10]; IR11 = IRin[11]; IR12 = IRin[12]; IR13 = IRin[13]; IR14 = IRin[14];
  //   IR15 = IRin[15]
endmodule

// Inst Decoder
module InstDecoder (
  input  nRESET,
  input  CLK,
  input  [15:0] IRin,
  output IR_RA,
  output CTRL_PS0,
  output CTRL_PS1,
  output CTRL_PS2,
  output CTRL_PS3,
  output CTRL_SL0,
  output CTRL_SL1,
  output CTRL_BR0,
  output CTRL_BR1,
  output CTRL_CS0,
  output CTRL_CS1,
  output CTRL_CS2,
  output CTRL_GS0,
  output CTRL_GS1,
  output CTRL_SHR,
  output CTRL_CMP,
  output CTRL_P2,
  output CTRL_SH1,
  output CTRL_ALU_Q,
  output CTRL_A_M,
  output CTRL_M_Q,
  output CTRL_SHL8,
  output CTRL_SHR8,
  output CTRL_EXT,
  output CTRL_SEXT,
  output CTRL_R_A,
  output CTRL_SP_A,
  output CTRL_PC_A,
  output CTRL_R_B,
  output CTRL_K_B,
  output CTRL_D_Q,
  output CTRL_WRRD,
  output CTRL_WRSP,
  output CTRL_WRSR,
  output CTRL_WRMAR,
  output CTRL_WRPMAR,
  output CTRL_END,
  output [6:0] MIR
);

  wire Mir_Reg_2_q1, Mir_Reg_2_q2, Mir_Reg_2_q3, Mir_Reg_2_q4, Mir_Reg_2_q5, Mir_Reg_2_q6, Mir_Reg_2_q7,
       Mir_Reg_2_q8, MIRSel_q1, MIRSel_r1, Type_I1__I2__P_a, Type_I1_Sel_a, Type_J_a, Type_R2_a, Type_R3_a,
       undriven_2;
  wire [3:0] CTRL_5_q4, undriven;
  wire [6:0] Type_Mir_a1;
  wire [7:0] Mir_Reg_2_probe;

  IC_74x3251 Type_R2 (
    .A(Type_R2_a), .B1(IRin[15]), .B2(1'b1), .B3(1'b1), .B4(1'b1), .B5(1'b1), .B6(1'b1), .B7(1'b1),
    .B8(1'b1), .S0(IRin[12]), .S1(IRin[13]), .S2(IRin[14]), .nOE(1'b0));
  IC_74x3251 Type_R3 (
    .A(Type_R3_a), .B1(1'b1), .B2(IRin[15]), .B3(IRin[15]), .B4(1'b1), .B5(1'b1), .B6(1'b1), .B7(1'b1),
    .B8(1'b1), .S0(IRin[12]), .S1(IRin[13]), .S2(IRin[14]), .nOE(1'b0));
  IC_74x3251 Type_J (
    .A(Type_J_a), .B1(1'b1), .B2(1'b1), .B3(1'b1), .B4(IRin[15]), .B5(1'b1), .B6(1'b1), .B7(1'b1), .B8(1'b1),
    .S0(IRin[12]), .S1(IRin[13]), .S2(IRin[14]), .nOE(1'b0));
  IC_74x3251 Type_I1__I2__P (
    .A(Type_I1__I2__P_a), .B1(1'b1), .B2(1'b0), .B3(1'b0), .B4(1'b0), .B5(1'b0), .B6(1'b0), .B7(1'b0),
    .B8(1'b0), .S0(IRin[14]), .S1(IRin[15]), .S2(1'b0), .nOE(1'b0));
  IC_74x3251 Type_I1_Sel (
    .A(Type_I1_Sel_a), .B1(1'b1), .B2(1'b1), .B3(1'b0), .B4(1'b0), .B5(1'b0), .B6(1'b1), .B7(1'b1),
    .B8(1'b1), .S0(IRin[13]), .S1(IRin[14]), .S2(IRin[15]), .nOE(1'b0));
  IC_74x74half MIRSel (.R1(MIRSel_r1), .Q1(MIRSel_q1), .CLK1(CLK), .CLR1(1'b1), .SET1(nRESET), .D1(CTRL_END));
  IC_74x541 Type_R2_2 (
    .Q1(MIR[0]), .Q2(MIR[1]), .Q3(MIR[2]), .Q4(MIR[3]), .Q5(MIR[4]), .Q6(MIR[5]), .Q7(MIR[6]), .I1(IRin[7]),
    .I2(IRin[8]), .I3(IRin[9]), .I4(IRin[10]), .I5(IRin[11]), .I6(1'b0), .I7(1'b0), .I8(1'b0),
    .nOE1(Type_R2_a), .nOE2(MIRSel_r1));  // open: Q8
  IC_74x541 Type_R3_2 (
    .Q1(MIR[0]), .Q2(MIR[1]), .Q3(MIR[2]), .Q4(MIR[3]), .Q5(MIR[4]), .Q6(MIR[5]), .Q7(MIR[6]), .I1(IRin[9]),
    .I2(IRin[10]), .I3(IRin[11]), .I4(IRin[12]), .I5(IRin[13]), .I6(1'b1), .I7(1'b0), .I8(1'b0),
    .nOE1(Type_R3_a), .nOE2(MIRSel_r1));  // open: Q8
  IC_74x541 Type_J_2 (
    .Q1(MIR[0]), .Q2(MIR[1]), .Q3(MIR[2]), .Q4(MIR[3]), .Q5(MIR[4]), .Q6(MIR[5]), .Q7(MIR[6]), .I1(IRin[4]),
    .I2(IRin[5]), .I3(IRin[11]), .I4(IRin[12]), .I5(IRin[13]), .I6(1'b1), .I7(1'b0), .I8(1'b0),
    .nOE1(Type_J_a), .nOE2(MIRSel_r1));  // open: Q8
  IC_74x541 Type_I1__I2__P_2 (
    .Q1(MIR[0]), .Q2(MIR[1]), .Q3(MIR[2]), .Q4(MIR[3]), .Q5(MIR[4]), .Q6(MIR[5]), .Q7(MIR[6]), .I1(IRin[11]),
    .I2(IRin[12]), .I3(IRin[13]), .I4(IRin[14]), .I5(IRin[15]), .I6(1'b0), .I7(1'b1), .I8(1'b0),
    .nOE1(Type_I1__I2__P_a), .nOE2(MIRSel_r1));  // open: Q8
  logi7400ic_IC_74x574 MIR_Reg (
    .Q2(MIR[1]), .Q3(MIR[2]), .Q4(MIR[3]), .Q5(MIR[4]), .Q6(MIR[5]), .Q7(MIR[6]), .Q1(MIR[0]),
    .D2(CTRL_5_q4[1]), .D3(CTRL_5_q4[2]), .D4(CTRL_5_q4[3]), .D5(1'b0), .D6(1'b1), .D7(1'b1), .D8(1'b0),
    .CLK(CLK), .nOE(MIRSel_q1), .D1(CTRL_5_q4[0]));  // open: Probe, Q8
  IC_74x1G3157 RA (.A(IR_RA), .B1(Type_I1_Sel_a), .B2(1'b0), .S(MIRSel_r1));
  IC16V8C_1 CTRL_1 (
    .Q0(CTRL_PS0), .Q1(CTRL_PS1), .Q2(CTRL_PS2), .Q3(CTRL_PS3), .Q4(CTRL_SL0), .Q5(CTRL_SL1), .Q6(CTRL_BR0),
    .Q7(CTRL_BR1), .I0(MIR[0]), .I1(MIR[1]), .I2(MIR[2]), .I3(MIR[3]), .I4(MIR[4]), .I5(MIR[5]), .I6(MIR[6]),
    .I7(1'b0), .I8(1'b0), .I9(1'b0));
  IC16V8C_2 CTRL_2 (
    .Q0(CTRL_CS0), .Q1(CTRL_CS1), .Q2(CTRL_CS2), .Q3(CTRL_GS0), .Q4(CTRL_GS1), .Q5(CTRL_SHR), .Q6(CTRL_CMP),
    .Q7(CTRL_P2), .I0(MIR[0]), .I1(MIR[1]), .I2(MIR[2]), .I3(MIR[3]), .I4(MIR[4]), .I5(MIR[5]), .I6(MIR[6]),
    .I7(1'b0), .I8(1'b0), .I9(1'b0));
  IC16V8C_3 CTRL_3 (
    .Q0(CTRL_SH1), .Q1(CTRL_ALU_Q), .Q2(CTRL_A_M), .Q3(CTRL_M_Q), .Q4(CTRL_SHL8), .Q5(CTRL_SHR8),
    .Q6(CTRL_EXT), .Q7(CTRL_SEXT), .I0(MIR[0]), .I1(MIR[1]), .I2(MIR[2]), .I3(MIR[3]), .I4(MIR[4]),
    .I5(MIR[5]), .I6(MIR[6]), .I7(1'b0), .I8(1'b0), .I9(1'b0));
  IC16V8C_4 CTRL_4 (
    .Q0(CTRL_R_A), .Q1(CTRL_SP_A), .Q2(CTRL_PC_A), .Q3(CTRL_R_B), .Q4(CTRL_K_B), .Q5(CTRL_D_Q),
    .Q6(CTRL_WRRD), .Q7(CTRL_WRSP), .I0(MIR[0]), .I1(MIR[1]), .I2(MIR[2]), .I3(MIR[3]), .I4(MIR[4]),
    .I5(MIR[5]), .I6(MIR[6]), .I7(1'b0), .I8(1'b0), .I9(1'b0));
  IC16V8C_5 CTRL_5 (
    .Q0(CTRL_WRSR), .Q1(CTRL_WRMAR), .Q2(CTRL_WRPMAR), .Q3(CTRL_END), .Q4(CTRL_5_q4[0]), .Q5(CTRL_5_q4[1]),
    .Q6(CTRL_5_q4[2]), .Q7(CTRL_5_q4[3]), .I0(MIR[0]), .I1(MIR[1]), .I2(MIR[2]), .I3(MIR[3]), .I4(MIR[4]),
    .I5(MIR[5]), .I6(MIR[6]), .I7(1'b0), .I8(1'b0), .I9(1'b0));
  IC_74x273 Mir_Reg_2 (
    .Probe(Mir_Reg_2_probe), .Q1(Mir_Reg_2_q1), .Q2(Mir_Reg_2_q2), .Q3(Mir_Reg_2_q3), .Q4(Mir_Reg_2_q4),
    .Q5(Mir_Reg_2_q5), .Q6(Mir_Reg_2_q6), .Q7(Mir_Reg_2_q7), .Q8(Mir_Reg_2_q8), .D1(undriven[0]),
    .D2(undriven[1]), .D3(undriven[2]), .D4(undriven[3]), .D5(1'b0), .D6(1'b1), .D7(1'b1), .D8(undriven_2),
    .CLK(CLK), .nMR(nRESET));
  IC_74x3345 Type_Mir (
    .A3(Type_Mir_a1[2]), .A4(Type_Mir_a1[3]), .A5(Type_Mir_a1[4]), .A6(Type_Mir_a1[5]), .A7(Type_Mir_a1[6]),
    .A1(Type_Mir_a1[0]), .A2(Type_Mir_a1[1]), .B3(Mir_Reg_2_q3), .B4(Mir_Reg_2_q4), .B5(Mir_Reg_2_q5),
    .B6(Mir_Reg_2_q6), .B7(Mir_Reg_2_q7), .B8(1'b0), .OE(Mir_Reg_2_q8), .nOE(1'b1), .B1(Mir_Reg_2_q1),
    .B2(Mir_Reg_2_q2));  // open: A8

  // Other names for the same wires on the sheet: CLR_n = nRESET; IR4 = IRin[4]; IR5 = IRin[5]; IR7 = IRin[7];
  //   IR8 = IRin[8]; IR9 = IRin[9]; IR10 = IRin[10]; IR11 = IRin[11]; IR12 = IRin[12]; IR13 = IRin[13];
  //   IR14 = IRin[14]; IR15 = IRin[15]

  // Notes on the sheet:
  //   Note: 
  //   From the Immediate Decoder
endmodule

module PLA_ALL (
  input  [1:0] M,
  input  [4:0] I,
  output [3:0] PF,
  output [1:0] GS,
  output [2:0] CS,
  output [1:0] SL,
  output [1:0] BR,
  output SHR,
  output CMP,
  output P2,
  output SH1,
  output A_M,
  output SHL8,
  output SHR8,
  output EXT,
  output SEXT,
  output R_A,
  output SP_A,
  output PC_A,
  output R_B,
  output K_B,
  output ALUQ,
  output M_Q,
  output D_Q,
  output WRRD,
  output WRSP,
  output WRSR,
  output WMAR,
  output WPMAR,
  output HLT,
  output NXT,
  output [3:0] NEXT
);

  wire and_1_out, and_2_out, and_3_out, and_4_out, and_5_out, and_6_out, and_7_out, and_8_out, and_9_out,
       and_10_out, and_11_out, and_12_out, and_13_out, and_14_out, and_15_out, and_16_out, and_17_out,
       and_18_out, and_19_out, and_20_out, and_21_out, and_22_out, and_23_out, and_24_out, and_25_out,
       and_26_out, and_27_out, and_28_out, and_29_out, and_30_out, and_31_out, and_32_out, and_33_out,
       and_34_out, and_35_out, and_36_out, and_37_out, and_38_out, and_39_out, and_40_out, and_41_out,
       and_42_out, and_43_out, and_44_out, and_45_out, and_46_out, and_47_out, and_48_out, and_49_out,
       and_50_out, and_51_out, and_52_out, and_53_out, and_54_out, and_55_out, and_56_out, and_57_out,
       and_58_out, and_59_out, and_60_out, and_61_out, and_62_out, and_63_out, and_64_out, and_65_out,
       and_66_out, and_67_out, and_68_out, and_69_out, and_70_out, and_71_out, and_72_out, and_73_out,
       and_74_out, and_75_out, and_76_out, and_77_out, and_78_out, and_79_out, and_80_out, and_81_out,
       and_82_out, and_83_out, and_84_out, and_85_out, and_86_out, and_87_out, and_88_out, and_89_out,
       and_90_out, and_91_out, and_92_out, and_93_out, and_94_out, and_95_out, and_96_out, and_97_out,
       and_98_out, and_99_out, and_100_out, and_101_out, and_102_out, and_103_out, and_104_out, and_105_out,
       and_106_out, and_107_out, and_108_out, and_109_out, and_110_out, and_111_out, and_112_out,
       and_113_out, and_114_out, and_115_out, and_116_out, and_117_out, and_118_out, and_119_out,
       and_120_out, and_121_out, and_122_out, and_123_out, and_124_out, and_125_out, and_126_out,
       and_127_out, and_128_out, and_129_out, and_130_out, and_131_out, and_132_out, and_133_out,
       and_134_out, and_135_out, and_136_out, and_137_out, and_138_out, and_139_out, and_140_out,
       and_141_out, and_142_out, and_143_out, and_144_out, and_145_out, and_146_out, and_147_out,
       and_148_out, and_149_out, and_150_out, and_151_out, and_152_out, and_153_out, and_154_out,
       and_155_out, and_156_out, and_157_out, and_158_out, and_159_out, and_160_out, and_161_out,
       and_162_out, and_163_out, and_165_out, and_166_out, and_167_out, and_168_out, and_169_out,
       and_170_out, and_171_out, and_172_out, and_173_out, and_174_out, and_175_out, and_176_out,
       and_177_out, and_178_out, and_179_out, and_180_out, and_181_out, and_182_out, and_183_out,
       and_184_out, and_185_out, and_186_out, and_187_out, and_188_out, and_189_out, and_190_out,
       and_191_out, and_192_out, and_193_out, and_194_out, and_195_out, and_198_out, and_199_out,
       and_200_out, and_201_out, and_202_out, and_203_out, and_204_out, and_205_out, and_206_out,
       and_207_out, and_208_out, and_209_out, and_210_out, and_211_out, and_212_out, and_213_out,
       and_214_out, and_215_out, and_216_out, and_217_out, and_218_out, and_219_out, and_220_out,
       and_221_out, and_222_out, and_223_out;

  and and_1 (and_1_out, ~M[1], ~M[0], ~I[2], ~I[1], ~I[0]);  // AND_Gate
  and and_2 (and_2_out, ~I[4], ~I[3]);  // AND_Gate
  and and_3 (and_3_out, ~I[4], ~I[2]);  // AND_Gate
  and and_4 (and_4_out, ~I[4], ~I[1]);  // AND_Gate
  and and_5 (and_5_out, ~M[0], ~I[3], I[2], ~I[1]);  // AND_Gate
  and and_6 (and_6_out, M[0], ~I[4]);  // AND_Gate
  and and_7 (and_7_out, M[1], ~I[3], I[2], ~I[0]);  // AND_Gate
  and and_8 (and_8_out, M[1], I[4], I[3], I[2], I[0]);
  and and_9 (and_9_out, ~M[0], ~I[4], I[2], I[1], I[0]);  // AND_Gate
  and and_10 (and_10_out, ~M[0], ~I[4], I[3], I[2], I[1]);  // AND_Gate
  and and_11 (and_11_out, I[4], ~I[3], ~I[2], I[0]);  // AND_Gate
  and and_12 (and_12_out, ~M[1], M[0], I[2], ~I[1], I[0]);  // AND_Gate
  and and_13 (and_13_out, M[0], I[4]);
  and and_14 (and_14_out, M[1], ~M[0], ~I[2]);  // AND_Gate
  and and_15 (and_15_out, M[1], ~M[0], ~I[3], I[1], I[0]);  // AND_Gate
  and and_16 (and_16_out, M[1], ~I[4], I[2], I[1]);  // AND_Gate
  and and_17 (and_17_out, M[1], ~M[0], I[3], ~I[0]);  // AND_Gate
  and and_18 (and_18_out, M[1], I[3], ~I[2], ~I[1], I[0]);  // AND_Gate
  and and_19 (and_19_out, ~M[1], ~M[0], ~I[4], ~I[2]);  // AND_Gate
  and and_20 (and_20_out, ~M[1], ~M[0], ~I[4], ~I[1]);  // AND_Gate
  and and_21 (and_21_out, ~M[0], ~I[4], ~I[3]);  // AND_Gate
  and and_22 (and_22_out, ~I[4], ~I[3], ~I[2]);  // AND_Gate
  and and_23 (and_23_out, ~M[1], ~I[3], I[2], ~I[1]);  // AND_Gate
  and and_24 (and_24_out, I[4], ~I[2], ~I[1], ~I[0]);  // AND_Gate
  and and_25 (and_25_out, M[0], I[2], ~I[1], I[0]);  // AND_Gate
  and and_26 (and_26_out, ~M[1], M[0], I[2], I[1]);  // AND_Gate
  and and_27 (and_27_out, M[0], I[4]);
  and and_28 (and_28_out, M[1], ~M[0], ~I[4], I[2], I[1]);  // AND_Gate
  and and_29 (and_29_out, M[1], ~M[0], I[2], I[1], I[0]);  // AND_Gate
  and and_30 (and_30_out, M[1], I[4], ~I[2]);  // AND_Gate
  and and_31 (and_31_out, M[1], M[0], ~I[1], ~I[0]);  // AND_Gate
  and and_32 (and_32_out, M[1], M[0], ~I[2], I[1]);  // AND_Gate
  and and_33 (and_33_out, ~M[1], ~I[4], ~I[3], I[2], I[1], I[0]);  // AND_Gate
  and and_34 (and_34_out, ~M[1], ~M[0], ~I[4], I[3], I[2], I[1]);  // AND_Gate
  and and_35 (and_35_out, ~M[1], ~M[0], I[4], ~I[3], ~I[2], I[0]);  // AND_Gate
  and and_36 (and_36_out, ~M[1], M[0], ~I[4], ~I[2]);  // AND_Gate
  and and_37 (and_37_out, M[1], ~M[0], I[2], ~I[1], I[0]);  // AND_Gate
  and and_38 (and_38_out, M[1], I[4], I[2], ~I[1]);  // AND_Gate
  and and_39 (and_39_out, M[1], I[4], I[3], I[2], ~I[0]);  // AND_Gate
  and and_40 (and_40_out, I[4], ~I[3], ~I[2], ~I[1], I[0]);  // AND_Gate
  and and_41 (and_41_out, M[0], I[4], I[1]);
  and and_42 (and_42_out, M[0], I[4], I[2]);
  and and_43 (and_43_out, M[0], I[4], I[3]);
  and and_44 (and_44_out, M[1], ~M[0], ~I[3], I[1], I[0]);  // AND_Gate
  and and_45 (and_45_out, M[1], ~M[0], ~I[4], I[2], I[1]);  // AND_Gate
  and and_46 (and_46_out, M[1], I[4], ~I[2]);  // AND_Gate
  and and_47 (and_47_out, M[1], I[4], I[3], I[1], ~I[0]);  // AND_Gate
  and and_48 (and_48_out, ~M[1], ~M[0], I[4], ~I[3], ~I[2], ~I[1], I[0]);  // AND_Gate
  and and_49 (and_49_out, ~M[1], M[0], ~I[4], ~I[2]);  // AND_Gate
  and and_50 (and_50_out, M[1], ~M[0], ~I[3], I[2], ~I[1]);  // AND_Gate
  and and_51 (and_51_out, M[1], ~M[0], ~I[4], I[2], ~I[1], I[0]);  // AND_Gate
  and and_52 (and_52_out, M[1], I[4], I[3], I[2], I[1], ~I[0]);  // AND_Gate
  and and_53 (and_53_out, ~M[1], ~I[4], I[3], ~I[2], ~I[1], I[0]);  // AND_Gate
  and and_54 (and_54_out, ~M[1], M[0], ~I[3], ~I[2], ~I[1], I[0]);  // AND_Gate
  and and_55 (and_55_out, ~M[1], M[0], ~I[4], ~I[2], I[1], ~I[0]);  // AND_Gate
  and and_56 (and_56_out, M[1], ~M[0], ~I[3], I[2], ~I[1], I[0]);  // AND_Gate
  and and_57 (and_57_out, ~M[1], ~I[4], ~I[3], I[2], I[1], I[0]);  // AND_Gate
  and and_58 (and_58_out, ~M[1], ~M[0], ~I[4], I[3], ~I[2], I[1], ~I[0]);  // AND_Gate
  and and_59 (and_59_out, ~M[1], ~M[0], ~I[4], I[3], I[1], ~I[0]);  // AND_Gate
  and and_60 (and_60_out, ~M[1], ~M[0], I[4], ~I[3], I[2], I[1]);  // AND_Gate
  and and_61 (and_61_out, ~M[1], M[0], ~I[4], ~I[2], ~I[1], ~I[0]);  // AND_Gate
  and and_62 (and_62_out, ~M[1], M[0], ~I[4], ~I[2], I[1], I[0]);  // AND_Gate
  and and_63 (and_63_out, M[1], ~M[0], ~I[3], I[2], ~I[1], ~I[0]);  // AND_Gate
  and and_64 (and_64_out, M[1], ~M[0], ~I[4], I[2], ~I[1], I[0]);  // AND_Gate
  and and_65 (and_65_out, ~M[1], ~M[0], ~I[4], I[3], I[2], ~I[1], ~I[0]);  // AND_Gate
  and and_66 (and_66_out, ~M[1], ~M[0], I[4], ~I[3], I[2], I[1], ~I[0]);  // AND_Gate
  and and_67 (and_67_out, ~M[1], M[0], ~I[4], I[2], I[1], ~I[0]);  // AND_Gate
  and and_68 (and_68_out, ~M[1], ~M[0], ~I[4], I[3], I[2], ~I[1], I[0]);  // AND_Gate
  and and_69 (and_69_out, ~M[1], ~M[0], I[4], ~I[3], I[2], I[1], I[0]);  // AND_Gate
  and and_70 (and_70_out, ~M[1], M[0], ~I[4], I[2], I[1], ~I[0]);  // AND_Gate
  and and_71 (and_71_out, ~M[1], ~M[0], I[4], ~I[3], ~I[2], ~I[1], ~I[0]);  // AND_Gate
  and and_72 (and_72_out, M[0], I[4], I[3], I[2], ~I[1], ~I[0]);  // AND_Gate
  and and_73 (and_73_out, M[0], I[4], I[3], I[2], I[1], I[0]);
  and and_74 (and_74_out, M[1], ~I[4], ~I[3], I[2], I[1]);  // AND_Gate
  and and_75 (and_75_out, M[1], M[0], I[3], ~I[2], ~I[1]);  // AND_Gate
  and and_76 (and_76_out, M[1], M[0], I[3], ~I[1], ~I[0]);  // AND_Gate
  and and_77 (and_77_out, ~M[1], ~M[0], I[4], ~I[3], ~I[2], ~I[1], ~I[0]);  // AND_Gate
  and and_78 (and_78_out, M[0], I[4], I[3], I[2], I[0]);
  and and_79 (and_79_out, M[1], ~I[4], ~I[3], I[2], I[1]);  // AND_Gate
  and and_80 (and_80_out, M[1], M[0], I[3], ~I[2], ~I[1]);  // AND_Gate
  and and_81 (and_81_out, M[1], M[0], I[3], ~I[1], ~I[0]);  // AND_Gate
  and and_82 (and_82_out, ~M[1], ~M[0], ~I[4], I[3], ~I[2], ~I[1]);  // AND_Gate
  and and_83 (and_83_out, ~M[1], ~M[0], ~I[4], I[3], ~I[2], ~I[0]);  // AND_Gate
  and and_84 (and_84_out, ~M[1], M[0], ~I[4], ~I[2], ~I[1]);  // AND_Gate
  and and_85 (and_85_out, M[1], ~M[0], ~I[3], I[2], ~I[1]);  // AND_Gate
  and and_86 (and_86_out, ~M[1], ~M[0], I[4], ~I[3], ~I[2], ~I[1], I[0]);  // AND_Gate
  and and_87 (and_87_out, M[1], I[4], I[3], I[2], I[1], ~I[0]);  // AND_Gate
  and and_88 (and_88_out, M[1], M[0], I[3], ~I[2], I[1], ~I[0]);  // AND_Gate
  and and_89 (and_89_out, ~M[1], M[0], ~I[3], ~I[2], I[1], I[0]);  // AND_Gate
  and and_90 (and_90_out, M[0], I[4], I[2], I[1], ~I[0]);  // AND_Gate
  and and_91 (and_91_out, M[1], ~M[0], ~I[2], ~I[0]);  // AND_Gate
  and and_92 (and_92_out, M[1], ~M[0], ~I[4], I[2], I[1], I[0]);  // AND_Gate
  and and_93 (and_93_out, ~M[1], ~I[4], ~I[3], ~I[2], I[1]);  // AND_Gate
  and and_94 (and_94_out, ~I[4], ~I[3], I[2], ~I[1]);  // AND_Gate
  and and_95 (and_95_out, ~I[4], ~I[3], I[2], ~I[0]);  // AND_Gate
  and and_96 (and_96_out, M[1], ~I[4], ~I[3], I[2]);  // AND_Gate
  and and_97 (and_97_out, ~M[1], ~I[4], ~I[3], I[2], I[1], ~I[0]);  // AND_Gate
  and and_98 (and_98_out, ~M[1], M[0], ~I[3], I[2], I[1], I[0]);  // AND_Gate
  and and_99 (and_99_out, M[1], ~M[0], ~I[2], I[1], I[0]);  // AND_Gate
  and and_100 (and_100_out, ~M[1], ~I[4], ~I[3], I[2], ~I[1]);  // AND_Gate
  and and_101 (and_101_out, ~M[1], M[0], ~I[3], I[2]);  // AND_Gate
  and and_102 (and_102_out, M[1], ~M[0], ~I[2], I[0]);  // AND_Gate
  and and_103 (and_103_out, ~M[1], ~I[4], ~I[3], ~I[2], I[1]);  // AND_Gate
  and and_104 (and_104_out, ~M[1], ~I[4], ~I[3], I[2], ~I[1]);  // AND_Gate
  and and_105 (and_105_out, ~M[1], M[0], ~I[3], I[2]);  // AND_Gate
  and and_106 (and_106_out, M[1], ~M[0], ~I[2], I[0]);  // AND_Gate
  and and_107 (and_107_out, ~M[0], I[0]);  // AND_Gate
  and and_108 (and_108_out, ~I[3], I[0]);  // AND_Gate
  and and_109 (and_109_out, ~M[1], ~I[4]);  // AND_Gate
  and and_110 (and_110_out, ~M[1], ~I[3], ~I[2], ~I[1], ~I[0]);  // AND_Gate
  and and_111 (and_111_out, ~M[0], ~I[4], ~I[1]);  // AND_Gate
  and and_112 (and_112_out, ~M[0], ~I[4], ~I[0]);  // AND_Gate
  and and_113 (and_113_out, ~I[4], ~I[3], I[2], ~I[1], ~I[0]);  // AND_Gate
  and and_114 (and_114_out, ~M[1], ~I[3], I[2], I[1]);  // AND_Gate
  and and_115 (and_115_out, ~I[4], I[3], ~I[2], ~I[1], ~I[0]);  // AND_Gate
  and and_116 (and_116_out, ~M[1], M[0], ~I[3]);  // AND_Gate
  and and_117 (and_117_out, M[1], ~M[0], ~I[3], I[2]);  // AND_Gate
  and and_118 (and_118_out, M[1], ~M[0], I[3], ~I[2]);  // AND_Gate
  and and_119 (and_119_out, ~M[0], I[4], ~I[3], ~I[2], ~I[1], I[0]);  // AND_Gate
  and and_120 (and_120_out, ~M[1], ~M[0], I[4], I[3], ~I[2], ~I[1], ~I[0]);  // AND_Gate
  and and_121 (and_121_out, M[0], I[4], I[3], I[2], I[1], ~I[0]);  // AND_Gate
  and and_122 (and_122_out, M[1], ~M[0], ~I[3], ~I[2]);  // AND_Gate
  and and_123 (and_123_out, M[1], ~M[0], ~I[4], I[2], I[1], I[0]);  // AND_Gate
  and and_124 (and_124_out, M[1], I[4], I[3], I[2], I[1], ~I[0]);  // AND_Gate
  and and_125 (and_125_out, M[1], M[0], I[3], I[1], ~I[0]);  // AND_Gate
  and and_126 (and_126_out, M[0], I[4], I[3], ~I[2]);  // AND_Gate
  and and_127 (and_127_out, M[0], I[4], I[3], ~I[1]);  // AND_Gate
  and and_128 (and_128_out, M[0], I[4], I[3], I[0]);
  and and_129 (and_129_out, M[1], M[0], I[2], I[1]);
  and and_130 (and_130_out, M[1], M[0], I[3], I[2]);
  and and_131 (and_131_out, ~M[1], ~M[0], ~I[2], ~I[1], ~I[0]);  // AND_Gate
  and and_132 (and_132_out, ~M[1], ~I[4]);  // AND_Gate
  and and_133 (and_133_out, ~M[1], ~I[3], ~I[2], ~I[1]);  // AND_Gate
  and and_134 (and_134_out, ~M[1], ~I[3], I[2], I[1]);  // AND_Gate
  and and_135 (and_135_out, ~I[4], ~I[3], I[2], I[1], I[0]);  // AND_Gate
  and and_136 (and_136_out, ~M[1], M[0], ~I[3]);  // AND_Gate
  and and_137 (and_137_out, M[1], I[4], I[3], I[2], I[1], ~I[0]);  // AND_Gate
  and and_138 (and_138_out, M[0], I[4], I[3]);
  and and_139 (and_139_out, M[1], ~M[0], ~I[4]);  // AND_Gate
  and and_140 (and_140_out, M[1], ~M[0], ~I[3]);  // AND_Gate
  and and_141 (and_141_out, M[1], ~M[0], ~I[2]);  // AND_Gate
  and and_142 (and_142_out, M[1], ~I[4], I[2], ~I[0]);  // AND_Gate
  and and_143 (and_143_out, M[1], ~I[4], I[3], ~I[0]);  // AND_Gate
  and and_144 (and_144_out, ~M[0], ~I[3], ~I[2], ~I[1]);  // AND_Gate
  and and_145 (and_145_out, ~M[0], ~I[2], ~I[1], ~I[0]);  // AND_Gate
  and and_146 (and_146_out, ~I[3], I[2], I[1], I[0]);  // AND_Gate
  and and_147 (and_147_out, ~M[0], ~I[4], I[3]);  // AND_Gate
  and and_148 (and_148_out, ~I[4], I[3], ~I[2], ~I[0]);  // AND_Gate
  and and_149 (and_149_out, ~I[4], I[3], ~I[1], ~I[0]);  // AND_Gate
  and and_150 (and_150_out, I[4], ~I[3], I[2], I[1]);  // AND_Gate
  and and_151 (and_151_out, ~M[1], M[0], ~I[4], ~I[2]);  // AND_Gate
  and and_152 (and_152_out, ~M[1], M[0], ~I[4], ~I[1]);  // AND_Gate
  and and_153 (and_153_out, ~M[1], M[0], ~I[4], ~I[0]);  // AND_Gate
  and and_154 (and_154_out, ~M[1], M[0], ~I[3]);  // AND_Gate
  and and_155 (and_155_out, M[0], I[4], I[2]);
  and and_156 (and_156_out, M[1], ~M[0], ~I[3]);  // AND_Gate
  and and_157 (and_157_out, M[1], ~M[0], ~I[2]);  // AND_Gate
  and and_158 (and_158_out, M[1], ~M[0], I[1], ~I[0]);  // AND_Gate
  and and_159 (and_159_out, M[1], ~I[3], I[2], I[1]);  // AND_Gate
  and and_160 (and_160_out, ~I[4], ~I[3], ~I[2], I[1]);  // AND_Gate
  and and_161 (and_161_out, ~M[1], ~I[4], ~I[3], I[2], ~I[1]);  // AND_Gate
  and and_162 (and_162_out, ~M[1], ~I[4], ~I[3], I[2], ~I[0]);  // AND_Gate
  and and_163 (and_163_out, M[1], M[0], ~I[2], ~I[1], I[0]);  // AND_Gate
  and and_164 (D_Q, M[1], M[0], I[3], ~I[2], I[1], I[0]);  // AND_Gate
  and and_165 (and_165_out, ~M[0], ~I[4], ~I[3], ~I[0]);  // AND_Gate
  and and_166 (and_166_out, ~M[1], ~I[4], I[1], ~I[0]);  // AND_Gate
  and and_167 (and_167_out, ~I[4], ~I[3], ~I[2], I[1]);  // AND_Gate
  and and_168 (and_168_out, ~M[1], ~I[4], I[2], ~I[1]);  // AND_Gate
  and and_169 (and_169_out, ~M[0], ~I[4], I[2]);  // AND_Gate
  and and_170 (and_170_out, ~M[0], ~I[3], I[2], I[1]);  // AND_Gate
  and and_171 (and_171_out, ~M[1], ~M[0], ~I[4], I[3], ~I[1]);  // AND_Gate
  and and_172 (and_172_out, ~M[1], M[0], ~I[3], ~I[2], ~I[1]);  // AND_Gate
  and and_173 (and_173_out, ~M[1], M[0], ~I[3], ~I[2], ~I[0]);  // AND_Gate
  and and_174 (and_174_out, M[0], ~I[4], ~I[2], I[1], I[0]);  // AND_Gate
  and and_175 (and_175_out, M[1], ~I[4], ~I[3], ~I[2], I[0]);  // AND_Gate
  and and_176 (and_176_out, ~M[1], ~M[0], ~I[3], ~I[2], ~I[1], I[0]);  // AND_Gate
  and and_177 (and_177_out, M[0], I[4], I[3], I[2], I[1], ~I[0]);  // AND_Gate
  and and_178 (and_178_out, M[1], I[4], I[3], I[2], I[1], ~I[0]);  // AND_Gate
  and and_179 (and_179_out, M[1], M[0], I[3], ~I[2], I[1], ~I[0]);  // AND_Gate
  and and_180 (and_180_out, ~M[1], ~I[4], I[3], ~I[2], ~I[1]);  // AND_Gate
  and and_181 (and_181_out, ~M[1], ~I[4], I[3], ~I[2], ~I[0]);  // AND_Gate
  and and_182 (and_182_out, ~M[1], M[0], ~I[4], ~I[2]);  // AND_Gate
  and and_183 (and_183_out, ~M[1], M[0], ~I[4], ~I[1]);  // AND_Gate
  and and_184 (and_184_out, ~M[1], M[0], ~I[3], ~I[2], ~I[1]);  // AND_Gate
  and and_185 (and_185_out, ~M[1], M[0], ~I[3], ~I[2], ~I[0]);  // AND_Gate
  and and_186 (and_186_out, M[1], ~M[0], ~I[3], I[2], ~I[1]);  // AND_Gate
  and and_187 (and_187_out, M[1], ~M[0], ~I[3], I[2], ~I[0]);  // AND_Gate
  and and_188 (and_188_out, M[1], ~M[0], ~I[4], I[2], ~I[1], I[0]);  // AND_Gate
  and and_189 (and_189_out, M[1], ~M[0], ~I[4], I[2], I[1], ~I[0]);  // AND_Gate
  and and_190 (and_190_out, ~M[0], I[4], ~I[3], ~I[2], ~I[1], I[0]);  // AND_Gate
  and and_191 (and_191_out, ~M[0], I[4], I[3], ~I[2], ~I[1], ~I[0]);  // AND_Gate
  and and_192 (and_192_out, ~M[1], M[0], ~I[3], I[1], I[0]);  // AND_Gate
  and and_193 (and_193_out, ~M[1], M[0], ~I[3], I[2]);  // AND_Gate
  and and_194 (and_194_out, M[1], ~M[0], ~I[2]);  // AND_Gate
  and and_195 (and_195_out, M[1], I[4], I[3], I[1], ~I[0]);  // AND_Gate
  and and_196 (WPMAR, ~M[1], ~M[0], ~I[4], I[3], ~I[2], I[1], I[0]);  // AND_Gate
  and and_197 (HLT, ~M[1], ~M[0], I[4], I[3], I[2], ~I[1], ~I[0]);  // AND_Gate
  and and_198 (and_198_out, ~M[0], ~I[4], I[3], ~I[2], I[1], I[0]);  // AND_Gate
  and and_199 (and_199_out, ~M[0], I[4], ~I[3], ~I[2], ~I[1], I[0]);  // AND_Gate
  and and_200 (and_200_out, ~M[0], I[4], I[3], ~I[2], ~I[1], ~I[0]);  // AND_Gate
  and and_201 (and_201_out, ~M[1], M[0], ~I[3], I[1], I[0]);  // AND_Gate
  and and_202 (and_202_out, ~M[1], M[0], ~I[3], I[2]);  // AND_Gate
  and and_203 (and_203_out, M[1], ~M[0], ~I[2]);  // AND_Gate
  and and_204 (and_204_out, M[1], I[3], ~I[2], I[0]);  // AND_Gate
  and and_205 (and_205_out, M[1], I[4], I[3], I[1], ~I[0]);  // AND_Gate
  and and_206 (and_206_out, ~M[1], ~M[0], ~I[4], I[3], ~I[2], I[1], I[0]);  // AND_Gate
  and and_207 (and_207_out, ~M[1], ~M[0], I[4], I[3], ~I[2], ~I[1], ~I[0]);  // AND_Gate
  and and_208 (and_208_out, M[1], M[0], I[3], ~I[2], I[0]);  // AND_Gate
  and and_209 (and_209_out, ~M[1], ~M[0], I[4], ~I[3], ~I[2], ~I[1], I[0]);  // AND_Gate
  and and_210 (and_210_out, ~M[1], M[0], ~I[3], I[2], I[1]);  // AND_Gate
  and and_211 (and_211_out, M[1], ~M[0], ~I[2], I[1]);  // AND_Gate
  and and_212 (and_212_out, M[1], I[3], ~I[2], I[1], I[0]);  // AND_Gate
  and and_213 (and_213_out, M[1], I[4], I[3], I[1], ~I[0]);  // AND_Gate
  and and_214 (and_214_out, ~M[1], ~M[0], ~I[4], I[3], ~I[2], I[1], I[0]);  // AND_Gate
  and and_215 (and_215_out, ~M[1], ~M[0], I[4], ~I[3], ~I[2], ~I[1], I[0]);  // AND_Gate
  and and_216 (and_216_out, M[1], I[4], I[3], I[2], I[1], ~I[0]);  // AND_Gate
  and and_217 (and_217_out, M[1], M[0], I[3], ~I[2], ~I[1], I[0]);  // AND_Gate
  and and_218 (and_218_out, ~M[1], ~M[0], ~I[4], I[3], ~I[2], I[1], I[0]);  // AND_Gate
  and and_219 (and_219_out, ~M[0], I[4], ~I[3], ~I[2], ~I[1], I[0]);  // AND_Gate
  and and_220 (and_220_out, ~M[0], I[4], I[3], ~I[2], ~I[1], ~I[0]);  // AND_Gate
  and and_221 (and_221_out, ~M[1], M[0], ~I[3], ~I[2], I[1], I[0]);  // AND_Gate
  and and_222 (and_222_out, ~M[1], M[0], ~I[3], I[2], ~I[1]);  // AND_Gate
  and and_223 (and_223_out, M[1], ~M[0], ~I[2], ~I[1]);  // AND_Gate
  or or_1 (PF[3], and_1_out, and_2_out, and_3_out, and_4_out, and_5_out, and_6_out, and_7_out, and_8_out);
  or or_2 (PF[2], and_9_out, and_10_out, and_11_out, and_12_out, and_13_out, and_14_out, and_15_out, and_16_out, and_17_out, and_18_out);
  or or_3 (PF[1], and_19_out, and_20_out, and_21_out, and_22_out, and_23_out, and_24_out, and_25_out, and_26_out, and_27_out, and_28_out, and_29_out, and_30_out, and_31_out, and_32_out);
  or or_4 (PF[0], and_33_out, and_34_out, and_35_out, and_36_out, and_37_out, and_38_out, and_39_out);
  or or_5 (GS[1], and_40_out, and_41_out, and_42_out, and_43_out, and_44_out, and_45_out, and_46_out, and_47_out);
  or or_6 (GS[0], and_48_out, and_49_out, and_50_out, and_51_out, and_52_out);
  or or_7 (CS[2], and_53_out, and_54_out, and_55_out, and_56_out);
  or or_8 (CS[1], and_57_out, and_58_out);
  or or_9 (CS[0], and_59_out, and_60_out, and_61_out, and_62_out, and_63_out, and_64_out);
  or or_10 (SL[1], and_65_out, and_66_out, and_67_out);
  or or_11 (SL[0], and_68_out, and_69_out, and_70_out);
  or or_12 (BR[1], and_71_out, and_72_out, and_73_out, and_74_out, and_75_out, and_76_out);
  or or_13 (BR[0], and_77_out, and_78_out, and_79_out, and_80_out, and_81_out);
  or or_14 (SHR, and_82_out, and_83_out);
  or or_15 (CMP, and_84_out, and_85_out);
  or or_16 (P2, and_86_out, and_87_out, and_88_out);
  or or_17 (SH1, and_89_out, and_90_out, and_91_out, and_92_out);
  or or_18 (A_M, and_93_out, and_94_out, and_95_out, and_96_out);
  or or_19 (SHL8, and_97_out, and_98_out, and_99_out);
  or or_20 (SHR8, and_100_out, and_101_out, and_102_out);
  or or_21 (EXT, and_103_out, and_104_out, and_105_out, and_106_out);
  or or_22 (SEXT, and_107_out, and_108_out);
  or or_23 (R_A, and_109_out, and_110_out, and_111_out, and_112_out, and_113_out, and_114_out, and_115_out, and_116_out, and_117_out, and_118_out);
  or or_24 (SP_A, and_119_out, and_120_out, and_121_out, and_122_out, and_123_out, and_124_out, and_125_out);
  or or_25 (PC_A, and_126_out, and_127_out, and_128_out, and_129_out, and_130_out);
  or or_26 (R_B, and_131_out, and_132_out, and_133_out, and_134_out, and_135_out, and_136_out, and_137_out);
  or or_27 (K_B, and_138_out, and_139_out, and_140_out, and_141_out, and_142_out, and_143_out);
  or or_28 (ALUQ, and_144_out, and_145_out, and_146_out, and_147_out, and_148_out, and_149_out, and_150_out, and_151_out, and_152_out, and_153_out, and_154_out, and_155_out, and_156_out, and_157_out, and_158_out, and_159_out);
  or or_29 (M_Q, and_160_out, and_161_out, and_162_out, and_163_out);
  or or_30 (WRRD, and_165_out, and_166_out, and_167_out, and_168_out, and_169_out, and_170_out, and_171_out, and_172_out, and_173_out, and_174_out, and_175_out);
  or or_31 (WRSP, and_176_out, and_177_out, and_178_out, and_179_out);
  or or_32 (WRSR, and_180_out, and_181_out, and_182_out, and_183_out, and_184_out, and_185_out, and_186_out, and_187_out, and_188_out, and_189_out);
  or or_33 (WMAR, and_190_out, and_191_out, and_192_out, and_193_out, and_194_out, and_195_out);
  or or_34 (NXT, and_198_out, and_199_out, and_200_out, and_201_out, and_202_out, and_203_out, and_204_out, and_205_out);
  or or_35 (NEXT[3], and_206_out, and_207_out, and_208_out);
  or or_36 (NEXT[2], and_209_out, and_210_out, and_211_out, and_212_out, and_213_out);
  or or_37 (NEXT[1], and_214_out, and_215_out, and_216_out, and_217_out);
  or or_38 (NEXT[0], and_218_out, and_219_out, and_220_out, and_221_out, and_222_out, and_223_out);
endmodule

// Pfx
module ImmDecoder (
  input  nRESET,
  input  cpPfix,
  input  nOE,
  input  [15:0] IR,
  output [15:0] IMM_OUT,
  output [15:0] PFix
);

  wire J_out, P_out, PFIX_Reg_2_q4, Pfx_2_out, Pfx_out, Type_I1_Sel_a, Type_I2_Sel_a, Zero_Sign_Ext_y1,
       Zero_Sign_Ext_y2;
  wire [11:0] Imm_0__3_y2_1;

  nand P (P_out, IR[13], IR[14], IR[15]);
  nand Pfx (Pfx_out, IR[11], IR[12], 1'b1);
  or J (J_out, IR[14], IR[15]);
  IC_74x153 Zero_Sign_Ext (
    .Y1(Zero_Sign_Ext_y1), .Y2(Zero_Sign_Ext_y2), .C1_0(1'b0), .C1_1(1'b0), .C1_2(IR[4]), .C1_3(1'b0),
    .C2_0(1'b0), .C2_1(1'b0), .C2_2(IR[7]), .C2_3(1'b0), .A(IR[12]), .B(IR[13]), .nG1(1'b0), .nG2(IR[11]));
  or Pfx_2 (Pfx_2_out, P_out, Pfx_out);
  IC_74x3251 Type_I2_Sel (
    .A(Type_I2_Sel_a), .B1(1'b1), .B2(1'b1), .B3(1'b1), .B4(1'b1), .B5(1'b1), .B6(1'b0), .B7(1'b0),
    .B8(1'b1), .S0(IR[13]), .S1(IR[14]), .S2(IR[15]), .nOE(1'b0));
  IC_74x3251 Type_I1_Sel (
    .A(Type_I1_Sel_a), .B1(1'b1), .B2(1'b1), .B3(1'b0), .B4(1'b0), .B5(1'b0), .B6(1'b1), .B7(1'b1),
    .B8(1'b1), .S0(IR[13]), .S1(IR[14]), .S2(IR[15]), .nOE(1'b0));
  IC_74x11244 Imm_0__3 (
    .Y1_3(IMM_OUT[2]), .Y1_4(IMM_OUT[3]), .Y2_1(Imm_0__3_y2_1[0]), .Y2_2(Imm_0__3_y2_1[1]),
    .Y2_3(Imm_0__3_y2_1[2]), .Y2_4(Imm_0__3_y2_1[3]), .Y1_1(IMM_OUT[0]), .Y1_2(IMM_OUT[1]),
    .A1_3(Imm_0__3_y2_1[2]), .A1_4(Imm_0__3_y2_1[3]), .nOE1(nOE), .A2_1(IR[0]), .A2_2(IR[1]), .A2_3(IR[2]),
    .A2_4(IR[3]), .A1_1(Imm_0__3_y2_1[0]), .nOE2(1'b0), .A1_2(Imm_0__3_y2_1[1]));
  IC_74x541 Imm_P (
    .Q1(Imm_0__3_y2_1[4]), .Q2(Imm_0__3_y2_1[5]), .Q3(Imm_0__3_y2_1[6]), .Q4(Imm_0__3_y2_1[7]),
    .Q5(Imm_0__3_y2_1[8]), .Q6(Imm_0__3_y2_1[9]), .Q7(Imm_0__3_y2_1[10]), .Q8(Imm_0__3_y2_1[11]), .I1(IR[4]),
    .I2(IR[5]), .I3(IR[6]), .I4(IR[7]), .I5(IR[8]), .I6(IR[9]), .I7(IR[10]), .I8(1'b0), .nOE1(1'b0),
    .nOE2(P_out));
  IC_74x541 Imm_I2 (
    .Q1(Imm_0__3_y2_1[4]), .Q2(Imm_0__3_y2_1[5]), .Q3(Imm_0__3_y2_1[6]), .Q4(Imm_0__3_y2_1[7]),
    .Q5(Imm_0__3_y2_1[8]), .Q6(Imm_0__3_y2_1[9]), .Q7(Imm_0__3_y2_1[10]), .Q8(Imm_0__3_y2_1[11]), .I1(IR[4]),
    .I2(Zero_Sign_Ext_y1), .I3(Zero_Sign_Ext_y1), .I4(Zero_Sign_Ext_y1), .I5(Zero_Sign_Ext_y1),
    .I6(Zero_Sign_Ext_y1), .I7(Zero_Sign_Ext_y1), .I8(Zero_Sign_Ext_y1), .nOE1(1'b0), .nOE2(Type_I2_Sel_a));
  IC_74x541 Imm_I1 (
    .Q1(Imm_0__3_y2_1[4]), .Q2(Imm_0__3_y2_1[5]), .Q3(Imm_0__3_y2_1[6]), .Q4(Imm_0__3_y2_1[7]),
    .Q5(Imm_0__3_y2_1[8]), .Q6(Imm_0__3_y2_1[9]), .Q7(Imm_0__3_y2_1[10]), .Q8(Imm_0__3_y2_1[11]), .I1(IR[4]),
    .I2(IR[5]), .I3(IR[6]), .I4(IR[7]), .I5(Zero_Sign_Ext_y2), .I6(Zero_Sign_Ext_y2), .I7(Zero_Sign_Ext_y2),
    .I8(Zero_Sign_Ext_y2), .nOE1(1'b0), .nOE2(Type_I1_Sel_a));
  IC_74x541 Imm_J (
    .Q1(Imm_0__3_y2_1[4]), .Q2(Imm_0__3_y2_1[5]), .Q3(Imm_0__3_y2_1[6]), .Q4(Imm_0__3_y2_1[7]),
    .Q5(Imm_0__3_y2_1[8]), .Q6(Imm_0__3_y2_1[9]), .Q7(Imm_0__3_y2_1[10]), .Q8(Imm_0__3_y2_1[11]), .I1(IR[4]),
    .I2(IR[5]), .I3(IR[6]), .I4(IR[7]), .I5(IR[8]), .I6(IR[8]), .I7(IR[8]), .I8(IR[8]), .nOE1(1'b0),
    .nOE2(J_out));
  IC_74x273 PFIX_Reg (
    .Q1(PFix[5]), .Q2(PFix[6]), .Q3(PFix[7]), .Q4(PFix[8]), .Q5(PFix[9]), .Q6(PFix[10]), .Q7(PFix[11]),
    .Q8(PFix[12]), .D1(Imm_0__3_y2_1[0]), .D2(Imm_0__3_y2_1[1]), .D3(Imm_0__3_y2_1[2]),
    .D4(Imm_0__3_y2_1[3]), .D5(Imm_0__3_y2_1[4]), .D6(Imm_0__3_y2_1[5]), .D7(Imm_0__3_y2_1[6]),
    .D8(Imm_0__3_y2_1[7]), .CLK(cpPfix), .nMR(nRESET));  // open: Probe
  IC_74175 PFIX_Reg_2 (
    .Q2(PFix[14]), .Q3(PFix[15]), .Q1(PFix[13]), .Q4(PFIX_Reg_2_q4), .D2(Imm_0__3_y2_1[9]),
    .D3(Imm_0__3_y2_1[10]), .D1(Imm_0__3_y2_1[8]), .D4(Pfx_2_out), .CLK(cpPfix), .CLR(nRESET));  // open: R2, R3, R4, R1
  IC_74x257 _4__7 (
    .Y1(IMM_OUT[4]), .Y2(IMM_OUT[5]), .Y3(IMM_OUT[6]), .Y4(IMM_OUT[7]), .I1_0(Imm_0__3_y2_1[4]),
    .I2_0(Imm_0__3_y2_1[4]), .I1_1(PFix[5]), .I2_1(Imm_0__3_y2_1[5]), .I1_2(PFix[6]),
    .I2_2(Imm_0__3_y2_1[6]), .I1_3(PFix[7]), .I2_3(Imm_0__3_y2_1[7]), .nA_B(PFIX_Reg_2_q4), .nOE(nOE));
  IC_74x257 _8__11 (
    .Y1(IMM_OUT[8]), .Y2(IMM_OUT[9]), .Y3(IMM_OUT[10]), .Y4(IMM_OUT[11]), .I1_0(PFix[8]),
    .I2_0(Imm_0__3_y2_1[8]), .I1_1(PFix[9]), .I2_1(Imm_0__3_y2_1[9]), .I1_2(PFix[10]),
    .I2_2(Imm_0__3_y2_1[10]), .I1_3(PFix[11]), .I2_3(Imm_0__3_y2_1[11]), .nA_B(PFIX_Reg_2_q4), .nOE(nOE));
  IC_74x257 _12__15 (
    .Y1(IMM_OUT[12]), .Y2(IMM_OUT[13]), .Y3(IMM_OUT[14]), .Y4(IMM_OUT[15]), .I1_0(PFix[12]),
    .I2_0(Imm_0__3_y2_1[11]), .I1_1(PFix[13]), .I2_1(Imm_0__3_y2_1[11]), .I1_2(PFix[14]),
    .I2_2(Imm_0__3_y2_1[11]), .I1_3(PFix[15]), .I2_3(Imm_0__3_y2_1[11]), .nA_B(PFIX_Reg_2_q4), .nOE(nOE));

  assign PFix[4] = 1'b0;

  // Other names for the same wires on the sheet: CLK_PFIX = cpPfix; CLR_n = nRESET; OE_n = nOE
endmodule

module ALU (
  input  PS0,
  input  PS1,
  input  PS2,
  input  PS3,
  input  C,
  input  CS0,
  input  CS1,
  input  CS2,
  input  GS0,
  input  GS1,
  input  SHR,
  input  P2,
  input  [15:0] A,
  input  [15:0] B,
  input  T,
  input  F,
  input  SL0,
  input  SL1,
  input  nOE,
  input  BR0,
  input  BR1,
  output [15:0] Pipe,
  output ALUCore_C,
  output ALUCore_Cx,
  output [15:0] Q,
  output ALU_BR
);

  wire A15, CS_Select_a, nA15;

  buf buffer_1 (A15, A[15]);
  not not_1 (nA15, A[15]);
  IC_74x3251 CS_Select (
    .A(CS_Select_a), .B1(1'b0), .B2(1'b1), .B3(nA15), .B4(A15), .B5(C), .B6(C), .B7(C), .B8(C), .S0(CS0),
    .S1(CS1), .S2(CS2), .nOE(1'b0));
  // Probe on A
  IC_74x3253 BR_Select (
    .A1(ALU_BR), .B1_1(1'b0), .B1_2(T), .B1_3(F), .B1_4(1'b1), .B2_1(1'b0), .B2_2(1'b0), .B2_3(1'b0),
    .B2_4(1'b0), .S0(BR0), .S1(BR1), .nOE1(1'b0), .nOE2(1'b0));  // open: A2
  // Probe on B
  ALUCore alucore_1 (
    .Cx(ALUCore_Cx), .C(ALUCore_C), .Q(Pipe), .A(A), .B(B), .PS({PS3, PS2, PS1, PS0}), .GS({GS1, GS0}),
    .SHR(SHR), .CS(CS_Select_a), .P2(P2));
  // Probe on Pipe
  ALUSel alusel_1 (.Q(Q), .T(T), .nT(F), .SL0(SL0), .SL1(SL1), .A(Pipe), .B(B), .nOE(nOE));

  // Notes on the sheet:
  //   BR Select
  //   (Branch)
  //   --------
  //   00 (never)
  //   01 (if T)
  //   10 (if F)
  //   11 (always)
  //   PS Select
  //   (See ALU CORE)
  //   CS Select
  //   (GSSel)
  //   --------
  //   000
  //   001
  //   010
  //   011
  //   1xx
  //   Efective
  //   CS
  //   -------
  //   0
  //   1
  //   /A15
  //   A15
  //   Cy
  //   Efective
  //   BR
  //   -------
  //   0
  //   T
  //   /T
  //   1
  //   SL Select
  //   (See ALU SEL)
endmodule

module RegSR (
  input  cpWR,
  input  Cin,
  input  Cxin,
  input  [2:0] CC,
  input  CMP,
  input  CS2,
  input  [15:0] IN,
  output SR_C,
  output SR_T,
  output SR_F
);

  wire ALUCore_C, ALUCore_Cx, ALUCore_nZ, ALUCore_S, AluPipe_2_q1, AluPipe_2_q2, AluPipe_2_q3, AluPipe_2_q4,
       AluPipe_2_q5, AluPipe_2_q6, AluPipe_2_q7, AluPipe_q1, AluPipe_q2, AluPipe_q3, AluPipe_q4, AluPipe_q5,
       AluPipe_q6, AluPipe_q7, AluPipe_q8, and_1_out, and_2_out, buffer_1_out, buffer_3_out, buffer_4_out,
       buffer_5_out, buffer_6_out, nand_1_out, nand_2_out, nand_3_out, not_1_out, not_2_out, not_3_out,
       not_4_out, not_5_out, not_6_out, Pipe_CMP, Pipe_q8, xnor_1_out, xor_1_out, Zero_Detect_2_y1,
       Zero_Detect_2_y2, Zero_Detect_2_y3, Zero_Detect_y1, Zero_Detect_y2, Zero_Detect_y3;
  wire [2:0] CondCode_y1, Pipe_CC;

  // Probe on IN
  nand nand_1 (nand_1_out, CS2, ALUCore_nZ);
  xor xor_1 (xor_1_out, ALUCore_C, ALUCore_Cx);
  IC_74x273 Pipe (
    .Q2(ALUCore_C), .Q3(ALUCore_Cx), .Q4(Pipe_CC[0]), .Q5(Pipe_CC[1]), .Q6(Pipe_CC[2]), .Q7(Pipe_CMP),
    .Q8(Pipe_q8), .D2(Cin), .D3(Cxin), .D4(CC[0]), .D5(CC[1]), .D6(CC[2]), .D7(CMP), .D8(nand_1_out),
    .CLK(cpWR), .nMR(1'b1));  // open: Probe, Q1, D1
  IC_74x273 AluPipe (
    .Q1(AluPipe_q1), .Q2(AluPipe_q2), .Q3(AluPipe_q3), .Q4(AluPipe_q4), .Q5(AluPipe_q5), .Q6(AluPipe_q6),
    .Q7(AluPipe_q7), .Q8(AluPipe_q8), .D1(IN[0]), .D2(IN[1]), .D3(IN[2]), .D4(IN[3]), .D5(IN[4]), .D6(IN[5]),
    .D7(IN[6]), .D8(IN[7]), .CLK(cpWR), .nMR(1'b1));  // open: Probe
  IC_74x273 AluPipe_2 (
    .Q1(AluPipe_2_q1), .Q2(AluPipe_2_q2), .Q3(AluPipe_2_q3), .Q4(AluPipe_2_q4), .Q5(AluPipe_2_q5),
    .Q6(AluPipe_2_q6), .Q7(AluPipe_2_q7), .Q8(ALUCore_S), .D1(IN[8]), .D2(IN[9]), .D3(IN[10]), .D4(IN[11]),
    .D5(IN[12]), .D6(IN[13]), .D7(IN[14]), .D8(IN[15]), .CLK(cpWR), .nMR(1'b1));  // open: Probe
  xnor xnor_1 (xnor_1_out, xor_1_out, ALUCore_S);
  IC_74x257 CondCode (
    .Y1(CondCode_y1[0]), .Y2(CondCode_y1[1]), .Y3(CondCode_y1[2]), .I1_0(1'b0), .I2_0(Pipe_CC[0]),
    .I1_1(1'b0), .I2_1(Pipe_CC[1]), .I1_2(1'b0), .I2_2(Pipe_CC[2]), .I1_3(1'b0), .I2_3(1'b0),
    .nA_B(Pipe_CMP), .nOE(1'b0));  // open: Y4
  IC_74x27 Zero_Detect (
    .Y2(Zero_Detect_y2), .Y3(Zero_Detect_y3), .Y1(Zero_Detect_y1), .A2(AluPipe_q4), .B2(AluPipe_q5),
    .C2(AluPipe_q6), .A3(AluPipe_q7), .B3(AluPipe_q8), .C3(AluPipe_2_q1), .A1(AluPipe_q1), .B1(AluPipe_q2),
    .C1(AluPipe_q3));
  IC_74x27 Zero_Detect_2 (
    .Y2(Zero_Detect_2_y2), .Y3(Zero_Detect_2_y3), .Y1(Zero_Detect_2_y1), .A2(AluPipe_2_q5),
    .B2(AluPipe_2_q6), .C2(AluPipe_2_q7), .A3(ALUCore_S), .B3(1'b0), .C3(1'b0), .A1(AluPipe_2_q2),
    .B1(AluPipe_2_q3), .C1(AluPipe_2_q4));
  not not_1 (not_1_out, ALUCore_nZ);
  buf buffer_1 (buffer_1_out, ALUCore_nZ);
  buf buffer_2 (SR_C, ALUCore_C);
  not not_2 (not_2_out, ALUCore_C);
  buf buffer_3 (buffer_3_out, xnor_1_out);
  not not_3 (not_3_out, xnor_1_out);
  and and_1 (and_1_out, ALUCore_C, ALUCore_nZ);
  and and_2 (and_2_out, ALUCore_nZ, xnor_1_out);
  buf buffer_4 (buffer_4_out, ALUCore_nZ);
  not not_4 (not_4_out, ALUCore_nZ);
  not not_5 (not_5_out, ALUCore_C);
  buf buffer_5 (buffer_5_out, ALUCore_C);
  not not_6 (not_6_out, xnor_1_out);
  buf buffer_6 (buffer_6_out, xnor_1_out);
  nand nand_2 (nand_2_out, ALUCore_C, ALUCore_nZ);
  nand nand_3 (nand_3_out, ALUCore_nZ, xnor_1_out);
  IC_74x30 Zero_Detect_3 (
    .Y(ALUCore_nZ), .C(Zero_Detect_y2), .D(Zero_Detect_y3), .E(Zero_Detect_2_y1), .F(Zero_Detect_2_y2),
    .G(Zero_Detect_2_y3), .A(Pipe_q8), .H(1'b1), .B(Zero_Detect_y1));
  IC_74x3251 ic_74x3251_1 (
    .A(SR_T), .B1(not_1_out), .B2(buffer_1_out), .B3(SR_C), .B4(not_2_out), .B5(buffer_3_out),
    .B6(not_3_out), .B7(and_1_out), .B8(and_2_out), .S0(CondCode_y1[0]), .S1(CondCode_y1[1]),
    .S2(CondCode_y1[2]), .nOE(1'b0));
  IC_74x3251 ic_74x3251_2 (
    .A(SR_F), .B1(buffer_4_out), .B2(not_4_out), .B3(not_5_out), .B4(buffer_5_out), .B5(not_6_out),
    .B6(buffer_6_out), .B7(nand_2_out), .B8(nand_3_out), .S0(CondCode_y1[0]), .S1(CondCode_y1[1]),
    .S2(CondCode_y1[2]), .nOE(1'b0));

  // Other names for the same wires on the sheet: CLK_WR = cpWR

  // Notes on the sheet:
  //   Conditon 
  //   Code (CC)
  //   ---------
  //   000 (EQ)
  //   001 (NE)
  //   010 (UGE)
  //   011 (ULT)
  //   100 (GE)
  //   101 (LT)
  //   110 (UGT)
  //   111 (GT)
  //   Logic 
  //   Function (T)
  //   ------------
  //   Z
  //   /Z
  //   C
  //   /C
  //   S == V
  //   S != V
  //   C AND /Z
  //   (S==V) AND /Z
endmodule

// ALU CORE
module ALUCore (
  input  [15:0] A,
  input  [15:0] B,
  input  [3:0] PS,
  input  [1:0] GS,
  input  SHR,
  input  CS,
  input  P2,
  output C,
  output [15:0] Q,
  output Cx
);

  wire ADD_2_c1, ADD_2_c2, ADD_2_c3, ADD_3_c1, ADD_3_c2, ADD_3_c3, ADD_4_c1, ADD_4_c2, ADD_4_c3, ADD_5_c1,
       ADD_5_c2, ADD_c4, Cy_in_a, gC4, gC8, gC12, LU_a1, LU_a2;
  wire [3:0] gG, gP, LU_2_a1, LU_2_a2, LU_3_a1, LU_3_a2, LU_4_a1, LU_4_a2, P2_2_a, P2_a, SHR_2_y1, SHR_3_y1,
       SHR_4_y1, SHR_y1;

  IC_74x3253 LU (
    .A1(LU_a1), .A2(LU_a2), .B1_1(PS[0]), .B1_2(PS[1]), .B1_3(PS[2]), .B1_4(PS[3]), .B2_1(1'b0),
    .B2_2(GS[0]), .B2_3(1'b0), .B2_4(GS[1]), .S0(A[0]), .S1(B[0]), .nOE1(1'b0), .nOE2(1'b0));
  IC_74x1G3157 u_P2 (.A(P2_a[0]), .B1(LU_a1), .B2(A[0]), .S(P2));
  IC_74x1G3157 P2_2 (.A(P2_2_a[0]), .B1(LU_a2), .B2(PS[3]), .S(P2));
  IC_74x3253 LU_2 (
    .A1(LU_2_a1[0]), .A2(LU_2_a2[0]), .B1_1(PS[0]), .B1_2(PS[1]), .B1_3(PS[2]), .B1_4(PS[3]), .B2_1(1'b0),
    .B2_2(GS[0]), .B2_3(1'b0), .B2_4(GS[1]), .S0(A[4]), .S1(B[4]), .nOE1(1'b0), .nOE2(1'b0));
  IC_74x3253 LU_3 (
    .A1(LU_3_a1[0]), .A2(LU_3_a2[0]), .B1_1(PS[0]), .B1_2(PS[1]), .B1_3(PS[2]), .B1_4(PS[3]), .B2_1(1'b0),
    .B2_2(GS[0]), .B2_3(1'b0), .B2_4(GS[1]), .S0(A[8]), .S1(B[8]), .nOE1(1'b0), .nOE2(1'b0));
  IC_74x3253 LU_4 (
    .A1(LU_4_a1[0]), .A2(LU_4_a2[0]), .B1_1(PS[0]), .B1_2(PS[1]), .B1_3(PS[2]), .B1_4(PS[3]), .B2_1(1'b0),
    .B2_2(GS[0]), .B2_3(1'b0), .B2_4(GS[1]), .S0(A[12]), .S1(B[12]), .nOE1(1'b0), .nOE2(1'b0));
  IC_74x3253 LU_5 (
    .A1(P2_a[1]), .A2(P2_2_a[1]), .B1_1(PS[0]), .B1_2(PS[1]), .B1_3(PS[2]), .B1_4(PS[3]), .B2_1(1'b0),
    .B2_2(GS[0]), .B2_3(1'b0), .B2_4(GS[1]), .S0(A[1]), .S1(B[1]), .nOE1(1'b0), .nOE2(1'b0));
  IC_74x3253 LU_6 (
    .A1(LU_2_a1[1]), .A2(LU_2_a2[1]), .B1_1(PS[0]), .B1_2(PS[1]), .B1_3(PS[2]), .B1_4(PS[3]), .B2_1(1'b0),
    .B2_2(GS[0]), .B2_3(1'b0), .B2_4(GS[1]), .S0(A[5]), .S1(B[5]), .nOE1(1'b0), .nOE2(1'b0));
  IC_74x3253 LU_7 (
    .A1(LU_3_a1[1]), .A2(LU_3_a2[1]), .B1_1(PS[0]), .B1_2(PS[1]), .B1_3(PS[2]), .B1_4(PS[3]), .B2_1(1'b0),
    .B2_2(GS[0]), .B2_3(1'b0), .B2_4(GS[1]), .S0(A[9]), .S1(B[9]), .nOE1(1'b0), .nOE2(1'b0));
  IC_74x3253 LU_8 (
    .A1(LU_4_a1[1]), .A2(LU_4_a2[1]), .B1_1(PS[0]), .B1_2(PS[1]), .B1_3(PS[2]), .B1_4(PS[3]), .B2_1(1'b0),
    .B2_2(GS[0]), .B2_3(1'b0), .B2_4(GS[1]), .S0(A[13]), .S1(B[13]), .nOE1(1'b0), .nOE2(1'b0));
  IC_74x3253 LU_9 (
    .A1(P2_a[2]), .A2(P2_2_a[2]), .B1_1(PS[0]), .B1_2(PS[1]), .B1_3(PS[2]), .B1_4(PS[3]), .B2_1(1'b0),
    .B2_2(GS[0]), .B2_3(1'b0), .B2_4(GS[1]), .S0(A[2]), .S1(B[2]), .nOE1(1'b0), .nOE2(1'b0));
  IC_74x3253 LU_10 (
    .A1(LU_2_a1[2]), .A2(LU_2_a2[2]), .B1_1(PS[0]), .B1_2(PS[1]), .B1_3(PS[2]), .B1_4(PS[3]), .B2_1(1'b0),
    .B2_2(GS[0]), .B2_3(1'b0), .B2_4(GS[1]), .S0(A[6]), .S1(B[6]), .nOE1(1'b0), .nOE2(1'b0));
  IC_74x3253 LU_11 (
    .A1(LU_3_a1[2]), .A2(LU_3_a2[2]), .B1_1(PS[0]), .B1_2(PS[1]), .B1_3(PS[2]), .B1_4(PS[3]), .B2_1(1'b0),
    .B2_2(GS[0]), .B2_3(1'b0), .B2_4(GS[1]), .S0(A[10]), .S1(B[10]), .nOE1(1'b0), .nOE2(1'b0));
  IC_74x3253 LU_12 (
    .A1(LU_4_a1[2]), .A2(LU_4_a2[2]), .B1_1(PS[0]), .B1_2(PS[1]), .B1_3(PS[2]), .B1_4(PS[3]), .B2_1(1'b0),
    .B2_2(GS[0]), .B2_3(1'b0), .B2_4(GS[1]), .S0(A[14]), .S1(B[14]), .nOE1(1'b0), .nOE2(1'b0));
  IC_74x3253 LU_13 (
    .A1(P2_a[3]), .A2(P2_2_a[3]), .B1_1(PS[0]), .B1_2(PS[1]), .B1_3(PS[2]), .B1_4(PS[3]), .B2_1(1'b0),
    .B2_2(GS[0]), .B2_3(1'b0), .B2_4(GS[1]), .S0(A[3]), .S1(B[3]), .nOE1(1'b0), .nOE2(1'b0));
  IC_74x3253 LU_14 (
    .A1(LU_2_a1[3]), .A2(LU_2_a2[3]), .B1_1(PS[0]), .B1_2(PS[1]), .B1_3(PS[2]), .B1_4(PS[3]), .B2_1(1'b0),
    .B2_2(GS[0]), .B2_3(1'b0), .B2_4(GS[1]), .S0(A[7]), .S1(B[7]), .nOE1(1'b0), .nOE2(1'b0));
  IC_74x3253 LU_15 (
    .A1(LU_3_a1[3]), .A2(LU_3_a2[3]), .B1_1(PS[0]), .B1_2(PS[1]), .B1_3(PS[2]), .B1_4(PS[3]), .B2_1(1'b0),
    .B2_2(GS[0]), .B2_3(1'b0), .B2_4(GS[1]), .S0(A[11]), .S1(B[11]), .nOE1(1'b0), .nOE2(1'b0));
  IC_74x3253 LU_16 (
    .A1(LU_4_a1[3]), .A2(LU_4_a2[3]), .B1_1(PS[0]), .B1_2(PS[1]), .B1_3(PS[2]), .B1_4(PS[3]), .B2_1(1'b0),
    .B2_2(GS[0]), .B2_3(1'b0), .B2_4(GS[1]), .S0(A[15]), .S1(B[15]), .nOE1(1'b0), .nOE2(1'b0));
  IC_74x1G3157 Cy_in (.A(Cy_in_a), .B1(CS), .B2(1'b0), .S(SHR));
  IC_74x257 u_SHR (
    .Y1(SHR_y1[0]), .Y2(SHR_y1[1]), .Y3(SHR_y1[2]), .Y4(SHR_y1[3]), .I1_0(P2_a[0]), .I2_0(P2_a[1]),
    .I1_1(P2_a[1]), .I2_1(P2_a[2]), .I1_2(P2_a[2]), .I2_2(P2_a[3]), .I1_3(P2_a[3]), .I2_3(LU_2_a1[0]),
    .nA_B(SHR), .nOE(1'b0));
  IC_74x257 SHR_2 (
    .Y1(SHR_2_y1[0]), .Y2(SHR_2_y1[1]), .Y3(SHR_2_y1[2]), .Y4(SHR_2_y1[3]), .I1_0(LU_2_a1[0]),
    .I2_0(LU_2_a1[1]), .I1_1(LU_2_a1[1]), .I2_1(LU_2_a1[2]), .I1_2(LU_2_a1[2]), .I2_2(LU_2_a1[3]),
    .I1_3(LU_2_a1[3]), .I2_3(LU_3_a1[0]), .nA_B(SHR), .nOE(1'b0));
  IC_74x257 SHR_3 (
    .Y1(SHR_3_y1[0]), .Y2(SHR_3_y1[1]), .Y3(SHR_3_y1[2]), .Y4(SHR_3_y1[3]), .I1_0(LU_3_a1[0]),
    .I2_0(LU_3_a1[1]), .I1_1(LU_3_a1[1]), .I2_1(LU_3_a1[2]), .I1_2(LU_3_a1[2]), .I2_2(LU_3_a1[3]),
    .I1_3(LU_3_a1[3]), .I2_3(LU_4_a1[0]), .nA_B(SHR), .nOE(1'b0));
  IC_74x257 SHR_4 (
    .Y1(SHR_4_y1[0]), .Y2(SHR_4_y1[1]), .Y3(SHR_4_y1[2]), .Y4(SHR_4_y1[3]), .I1_0(LU_4_a1[0]),
    .I2_0(LU_4_a1[1]), .I1_1(LU_4_a1[1]), .I2_1(LU_4_a1[2]), .I1_2(LU_4_a1[2]), .I2_2(LU_4_a1[3]),
    .I1_3(LU_4_a1[3]), .I2_3(CS), .nA_B(SHR), .nOE(1'b0));
  CarryLookAhead ADD (
    .C1(gC4), .C2(gC8), .C3(gC12), .C4(ADD_c4), .C0in(Cy_in_a), .P0(gP[0]), .G0(gG[0]), .P1(gP[1]),
    .G1(gG[1]), .P2(gP[2]), .G2(gG[2]), .P3(gP[3]), .G3(gG[3]));  // open: gP, gG
  CarryLookAhead ADD_2 (
    .gP(gP[0]), .gG(gG[0]), .C1(ADD_2_c1), .C2(ADD_2_c2), .C3(ADD_2_c3), .C0in(Cy_in_a), .P0(P2_a[0]),
    .G0(P2_2_a[0]), .P1(P2_a[1]), .G1(P2_2_a[1]), .P2(P2_a[2]), .G2(P2_2_a[2]), .P3(P2_a[3]), .G3(P2_2_a[3]));  // open: C4
  CarryLookAhead ADD_3 (
    .gP(gP[1]), .gG(gG[1]), .C1(ADD_3_c1), .C2(ADD_3_c2), .C3(ADD_3_c3), .C0in(gC4), .P0(LU_2_a1[0]),
    .G0(LU_2_a2[0]), .P1(LU_2_a1[1]), .G1(LU_2_a2[1]), .P2(LU_2_a1[2]), .G2(LU_2_a2[2]), .P3(LU_2_a1[3]),
    .G3(LU_2_a2[3]));  // open: C4
  CarryLookAhead ADD_4 (
    .gP(gP[2]), .gG(gG[2]), .C1(ADD_4_c1), .C2(ADD_4_c2), .C3(ADD_4_c3), .C0in(gC8), .P0(LU_3_a1[0]),
    .G0(LU_3_a2[0]), .P1(LU_3_a1[1]), .G1(LU_3_a2[1]), .P2(LU_3_a1[2]), .G2(LU_3_a2[2]), .P3(LU_3_a1[3]),
    .G3(LU_3_a2[3]));  // open: C4
  CarryLookAhead ADD_5 (
    .gP(gP[3]), .gG(gG[3]), .C1(ADD_5_c1), .C2(ADD_5_c2), .C3(Cx), .C0in(gC12), .P0(LU_4_a1[0]),
    .G0(LU_4_a2[0]), .P1(LU_4_a1[1]), .G1(LU_4_a2[1]), .P2(LU_4_a1[2]), .G2(LU_4_a2[2]), .P3(LU_4_a1[3]),
    .G3(LU_4_a2[3]));  // open: C4
  IC_74x1G3157 SHR_Cy__out (.A(C), .B1(ADD_c4), .B2(P2_a[0]), .S(SHR));
  IC_7486 ADD_6 (
    .Y3(Q[2]), .Y4(Q[3]), .Y1(Q[0]), .Y2(Q[1]), .A3(ADD_2_c2), .A4(ADD_2_c3), .B1(SHR_y1[0]), .B2(SHR_y1[1]),
    .A1(Cy_in_a), .B3(SHR_y1[2]), .B4(SHR_y1[3]), .A2(ADD_2_c1));
  IC_7486 ADD_7 (
    .Y3(Q[6]), .Y4(Q[7]), .Y1(Q[4]), .Y2(Q[5]), .A3(ADD_3_c2), .A4(ADD_3_c3), .B1(SHR_2_y1[0]),
    .B2(SHR_2_y1[1]), .A1(gC4), .B3(SHR_2_y1[2]), .B4(SHR_2_y1[3]), .A2(ADD_3_c1));
  IC_7486 ADD_8 (
    .Y3(Q[10]), .Y4(Q[11]), .Y1(Q[8]), .Y2(Q[9]), .A3(ADD_4_c2), .A4(ADD_4_c3), .B1(SHR_3_y1[0]),
    .B2(SHR_3_y1[1]), .A1(gC8), .B3(SHR_3_y1[2]), .B4(SHR_3_y1[3]), .A2(ADD_4_c1));
  IC_7486 ADD_9 (
    .Y3(Q[14]), .Y4(Q[15]), .Y1(Q[12]), .Y2(Q[13]), .A3(ADD_5_c2), .A4(Cx), .B1(SHR_4_y1[0]),
    .B2(SHR_4_y1[1]), .A1(gC12), .B3(SHR_4_y1[2]), .B4(SHR_4_y1[3]), .A2(ADD_5_c1));

  // Other names for the same wires on the sheet: A0_3[3:0] = A[3:0]; A4_7[3:0] = A[7:4]; A8_11[3:0] = A[11:8];
  //   A12_15[3:0] = A[15:12]; B0_3[3:0] = B[3:0]; B4_7[3:0] = B[7:4]; B8_11[3:0] = B[11:8]; B12_15[3:0] = B[15:12];
  //   C0 = CS; sGS (some bits) = GS; sPS[3:0] = PS

  // Notes on the sheet:
  //   Function
  //   -----------
  //   SELECT 0
  //   SELECT 1
  //   SELECT A
  //   SELECT B
  //   OR A, B
  //   AND A, B
  //   XOR A, B
  //   NOT A
  //   ADD A, B
  //   ADDC A, B
  //   SUB A, B
  //   SUBC A, B
  //   NEG A
  //   SEXTW A
  //   LSR A
  //   LSRC A
  //   ASR A
  //   INC A
  //   DEC A
  //   A+2
  //   A-2 
  //   (other functions are possible)
  //   PS
  //   -------------
  //   0000 (0x0)
  //   0000 (0x0)
  //   1010 (A)
  //   1100 (B)
  //   1110 (A OR B)
  //   1000 (A AND B)
  //   0110 (A XOR B)
  //   0101 (/A)
  //   0110 (A XOR B)
  //   0110 (A XOR B)
  //   1001 (A XOR /B)
  //   1001 (A XOR /B)
  //   0101 (/A)
  //   1111 (0xffff)
  //   1010 (A)
  //   1010 (A)
  //   1010 (A)
  //   1010 (A)
  //   0101 (/A)
  //   1010 (A)
  //   0101 (/A)
  //   GS
  //   -----------
  //   00 (0x0)
  //   00 (0x0)
  //   00 (0x0)
  //   00 (0x0)
  //   00 (0x0)
  //   00 (0x0)
  //   00 (0x0)
  //   00 (0x0)
  //   10 (A AND B)
  //   10 (A AND B)
  //   01 (A AND /B)
  //   01 (A AND /B)
  //   00 (0x0)
  //   00 (0x0)
  //   00 (0x0)
  //   00 (0x0)
  //   00 (0x0)
  //   00 (0x0)
  //   11 (A)
  //   00 (0x0)
  //   11 (A)
  //   P2
  //   ---
  //   0
  //   0
  //   0
  //   0
  //   0
  //   0
  //   0
  //   0
  //   0
  //   0
  //   0
  //   0
  //   0
  //   0
  //   0
  //   0
  //   0
  //   0
  //   0
  //   1
  //   1
  //   SHR
  //   ---
  //   0
  //   0
  //   0
  //   0
  //   0
  //   0
  //   0
  //   0
  //   0
  //   0
  //   0
  //   0
  //   0
  //   0
  //   1
  //   1
  //   1
  //   0
  //   0
  //   0
  //   0
  //   CS
  //   --------
  //   0
  //   1
  //   0
  //   0
  //   0
  //   0
  //   0
  //   0
  //   0
  //   Prev Carry
  //   1
  //   Prev Carry
  //   1
  //   /A15
  //   0
  //   Prev Carry
  //   A15
  //   1
  //   0
  //   0
  //   0
endmodule

// ALU SEL
module ALUSel (
  input  nOE,
  input  T,
  input  nT,
  input  SL0,
  input  SL1,
  input  [15:0] A,
  input  [15:0] B,
  output [15:0] Q
);

  wire BSel, TSel;
  wire [15:0] BSel_a1;

  IC_74x3257 u_BSel (
    .A1(BSel_a1[0]), .A2(BSel_a1[1]), .A3(BSel_a1[2]), .A4(BSel_a1[3]), .B2_1(B[0]), .B1_2(1'b0),
    .B2_2(B[1]), .B1_3(1'b0), .B2_3(B[2]), .B1_4(1'b0), .B2_4(B[3]), .S(BSel), .nOE(1'b0), .B1_1(1'b0));
  IC_74x3257 BSel_2 (
    .A1(BSel_a1[4]), .A2(BSel_a1[5]), .A3(BSel_a1[6]), .A4(BSel_a1[7]), .B2_1(B[4]), .B1_2(1'b0),
    .B2_2(B[5]), .B1_3(1'b0), .B2_3(B[6]), .B1_4(1'b0), .B2_4(B[7]), .S(BSel), .nOE(1'b0), .B1_1(1'b0));
  IC_74x3257 BSel_3 (
    .A1(BSel_a1[8]), .A2(BSel_a1[9]), .A3(BSel_a1[10]), .A4(BSel_a1[11]), .B2_1(B[8]), .B1_2(1'b0),
    .B2_2(B[9]), .B1_3(1'b0), .B2_3(B[10]), .B1_4(1'b0), .B2_4(B[11]), .S(BSel), .nOE(1'b0), .B1_1(1'b0));
  IC_74x3257 BSel_4 (
    .A1(BSel_a1[12]), .A2(BSel_a1[13]), .A3(BSel_a1[14]), .A4(BSel_a1[15]), .B2_1(B[12]), .B1_2(1'b0),
    .B2_2(B[13]), .B1_3(1'b0), .B2_3(B[14]), .B1_4(1'b0), .B2_4(B[15]), .S(BSel), .nOE(1'b0), .B1_1(1'b0));
  IC_74x3253 AluSel (
    .A1(TSel), .A2(BSel), .B1_1(1'b1), .B1_2(T), .B1_3(nT), .B1_4(T), .B2_1(1'b0), .B2_2(1'b0), .B2_3(1'b0),
    .B2_4(1'b1), .S0(SL0), .S1(SL1), .nOE1(1'b0), .nOE2(1'b0));
  IC_74x3257 u_TSel (
    .A1(Q[0]), .A2(Q[1]), .A3(Q[2]), .A4(Q[3]), .B2_1(A[0]), .B1_2(BSel_a1[1]), .B2_2(A[1]),
    .B1_3(BSel_a1[2]), .B2_3(A[2]), .B1_4(BSel_a1[3]), .B2_4(A[3]), .S(TSel), .nOE(nOE), .B1_1(BSel_a1[0]));
  IC_74x3257 TSel_2 (
    .A1(Q[4]), .A2(Q[5]), .A3(Q[6]), .A4(Q[7]), .B2_1(A[4]), .B1_2(BSel_a1[5]), .B2_2(A[5]),
    .B1_3(BSel_a1[6]), .B2_3(A[6]), .B1_4(BSel_a1[7]), .B2_4(A[7]), .S(TSel), .nOE(nOE), .B1_1(BSel_a1[4]));
  IC_74x3257 TSel_3 (
    .A1(Q[8]), .A2(Q[9]), .A3(Q[10]), .A4(Q[11]), .B2_1(A[8]), .B1_2(BSel_a1[9]), .B2_2(A[9]),
    .B1_3(BSel_a1[10]), .B2_3(A[10]), .B1_4(BSel_a1[11]), .B2_4(A[11]), .S(TSel), .nOE(nOE), .B1_1(BSel_a1[8]));
  IC_74x3257 TSel_4 (
    .A1(Q[12]), .A2(Q[13]), .A3(Q[14]), .A4(Q[15]), .B2_1(A[12]), .B1_2(BSel_a1[13]), .B2_2(A[13]),
    .B1_3(BSel_a1[14]), .B2_3(A[14]), .B1_4(BSel_a1[15]), .B2_4(A[15]), .S(TSel), .nOE(nOE),
    .B1_1(BSel_a1[12]));

  // Other names for the same wires on the sheet: F = nT; OE_n = nOE

  // Notes on the sheet:
  //   Function    A  B   SL  
  //   ---------------------------
  //   SELECT A    A  x   00
  //   SELT A, 0   A  x   01
  //   SETT        1  x   01
  //   SELF A, 0   A  x   10
  //   SETF        1  x   10
  //   SEL A, B    A  B   11
endmodule

// CY LOOK AHEAD
module CarryLookAhead (
  input  C0in,
  input  P0,
  input  G0,
  input  P1,
  input  G1,
  input  P2,
  input  G2,
  input  P3,
  input  G3,
  output C1,
  output C2,
  output C3,
  output C4,
  output gP,
  output gG
);

  wire and_1_out, and_2_out, and_3_out, and_4_out, and_5_out, and_6_out, and_7_out, and_8_out, and_9_out,
       and_10_out, and_12_out, and_13_out, and_14_out, buffer_1_out, buffer_2_out, buffer_3_out,
       buffer_4_out, buffer_5_out;

  buf buffer_1 (buffer_1_out, G0);
  and and_1 (and_1_out, C0in, P0);
  buf buffer_2 (buffer_2_out, G1);
  and and_2 (and_2_out, G0, P1);
  and and_3 (and_3_out, C0in, P0, P1);
  buf buffer_3 (buffer_3_out, G2);
  and and_4 (and_4_out, G1, P2);
  and and_5 (and_5_out, G0, P1, P2);
  and and_6 (and_6_out, C0in, P0, P1, P2);
  buf buffer_4 (buffer_4_out, G3);
  and and_7 (and_7_out, G2, P3);
  and and_8 (and_8_out, G1, P2, P3);
  and and_9 (and_9_out, G0, P1, P2, P3);
  and and_10 (and_10_out, C0in, P0, P1, P2, P3);
  and and_11 (gP, P0, P1, P2, P3);
  buf buffer_5 (buffer_5_out, G3);
  and and_12 (and_12_out, G2, P3);
  and and_13 (and_13_out, G1, P2, P3);
  and and_14 (and_14_out, G0, P1, P2, P3);
  or or_1 (C1, buffer_1_out, and_1_out);
  or or_2 (C2, buffer_2_out, and_2_out, and_3_out);
  or or_3 (C3, buffer_3_out, and_4_out, and_5_out, and_6_out);
  or or_4 (C4, buffer_4_out, and_7_out, and_8_out, and_9_out, and_10_out);
  or or_5 (gG, buffer_5_out, and_12_out, and_13_out, and_14_out);

  // Notes on the sheet:
  //   C0
  //   G0
  //   G1
  //   G2
  //   G3
  //   P0
  //   P1
  //   P2
  //   P3
  //   Logic Function
  //   -----------------------------------------------------------------
  //   C1 = (Cin . P0) + G0 
  //   C2 = (Cin . P1 . P0) + (G0 . P1) + G1
  //   C3 = (Cin . P2 . P1 . P0) + (G0 . P2 . P1) + (G1 . P2) + G2 
  //   C4 = (Cin . P3 . P2 . P1 . P0) + (G0 . P3 . P2 . P1) + (G1 . P3 . P2) + ( G2 . P3 ) + G3
  //   gP = (P3 . P2 . P1 . P0 )
  //   gG = (G0 . P3 . P2 . P1) + (G1 . P3 . P2) + (G2 . P3) + G3
endmodule

// SCALE
module SHL1 (
  input  [15:0] B_BUS_IN,
  input  ISw,
  output [15:0] Out
);

  IC_74x3257 SHL8 (
    .A1(Out[0]), .A2(Out[1]), .A3(Out[2]), .A4(Out[3]), .B2_1(1'b0), .B1_2(B_BUS_IN[1]), .B2_2(B_BUS_IN[0]),
    .B1_3(B_BUS_IN[2]), .B2_3(B_BUS_IN[1]), .B1_4(B_BUS_IN[3]), .B2_4(B_BUS_IN[2]), .S(ISw), .nOE(1'b0),
    .B1_1(B_BUS_IN[0]));
  IC_74x3257 SHL8_2 (
    .A1(Out[4]), .A2(Out[5]), .A3(Out[6]), .A4(Out[7]), .B2_1(B_BUS_IN[3]), .B1_2(B_BUS_IN[5]),
    .B2_2(B_BUS_IN[4]), .B1_3(B_BUS_IN[6]), .B2_3(B_BUS_IN[5]), .B1_4(B_BUS_IN[7]), .B2_4(B_BUS_IN[6]),
    .S(ISw), .nOE(1'b0), .B1_1(B_BUS_IN[4]));
  IC_74x3257 SHL8_3 (
    .A1(Out[8]), .A2(Out[9]), .A3(Out[10]), .A4(Out[11]), .B2_1(B_BUS_IN[7]), .B1_2(B_BUS_IN[9]),
    .B2_2(B_BUS_IN[8]), .B1_3(B_BUS_IN[10]), .B2_3(B_BUS_IN[9]), .B1_4(B_BUS_IN[11]), .B2_4(B_BUS_IN[10]),
    .S(ISw), .nOE(1'b0), .B1_1(B_BUS_IN[8]));
  IC_74x3257 SHL8_4 (
    .A1(Out[12]), .A2(Out[13]), .A3(Out[14]), .A4(Out[15]), .B2_1(B_BUS_IN[11]), .B1_2(B_BUS_IN[13]),
    .B2_2(B_BUS_IN[12]), .B1_3(B_BUS_IN[14]), .B2_3(B_BUS_IN[13]), .B1_4(B_BUS_IN[15]), .B2_4(B_BUS_IN[14]),
    .S(ISw), .nOE(1'b0), .B1_1(B_BUS_IN[12]));
endmodule

// MAR-CTRL
module MARCTRL (
  input  RESET,
  input  CLK,
  input  nExt,
  input  SEx,
  input  ISh,
  input  OSh,
  input  WRMAR,
  input  nIE,
  input  nOE,
  input  cpWRMAR,
  input  [15:0] Q_BUS_IN,
  output nOExt,
  output SExt,
  output IShift,
  output OShift,
  output nMWE,
  output nIE_2,
  output nOE_2,
  output nMOE,
  output nCE0,
  output nCE1,
  output [14:0] ADDR,
  output [15:0] Addr_2
);

  wire Addr0, and_1_out, and_2_out, CE_Sel_a1, CE_Sel_a2, Mem_En_a1, MemCy2_q1, MemCy2_q2, MemCy2_q3,
       MemCy2_q4, MemCy2_q6, MemCy2_q8;

  IC_74x273 MemCy2 (
    .Q1(MemCy2_q1), .Q2(MemCy2_q2), .Q3(MemCy2_q3), .Q4(MemCy2_q4), .Q6(MemCy2_q6), .Q8(MemCy2_q8),
    .D1(nExt), .D2(SEx), .D3(ISh), .D4(OSh), .D6(WRMAR), .D8(Mem_En_a1), .CLK(CLK), .nMR(RESET));  // open: Probe, Q5, Q7, D5, D7
  IC_74x273 MAR (
    .Probe(Addr_2[7:0]), .Q1(Addr0), .Q2(ADDR[0]), .Q3(ADDR[1]), .Q4(ADDR[2]), .Q5(ADDR[3]), .Q6(ADDR[4]),
    .Q7(ADDR[5]), .Q8(ADDR[6]), .D1(Q_BUS_IN[0]), .D2(Q_BUS_IN[1]), .D3(Q_BUS_IN[2]), .D4(Q_BUS_IN[3]),
    .D5(Q_BUS_IN[4]), .D6(Q_BUS_IN[5]), .D7(Q_BUS_IN[6]), .D8(Q_BUS_IN[7]), .CLK(cpWRMAR), .nMR(1'b1));
  IC_74x273 MAR_2 (
    .Probe(Addr_2[15:8]), .Q1(ADDR[7]), .Q2(ADDR[8]), .Q3(ADDR[9]), .Q4(ADDR[10]), .Q5(ADDR[11]),
    .Q6(ADDR[12]), .Q7(ADDR[13]), .Q8(ADDR[14]), .D1(Q_BUS_IN[8]), .D2(Q_BUS_IN[9]), .D3(Q_BUS_IN[10]),
    .D4(Q_BUS_IN[11]), .D5(Q_BUS_IN[12]), .D6(Q_BUS_IN[13]), .D7(Q_BUS_IN[14]), .D8(Q_BUS_IN[15]),
    .CLK(cpWRMAR), .nMR(1'b1));
  and and_1 (and_1_out, MemCy2_q3, Addr0);
  and and_2 (and_2_out, Addr0, MemCy2_q4);
  IC_74x3253 CE_Sel (
    .A1(CE_Sel_a1), .A2(CE_Sel_a2), .B1_1(1'b0), .B1_2(1'b0), .B1_3(1'b0), .B1_4(1'b1), .B2_1(1'b0),
    .B2_2(1'b0), .B2_3(1'b1), .B2_4(1'b0), .S0(Addr0), .S1(MemCy2_q3), .nOE1(1'b0), .nOE2(1'b0));
  IC_74x3257 Ctrl_Sel (
    .A1(nOExt), .A2(SExt), .A3(IShift), .A4(OShift), .B2_1(MemCy2_q1), .B1_2(SEx), .B2_2(MemCy2_q2),
    .B1_3(ISh), .B2_3(and_1_out), .B1_4(OSh), .B2_4(and_2_out), .S(MemCy2_q6), .nOE(1'b0), .B1_1(nExt));
  IC_74x1G3157 WE (.A(nMWE), .B1(1'b1), .B2(Mem_En_a1), .S(MemCy2_q8));
  IC_74x3257 Mem_En (
    .A1(Mem_En_a1), .A2(nMOE), .A3(nCE0), .A4(nCE1), .B2_1(nIE), .B1_2(1'b1), .B2_2(nOE), .B1_3(1'b1),
    .B2_3(CE_Sel_a1), .B1_4(1'b1), .B2_4(CE_Sel_a2), .S(MemCy2_q6), .nOE(1'b0), .B1_1(1'b1));

  assign nIE_2 = nIE;
  assign nOE_2 = nOE;

  // Other names for the same wires on the sheet: CLR_n = RESET

  // Notes on the sheet:
  //   Operation
  //   ---------
  //   ST.W
  //   ST.B
  //   LD.W
  //   LD.SB
  //   LD.ZB
  //   PASTHR
  //   SEXT
  //   ZEXT
  //   ASR8
  //   LSR8
  //   LSL8
  //   Hi Z
  //           CYCLE 1
  //   Mem nIE nOE ISh OSh nEx SEx
  //   ---------------------------
  //    1   1   1   0   x   x   x 
  //    1   1   1   1   x   x   x
  //    1   1   1   0   0   1   x
  //    1   1   1   0   1   0   1
  //    1   1   1   0   1   0   0
  //    0   0   0   0   0   1   x
  //    0   0   0   0   0   0   1
  //    0   0   0   0   0   0   0
  //    0   0   0   0   1   0   1
  //    0   0   0   0   1   0   0
  //    0   0   0   1   0   1   x
  //    0   1   1   x   x   x   x
  //            CYCLE 2
  //   Mem nIE nOE ISh OSh nEx SEx
  //   ---------------------------
  //    0   0   1   x   x   x   x 
  //    0   0   1   x   x   x   x
  //    0   1   0   x   x   x   x
  //    0   1   0   x   x   x   x
  //    0   1   0   x   x   x   x
  //    -   -   -   -   -   -   -
  //    -   -   -   -   -   -   -
  //    -   -   -   -   -   -   -
  //    -   -   -   -   -   -   -
  //    -   -   -   -   -   -   -
  //    -   -   -   -   -   -   -
  //    -   -   -   -   -   -   -
endmodule

module SHL8 (
  input  nIE,
  input  [15:0] A_BUS_IN,
  input  ISh,
  output [7:0] D_LOW,
  output [7:0] D_HIGH
);

  IC_74x3257 SHL8 (
    .A1(D_LOW[0]), .A2(D_LOW[1]), .A3(D_LOW[2]), .A4(D_LOW[3]), .B2_1(1'b0), .B1_2(A_BUS_IN[1]), .B2_2(1'b0),
    .B1_3(A_BUS_IN[2]), .B2_3(1'b0), .B1_4(A_BUS_IN[3]), .B2_4(1'b0), .S(ISh), .nOE(nIE), .B1_1(A_BUS_IN[0]));
  IC_74x3257 SHL8_2 (
    .A1(D_LOW[4]), .A2(D_LOW[5]), .A3(D_LOW[6]), .A4(D_LOW[7]), .B2_1(1'b0), .B1_2(A_BUS_IN[5]), .B2_2(1'b0),
    .B1_3(A_BUS_IN[6]), .B2_3(1'b0), .B1_4(A_BUS_IN[7]), .B2_4(1'b0), .S(ISh), .nOE(nIE), .B1_1(A_BUS_IN[4]));
  IC_74x3257 SHL8_3 (
    .A1(D_HIGH[0]), .A2(D_HIGH[1]), .A3(D_HIGH[2]), .A4(D_HIGH[3]), .B2_1(A_BUS_IN[0]), .B1_2(A_BUS_IN[9]),
    .B2_2(A_BUS_IN[1]), .B1_3(A_BUS_IN[10]), .B2_3(A_BUS_IN[2]), .B1_4(A_BUS_IN[11]), .B2_4(A_BUS_IN[3]),
    .S(ISh), .nOE(nIE), .B1_1(A_BUS_IN[8]));
  IC_74x3257 SHL8_4 (
    .A1(D_HIGH[4]), .A2(D_HIGH[5]), .A3(D_HIGH[6]), .A4(D_HIGH[7]), .B2_1(A_BUS_IN[4]), .B1_2(A_BUS_IN[13]),
    .B2_2(A_BUS_IN[5]), .B1_3(A_BUS_IN[14]), .B2_3(A_BUS_IN[6]), .B1_4(A_BUS_IN[15]), .B2_4(A_BUS_IN[7]),
    .S(ISh), .nOE(nIE), .B1_1(A_BUS_IN[12]));

  // Other names for the same wires on the sheet: IE_n = nIE
endmodule

module SHR8EXT (
  input  nOE,
  input  OSh,
  input  SEx,
  input  [7:0] IN_LO,
  input  [7:0] IN_HI,
  input  nExt,
  output [15:0] Q_BUS_OUT
);

  wire OSH_a, SEX_a;

  IC_74x1G3157 u_OSH (.A(OSH_a), .B1(IN_LO[7]), .B2(IN_HI[7]), .S(OSh));
  IC_74x1G3157 u_SEX (.A(SEX_a), .B1(1'b0), .B2(OSH_a), .S(SEx));
  IC_74x3257 SHR8 (
    .A1(Q_BUS_OUT[0]), .A2(Q_BUS_OUT[1]), .A3(Q_BUS_OUT[2]), .A4(Q_BUS_OUT[3]), .B2_1(IN_HI[0]),
    .B1_2(IN_LO[1]), .B2_2(IN_HI[1]), .B1_3(IN_LO[2]), .B2_3(IN_HI[2]), .B1_4(IN_LO[3]), .B2_4(IN_HI[3]),
    .S(OSh), .nOE(nOE), .B1_1(IN_LO[0]));
  IC_74x3257 SHR8_2 (
    .A1(Q_BUS_OUT[4]), .A2(Q_BUS_OUT[5]), .A3(Q_BUS_OUT[6]), .A4(Q_BUS_OUT[7]), .B2_1(IN_HI[4]),
    .B1_2(IN_LO[5]), .B2_2(IN_HI[5]), .B1_3(IN_LO[6]), .B2_3(IN_HI[6]), .B1_4(IN_LO[7]), .B2_4(IN_HI[7]),
    .S(OSh), .nOE(nOE), .B1_1(IN_LO[4]));
  IC_74x3257 SHR8_3 (
    .A1(Q_BUS_OUT[8]), .A2(Q_BUS_OUT[9]), .A3(Q_BUS_OUT[10]), .A4(Q_BUS_OUT[11]), .B2_1(IN_HI[0]),
    .B1_2(SEX_a), .B2_2(IN_HI[1]), .B1_3(SEX_a), .B2_3(IN_HI[2]), .B1_4(SEX_a), .B2_4(IN_HI[3]), .S(nExt),
    .nOE(nOE), .B1_1(SEX_a));
  IC_74x3257 SHR8_4 (
    .A1(Q_BUS_OUT[12]), .A2(Q_BUS_OUT[13]), .A3(Q_BUS_OUT[14]), .A4(Q_BUS_OUT[15]), .B2_1(IN_HI[4]),
    .B1_2(SEX_a), .B2_2(IN_HI[5]), .B1_3(SEX_a), .B2_3(IN_HI[6]), .B1_4(SEX_a), .B2_4(IN_HI[7]), .S(nExt),
    .nOE(nOE), .B1_1(SEX_a));

  // Other names for the same wires on the sheet: OE_n = nOE
endmodule

// SWAP - MEM - EXT
module SRAM (
  input  RESET,
  input  CLK,
  input  cpWRMAR,
  input  nExt,
  input  SEx,
  input  ISw,
  input  OSh,
  input  WRMAR,
  input  nIE,
  input  nOE,
  input  [15:0] A_BUS_IN,
  input  [15:0] Q_BUS_IN,
  output [15:0] Q_BUS_OUT
);

  wire Addr0, and_1_out, and_2_out, and_3_out, and_4_out, and_5_out, and_6_out, CE0_n, CE1_n, CE_a1, CE_a2,
       ic_74x1g3157_1_a, ic_74x1g3157_2_a, ic_74x3257_5_a1, ISwap, MemCy2_q1, MemCy2_q2, MemCy2_q3,
       MemCy2_q4, MemCy2_q6, MemCy2_q8, MOE_n, MWE_n, OExt_n, OShift, SExt;
  wire [7:0] ic_74x3257_1_a1, ic_74x3257_3_a1;
  wire [14:0] MAR_q2;

  IC_74x273 MemCy2 (
    .Q1(MemCy2_q1), .Q2(MemCy2_q2), .Q3(MemCy2_q3), .Q4(MemCy2_q4), .Q6(MemCy2_q6), .Q8(MemCy2_q8),
    .D1(nExt), .D2(SEx), .D3(ISw), .D4(OSh), .D6(WRMAR), .D8(ic_74x3257_5_a1), .CLK(CLK), .nMR(RESET));  // open: Probe, Q5, Q7, D5, D7
  IC_74x3257 ic_74x3257_1 (
    .A1(ic_74x3257_1_a1[0]), .A2(ic_74x3257_1_a1[1]), .A3(ic_74x3257_1_a1[2]), .A4(ic_74x3257_1_a1[3]),
    .B2_1(1'b0), .B1_2(A_BUS_IN[1]), .B2_2(1'b0), .B1_3(A_BUS_IN[2]), .B2_3(1'b0), .B1_4(A_BUS_IN[3]),
    .B2_4(1'b0), .S(ISwap), .nOE(nIE), .B1_1(A_BUS_IN[0]));
  IC_74x3257 ic_74x3257_2 (
    .A1(ic_74x3257_1_a1[4]), .A2(ic_74x3257_1_a1[5]), .A3(ic_74x3257_1_a1[6]), .A4(ic_74x3257_1_a1[7]),
    .B2_1(1'b0), .B1_2(A_BUS_IN[5]), .B2_2(1'b0), .B1_3(A_BUS_IN[6]), .B2_3(1'b0), .B1_4(A_BUS_IN[7]),
    .B2_4(1'b0), .S(ISwap), .nOE(nIE), .B1_1(A_BUS_IN[4]));
  IC_74x3257 ic_74x3257_3 (
    .A1(ic_74x3257_3_a1[0]), .A2(ic_74x3257_3_a1[1]), .A3(ic_74x3257_3_a1[2]), .A4(ic_74x3257_3_a1[3]),
    .B2_1(A_BUS_IN[0]), .B1_2(A_BUS_IN[9]), .B2_2(A_BUS_IN[1]), .B1_3(A_BUS_IN[10]), .B2_3(A_BUS_IN[2]),
    .B1_4(A_BUS_IN[11]), .B2_4(A_BUS_IN[3]), .S(ISwap), .nOE(nIE), .B1_1(A_BUS_IN[8]));
  IC_74x3257 ic_74x3257_4 (
    .A1(ic_74x3257_3_a1[4]), .A2(ic_74x3257_3_a1[5]), .A3(ic_74x3257_3_a1[6]), .A4(ic_74x3257_3_a1[7]),
    .B2_1(A_BUS_IN[4]), .B1_2(A_BUS_IN[13]), .B2_2(A_BUS_IN[5]), .B1_3(A_BUS_IN[14]), .B2_3(A_BUS_IN[6]),
    .B1_4(A_BUS_IN[15]), .B2_4(A_BUS_IN[7]), .S(ISwap), .nOE(nIE), .B1_1(A_BUS_IN[12]));
  IC_74x273 MAR (
    .Q1(Addr0), .Q2(MAR_q2[0]), .Q3(MAR_q2[1]), .Q4(MAR_q2[2]), .Q5(MAR_q2[3]), .Q6(MAR_q2[4]),
    .Q7(MAR_q2[5]), .Q8(MAR_q2[6]), .D1(Q_BUS_IN[0]), .D2(Q_BUS_IN[1]), .D3(Q_BUS_IN[2]), .D4(Q_BUS_IN[3]),
    .D5(Q_BUS_IN[4]), .D6(Q_BUS_IN[5]), .D7(Q_BUS_IN[6]), .D8(Q_BUS_IN[7]), .CLK(cpWRMAR), .nMR(1'b1));  // open: Probe
  IC_74x273 MAR_2 (
    .Q1(MAR_q2[7]), .Q2(MAR_q2[8]), .Q3(MAR_q2[9]), .Q4(MAR_q2[10]), .Q5(MAR_q2[11]), .Q6(MAR_q2[12]),
    .Q7(MAR_q2[13]), .Q8(MAR_q2[14]), .D1(Q_BUS_IN[8]), .D2(Q_BUS_IN[9]), .D3(Q_BUS_IN[10]),
    .D4(Q_BUS_IN[11]), .D5(Q_BUS_IN[12]), .D6(Q_BUS_IN[13]), .D7(Q_BUS_IN[14]), .D8(Q_BUS_IN[15]),
    .CLK(cpWRMAR), .nMR(1'b1));  // open: Probe
  and and_1 (and_1_out, MemCy2_q3, Addr0);
  and and_2 (and_2_out, Addr0, MemCy2_q4);
  IC_74x3253 CE (
    .A1(CE_a1), .A2(CE_a2), .B1_1(1'b0), .B1_2(1'b0), .B1_3(1'b0), .B1_4(1'b1), .B2_1(1'b0), .B2_2(1'b0),
    .B2_3(1'b1), .B2_4(1'b0), .S0(Addr0), .S1(MemCy2_q3), .nOE1(1'b0), .nOE2(1'b0));
  IC_74x1G3157 ic_74x1g3157_1 (.A(ic_74x1g3157_1_a), .B1(ic_74x3257_1_a1[7]), .B2(ic_74x3257_3_a1[7]), .S(OShift));
  IC_74x1G3157 ic_74x1g3157_2 (.A(ic_74x1g3157_2_a), .B1(1'b0), .B2(ic_74x1g3157_1_a), .S(SExt));
  and and_3 (and_3_out, ~MOE_n, MWE_n, ~CE0_n);  // AND_Gate
  and and_4 (and_4_out, ~CE0_n, ~MWE_n);  // AND_Gate
  and and_5 (and_5_out, ~MOE_n, MWE_n, ~CE1_n);  // AND_Gate
  and and_6 (and_6_out, ~CE1_n, ~MWE_n);  // AND_Gate
  RAM #(.addrWidth(15), .databus("bidir"), .trigger("low")) Low_Byte (
    .addr(MAR_q2), .data(ic_74x3257_1_a1));  // open: we, oe, clk
  RAM #(.addrWidth(15), .databus("bidir"), .trigger("low")) High_Byte (
    .addr(MAR_q2), .data(ic_74x3257_3_a1));  // open: we, oe, clk
  IC_74x3257 CtrlSel (
    .A1(OExt_n), .A2(SExt), .A3(ISwap), .A4(OShift), .B2_1(MemCy2_q1), .B1_2(SEx), .B2_2(MemCy2_q2),
    .B1_3(ISw), .B2_3(and_1_out), .B1_4(OSh), .B2_4(and_2_out), .S(MemCy2_q6), .nOE(1'b0), .B1_1(nExt));
  IC_74x1G3157 ic_74x1g3157_3 (.A(MWE_n), .B1(1'b1), .B2(ic_74x3257_5_a1), .S(MemCy2_q8));
  IC_74x3257 ic_74x3257_5 (
    .A1(ic_74x3257_5_a1), .A2(MOE_n), .A3(CE0_n), .A4(CE1_n), .B2_1(nIE), .B1_2(1'b1), .B2_2(nOE),
    .B1_3(1'b1), .B2_3(CE_a1), .B1_4(1'b1), .B2_4(CE_a2), .S(MemCy2_q6), .nOE(1'b0), .B1_1(1'b1));
  IC_74x3257 ic_74x3257_6 (
    .A1(Q_BUS_OUT[0]), .A2(Q_BUS_OUT[1]), .A3(Q_BUS_OUT[2]), .A4(Q_BUS_OUT[3]), .B2_1(ic_74x3257_3_a1[0]),
    .B1_2(ic_74x3257_1_a1[1]), .B2_2(ic_74x3257_3_a1[1]), .B1_3(ic_74x3257_1_a1[2]),
    .B2_3(ic_74x3257_3_a1[2]), .B1_4(ic_74x3257_1_a1[3]), .B2_4(ic_74x3257_3_a1[3]), .S(OShift), .nOE(nOE),
    .B1_1(ic_74x3257_1_a1[0]));
  IC_74x3257 ic_74x3257_7 (
    .A1(Q_BUS_OUT[4]), .A2(Q_BUS_OUT[5]), .A3(Q_BUS_OUT[6]), .A4(Q_BUS_OUT[7]), .B2_1(ic_74x3257_3_a1[4]),
    .B1_2(ic_74x3257_1_a1[5]), .B2_2(ic_74x3257_3_a1[5]), .B1_3(ic_74x3257_1_a1[6]),
    .B2_3(ic_74x3257_3_a1[6]), .B1_4(ic_74x3257_1_a1[7]), .B2_4(ic_74x3257_3_a1[7]), .S(OShift), .nOE(nOE),
    .B1_1(ic_74x3257_1_a1[4]));
  IC_74x3257 ic_74x3257_8 (
    .A1(Q_BUS_OUT[8]), .A2(Q_BUS_OUT[9]), .A3(Q_BUS_OUT[10]), .A4(Q_BUS_OUT[11]), .B2_1(ic_74x3257_3_a1[0]),
    .B1_2(ic_74x1g3157_2_a), .B2_2(ic_74x3257_3_a1[1]), .B1_3(ic_74x1g3157_2_a), .B2_3(ic_74x3257_3_a1[2]),
    .B1_4(ic_74x1g3157_2_a), .B2_4(ic_74x3257_3_a1[3]), .S(OExt_n), .nOE(nOE), .B1_1(ic_74x1g3157_2_a));
  IC_74x3257 ic_74x3257_9 (
    .A1(Q_BUS_OUT[12]), .A2(Q_BUS_OUT[13]), .A3(Q_BUS_OUT[14]), .A4(Q_BUS_OUT[15]),
    .B2_1(ic_74x3257_3_a1[4]), .B1_2(ic_74x1g3157_2_a), .B2_2(ic_74x3257_3_a1[5]), .B1_3(ic_74x1g3157_2_a),
    .B2_3(ic_74x3257_3_a1[6]), .B1_4(ic_74x1g3157_2_a), .B2_4(ic_74x3257_3_a1[7]), .S(OExt_n), .nOE(nOE),
    .B1_1(ic_74x1g3157_2_a));

  // Other names for the same wires on the sheet: CLK_WRMAR = cpWRMAR; CLR_n = RESET; IE_n = nIE; OE_n = nOE

  // Notes on the sheet:
  //   Operation
  //   ---------
  //   ST.W
  //   ST.B
  //   LD.W
  //   LD.SB
  //   LD.ZB
  //   PASTHR
  //   SEXT
  //   ZEXT
  //   ASR8
  //   LSR8
  //   LSL8
  //           CYCLE 1
  //   Mem nIE nOE nEx SEx ISw OSh
  //   ---------------------------
  //    1   1   1   x   x   0   x 
  //    1   1   1   x   x   1   x
  //    1   1   1   1   x   0   0
  //    1   1   1   0   1   0   1
  //    1   1   1   0   0   0   1
  //    0   0   0   1   x   0   0
  //    0   0   0   0   1   0   0
  //    0   0   0   0   0   0   0
  //    0   0   0   0   1   0   1
  //    0   0   0   0   0   0   1
  //    0   0   0   1   x   1   0
  //            CYCLE 2
  //   Mem nIE nOE nEx SEx ISw OSh
  //   ---------------------------
  //    0   0   1   x   x   x   x 
  //    0   0   1   x   x   x   x
  //    0   1   0   x   x   x   x
  //    0   1   0   x   x   x   x
  //    0   1   0   x   x   x   x
  //    -   -   -   -   -   -   -
  //    -   -   -   -   -   -   -
  //    -   -   -   -   -   -   -
  //    -   -   -   -   -   -   -
  //    -   -   -   -   -   -   -
  //    -   -   -   -   -   -   -
endmodule
// Register File
module Registers (
  input  CLK,
  input  WR,
  input  nR_TO_A,
  input  nR_TO_B,
  input  IR_A,
  input  [15:0] IN,
  input  [2:0] RD,
  input  [2:0] RS,
  input  [2:0] RN,
  output [15:0] R0,
  output [15:0] R4,
  output [15:0] R1,
  output [15:0] R5,
  output [15:0] R2,
  output [15:0] R6,
  output [15:0] R3,
  output [15:0] R7,
  output [15:0] REG_B,
  output [15:0] REG_A
);

  wire ic_74x573_1_q1, ic_74x573_1_q2, ic_74x573_1_q3, ic_74x573_1_q4, ic_74x573_1_q5, ic_74x573_1_q6,
       ic_74x573_1_q7, ic_74x573_1_q8, not_1_out, nRA_0, nRA_1, nRA_2, nRA_3, nRA_4, nRA_5, nRA_6, nRA_7,
       nRB_0, nRB_1, nRB_2, nRB_3, nRB_4, nRB_5, nRB_6, nRB_7, RDSelA_y0, RDSelA_y1, RDSelA_y2, RDSelA_y3,
       RDSelA_y4, RDSelA_y5, RDSelA_y6, RDSelA_y7, RDSelB_y0, RDSelB_y1, RDSelB_y2, RDSelB_y3, RDSelB_y4,
       RDSelB_y5, RDSelB_y6, RDSelB_y7, RSelB_2_y0, RSelB_2_y1, RSelB_2_y2, RSelB_2_y3, RSelB_2_y4,
       RSelB_2_y5, RSelB_2_y6, RSelB_2_y7, RSelB_y0, RSelB_y1, RSelB_y2, RSelB_y3, RSelB_y4, RSelB_y5,
       RSelB_y6, RSelB_y7, RSSelA_y0, RSSelA_y1, RSSelA_y2, RSSelA_y3, RSSelA_y4, RSSelA_y5, RSSelA_y6,
       RSSelA_y7, RWriteEn_y0, RWriteEn_y1, RWriteEn_y2, RWriteEn_y3, RWriteEn_y4, RWriteEn_y5, RWriteEn_y6,
       RWriteEn_y7, WR_R0, WR_R1, WR_R2, WR_R3, WR_R4, WR_R5, WR_R6, WR_R7;
  wire [2:0] undriven;
  wire [15:0] ic_74x574_1_q1, ic_74x574_9_q1;

  logi7400ic_IC_74x574 ic_74x574_1 (
    .Q2(ic_74x574_1_q1[1]), .Q3(ic_74x574_1_q1[2]), .Q4(ic_74x574_1_q1[3]), .Q5(ic_74x574_1_q1[4]),
    .Q6(ic_74x574_1_q1[5]), .Q7(ic_74x574_1_q1[6]), .Q8(ic_74x574_1_q1[7]), .Q1(ic_74x574_1_q1[0]),
    .D2(IN[1]), .D3(IN[2]), .D4(IN[3]), .D5(IN[4]), .D6(IN[5]), .D7(IN[6]), .D8(IN[7]), .CLK(WR_R0),
    .nOE(nRA_0), .D1(IN[0]));  // open: Probe
  logi7400ic_IC_74x574 ic_74x574_2 (
    .Q2(ic_74x574_1_q1[9]), .Q3(ic_74x574_1_q1[10]), .Q4(ic_74x574_1_q1[11]), .Q5(ic_74x574_1_q1[12]),
    .Q6(ic_74x574_1_q1[13]), .Q7(ic_74x574_1_q1[14]), .Q8(ic_74x574_1_q1[15]), .Q1(ic_74x574_1_q1[8]),
    .D2(IN[9]), .D3(IN[10]), .D4(IN[11]), .D5(IN[12]), .D6(IN[13]), .D7(IN[14]), .D8(IN[15]), .CLK(WR_R0),
    .nOE(nRA_0), .D1(IN[8]));  // open: Probe
  logi7400ic_IC_74x574 ic_74x574_3 (
    .Q2(ic_74x574_1_q1[1]), .Q3(ic_74x574_1_q1[2]), .Q4(ic_74x574_1_q1[3]), .Q5(ic_74x574_1_q1[4]),
    .Q6(ic_74x574_1_q1[5]), .Q7(ic_74x574_1_q1[6]), .Q8(ic_74x574_1_q1[7]), .Q1(ic_74x574_1_q1[0]),
    .D2(IN[1]), .D3(IN[2]), .D4(IN[3]), .D5(IN[4]), .D6(IN[5]), .D7(IN[6]), .D8(IN[7]), .CLK(WR_R1),
    .nOE(nRA_1), .D1(IN[0]));  // open: Probe
  logi7400ic_IC_74x574 ic_74x574_4 (
    .Q2(ic_74x574_1_q1[9]), .Q3(ic_74x574_1_q1[10]), .Q4(ic_74x574_1_q1[11]), .Q5(ic_74x574_1_q1[12]),
    .Q6(ic_74x574_1_q1[13]), .Q7(ic_74x574_1_q1[14]), .Q8(ic_74x574_1_q1[15]), .Q1(ic_74x574_1_q1[8]),
    .D2(IN[9]), .D3(IN[10]), .D4(IN[11]), .D5(IN[12]), .D6(IN[13]), .D7(IN[14]), .D8(IN[15]), .CLK(WR_R1),
    .nOE(nRA_1), .D1(IN[8]));  // open: Probe
  logi7400ic_IC_74x574 ic_74x574_5 (
    .Q2(ic_74x574_1_q1[1]), .Q3(ic_74x574_1_q1[2]), .Q4(ic_74x574_1_q1[3]), .Q5(ic_74x574_1_q1[4]),
    .Q6(ic_74x574_1_q1[5]), .Q7(ic_74x574_1_q1[6]), .Q8(ic_74x574_1_q1[7]), .Q1(ic_74x574_1_q1[0]),
    .D2(IN[1]), .D3(IN[2]), .D4(IN[3]), .D5(IN[4]), .D6(IN[5]), .D7(IN[6]), .D8(IN[7]), .CLK(WR_R2),
    .nOE(nRA_2), .D1(IN[0]));  // open: Probe
  logi7400ic_IC_74x574 ic_74x574_6 (
    .Q2(ic_74x574_1_q1[9]), .Q3(ic_74x574_1_q1[10]), .Q4(ic_74x574_1_q1[11]), .Q5(ic_74x574_1_q1[12]),
    .Q6(ic_74x574_1_q1[13]), .Q7(ic_74x574_1_q1[14]), .Q8(ic_74x574_1_q1[15]), .Q1(ic_74x574_1_q1[8]),
    .D2(IN[9]), .D3(IN[10]), .D4(IN[11]), .D5(IN[12]), .D6(IN[13]), .D7(IN[14]), .D8(IN[15]), .CLK(WR_R2),
    .nOE(nRA_2), .D1(IN[8]));  // open: Probe
  logi7400ic_IC_74x574 ic_74x574_7 (
    .Q2(ic_74x574_1_q1[1]), .Q3(ic_74x574_1_q1[2]), .Q4(ic_74x574_1_q1[3]), .Q5(ic_74x574_1_q1[4]),
    .Q6(ic_74x574_1_q1[5]), .Q7(ic_74x574_1_q1[6]), .Q8(ic_74x574_1_q1[7]), .Q1(ic_74x574_1_q1[0]),
    .D2(IN[1]), .D3(IN[2]), .D4(IN[3]), .D5(IN[4]), .D6(IN[5]), .D7(IN[6]), .D8(IN[7]), .CLK(WR_R3),
    .nOE(nRA_3), .D1(IN[0]));  // open: Probe
  logi7400ic_IC_74x574 ic_74x574_8 (
    .Q2(ic_74x574_1_q1[9]), .Q3(ic_74x574_1_q1[10]), .Q4(ic_74x574_1_q1[11]), .Q5(ic_74x574_1_q1[12]),
    .Q6(ic_74x574_1_q1[13]), .Q7(ic_74x574_1_q1[14]), .Q8(ic_74x574_1_q1[15]), .Q1(ic_74x574_1_q1[8]),
    .D2(IN[9]), .D3(IN[10]), .D4(IN[11]), .D5(IN[12]), .D6(IN[13]), .D7(IN[14]), .D8(IN[15]), .CLK(WR_R3),
    .nOE(nRA_3), .D1(IN[8]));  // open: Probe
  logi7400ic_IC_74x574 ic_74x574_9 (
    .Probe(R0[7:0]), .Q2(ic_74x574_9_q1[1]), .Q3(ic_74x574_9_q1[2]), .Q4(ic_74x574_9_q1[3]),
    .Q5(ic_74x574_9_q1[4]), .Q6(ic_74x574_9_q1[5]), .Q7(ic_74x574_9_q1[6]), .Q8(ic_74x574_9_q1[7]),
    .Q1(ic_74x574_9_q1[0]), .D2(IN[1]), .D3(IN[2]), .D4(IN[3]), .D5(IN[4]), .D6(IN[5]), .D7(IN[6]),
    .D8(IN[7]), .CLK(WR_R0), .nOE(nRB_0), .D1(IN[0]));
  logi7400ic_IC_74x574 ic_74x574_10 (
    .Probe(R0[15:8]), .Q2(ic_74x574_9_q1[9]), .Q3(ic_74x574_9_q1[10]), .Q4(ic_74x574_9_q1[11]),
    .Q5(ic_74x574_9_q1[12]), .Q6(ic_74x574_9_q1[13]), .Q7(ic_74x574_9_q1[14]), .Q8(ic_74x574_9_q1[15]),
    .Q1(ic_74x574_9_q1[8]), .D2(IN[9]), .D3(IN[10]), .D4(IN[11]), .D5(IN[12]), .D6(IN[13]), .D7(IN[14]),
    .D8(IN[15]), .CLK(WR_R0), .nOE(nRB_0), .D1(IN[8]));
  logi7400ic_IC_74x574 ic_74x574_11 (
    .Probe(R1[7:0]), .Q2(ic_74x574_9_q1[1]), .Q3(ic_74x574_9_q1[2]), .Q4(ic_74x574_9_q1[3]),
    .Q5(ic_74x574_9_q1[4]), .Q6(ic_74x574_9_q1[5]), .Q7(ic_74x574_9_q1[6]), .Q8(ic_74x574_9_q1[7]),
    .Q1(ic_74x574_9_q1[0]), .D2(IN[1]), .D3(IN[2]), .D4(IN[3]), .D5(IN[4]), .D6(IN[5]), .D7(IN[6]),
    .D8(IN[7]), .CLK(WR_R1), .nOE(nRB_1), .D1(IN[0]));
  logi7400ic_IC_74x574 ic_74x574_12 (
    .Probe(R1[15:8]), .Q2(ic_74x574_9_q1[9]), .Q3(ic_74x574_9_q1[10]), .Q4(ic_74x574_9_q1[11]),
    .Q5(ic_74x574_9_q1[12]), .Q6(ic_74x574_9_q1[13]), .Q7(ic_74x574_9_q1[14]), .Q8(ic_74x574_9_q1[15]),
    .Q1(ic_74x574_9_q1[8]), .D2(IN[9]), .D3(IN[10]), .D4(IN[11]), .D5(IN[12]), .D6(IN[13]), .D7(IN[14]),
    .D8(IN[15]), .CLK(WR_R1), .nOE(nRB_1), .D1(IN[8]));
  logi7400ic_IC_74x574 ic_74x574_13 (
    .Probe(R2[7:0]), .Q2(ic_74x574_9_q1[1]), .Q3(ic_74x574_9_q1[2]), .Q4(ic_74x574_9_q1[3]),
    .Q5(ic_74x574_9_q1[4]), .Q6(ic_74x574_9_q1[5]), .Q7(ic_74x574_9_q1[6]), .Q8(ic_74x574_9_q1[7]),
    .Q1(ic_74x574_9_q1[0]), .D2(IN[1]), .D3(IN[2]), .D4(IN[3]), .D5(IN[4]), .D6(IN[5]), .D7(IN[6]),
    .D8(IN[7]), .CLK(WR_R2), .nOE(nRB_2), .D1(IN[0]));
  logi7400ic_IC_74x574 ic_74x574_14 (
    .Probe(R2[15:8]), .Q2(ic_74x574_9_q1[9]), .Q3(ic_74x574_9_q1[10]), .Q4(ic_74x574_9_q1[11]),
    .Q5(ic_74x574_9_q1[12]), .Q6(ic_74x574_9_q1[13]), .Q7(ic_74x574_9_q1[14]), .Q8(ic_74x574_9_q1[15]),
    .Q1(ic_74x574_9_q1[8]), .D2(IN[9]), .D3(IN[10]), .D4(IN[11]), .D5(IN[12]), .D6(IN[13]), .D7(IN[14]),
    .D8(IN[15]), .CLK(WR_R2), .nOE(nRB_2), .D1(IN[8]));
  logi7400ic_IC_74x574 ic_74x574_15 (
    .Probe(R3[7:0]), .Q2(ic_74x574_9_q1[1]), .Q3(ic_74x574_9_q1[2]), .Q4(ic_74x574_9_q1[3]),
    .Q5(ic_74x574_9_q1[4]), .Q6(ic_74x574_9_q1[5]), .Q7(ic_74x574_9_q1[6]), .Q8(ic_74x574_9_q1[7]),
    .Q1(ic_74x574_9_q1[0]), .D2(IN[1]), .D3(IN[2]), .D4(IN[3]), .D5(IN[4]), .D6(IN[5]), .D7(IN[6]),
    .D8(IN[7]), .CLK(WR_R3), .nOE(nRB_3), .D1(IN[0]));
  logi7400ic_IC_74x574 ic_74x574_16 (
    .Probe(R3[15:8]), .Q2(ic_74x574_9_q1[9]), .Q3(ic_74x574_9_q1[10]), .Q4(ic_74x574_9_q1[11]),
    .Q5(ic_74x574_9_q1[12]), .Q6(ic_74x574_9_q1[13]), .Q7(ic_74x574_9_q1[14]), .Q8(ic_74x574_9_q1[15]),
    .Q1(ic_74x574_9_q1[8]), .D2(IN[9]), .D3(IN[10]), .D4(IN[11]), .D5(IN[12]), .D6(IN[13]), .D7(IN[14]),
    .D8(IN[15]), .CLK(WR_R3), .nOE(nRB_3), .D1(IN[8]));
  IC_74x238 RWriteEn (
    .Y0(RWriteEn_y0), .Y1(RWriteEn_y1), .Y2(RWriteEn_y2), .Y3(RWriteEn_y3), .Y4(RWriteEn_y4),
    .Y5(RWriteEn_y5), .Y6(RWriteEn_y6), .Y7(RWriteEn_y7), .A(RD[0]), .B(RD[1]), .C(RD[2]), .nG2A(1'b0),
    .nG2B(1'b0), .G1(WR));
  IC_74x138 RDSelA (
    .Y0(RDSelA_y0), .Y1(RDSelA_y1), .Y2(RDSelA_y2), .Y3(RDSelA_y3), .Y4(RDSelA_y4), .Y5(RDSelA_y5),
    .Y6(RDSelA_y6), .Y7(RDSelA_y7), .A(RD[0]), .B(RD[1]), .C(RD[2]), .nG2A(1'b0), .nG2B(1'b0), .G1(1'b1));
  IC_74x138 RSSelA (
    .Y0(RSSelA_y0), .Y1(RSSelA_y1), .Y2(RSSelA_y2), .Y3(RSSelA_y3), .Y4(RSSelA_y4), .Y5(RSSelA_y5),
    .Y6(RSSelA_y6), .Y7(RSSelA_y7), .A(RS[0]), .B(RS[1]), .C(RS[2]), .nG2A(1'b0), .nG2B(1'b0), .G1(1'b1));
  IC_74x138 RDSelB (
    .Y0(RDSelB_y0), .Y1(RDSelB_y1), .Y2(RDSelB_y2), .Y3(RDSelB_y3), .Y4(RDSelB_y4), .Y5(RDSelB_y5),
    .Y6(RDSelB_y6), .Y7(RDSelB_y7), .A(RD[0]), .B(RD[1]), .C(RD[2]), .nG2A(1'b0), .nG2B(1'b0), .G1(1'b1));
  IC_74x138 RSelB (
    .Y0(RSelB_y0), .Y1(RSelB_y1), .Y2(RSelB_y2), .Y3(RSelB_y3), .Y4(RSelB_y4), .Y5(RSelB_y5), .Y6(RSelB_y6),
    .Y7(RSelB_y7), .A(RN[0]), .B(RN[1]), .C(RN[2]), .nG2A(1'b0), .nG2B(1'b0), .G1(1'b1));
  not not_1 (not_1_out, CLK);
  IC_74x573 ic_74x573_1 (
    .Q2(ic_74x573_1_q2), .Q3(ic_74x573_1_q3), .Q4(ic_74x573_1_q4), .Q5(ic_74x573_1_q5), .Q6(ic_74x573_1_q6),
    .Q7(ic_74x573_1_q7), .Q8(ic_74x573_1_q8), .Q1(ic_74x573_1_q1), .D2(RWriteEn_y1), .D3(RWriteEn_y2),
    .D4(RWriteEn_y3), .D5(RWriteEn_y4), .D6(RWriteEn_y5), .D7(RWriteEn_y6), .D8(RWriteEn_y7), .LE(not_1_out),
    .nOE(1'b0), .D1(RWriteEn_y0));  // open: Probe
  and and_1 (WR_R0, CLK, ic_74x573_1_q1);
  and and_2 (WR_R1, CLK, ic_74x573_1_q2);
  and and_3 (WR_R2, CLK, ic_74x573_1_q3);
  and and_4 (WR_R3, CLK, ic_74x573_1_q4);
  and and_5 (WR_R4, CLK, ic_74x573_1_q5);
  and and_6 (WR_R5, CLK, ic_74x573_1_q6);
  and and_7 (WR_R6, CLK, ic_74x573_1_q7);
  and and_8 (WR_R7, CLK, ic_74x573_1_q8);
  IC_74x3257 REnA (
    .A1(nRA_0), .A2(nRA_1), .A3(nRA_2), .A4(nRA_3), .B2_1(RSSelA_y0), .B1_2(RDSelA_y1), .B2_2(RSSelA_y1),
    .B1_3(RDSelA_y2), .B2_3(RSSelA_y2), .B1_4(RDSelA_y3), .B2_4(RSSelA_y3), .S(IR_A), .nOE(1'b0),
    .B1_1(RDSelA_y0));
  IC_74x3257 REnB (
    .A1(nRA_4), .A2(nRA_5), .A3(nRA_6), .A4(nRA_7), .B2_1(RSSelA_y4), .B1_2(RDSelA_y5), .B2_2(RSSelA_y5),
    .B1_3(RDSelA_y6), .B2_3(RSSelA_y6), .B1_4(RDSelA_y7), .B2_4(RSSelA_y7), .S(IR_A), .nOE(1'b0),
    .B1_1(RDSelA_y4));
  IC_74x3257 REnA_2 (
    .A1(nRB_0), .A2(nRB_1), .A3(nRB_2), .A4(nRB_3), .B2_1(RSelB_y0), .B1_2(RDSelB_y1), .B2_2(RSelB_y1),
    .B1_3(RDSelB_y2), .B2_3(RSelB_y2), .B1_4(RDSelB_y3), .B2_4(RSelB_y3), .S(IR_A), .nOE(1'b0),
    .B1_1(RDSelB_y0));
  IC_74x3257 REnB_2 (
    .A1(nRB_4), .A2(nRB_5), .A3(nRB_6), .A4(nRB_7), .B2_1(RSelB_y4), .B1_2(RDSelB_y5), .B2_2(RSelB_y5),
    .B1_3(RDSelB_y6), .B2_3(RSelB_y6), .B1_4(RDSelB_y7), .B2_4(RSelB_y7), .S(IR_A), .nOE(1'b0),
    .B1_1(RDSelB_y4));
  logi7400ic_IC_74x574 ic_74x574_17 (
    .Q2(ic_74x574_1_q1[1]), .Q3(ic_74x574_1_q1[2]), .Q4(ic_74x574_1_q1[3]), .Q5(ic_74x574_1_q1[4]),
    .Q6(ic_74x574_1_q1[5]), .Q7(ic_74x574_1_q1[6]), .Q8(ic_74x574_1_q1[7]), .Q1(ic_74x574_1_q1[0]),
    .D2(IN[1]), .D3(IN[2]), .D4(IN[3]), .D5(IN[4]), .D6(IN[5]), .D7(IN[6]), .D8(IN[7]), .CLK(WR_R4),
    .nOE(nRA_4), .D1(IN[0]));  // open: Probe
  logi7400ic_IC_74x574 ic_74x574_18 (
    .Q2(ic_74x574_1_q1[9]), .Q3(ic_74x574_1_q1[10]), .Q4(ic_74x574_1_q1[11]), .Q5(ic_74x574_1_q1[12]),
    .Q6(ic_74x574_1_q1[13]), .Q7(ic_74x574_1_q1[14]), .Q8(ic_74x574_1_q1[15]), .Q1(ic_74x574_1_q1[8]),
    .D2(IN[9]), .D3(IN[10]), .D4(IN[11]), .D5(IN[12]), .D6(IN[13]), .D7(IN[14]), .D8(IN[15]), .CLK(WR_R4),
    .nOE(nRA_4), .D1(IN[8]));  // open: Probe
  logi7400ic_IC_74x574 ic_74x574_19 (
    .Q2(ic_74x574_1_q1[1]), .Q3(ic_74x574_1_q1[2]), .Q4(ic_74x574_1_q1[3]), .Q5(ic_74x574_1_q1[4]),
    .Q6(ic_74x574_1_q1[5]), .Q7(ic_74x574_1_q1[6]), .Q8(ic_74x574_1_q1[7]), .Q1(ic_74x574_1_q1[0]),
    .D2(IN[1]), .D3(IN[2]), .D4(IN[3]), .D5(IN[4]), .D6(IN[5]), .D7(IN[6]), .D8(IN[7]), .CLK(WR_R5),
    .nOE(nRA_5), .D1(IN[0]));  // open: Probe
  logi7400ic_IC_74x574 ic_74x574_20 (
    .Q2(ic_74x574_1_q1[9]), .Q3(ic_74x574_1_q1[10]), .Q4(ic_74x574_1_q1[11]), .Q5(ic_74x574_1_q1[12]),
    .Q6(ic_74x574_1_q1[13]), .Q7(ic_74x574_1_q1[14]), .Q8(ic_74x574_1_q1[15]), .Q1(ic_74x574_1_q1[8]),
    .D2(IN[9]), .D3(IN[10]), .D4(IN[11]), .D5(IN[12]), .D6(IN[13]), .D7(IN[14]), .D8(IN[15]), .CLK(WR_R5),
    .nOE(nRA_5), .D1(IN[8]));  // open: Probe
  logi7400ic_IC_74x574 ic_74x574_21 (
    .Q2(ic_74x574_1_q1[1]), .Q3(ic_74x574_1_q1[2]), .Q4(ic_74x574_1_q1[3]), .Q5(ic_74x574_1_q1[4]),
    .Q6(ic_74x574_1_q1[5]), .Q7(ic_74x574_1_q1[6]), .Q8(ic_74x574_1_q1[7]), .Q1(ic_74x574_1_q1[0]),
    .D2(IN[1]), .D3(IN[2]), .D4(IN[3]), .D5(IN[4]), .D6(IN[5]), .D7(IN[6]), .D8(IN[7]), .CLK(WR_R6),
    .nOE(nRA_6), .D1(IN[0]));  // open: Probe
  logi7400ic_IC_74x574 ic_74x574_22 (
    .Q2(ic_74x574_1_q1[9]), .Q3(ic_74x574_1_q1[10]), .Q4(ic_74x574_1_q1[11]), .Q5(ic_74x574_1_q1[12]),
    .Q6(ic_74x574_1_q1[13]), .Q7(ic_74x574_1_q1[14]), .Q8(ic_74x574_1_q1[15]), .Q1(ic_74x574_1_q1[8]),
    .D2(IN[9]), .D3(IN[10]), .D4(IN[11]), .D5(IN[12]), .D6(IN[13]), .D7(IN[14]), .D8(IN[15]), .CLK(WR_R6),
    .nOE(nRA_6), .D1(IN[8]));  // open: Probe
  logi7400ic_IC_74x574 ic_74x574_23 (
    .Q2(ic_74x574_1_q1[1]), .Q3(ic_74x574_1_q1[2]), .Q4(ic_74x574_1_q1[3]), .Q5(ic_74x574_1_q1[4]),
    .Q6(ic_74x574_1_q1[5]), .Q7(ic_74x574_1_q1[6]), .Q8(ic_74x574_1_q1[7]), .Q1(ic_74x574_1_q1[0]),
    .D2(IN[1]), .D3(IN[2]), .D4(IN[3]), .D5(IN[4]), .D6(IN[5]), .D7(IN[6]), .D8(IN[7]), .CLK(WR_R7),
    .nOE(nRA_7), .D1(IN[0]));  // open: Probe
  logi7400ic_IC_74x574 ic_74x574_24 (
    .Q2(ic_74x574_1_q1[9]), .Q3(ic_74x574_1_q1[10]), .Q4(ic_74x574_1_q1[11]), .Q5(ic_74x574_1_q1[12]),
    .Q6(ic_74x574_1_q1[13]), .Q7(ic_74x574_1_q1[14]), .Q8(ic_74x574_1_q1[15]), .Q1(ic_74x574_1_q1[8]),
    .D2(IN[9]), .D3(IN[10]), .D4(IN[11]), .D5(IN[12]), .D6(IN[13]), .D7(IN[14]), .D8(IN[15]), .CLK(WR_R7),
    .nOE(nRA_7), .D1(IN[8]));  // open: Probe
  IC_74x541 R_A (
    .Q1(REG_A[0]), .Q2(REG_A[1]), .Q3(REG_A[2]), .Q4(REG_A[3]), .Q5(REG_A[4]), .Q6(REG_A[5]), .Q7(REG_A[6]),
    .Q8(REG_A[7]), .I1(ic_74x574_1_q1[0]), .I2(ic_74x574_1_q1[1]), .I3(ic_74x574_1_q1[2]),
    .I4(ic_74x574_1_q1[3]), .I5(ic_74x574_1_q1[4]), .I6(ic_74x574_1_q1[5]), .I7(ic_74x574_1_q1[6]),
    .I8(ic_74x574_1_q1[7]), .nOE1(1'b0), .nOE2(nR_TO_A));
  IC_74x541 R_A_2 (
    .Q1(REG_A[8]), .Q2(REG_A[9]), .Q3(REG_A[10]), .Q4(REG_A[11]), .Q5(REG_A[12]), .Q6(REG_A[13]),
    .Q7(REG_A[14]), .Q8(REG_A[15]), .I1(ic_74x574_1_q1[8]), .I2(ic_74x574_1_q1[9]), .I3(ic_74x574_1_q1[10]),
    .I4(ic_74x574_1_q1[11]), .I5(ic_74x574_1_q1[12]), .I6(ic_74x574_1_q1[13]), .I7(ic_74x574_1_q1[14]),
    .I8(ic_74x574_1_q1[15]), .nOE1(1'b0), .nOE2(nR_TO_A));
  logi7400ic_IC_74x574 ic_74x574_25 (
    .Probe(R4[7:0]), .Q2(ic_74x574_9_q1[1]), .Q3(ic_74x574_9_q1[2]), .Q4(ic_74x574_9_q1[3]),
    .Q5(ic_74x574_9_q1[4]), .Q6(ic_74x574_9_q1[5]), .Q7(ic_74x574_9_q1[6]), .Q8(ic_74x574_9_q1[7]),
    .Q1(ic_74x574_9_q1[0]), .D2(IN[1]), .D3(IN[2]), .D4(IN[3]), .D5(IN[4]), .D6(IN[5]), .D7(IN[6]),
    .D8(IN[7]), .CLK(WR_R4), .nOE(nRB_4), .D1(IN[0]));
  logi7400ic_IC_74x574 ic_74x574_26 (
    .Probe(R4[15:8]), .Q2(ic_74x574_9_q1[9]), .Q3(ic_74x574_9_q1[10]), .Q4(ic_74x574_9_q1[11]),
    .Q5(ic_74x574_9_q1[12]), .Q6(ic_74x574_9_q1[13]), .Q7(ic_74x574_9_q1[14]), .Q8(ic_74x574_9_q1[15]),
    .Q1(ic_74x574_9_q1[8]), .D2(IN[9]), .D3(IN[10]), .D4(IN[11]), .D5(IN[12]), .D6(IN[13]), .D7(IN[14]),
    .D8(IN[15]), .CLK(WR_R4), .nOE(nRB_4), .D1(IN[8]));
  logi7400ic_IC_74x574 ic_74x574_27 (
    .Probe(R5[7:0]), .Q2(ic_74x574_9_q1[1]), .Q3(ic_74x574_9_q1[2]), .Q4(ic_74x574_9_q1[3]),
    .Q5(ic_74x574_9_q1[4]), .Q6(ic_74x574_9_q1[5]), .Q7(ic_74x574_9_q1[6]), .Q8(ic_74x574_9_q1[7]),
    .Q1(ic_74x574_9_q1[0]), .D2(IN[1]), .D3(IN[2]), .D4(IN[3]), .D5(IN[4]), .D6(IN[5]), .D7(IN[6]),
    .D8(IN[7]), .CLK(WR_R5), .nOE(nRB_5), .D1(IN[0]));
  logi7400ic_IC_74x574 ic_74x574_28 (
    .Probe(R5[15:8]), .Q2(ic_74x574_9_q1[9]), .Q3(ic_74x574_9_q1[10]), .Q4(ic_74x574_9_q1[11]),
    .Q5(ic_74x574_9_q1[12]), .Q6(ic_74x574_9_q1[13]), .Q7(ic_74x574_9_q1[14]), .Q8(ic_74x574_9_q1[15]),
    .Q1(ic_74x574_9_q1[8]), .D2(IN[9]), .D3(IN[10]), .D4(IN[11]), .D5(IN[12]), .D6(IN[13]), .D7(IN[14]),
    .D8(IN[15]), .CLK(WR_R5), .nOE(nRB_5), .D1(IN[8]));
  logi7400ic_IC_74x574 ic_74x574_29 (
    .Probe(R6[7:0]), .Q2(ic_74x574_9_q1[1]), .Q3(ic_74x574_9_q1[2]), .Q4(ic_74x574_9_q1[3]),
    .Q5(ic_74x574_9_q1[4]), .Q6(ic_74x574_9_q1[5]), .Q7(ic_74x574_9_q1[6]), .Q8(ic_74x574_9_q1[7]),
    .Q1(ic_74x574_9_q1[0]), .D2(IN[1]), .D3(IN[2]), .D4(IN[3]), .D5(IN[4]), .D6(IN[5]), .D7(IN[6]),
    .D8(IN[7]), .CLK(WR_R6), .nOE(nRB_6), .D1(IN[0]));
  logi7400ic_IC_74x574 ic_74x574_30 (
    .Probe(R6[15:8]), .Q2(ic_74x574_9_q1[9]), .Q3(ic_74x574_9_q1[10]), .Q4(ic_74x574_9_q1[11]),
    .Q5(ic_74x574_9_q1[12]), .Q6(ic_74x574_9_q1[13]), .Q7(ic_74x574_9_q1[14]), .Q8(ic_74x574_9_q1[15]),
    .Q1(ic_74x574_9_q1[8]), .D2(IN[9]), .D3(IN[10]), .D4(IN[11]), .D5(IN[12]), .D6(IN[13]), .D7(IN[14]),
    .D8(IN[15]), .CLK(WR_R6), .nOE(nRB_6), .D1(IN[8]));
  logi7400ic_IC_74x574 ic_74x574_31 (
    .Probe(R7[7:0]), .Q2(ic_74x574_9_q1[1]), .Q3(ic_74x574_9_q1[2]), .Q4(ic_74x574_9_q1[3]),
    .Q5(ic_74x574_9_q1[4]), .Q6(ic_74x574_9_q1[5]), .Q7(ic_74x574_9_q1[6]), .Q8(ic_74x574_9_q1[7]),
    .Q1(ic_74x574_9_q1[0]), .D2(IN[1]), .D3(IN[2]), .D4(IN[3]), .D5(IN[4]), .D6(IN[5]), .D7(IN[6]),
    .D8(IN[7]), .CLK(WR_R7), .nOE(nRB_7), .D1(IN[0]));
  logi7400ic_IC_74x574 ic_74x574_32 (
    .Probe(R7[15:8]), .Q2(ic_74x574_9_q1[9]), .Q3(ic_74x574_9_q1[10]), .Q4(ic_74x574_9_q1[11]),
    .Q5(ic_74x574_9_q1[12]), .Q6(ic_74x574_9_q1[13]), .Q7(ic_74x574_9_q1[14]), .Q8(ic_74x574_9_q1[15]),
    .Q1(ic_74x574_9_q1[8]), .D2(IN[9]), .D3(IN[10]), .D4(IN[11]), .D5(IN[12]), .D6(IN[13]), .D7(IN[14]),
    .D8(IN[15]), .CLK(WR_R7), .nOE(nRB_7), .D1(IN[8]));
  IC_74x541 R_B (
    .Q1(REG_B[0]), .Q2(REG_B[1]), .Q3(REG_B[2]), .Q4(REG_B[3]), .Q5(REG_B[4]), .Q6(REG_B[5]), .Q7(REG_B[6]),
    .Q8(REG_B[7]), .I1(ic_74x574_9_q1[0]), .I2(ic_74x574_9_q1[1]), .I3(ic_74x574_9_q1[2]),
    .I4(ic_74x574_9_q1[3]), .I5(ic_74x574_9_q1[4]), .I6(ic_74x574_9_q1[5]), .I7(ic_74x574_9_q1[6]),
    .I8(ic_74x574_9_q1[7]), .nOE1(1'b0), .nOE2(nR_TO_B));
  IC_74x541 R_B_2 (
    .Q1(REG_B[8]), .Q2(REG_B[9]), .Q3(REG_B[10]), .Q4(REG_B[11]), .Q5(REG_B[12]), .Q6(REG_B[13]),
    .Q7(REG_B[14]), .Q8(REG_B[15]), .I1(ic_74x574_9_q1[8]), .I2(ic_74x574_9_q1[9]), .I3(ic_74x574_9_q1[10]),
    .I4(ic_74x574_9_q1[11]), .I5(ic_74x574_9_q1[12]), .I6(ic_74x574_9_q1[13]), .I7(ic_74x574_9_q1[14]),
    .I8(ic_74x574_9_q1[15]), .nOE1(1'b0), .nOE2(nR_TO_B));
  IC_74x138 RSelB_2 (
    .Y0(RSelB_2_y0), .Y1(RSelB_2_y1), .Y2(RSelB_2_y2), .Y3(RSelB_2_y3), .Y4(RSelB_2_y4), .Y5(RSelB_2_y5),
    .Y6(RSelB_2_y6), .Y7(RSelB_2_y7), .A(undriven[0]), .B(undriven[1]), .C(undriven[2]), .nG2A(1'b0),
    .nG2B(1'b0), .G1(1'b1));

  // Other names for the same wires on the sheet: nR_A = nR_TO_A; nR_B = nR_TO_B; Q_R = WR
endmodule

// PC
module RegPC_pre (
  input  CLK,
  input  RESET,
  input  cpWRPC,
  input  cpWRPMAR,
  input  nWRPMAR,
  input  nOE_PC,
  input  nBR,
  input  [15:0] IN,
  output [15:0] PC,
  output [15:0] MEM
);

  wire nOE_PMAR, PC_2_tc, PC_3_tc, PC_tc;
  wire [15:0] PC_q1;

  IC_74x161 u_PC (
    .Q1(PC_q1[0]), .Q2(PC_q1[1]), .Q3(PC_q1[2]), .Q4(PC_q1[3]), .TC(PC_tc), .nLD(nBR), .CEP(nBR), .CET(nBR),
    .D1(IN[0]), .CLK(cpWRPC), .D2(IN[1]), .D3(IN[2]), .D4(IN[3]), .nCLR(RESET));
  IC_74x74half ic_74x74half_1 (.Q1(nOE_PMAR), .CLK1(CLK), .CLR1(1'b1), .SET1(1'b1), .D1(nWRPMAR));  // open: R1
  IC_74x161 PC_2 (
    .Q1(PC_q1[4]), .Q2(PC_q1[5]), .Q3(PC_q1[6]), .Q4(PC_q1[7]), .TC(PC_2_tc), .nLD(nBR), .CEP(nBR),
    .CET(PC_tc), .D1(IN[4]), .CLK(cpWRPC), .D2(IN[5]), .D3(IN[6]), .D4(IN[7]), .nCLR(RESET));
  IC_74x161 PC_3 (
    .Q1(PC_q1[8]), .Q2(PC_q1[9]), .Q3(PC_q1[10]), .Q4(PC_q1[11]), .TC(PC_3_tc), .nLD(nBR), .CEP(nBR),
    .CET(PC_2_tc), .D1(IN[8]), .CLK(cpWRPC), .D2(IN[9]), .D3(IN[10]), .D4(IN[11]), .nCLR(RESET));
  IC_74x161 PC_4 (
    .Q1(PC_q1[12]), .Q2(PC_q1[13]), .Q3(PC_q1[14]), .Q4(PC_q1[15]), .nLD(nBR), .CEP(nBR), .CET(PC_3_tc),
    .D1(IN[12]), .CLK(cpWRPC), .D2(IN[13]), .D3(IN[14]), .D4(IN[15]), .nCLR(RESET));  // open: TC
  IC_74x541 PCData (
    .Q1(PC[0]), .Q2(PC[1]), .Q3(PC[2]), .Q4(PC[3]), .Q5(PC[4]), .Q6(PC[5]), .Q7(PC[6]), .Q8(PC[7]),
    .I1(PC_q1[0]), .I2(PC_q1[1]), .I3(PC_q1[2]), .I4(PC_q1[3]), .I5(PC_q1[4]), .I6(PC_q1[5]), .I7(PC_q1[6]),
    .I8(PC_q1[7]), .nOE1(1'b0), .nOE2(nOE_PC));
  IC_74x541 PCData_2 (
    .Q1(PC[8]), .Q2(PC[9]), .Q3(PC[10]), .Q4(PC[11]), .Q5(PC[12]), .Q6(PC[13]), .Q7(PC[14]), .Q8(PC[15]),
    .I1(PC_q1[8]), .I2(PC_q1[9]), .I3(PC_q1[10]), .I4(PC_q1[11]), .I5(PC_q1[12]), .I6(PC_q1[13]),
    .I7(PC_q1[14]), .I8(PC_q1[15]), .nOE1(1'b0), .nOE2(nOE_PC));
  IC_74x3345 PCMem (
    .A3(MEM[2]), .A4(MEM[3]), .A5(MEM[4]), .A6(MEM[5]), .A7(MEM[6]), .A8(MEM[7]), .A1(MEM[0]), .A2(MEM[1]),
    .B3(PC_q1[2]), .B4(PC_q1[3]), .B5(PC_q1[4]), .B6(PC_q1[5]), .B7(PC_q1[6]), .B8(PC_q1[7]), .OE(nOE_PMAR),
    .nOE(1'b1), .B1(PC_q1[0]), .B2(PC_q1[1]));
  IC_74x3345 PCMem_2 (
    .A3(MEM[10]), .A4(MEM[11]), .A5(MEM[12]), .A6(MEM[13]), .A7(MEM[14]), .A8(MEM[15]), .A1(MEM[8]),
    .A2(MEM[9]), .B3(PC_q1[10]), .B4(PC_q1[11]), .B5(PC_q1[12]), .B6(PC_q1[13]), .B7(PC_q1[14]),
    .B8(PC_q1[15]), .OE(nOE_PMAR), .nOE(1'b1), .B1(PC_q1[8]), .B2(PC_q1[9]));
  logi7400ic_IC_74x574 PMAR (
    .Q2(MEM[1]), .Q3(MEM[2]), .Q4(MEM[3]), .Q5(MEM[4]), .Q6(MEM[5]), .Q7(MEM[6]), .Q8(MEM[7]), .Q1(MEM[0]),
    .D2(IN[1]), .D3(IN[2]), .D4(IN[3]), .D5(IN[4]), .D6(IN[5]), .D7(IN[6]), .D8(IN[7]), .CLK(cpWRPMAR),
    .nOE(nOE_PMAR), .D1(IN[0]));  // open: Probe
  logi7400ic_IC_74x574 PMAR_2 (
    .Q2(MEM[9]), .Q3(MEM[10]), .Q4(MEM[11]), .Q5(MEM[12]), .Q6(MEM[13]), .Q7(MEM[14]), .Q8(MEM[15]),
    .Q1(MEM[8]), .D2(IN[9]), .D3(IN[10]), .D4(IN[11]), .D5(IN[12]), .D6(IN[13]), .D7(IN[14]), .D8(IN[15]),
    .CLK(cpWRPMAR), .nOE(nOE_PMAR), .D1(IN[8]));  // open: Probe

  // Other names for the same wires on the sheet: BRANCH_n = nBR; CLK_WRPC = cpWRPC; CLK_WRPMAR = cpWRPMAR;
  //   CLR_n = RESET; nWR_PMAR = nWRPMAR
endmodule

// PC
module RegPC (
  input  CLK,
  input  cpWRPC,
  input  cpWRPMAR,
  input  nRESET,
  input  nOE_PC,
  input  PMEM,
  input  BR,
  input  [15:0] IN,
  output [15:0] PC_OUT,
  output [15:0] PC,
  output [15:0] MEM_ADDR
);

  wire ic_74x283_1_cout, ic_74x283_2_cout, ic_74x283_3_cout, or_1_out;
  wire [3:0] ic_74x283_1_y1;
  wire [7:4] ic_74x283_2_y1;
  wire [11:8] ic_74x283_3_y1, SkipAdd_a1;
  wire [15:0] In_Sel_a1, PC_q1;
  wire [15:12] ic_74x283_4_y1, SkipAdd_2_a1;

  IC_74x283 ic_74x283_1 (
    .Y1(ic_74x283_1_y1[0]), .Y2(ic_74x283_1_y1[1]), .Y3(ic_74x283_1_y1[2]), .Y4(ic_74x283_1_y1[3]),
    .COUT(ic_74x283_1_cout), .A1(PC_q1[0]), .A2(PC_q1[1]), .A3(PC_q1[2]), .A4(PC_q1[3]), .B1(1'b0),
    .B2(1'b0), .B3(1'b0), .B4(1'b0), .CIN(1'b1));
  IC_74x283 ic_74x283_2 (
    .Y1(ic_74x283_2_y1[4]), .Y2(ic_74x283_2_y1[5]), .Y3(ic_74x283_2_y1[6]), .Y4(ic_74x283_2_y1[7]),
    .COUT(ic_74x283_2_cout), .A1(PC_q1[4]), .A2(PC_q1[5]), .A3(PC_q1[6]), .A4(PC_q1[7]), .B1(1'b0),
    .B2(1'b0), .B3(1'b0), .B4(1'b0), .CIN(ic_74x283_1_cout));
  IC_74x283 ic_74x283_3 (
    .Y1(ic_74x283_3_y1[8]), .Y2(ic_74x283_3_y1[9]), .Y3(ic_74x283_3_y1[10]), .Y4(ic_74x283_3_y1[11]),
    .COUT(ic_74x283_3_cout), .A1(PC_q1[8]), .A2(PC_q1[9]), .A3(PC_q1[10]), .A4(PC_q1[11]), .B1(1'b0),
    .B2(1'b0), .B3(1'b0), .B4(1'b0), .CIN(1'b1));
  IC_74x283 ic_74x283_4 (
    .Y1(ic_74x283_4_y1[12]), .Y2(ic_74x283_4_y1[13]), .Y3(ic_74x283_4_y1[14]), .Y4(ic_74x283_4_y1[15]),
    .A1(PC_q1[12]), .A2(PC_q1[13]), .A3(PC_q1[14]), .A4(PC_q1[15]), .B1(1'b0), .B2(1'b0), .B3(1'b0),
    .B4(1'b0), .CIN(ic_74x283_3_cout));  // open: COUT
  // Probe on IN
  IC_74x3257 SkipAdd (
    .A1(SkipAdd_a1[8]), .A2(SkipAdd_a1[9]), .A3(SkipAdd_a1[10]), .A4(SkipAdd_a1[11]),
    .B2_1(ic_74x283_3_y1[8]), .B1_2(PC_q1[9]), .B2_2(ic_74x283_3_y1[9]), .B1_3(PC_q1[10]),
    .B2_3(ic_74x283_3_y1[10]), .B1_4(PC_q1[11]), .B2_4(ic_74x283_3_y1[11]), .S(ic_74x283_2_cout), .nOE(1'b0),
    .B1_1(PC_q1[8]));
  IC_74x3257 SkipAdd_2 (
    .A1(SkipAdd_2_a1[12]), .A2(SkipAdd_2_a1[13]), .A3(SkipAdd_2_a1[14]), .A4(SkipAdd_2_a1[15]),
    .B2_1(ic_74x283_4_y1[12]), .B1_2(PC_q1[13]), .B2_2(ic_74x283_4_y1[13]), .B1_3(PC_q1[14]),
    .B2_3(ic_74x283_4_y1[14]), .B1_4(PC_q1[15]), .B2_4(ic_74x283_4_y1[15]), .S(ic_74x283_2_cout), .nOE(1'b0),
    .B1_1(PC_q1[12]));
  or or_1 (or_1_out, PMEM, BR);
  IC_74x3257 In_Sel (
    .A1(In_Sel_a1[0]), .A2(In_Sel_a1[1]), .A3(In_Sel_a1[2]), .A4(In_Sel_a1[3]), .B2_1(IN[0]),
    .B1_2(ic_74x283_1_y1[1]), .B2_2(IN[1]), .B1_3(ic_74x283_1_y1[2]), .B2_3(IN[2]), .B1_4(ic_74x283_1_y1[3]),
    .B2_4(IN[3]), .S(or_1_out), .nOE(1'b0), .B1_1(ic_74x283_1_y1[0]));
  IC_74x3257 In_Sel_2 (
    .A1(In_Sel_a1[4]), .A2(In_Sel_a1[5]), .A3(In_Sel_a1[6]), .A4(In_Sel_a1[7]), .B2_1(IN[4]),
    .B1_2(ic_74x283_2_y1[5]), .B2_2(IN[5]), .B1_3(ic_74x283_2_y1[6]), .B2_3(IN[6]), .B1_4(ic_74x283_2_y1[7]),
    .B2_4(IN[7]), .S(or_1_out), .nOE(1'b0), .B1_1(ic_74x283_2_y1[4]));
  IC_74x3257 In_Sel_3 (
    .A1(In_Sel_a1[8]), .A2(In_Sel_a1[9]), .A3(In_Sel_a1[10]), .A4(In_Sel_a1[11]), .B2_1(IN[8]),
    .B1_2(SkipAdd_a1[9]), .B2_2(IN[9]), .B1_3(SkipAdd_a1[10]), .B2_3(IN[10]), .B1_4(SkipAdd_a1[11]),
    .B2_4(IN[11]), .S(or_1_out), .nOE(1'b0), .B1_1(SkipAdd_a1[8]));
  IC_74x3257 In_Sel_4 (
    .A1(In_Sel_a1[12]), .A2(In_Sel_a1[13]), .A3(In_Sel_a1[14]), .A4(In_Sel_a1[15]), .B2_1(IN[12]),
    .B1_2(SkipAdd_2_a1[13]), .B2_2(IN[13]), .B1_3(SkipAdd_2_a1[14]), .B2_3(IN[14]), .B1_4(SkipAdd_2_a1[15]),
    .B2_4(IN[15]), .S(or_1_out), .nOE(1'b0), .B1_1(SkipAdd_2_a1[12]));
  // Probe on In_Sel_a1
  IC_74x273 u_PC (
    .Probe(PC[7:0]), .Q1(PC_q1[0]), .Q2(PC_q1[1]), .Q3(PC_q1[2]), .Q4(PC_q1[3]), .Q5(PC_q1[4]),
    .Q6(PC_q1[5]), .Q7(PC_q1[6]), .Q8(PC_q1[7]), .D1(In_Sel_a1[0]), .D2(In_Sel_a1[1]), .D3(In_Sel_a1[2]),
    .D4(In_Sel_a1[3]), .D5(In_Sel_a1[4]), .D6(In_Sel_a1[5]), .D7(In_Sel_a1[6]), .D8(In_Sel_a1[7]),
    .CLK(cpWRPC), .nMR(nRESET));
  IC_74x273 PC_2 (
    .Probe(PC[15:8]), .Q1(PC_q1[8]), .Q2(PC_q1[9]), .Q3(PC_q1[10]), .Q4(PC_q1[11]), .Q5(PC_q1[12]),
    .Q6(PC_q1[13]), .Q7(PC_q1[14]), .Q8(PC_q1[15]), .D1(In_Sel_a1[8]), .D2(In_Sel_a1[9]), .D3(In_Sel_a1[10]),
    .D4(In_Sel_a1[11]), .D5(In_Sel_a1[12]), .D6(In_Sel_a1[13]), .D7(In_Sel_a1[14]), .D8(In_Sel_a1[15]),
    .CLK(cpWRPC), .nMR(nRESET));
  // Probe on PC_q1
  IC_74x541 u_PC_Out (
    .Q1(PC_OUT[0]), .Q2(PC_OUT[1]), .Q3(PC_OUT[2]), .Q4(PC_OUT[3]), .Q5(PC_OUT[4]), .Q6(PC_OUT[5]),
    .Q7(PC_OUT[6]), .Q8(PC_OUT[7]), .I1(PC_q1[0]), .I2(PC_q1[1]), .I3(PC_q1[2]), .I4(PC_q1[3]),
    .I5(PC_q1[4]), .I6(PC_q1[5]), .I7(PC_q1[6]), .I8(PC_q1[7]), .nOE1(1'b0), .nOE2(nOE_PC));
  IC_74x541 PC_Out_2 (
    .Q1(PC_OUT[8]), .Q2(PC_OUT[9]), .Q3(PC_OUT[10]), .Q4(PC_OUT[11]), .Q5(PC_OUT[12]), .Q6(PC_OUT[13]),
    .Q7(PC_OUT[14]), .Q8(PC_OUT[15]), .I1(PC_q1[8]), .I2(PC_q1[9]), .I3(PC_q1[10]), .I4(PC_q1[11]),
    .I5(PC_q1[12]), .I6(PC_q1[13]), .I7(PC_q1[14]), .I8(PC_q1[15]), .nOE1(1'b0), .nOE2(nOE_PC));
  IC_74x273 PMAR (
    .Q1(MEM_ADDR[0]), .Q2(MEM_ADDR[1]), .Q3(MEM_ADDR[2]), .Q4(MEM_ADDR[3]), .Q5(MEM_ADDR[4]),
    .Q6(MEM_ADDR[5]), .Q7(MEM_ADDR[6]), .Q8(MEM_ADDR[7]), .D1(In_Sel_a1[0]), .D2(In_Sel_a1[1]),
    .D3(In_Sel_a1[2]), .D4(In_Sel_a1[3]), .D5(In_Sel_a1[4]), .D6(In_Sel_a1[5]), .D7(In_Sel_a1[6]),
    .D8(In_Sel_a1[7]), .CLK(cpWRPMAR), .nMR(nRESET));  // open: Probe
  IC_74x273 PMAR_2 (
    .Q1(MEM_ADDR[8]), .Q2(MEM_ADDR[9]), .Q3(MEM_ADDR[10]), .Q4(MEM_ADDR[11]), .Q5(MEM_ADDR[12]),
    .Q6(MEM_ADDR[13]), .Q7(MEM_ADDR[14]), .Q8(MEM_ADDR[15]), .D1(In_Sel_a1[8]), .D2(In_Sel_a1[9]),
    .D3(In_Sel_a1[10]), .D4(In_Sel_a1[11]), .D5(In_Sel_a1[12]), .D6(In_Sel_a1[13]), .D7(In_Sel_a1[14]),
    .D8(In_Sel_a1[15]), .CLK(cpWRPMAR), .nMR(nRESET));  // open: Probe
  // Probe on MEM_ADDR

  // Other names for the same wires on the sheet: BRANCH = BR; CLK_WRPC = cpWRPC; CLK_WRPMAR = cpWRPMAR;
  //   CLR_n = nRESET; MEM = PMEM
endmodule

// IR
module RegIR (
  input  cpWR,
  input  ncpRST,
  input  nOE_D,
  input  [15:0] IN,
  output [15:0] D,
  output [15:0] IR,
  output [15:0] IR_2
);

  IC_74x541 IRData (
    .Q1(D[0]), .Q2(D[1]), .Q3(D[2]), .Q4(D[3]), .Q5(D[4]), .Q6(D[5]), .Q7(D[6]), .Q8(D[7]), .I1(IN[0]),
    .I2(IN[1]), .I3(IN[2]), .I4(IN[3]), .I5(IN[4]), .I6(IN[5]), .I7(IN[6]), .I8(IN[7]), .nOE1(1'b0),
    .nOE2(nOE_D));
  IC_74x541 IRData_2 (
    .Q1(D[8]), .Q2(D[9]), .Q3(D[10]), .Q4(D[11]), .Q5(D[12]), .Q6(D[13]), .Q7(D[14]), .Q8(D[15]), .I1(IN[8]),
    .I2(IN[9]), .I3(IN[10]), .I4(IN[11]), .I5(IN[12]), .I6(IN[13]), .I7(IN[14]), .I8(IN[15]), .nOE1(1'b0),
    .nOE2(nOE_D));
  IC_74x273 u_IR (
    .Probe(IR_2[7:0]), .Q1(IR[0]), .Q2(IR[1]), .Q3(IR[2]), .Q4(IR[3]), .Q5(IR[4]), .Q6(IR[5]), .Q7(IR[6]),
    .Q8(IR[7]), .D1(IN[0]), .D2(IN[1]), .D3(IN[2]), .D4(IN[3]), .D5(IN[4]), .D6(IN[5]), .D7(IN[6]),
    .D8(IN[7]), .CLK(cpWR), .nMR(ncpRST));
  IC_74x273 u_IR_2 (
    .Probe(IR_2[15:8]), .Q1(IR[8]), .Q2(IR[9]), .Q3(IR[10]), .Q4(IR[11]), .Q5(IR[12]), .Q6(IR[13]),
    .Q7(IR[14]), .Q8(IR[15]), .D1(IN[8]), .D2(IN[9]), .D3(IN[10]), .D4(IN[11]), .D5(IN[12]), .D6(IN[13]),
    .D7(IN[14]), .D8(IN[15]), .CLK(cpWR), .nMR(ncpRST));

  // Other names for the same wires on the sheet: CLK_WR = cpWR; nRST = ncpRST
endmodule

// SP
module RegSP (
  input  cpWR,
  input  nOE,
  input  [15:0] IN,
  output [15:0] SP,
  output [15:0] SP_2
);

  logi7400ic_IC_74x574 u_SP (
    .Probe(SP_2[7:0]), .Q2(SP[1]), .Q3(SP[2]), .Q4(SP[3]), .Q5(SP[4]), .Q6(SP[5]), .Q7(SP[6]), .Q8(SP[7]),
    .Q1(SP[0]), .D2(IN[1]), .D3(IN[2]), .D4(IN[3]), .D5(IN[4]), .D6(IN[5]), .D7(IN[6]), .D8(IN[7]),
    .CLK(cpWR), .nOE(nOE), .D1(IN[0]));
  logi7400ic_IC_74x574 u_SP_2 (
    .Probe(SP_2[15:8]), .Q2(SP[9]), .Q3(SP[10]), .Q4(SP[11]), .Q5(SP[12]), .Q6(SP[13]), .Q7(SP[14]),
    .Q8(SP[15]), .Q1(SP[8]), .D2(IN[9]), .D3(IN[10]), .D4(IN[11]), .D5(IN[12]), .D6(IN[13]), .D7(IN[14]),
    .D8(IN[15]), .CLK(cpWR), .nOE(nOE), .D1(IN[8]));

  // Other names for the same wires on the sheet: CLK_WR = cpWR
endmodule

// 16V8C
module IC16V8C_1 (
  input  I0,
  input  I1,
  input  I2,
  input  I3,
  input  I4,
  input  I5,
  input  I6,
  input  I7,
  input  I8,
  input  I9,
  output Q0,
  output Q1,
  output Q2,
  output Q3,
  output Q4,
  output Q5,
  output Q6,
  output Q7
);

  // PLA_ALL pla_all_1: pin names not known; wires that end beside it: {I6, I5}, {I4, I3, I2, I1, I0}, {Q3, Q2, Q1, Q0}, {Q5, Q4}, {Q7, Q6}
endmodule

module PLA_1 (
  input  [1:0] M,
  input  [4:0] I,
  output [3:0] PF,
  output [3:0] PT
);

  wire and_1_out, and_2_out, and_3_out, and_4_out, and_5_out, and_6_out, and_7_out, and_8_out, and_9_out,
       and_10_out, and_11_out, and_12_out, and_13_out, and_14_out, and_15_out, and_16_out, and_17_out,
       and_18_out, and_19_out, and_20_out, and_21_out, and_22_out, and_23_out, and_24_out, and_25_out,
       and_26_out, and_27_out, and_28_out, and_29_out, and_30_out, and_31_out, and_32_out, and_33_out,
       and_34_out, and_35_out, and_36_out, or_1_out, or_2_out, or_3_out, or_4_out, or_5_out, or_6_out,
       or_7_out, or_8_out, or_9_out, or_10_out, or_11_out, or_12_out, or_13_out, or_14_out;

  and and_1 (and_1_out, ~M[1], ~M[0], ~I[3], ~I[1]);  // AND_Gate
  and and_2 (and_2_out, ~I[4], ~I[3]);  // AND_Gate
  and and_3 (and_3_out, ~I[4], ~I[2]);  // AND_Gate
  and and_4 (and_4_out, ~I[4], ~I[1], I[0]);  // AND_Gate
  and and_5 (and_5_out, M[0], ~I[4]);  // AND_Gate
  and and_6 (and_6_out, M[1], I[3], I[2], ~I[1]);  // AND_Gate
  and and_7 (and_7_out, M[1], I[4], I[3], I[1]);
  and and_8 (and_8_out, ~M[0], ~I[4], ~I[3], I[2], ~I[1], I[0]);  // AND_Gate
  and and_9 (and_9_out, ~I[4], I[3], I[2], I[1]);  // AND_Gate
  and and_10 (and_10_out, ~M[1], M[0], I[2], I[0]);  // AND_Gate
  and and_11 (and_11_out, M[0], I[4]);
  and and_12 (and_12_out, M[1], ~M[0], ~I[3]);  // AND_Gate
  and and_13 (and_13_out, M[1], I[4], ~I[2], ~I[1]);  // AND_Gate
  or or_1 (or_1_out, M[1], I[4], ~I[3], ~I[2], I[0]);  // OR_Gate
  or or_2 (or_2_out, M[1], M[0], ~I[3], ~I[2], ~I[1]);  // OR_Gate
  or or_3 (or_3_out, M[1], M[0], ~I[4], ~I[1]);  // OR_Gate
  or or_4 (or_4_out, ~I[4], ~I[3], I[2], ~I[1]);  // OR_Gate
  or or_5 (or_5_out, M[0], ~I[4], ~I[3], ~I[2], I[1]);  // OR_Gate
  or or_6 (or_6_out, M[1], ~M[0], I[4], I[2]);  // OR_Gate
  or or_7 (or_7_out, ~M[1], ~I[3], ~I[2], I[1], ~I[0]);  // OR_Gate
  and and_14 (and_14_out, ~M[1], ~I[4], ~I[3], I[2], ~I[1], I[0]);  // AND_Gate
  and and_15 (and_15_out, ~M[1], ~M[0], I[3], I[2], I[1]);  // AND_Gate
  and and_16 (and_16_out, ~M[1], M[0], ~I[4], ~I[2]);  // AND_Gate
  and and_17 (and_17_out, M[1], I[3], I[2], ~I[1], I[0]);  // AND_Gate
  and and_18 (and_18_out, M[1], I[4], I[3], I[2], ~I[1]);  // AND_Gate
  and and_19 (and_19_out, ~M[1], ~M[0], ~I[3], ~I[1]);  // AND_Gate
  and and_20 (and_20_out, ~I[4], ~I[3]);  // AND_Gate
  and and_21 (and_21_out, ~I[4], ~I[2]);  // AND_Gate
  and and_22 (and_22_out, ~I[4], ~I[1], ~I[0]);  // AND_Gate
  and and_23 (and_23_out, M[0], ~I[4]);  // AND_Gate
  and and_24 (and_24_out, M[1], I[3], I[2], ~I[1]);  // AND_Gate
  and and_25 (and_25_out, M[1], I[4], I[3], I[1]);
  and and_26 (and_26_out, ~M[0], ~I[4], ~I[3], I[2], ~I[1], I[0]);  // AND_Gate
  and and_27 (and_27_out, ~M[0], ~I[4], I[3], I[2], I[1]);  // AND_Gate
  and and_28 (and_28_out, ~M[1], M[0], I[2], I[0]);  // AND_Gate
  and and_29 (and_29_out, M[0], I[4]);
  and and_30 (and_30_out, M[1], ~M[0], ~I[3]);  // AND_Gate
  and and_31 (and_31_out, M[1], I[4], ~I[2], ~I[1]);  // AND_Gate
  or or_8 (or_8_out, M[0], ~I[3], ~I[2], I[1], ~I[0]);  // OR_Gate
  or or_9 (or_9_out, M[1], M[0], ~I[3], ~I[2], ~I[1]);  // OR_Gate
  or or_10 (or_10_out, M[1], M[0], ~I[4], ~I[1]);  // OR_Gate
  or or_11 (or_11_out, ~I[4], ~I[3], I[2], ~I[1]);  // OR_Gate
  or or_12 (or_12_out, M[0], ~I[4], ~I[3], ~I[2], I[1]);  // OR_Gate
  or or_13 (or_13_out, M[1], ~M[0], I[4], I[2]);  // OR_Gate
  or or_14 (or_14_out, M[1], ~M[0], I[4], I[1], I[0]);  // OR_Gate
  and and_32 (and_32_out, ~M[1], ~I[4], ~I[3], I[2], ~I[1], I[0]);  // AND_Gate
  and and_33 (and_33_out, ~M[1], ~M[0], I[3], I[2], I[1]);  // AND_Gate
  and and_34 (and_34_out, ~M[1], M[0], ~I[4], ~I[2]);  // AND_Gate
  and and_35 (and_35_out, M[1], I[3], I[2], ~I[1], I[0]);  // AND_Gate
  and and_36 (and_36_out, M[1], I[4], I[3], I[2], ~I[1]);  // AND_Gate
  or or_15 (PF[3], and_1_out, and_2_out, and_3_out, and_4_out, and_5_out, and_6_out, and_7_out);
  or or_16 (PF[2], and_8_out, and_9_out, and_10_out, and_11_out, and_12_out, and_13_out);
  and and_37 (PF[1], or_1_out, or_2_out, or_3_out, or_4_out, or_5_out, or_6_out, or_7_out);
  or or_17 (PF[0], and_14_out, and_15_out, and_16_out, and_17_out, and_18_out);
  or or_18 (PT[3], and_19_out, and_20_out, and_21_out, and_22_out, and_23_out, and_24_out, and_25_out);
  or or_19 (PT[2], and_26_out, and_27_out, and_28_out, and_29_out, and_30_out, and_31_out);
  and and_38 (PT[1], or_8_out, or_9_out, or_10_out, or_11_out, or_12_out, or_13_out, or_14_out);
  or or_20 (PT[0], and_32_out, and_33_out, and_34_out, and_35_out, and_36_out);
endmodule

// 16V8C
module IC16V8C_2 (
  input  I0,
  input  I1,
  input  I2,
  input  I3,
  input  I4,
  input  I5,
  input  I6,
  input  I7,
  input  I8,
  input  I9,
  output Q0,
  output Q1,
  output Q2,
  output Q3,
  output Q4,
  output Q5,
  output Q6,
  output Q7
);

  // PLA_ALL pla_all_1: pin names not known; wires that end beside it: {I6, I5}, {I4, I3, I2, I1, I0}, {Q2, Q1, Q0}, {Q4, Q3}, Q5, Q6, Q7
endmodule

module PLA_2 (
  input  [1:0] M,
  input  [4:0] I,
  output [2:0] C,
  output [1:0] G,
  output SH,
  output CM
);

  wire and_1_out, and_2_out, and_3_out, and_4_out, and_5_out, and_6_out, and_7_out, and_8_out, and_9_out,
       and_10_out, and_11_out, and_12_out, and_13_out, and_14_out, and_15_out, and_16_out, and_17_out,
       and_18_out, and_19_out, and_20_out, and_21_out, and_22_out, and_23_out, and_24_out, and_25_out;

  and and_1 (and_1_out, ~I[4], ~I[3], I[2], ~I[1], I[0]);  // AND_Gate
  and and_2 (and_2_out, ~M[1], ~I[4], I[3], ~I[2], ~I[1], I[0]);  // AND_Gate
  and and_3 (and_3_out, ~M[1], ~I[4], I[3], ~I[2], I[1], ~I[0]);  // AND_Gate
  and and_4 (and_4_out, ~M[1], ~I[4], I[3], ~I[2], ~I[1], I[0]);  // AND_Gate
  and and_5 (and_5_out, ~M[1], ~M[0], I[4], ~I[3], I[1]);  // AND_Gate
  and and_6 (and_6_out, ~M[0], I[4], I[3], I[2], ~I[1], I[0]);  // AND_Gate
  and and_7 (and_7_out, M[0], ~I[2], ~I[1], I[0]);  // AND_Gate
  and and_8 (and_8_out, M[0], ~I[4], I[1], ~I[0]);  // AND_Gate
  and and_9 (and_9_out, ~M[1], ~I[4], I[3], I[1], ~I[0]);  // AND_Gate
  and and_10 (and_10_out, ~M[1], ~M[0], I[4], ~I[3], I[1], I[0]);  // AND_Gate
  and and_11 (and_11_out, ~M[0], I[4], I[3], I[2], ~I[1], I[0]);  // AND_Gate
  and and_12 (and_12_out, M[0], ~I[2], ~I[1], I[0]);  // AND_Gate
  and and_13 (and_13_out, M[0], ~I[3], I[0]);  // AND_Gate
  and and_14 (and_14_out, M[0], ~I[3], I[1]);  // AND_Gate
  and and_15 (and_15_out, M[0], I[4], I[2]);
  and and_16 (and_16_out, M[1], ~I[3]);  // AND_Gate
  and and_17 (and_17_out, M[1], ~I[4], I[2], I[1]);  // AND_Gate
  and and_18 (and_18_out, M[1], I[4], ~I[2], ~I[1]);  // AND_Gate
  and and_19 (and_19_out, M[0], ~I[4], ~I[2]);  // AND_Gate
  and and_20 (and_20_out, M[1], ~I[4], I[2], ~I[1], I[0]);  // AND_Gate
  and and_21 (and_21_out, M[1], I[4], I[3], I[2], ~I[1]);  // AND_Gate
  and and_22 (and_22_out, ~M[1], ~M[0], ~I[4], I[3], ~I[2], ~I[1]);  // AND_Gate
  and and_23 (and_23_out, ~M[1], ~M[0], ~I[4], I[3], ~I[2], ~I[0]);  // AND_Gate
  and and_24 (and_24_out, ~M[1], M[0], ~I[4], ~I[2], ~I[1]);  // AND_Gate
  and and_25 (and_25_out, M[1], I[4], I[3], I[2], ~I[1]);  // AND_Gate
  or or_1 (C[2], and_1_out, and_2_out, and_3_out);
  or or_2 (C[1], and_4_out, and_5_out, and_6_out, and_7_out, and_8_out);
  or or_3 (C[0], and_9_out, and_10_out, and_11_out, and_12_out);
  or or_4 (G[1], and_13_out, and_14_out, and_15_out, and_16_out, and_17_out, and_18_out);
  or or_5 (G[0], and_19_out, and_20_out, and_21_out);
  or or_6 (SH, and_22_out, and_23_out);
  or or_7 (CM, and_24_out, and_25_out);
endmodule

// 16V8C
module IC16V8C_3 (
  input  I0,
  input  I1,
  input  I2,
  input  I3,
  input  I4,
  input  I5,
  input  I6,
  input  I7,
  input  I8,
  input  I9,
  output Q0,
  output Q1,
  output Q2,
  output Q3,
  output Q4,
  output Q5,
  output Q6,
  output Q7
);

  wire pla_all_1_p4, pla_all_1_p5, pla_all_1_p6, pla_all_1_p9;

  // PLA_ALL pla_all_1: pin names not known; wires that end beside it: {I6, I5}, {I4, I3, I2, I1, I0}, Q0, pla_all_1_p4, pla_all_1_p5, pla_all_1_p6, Q4, Q5, pla_all_1_p9, Q7
  not not_1 (Q1, pla_all_1_p4);
  not not_2 (Q2, pla_all_1_p5);
  not not_3 (Q3, pla_all_1_p6);
  not not_4 (Q6, pla_all_1_p9);
endmodule

module PLA_3 (
  input  [1:0] M,
  input  [4:0] I,
  output [1:0] B,
  output M0,
  output M1
);

  wire and_1_out, and_2_out, and_3_out, and_4_out, and_5_out;

  and and_1 (and_1_out, ~M[1], ~M[0], I[4], ~I[3], ~I[2], ~I[1], ~I[0]);  // AND_Gate
  and and_2 (and_2_out, M[0], I[4], I[3], I[2], ~I[1], ~I[0]);  // AND_Gate
  and and_3 (and_3_out, M[0], I[4], I[3], I[2], I[1], I[0]);
  and and_4 (and_4_out, ~M[1], ~M[0], I[4], ~I[3], ~I[2], ~I[1], ~I[0]);  // AND_Gate
  and and_5 (and_5_out, M[0], I[4], I[3], I[2], I[0]);
  or or_1 (B[1], and_1_out, and_2_out, and_3_out);
  or or_2 (B[0], and_4_out, and_5_out);

  assign M0 = 1'b0;
  assign M1 = 1'b0;
endmodule

// 16V8C
module IC16V8C_4 (
  input  I0,
  input  I1,
  input  I2,
  input  I3,
  input  I4,
  input  I5,
  input  I6,
  input  I7,
  input  I8,
  input  I9,
  output Q0,
  output Q1,
  output Q2,
  output Q3,
  output Q4,
  output Q5,
  output Q6,
  output Q7
);

  wire pla_all_1_p3, pla_all_1_p4, pla_all_1_p5, pla_all_1_p6, pla_all_1_p7, pla_all_1_p8;

  // PLA_ALL pla_all_1: pin names not known; wires that end beside it: {I6, I5}, {I4, I3, I2, I1, I0}, pla_all_1_p3, pla_all_1_p4, pla_all_1_p5, pla_all_1_p6, pla_all_1_p7, pla_all_1_p8, Q6, Q7
  not not_1 (Q0, pla_all_1_p3);
  not not_2 (Q1, pla_all_1_p4);
  not not_3 (Q2, pla_all_1_p5);
  not not_4 (Q3, pla_all_1_p6);
  not not_5 (Q4, pla_all_1_p7);
  not not_6 (Q5, pla_all_1_p8);
endmodule

// 16V8C
module IC16V8C_5 (
  input  I0,
  input  I1,
  input  I2,
  input  I3,
  input  I4,
  input  I5,
  input  I6,
  input  I7,
  input  I8,
  input  I9,
  output Q0,
  output Q1,
  output Q2,
  output Q3,
  output Q4,
  output Q5,
  output Q6,
  output Q7
);

  wire pla_all_1_p6;

  // PLA_ALL pla_all_1: pin names not known; wires that end beside it: {I6, I5}, {I4, I3, I2, I1, I0}, Q0, Q1, Q2, pla_all_1_p6, {Q7, Q6, Q5, Q4}
  not not_1 (Q3, pla_all_1_p6);
endmodule

// 16V8B
module IC16V8B_ALL (
  input  I0,
  input  I1,
  input  I2,
  input  I3,
  input  I4,
  input  I5,
  input  I6,
  input  I7,
  input  I8,
  input  I9,
  output Q0,
  output Q1,
  output Q2,
  output Q3,
  output Q4,
  output Q5,
  output Q6,
  output Q7
);

  PLA #(.in_width(10), .out_width(8), .\table ("0000000000 00001000")) pla_1 (
    .in({I9, I8, I7, I6, I5, I4, I3, I2, I1, I0}), .out({Q7, Q6, Q5, Q4, Q3, Q2, Q1, Q0}));
endmodule

module VARIS_REFERENCIA (
);

  wire and_1_out, and_2_out, and_3_out, and_4_out, and_5_out, and_6_out, and_7_out, and_8_out, and_9_out,
       and_10_out, and_11_out, and_12_out, and_13_out, and_14_out, and_15_out, and_16_out, and_17_out,
       and_18_out, and_19_out, and_20_out, and_21_out, and_22_out, and_23_out, and_24_out, CLK, F,
       ic_74x74half_1_r1, ic_74x138_1_y0, ic_74x138_2_y0, ic_74x138_3_y0, ic_74x138_4_y0, ic_74x138_5_y0,
       ic_74x138_5_y1, ic_74x138_5_y2, ic_74x138_5_y3, ic_74x138_5_y4, ic_74x138_5_y5, ic_74x138_5_y6,
       ic_74x138_5_y7, ic_74x138_6_y0, ic_74x138_6_y1, ic_74x138_6_y2, ic_74x138_6_y3, ic_74x138_6_y4,
       ic_74x138_6_y5, ic_74x138_6_y6, ic_74x138_6_y7, ic_74x138_7_y0, ic_74x138_7_y1, ic_74x138_7_y2,
       ic_74x138_7_y3, ic_74x138_7_y4, ic_74x138_7_y5, ic_74x138_7_y6, ic_74x138_7_y7, ic_74x138_8_y0,
       ic_74x138_8_y1, ic_74x138_8_y2, ic_74x138_8_y3, ic_74x138_8_y4, ic_74x138_8_y5, ic_74x138_8_y6,
       ic_74x138_8_y7, ic_74x238_1_y0, ic_74x238_1_y1, ic_74x238_1_y2, ic_74x238_1_y3, ic_74x238_1_y4,
       ic_74x238_1_y5, ic_74x238_1_y6, ic_74x238_1_y7, ic_74x563_1_q1, ic_74x563_1_q2, ic_74x563_1_q3,
       ic_74x563_1_q4, ic_74x563_1_q5, ic_74x563_1_q6, ic_74x563_1_q7, ic_74x563_1_q8, ic_74x563_2_q1,
       ic_74x563_2_q2, ic_74x563_2_q3, ic_74x563_2_q4, ic_74x563_2_q5, ic_74x563_2_q6, ic_74x563_2_q7,
       ic_74x563_2_q8, ic_74x573_1_q1, ic_74x573_1_q2, ic_74x573_1_q3, ic_74x573_1_q4, ic_74x573_1_q5,
       ic_74x573_1_q6, ic_74x573_1_q7, ic_74x573_1_q8, ic_7402_1_y1, ic_7402_1_y2, ic_7402_1_y3,
       ic_7402_1_y4, ic_7402_2_y1, ic_7402_2_y2, ic_7402_2_y3, ic_7402_2_y4, ic_7402_3_y1, ic_7402_3_y2,
       ic_7402_3_y3, ic_7402_3_y4, ic_7402_4_y1, ic_7402_4_y2, ic_7402_4_y3, ic_7402_4_y4, ic_7410_1_y1,
       ic_7411_1_p10, ic_7411_1_p11, ic_7411_1_p12, ic_7420_1_y1, ic_7420_1_y2, IR11, IR12, IR13, IR14, IR15,
       nand_1_out, nCLK, nor_1_out, not_1_out, not_2_out, not_3_out, not_4_out, not_5_out, not_6_out,
       not_7_out, not_8_out, nQ_RD, nRD_A, nRS_A, nWR_RD, or_1_out, PFIX, pull_resistor_1_node, Q_RD_n,
       RWriteEn_y0, RWriteEn_y1, RWriteEn_y2, RWriteEn_y3, RWriteEn_y4, RWriteEn_y5, RWriteEn_y6,
       RWriteEn_y7, T, undriven_4, undriven_5, undriven_7, undriven_9, undriven_10, WR_R0, WR_R1, WR_R2,
       WR_R3, WR_R4, WR_R5, WR_R6, WR_R7;
  wire [2:0] RD, RS;
  wire [3:0] PS_Select_a1, undriven_8;
  wire [15:0] undriven, undriven_2, undriven_3, undriven_6;

  IC_74x138 ic_74x138_1 (
    .Y0(ic_74x138_1_y0), .A(undriven[0]), .B(undriven[1]), .C(undriven[2]), .nG2A(undriven[3]),
    .nG2B(undriven[4]), .G1(1'b1));  // open: Y1, Y2, Y3, Y4, Y5, Y6, Y7
  IC_74x138 ic_74x138_2 (
    .Y0(ic_74x138_2_y0), .A(undriven[5]), .B(undriven[6]), .C(undriven[7]), .nG2A(undriven[8]),
    .nG2B(undriven[9]), .G1(1'b1));  // open: Y1, Y2, Y3, Y4, Y5, Y6, Y7
  IC_74x138 ic_74x138_3 (
    .Y0(ic_74x138_3_y0), .A(undriven[10]), .B(undriven[11]), .C(undriven[12]), .nG2A(undriven[13]),
    .nG2B(undriven[14]), .G1(1'b1));  // open: Y1, Y2, Y3, Y4, Y5, Y6, Y7
  IC_7402 ic_7402_1 (
    .Y3(ic_7402_1_y3), .Y4(ic_7402_1_y4), .Y1(ic_7402_1_y1), .Y2(ic_7402_1_y2), .A3(undriven_2[2]),
    .A4(undriven_2[3]), .B1(undriven_2[4]), .B2(undriven_2[5]), .A1(undriven_2[0]), .B3(undriven_2[6]),
    .B4(undriven_2[7]), .A2(undriven_2[1]));
  IC_7402 ic_7402_2 (
    .Y3(ic_7402_2_y3), .Y4(ic_7402_2_y4), .Y1(ic_7402_2_y1), .Y2(ic_7402_2_y2), .A3(undriven_2[10]),
    .A4(undriven_2[11]), .B1(undriven_2[12]), .B2(undriven_2[13]), .A1(undriven_2[8]), .B3(undriven_2[14]),
    .B4(undriven_2[15]), .A2(undriven_2[9]));
  Pull_Resistor #(.pull(1)) pull_resistor_1 (.node(pull_resistor_1_node));
  IC_7405 ic_7405_1 (
    .Y3(pull_resistor_1_node), .Y4(pull_resistor_1_node), .Y5(pull_resistor_1_node),
    .Y6(pull_resistor_1_node), .Y1(pull_resistor_1_node), .Y2(pull_resistor_1_node), .A3(undriven_3[2]),
    .A4(undriven_3[3]), .A5(undriven_3[4]), .A6(undriven_3[5]), .A1(undriven_3[0]), .A2(undriven_3[1]));
  IC_7405 ic_7405_2 (
    .Y3(pull_resistor_1_node), .Y4(pull_resistor_1_node), .Y5(pull_resistor_1_node),
    .Y6(pull_resistor_1_node), .Y1(pull_resistor_1_node), .Y2(pull_resistor_1_node), .A3(undriven_3[8]),
    .A4(undriven_3[9]), .A5(undriven_3[10]), .A6(undriven_3[11]), .A1(undriven_3[6]), .A2(undriven_3[7]));
  IC_7405 ic_7405_3 (
    .Y3(pull_resistor_1_node), .Y4(pull_resistor_1_node), .Y1(pull_resistor_1_node),
    .Y2(pull_resistor_1_node), .A3(undriven_3[14]), .A4(undriven_3[15]), .A5(undriven_4), .A6(1'b0),
    .A1(undriven_3[12]), .A2(undriven_3[13]));  // open: Y5, Y6
  IC_74x3253 PS_Select (
    .A1(PS_Select_a1[0]), .A2(PS_Select_a1[1]), .B1_1(1'b0), .B1_2(1'b0), .B1_3(1'b0), .B1_4(1'b0),
    .B2_1(1'b1), .B2_2(T), .B2_3(F), .B2_4(T), .S0(undriven_8[0]), .S1(undriven_8[1]), .nOE1(1'b0),
    .nOE2(undriven_9));
  IC_7420 ic_7420_1 (
    .Y2(ic_7420_1_y2), .Y1(ic_7420_1_y1), .B1(ic_7402_1_y3), .B2(ic_7402_1_y4), .C1(ic_7402_2_y1),
    .A1(ic_7402_1_y1), .C2(ic_7402_2_y2), .D1(ic_7402_2_y3), .D2(ic_7402_2_y4), .A2(ic_7402_1_y2));
  IC_74x138 ic_74x138_4 (
    .Y0(ic_74x138_4_y0), .A(ic_74x138_1_y0), .B(ic_74x138_2_y0), .C(ic_74x138_3_y0), .nG2A(undriven[15]),
    .nG2B(undriven_5), .G1(1'b1));  // open: Y1, Y2, Y3, Y4, Y5, Y6, Y7
  nor nor_1 (nor_1_out, ic_7420_1_y1, ic_7420_1_y2);
  not not_1 (not_1_out, ic_74x138_4_y0);
  IC_74x3253 PS_Select_2 (
    .A1(PS_Select_a1[2]), .A2(PS_Select_a1[3]), .B1_1(1'b0), .B1_2(1'b0), .B1_3(1'b0), .B1_4(F), .B2_1(1'b1),
    .B2_2(T), .B2_3(F), .B2_4(1'b1), .S0(undriven_8[0]), .S1(undriven_8[1]), .nOE1(1'b0), .nOE2(undriven_9));
  not not_2 (not_2_out, undriven_7);
  IC_74x138 RWriteEn (
    .Y0(RWriteEn_y0), .Y1(RWriteEn_y1), .Y2(RWriteEn_y2), .Y3(RWriteEn_y3), .Y4(RWriteEn_y4),
    .Y5(RWriteEn_y5), .Y6(RWriteEn_y6), .Y7(RWriteEn_y7), .A(RD[0]), .B(RD[1]), .C(RD[2]), .nG2A(nWR_RD),
    .nG2B(1'b0), .G1(1'b1));
  IC_7402 ic_7402_3 (
    .Y3(ic_7402_3_y3), .Y4(ic_7402_3_y4), .Y1(ic_7402_3_y1), .Y2(ic_7402_3_y2), .A3(undriven_6[2]),
    .A4(undriven_6[3]), .B1(undriven_6[4]), .B2(undriven_6[5]), .A1(undriven_6[0]), .B3(undriven_6[6]),
    .B4(undriven_6[7]), .A2(undriven_6[1]));
  IC_7402 ic_7402_4 (
    .Y3(ic_7402_4_y3), .Y4(ic_7402_4_y4), .Y1(ic_7402_4_y1), .Y2(ic_7402_4_y2), .A3(undriven_6[10]),
    .A4(undriven_6[11]), .B1(undriven_6[12]), .B2(undriven_6[13]), .A1(undriven_6[8]), .B3(undriven_6[14]),
    .B4(undriven_6[15]), .A2(undriven_6[9]));
  IC_74x74half ic_74x74half_1 (
    .R1(ic_74x74half_1_r1), .CLK1(CLK), .CLR1(1'b1), .SET1(1'b1), .D1(undriven_10));  // open: Q1
  IC_74x573 ic_74x573_1 (
    .Q2(ic_74x573_1_q2), .Q3(ic_74x573_1_q3), .Q4(ic_74x573_1_q4), .Q5(ic_74x573_1_q5), .Q6(ic_74x573_1_q6),
    .Q7(ic_74x573_1_q7), .Q8(ic_74x573_1_q8), .Q1(ic_74x573_1_q1), .D2(RWriteEn_y1), .D3(RWriteEn_y2),
    .D4(RWriteEn_y3), .D5(RWriteEn_y4), .D6(RWriteEn_y5), .D7(RWriteEn_y6), .D8(RWriteEn_y7), .LE(nCLK),
    .nOE(1'b0), .D1(RWriteEn_y0));  // open: Probe
  IC_74x3345 PS_ByPass (
    .A5(PS_Select_a1[0]), .A6(PS_Select_a1[1]), .A7(PS_Select_a1[2]), .A8(PS_Select_a1[3]), .B3(1'b0),
    .B4(1'b0), .B5(undriven_8[0]), .B6(undriven_8[1]), .B7(undriven_8[2]), .B8(undriven_8[3]),
    .OE(undriven_9), .nOE(1'b1), .B1(1'b0), .B2(1'b0));  // open: A3, A4, A1, A2
  // IC_7411 ic_7411_1: pin names not known; wires that end beside it: not_2_out, ic_7402_3_y1, ic_7402_3_y2, ic_7402_3_y3, ic_7402_3_y4, ic_7402_4_y1, ic_7402_4_y2, ic_7402_4_y3, ic_7402_4_y4, ic_7411_1_p10, ic_7411_1_p11, ic_7411_1_p12
  or or_1 (or_1_out, ic_74x74half_1_r1, undriven_10);
  IC_7410 ic_7410_1 (
    .Y1(ic_7410_1_y1), .A3(ic_7411_1_p12), .A1(ic_7411_1_p10), .A2(ic_7411_1_p11));  // open: Y3, Y2, B1, B2, B3, C1, C2, C3
  nor nor_2 (WR_R0, nCLK, ic_74x573_1_q1);
  nor nor_3 (WR_R1, nCLK, ic_74x573_1_q2);
  nor nor_4 (WR_R2, nCLK, ic_74x573_1_q3);
  nor nor_5 (WR_R3, nCLK, ic_74x573_1_q4);
  nor nor_6 (WR_R4, nCLK, ic_74x573_1_q5);
  nor nor_7 (WR_R5, nCLK, ic_74x573_1_q6);
  nor nor_8 (WR_R6, nCLK, ic_74x573_1_q7);
  nor nor_9 (WR_R7, nCLK, ic_74x573_1_q8);
  IC_74x138 ic_74x138_5 (
    .Y0(ic_74x138_5_y0), .Y1(ic_74x138_5_y1), .Y2(ic_74x138_5_y2), .Y3(ic_74x138_5_y3), .Y4(ic_74x138_5_y4),
    .Y5(ic_74x138_5_y5), .Y6(ic_74x138_5_y6), .Y7(ic_74x138_5_y7), .A(RD[0]), .B(RD[1]), .C(RD[2]),
    .nG2A(nQ_RD), .nG2B(1'b0), .G1(1'b1));
  IC_74x238 ic_74x238_1 (
    .Y0(ic_74x238_1_y0), .Y1(ic_74x238_1_y1), .Y2(ic_74x238_1_y2), .Y3(ic_74x238_1_y3), .Y4(ic_74x238_1_y4),
    .Y5(ic_74x238_1_y5), .Y6(ic_74x238_1_y6), .Y7(ic_74x238_1_y7), .A(RD[0]), .B(RD[1]), .C(RD[2]),
    .nG2A(Q_RD_n), .nG2B(1'b0), .G1(1'b1));
  not not_3 (not_3_out, CLK);
  IC_74x138 ic_74x138_6 (
    .Y0(ic_74x138_6_y0), .Y1(ic_74x138_6_y1), .Y2(ic_74x138_6_y2), .Y3(ic_74x138_6_y3), .Y4(ic_74x138_6_y4),
    .Y5(ic_74x138_6_y5), .Y6(ic_74x138_6_y6), .Y7(ic_74x138_6_y7), .A(RD[0]), .B(RD[1]), .C(RD[2]),
    .nG2A(nRD_A), .nG2B(1'b0), .G1(1'b1));
  IC_74x138 ic_74x138_7 (
    .Y0(ic_74x138_7_y0), .Y1(ic_74x138_7_y1), .Y2(ic_74x138_7_y2), .Y3(ic_74x138_7_y3), .Y4(ic_74x138_7_y4),
    .Y5(ic_74x138_7_y5), .Y6(ic_74x138_7_y6), .Y7(ic_74x138_7_y7), .A(RS[0]), .B(RS[1]), .C(RS[2]),
    .nG2A(nRS_A), .nG2B(1'b0), .G1(1'b1));
  not not_4 (not_4_out, CLK);
  not not_5 (not_5_out, not_3_out);
  not not_6 (not_6_out, not_5_out);
  IC_74x151 u_PFIX (
    .Y(PFIX), .D1(1'b0), .D2(1'b0), .D3(1'b0), .D4(1'b0), .D5(1'b0), .D6(1'b0), .D7(IR11), .A(IR12),
    .B(IR13), .C(IR14), .nG(IR15), .D0(1'b0));  // open: W
  IC_74x563 ic_74x563_1 (
    .Q2(ic_74x563_1_q2), .Q3(ic_74x563_1_q3), .Q4(ic_74x563_1_q4), .Q5(ic_74x563_1_q5), .Q6(ic_74x563_1_q6),
    .Q7(ic_74x563_1_q7), .Q8(ic_74x563_1_q8), .Q1(ic_74x563_1_q1), .D2(ic_74x138_5_y1), .D3(ic_74x138_5_y2),
    .D4(ic_74x138_5_y3), .D5(ic_74x138_5_y4), .D6(ic_74x138_5_y5), .D7(ic_74x138_5_y6), .D8(ic_74x138_5_y7),
    .LE(not_4_out), .nOE(1'b0), .D1(ic_74x138_5_y0));  // open: Probe
  nand nand_1 (nand_1_out, not_3_out, not_7_out);
  not not_7 (not_7_out, not_6_out);
  // IC_74273 ic_74273_1: pin names not known; wires that end beside it: ic_74x238_1_y0, ic_74x238_1_y1, ic_74x238_1_y2, ic_74x238_1_y3, ic_74x238_1_y4, ic_74x238_1_y5, ic_74x238_1_y6, ic_74x238_1_y7, CLK, nand_1_out, WR_R0, WR_R1, WR_R2, WR_R3, WR_R4, WR_R5, WR_R6, WR_R7
  and and_1 (and_1_out, ic_74x138_6_y0, ic_74x138_7_y0);
  and and_2 (and_2_out, ic_74x138_6_y1, ic_74x138_7_y1);
  and and_3 (and_3_out, ic_74x138_6_y2, ic_74x138_7_y2);
  and and_4 (and_4_out, ic_74x138_6_y3, ic_74x138_7_y3);
  and and_5 (and_5_out, ic_74x138_6_y4, ic_74x138_7_y4);
  and and_6 (and_6_out, ic_74x138_6_y5, ic_74x138_7_y5);
  and and_7 (and_7_out, ic_74x138_6_y6, ic_74x138_7_y6);
  and and_8 (and_8_out, ic_74x138_6_y7, ic_74x138_7_y7);
  and and_9 (and_9_out, CLK, ic_74x563_1_q1);
  and and_10 (and_10_out, CLK, ic_74x563_1_q2);
  and and_11 (and_11_out, CLK, ic_74x563_1_q3);
  and and_12 (and_12_out, CLK, ic_74x563_1_q4);
  and and_13 (and_13_out, CLK, ic_74x563_1_q5);
  and and_14 (and_14_out, CLK, ic_74x563_1_q6);
  and and_15 (and_15_out, CLK, ic_74x563_1_q7);
  and and_16 (and_16_out, CLK, ic_74x563_1_q8);
  not not_8 (not_8_out, CLK);
  IC_74x138 ic_74x138_8 (
    .Y0(ic_74x138_8_y0), .Y1(ic_74x138_8_y1), .Y2(ic_74x138_8_y2), .Y3(ic_74x138_8_y3), .Y4(ic_74x138_8_y4),
    .Y5(ic_74x138_8_y5), .Y6(ic_74x138_8_y6), .Y7(ic_74x138_8_y7), .A(RD[0]), .B(RD[1]), .C(RD[2]),
    .nG2A(nWR_RD), .nG2B(1'b0), .G1(1'b1));
  IC_74x563 ic_74x563_2 (
    .Q2(ic_74x563_2_q2), .Q3(ic_74x563_2_q3), .Q4(ic_74x563_2_q4), .Q5(ic_74x563_2_q5), .Q6(ic_74x563_2_q6),
    .Q7(ic_74x563_2_q7), .Q8(ic_74x563_2_q8), .Q1(ic_74x563_2_q1), .D2(ic_74x138_8_y1), .D3(ic_74x138_8_y2),
    .D4(ic_74x138_8_y3), .D5(ic_74x138_8_y4), .D6(ic_74x138_8_y5), .D7(ic_74x138_8_y6), .D8(ic_74x138_8_y7),
    .LE(not_8_out), .nOE(1'b0), .D1(ic_74x138_8_y0));  // open: Probe
  and and_17 (and_17_out, CLK, ic_74x563_2_q1);
  and and_18 (and_18_out, CLK, ic_74x563_2_q2);
  and and_19 (and_19_out, CLK, ic_74x563_2_q3);
  and and_20 (and_20_out, CLK, ic_74x563_2_q4);
  and and_21 (and_21_out, CLK, ic_74x563_2_q5);
  and and_22 (and_22_out, CLK, ic_74x563_2_q6);
  and and_23 (and_23_out, CLK, ic_74x563_2_q7);
  and and_24 (and_24_out, CLK, ic_74x563_2_q8);

  // Notes on the sheet:
  //   PSFunc
  //   ----------
  //   0  PSSelect
  //   1  PSByPass
  //   PSSelect 
  //   (PSFunc=0)
  //   ----------------
  //   xx00 Q = A
  //   xx10 Q = SELt(A, 0)
  //   xx01 Q = SELf(A, 0)
  //   xx11 Q = SELt(A, B)
  //   PSSelect
  //   (PSFunc=1)
  //   -------------
  //   xxxx Q = bypas
  //   Efective 
  //   PS
  //   -------
  //   xxxx
  //   Efective 
  //   PS
  //   -------
  //   1010
  //   T0T0
  //   F0F0
  //   1FT0
endmodule

module ALUFlags_obsolete (
  input  ALU_nZ,
  input  ALU_C,
  input  ALU_S,
  input  ALU_V,
  input  [2:0] IR_CC,
  input  CTRL_nENCC,
  output Z,
  output C,
  output T
);

  wire and_1_out, and_2_out, not_2_out, not_3_out, xnor_1_out;
  wire [2:0] PS_Bypass_z1;

  IC_74x241 PS_Bypass (
    .Y3(PS_Bypass_z1[2]), .Z1(PS_Bypass_z1[0]), .Z2(PS_Bypass_z1[1]), .Z3(PS_Bypass_z1[2]),
    .Y1(PS_Bypass_z1[0]), .Y2(PS_Bypass_z1[1]), .A3(IR_CC[2]), .A4(1'b0), .nOEA(CTRL_nENCC), .B1(1'b0),
    .B2(1'b0), .B3(1'b0), .B4(1'b0), .A1(IR_CC[0]), .OEB(CTRL_nENCC), .A2(IR_CC[1]));  // open: Y4, Z4
  xnor xnor_1 (xnor_1_out, ALU_S, ALU_V);
  not not_1 (Z, ALU_nZ);
  not not_2 (not_2_out, ALU_C);
  not not_3 (not_3_out, xnor_1_out);
  and and_1 (and_1_out, ALU_C, ALU_nZ);
  and and_2 (and_2_out, xnor_1_out, ALU_nZ);
  IC_74x151 ic_74x151_1 (
    .Y(T), .D1(ALU_nZ), .D2(ALU_C), .D3(not_2_out), .D4(xnor_1_out), .D5(not_3_out), .D6(and_1_out),
    .D7(and_2_out), .A(PS_Bypass_z1[0]), .B(PS_Bypass_z1[1]), .C(PS_Bypass_z1[2]), .nG(1'b0), .D0(Z));  // open: W

  assign C = ALU_C;

  // Notes on the sheet:
  //   Conditon 
  //   Codes
  //   000 (EQ)
  //   001 (NE)
  //   010 (UGE)
  //   011 (ULT)
  //   100 (GE)
  //   101 (LT)
  //   110 (UGT)
  //   111 (GT)
  //   Logic 
  //   Function
  //   Z
  //   /Z
  //   C
  //   /C
  //   S == V
  //   S != V
  //   C AND /Z
  //   (S==V) AND /Z
endmodule

// ALU Ctrl
module ALUControl_obsolete (
  input  Cy,
  input  T,
  input  nT,
  input  A15,
  input  nA15,
  input  PSFunc,
  input  [3:0] PSin,
  input  [2:0] CSSel,
  output [3:0] PS,
  output CS
);

  IC_74x253 PS_Select (
    .Y1(PS[0]), .Y2(PS[1]), .I_n_0(1'b0), .I1_1(1'b0), .I1_2(1'b0), .I1_3(1'b0), .I2_0(1'b0), .I2_1(T),
    .I2_2(T), .I2_3(nT), .S0(PSin[0]), .S1(PSin[1]), .nOE1(PSFunc), .nOE2(PSFunc));
  IC_74x151 CS_Select (
    .Y(CS), .D1(1'b1), .D2(Cy), .D3(1'b0), .D4(nT), .D5(T), .D6(nA15), .D7(A15), .A(CSSel[0]), .B(CSSel[1]),
    .C(CSSel[2]), .nG(1'b0), .D0(1'b0));  // open: W
  IC_74x253 PS_Select_2 (
    .Y1(PS[2]), .Y2(PS[3]), .I_n_0(1'b0), .I1_1(nT), .I1_2(1'b0), .I1_3(1'b0), .I2_0(1'b0), .I2_1(1'b1),
    .I2_2(T), .I2_3(nT), .S0(PSin[0]), .S1(PSin[1]), .nOE1(PSFunc), .nOE2(PSFunc));
  IC_74x241 PS_Bypass (
    .Z1(PS[0]), .Z2(PS[1]), .Z3(PS[2]), .Z4(PS[3]), .A3(1'b0), .A4(1'b0), .nOEA(1'b0), .B1(PSin[0]),
    .B2(PSin[1]), .B3(PSin[2]), .B4(PSin[3]), .A1(1'b0), .OEB(PSFunc), .A2(1'b0));  // open: Y3, Y4, Y1, Y2

  // Other names for the same wires on the sheet: F = nT

  // Notes on the sheet:
  //   PSFunc
  //   0  PSSelect
  //   1  PSByPass
  //   PSSelect (PSFunc=0)
  //   xx00 Q = ZERO
  //   xx10 Q = SELt(A, 0)
  //   xx01 Q = SELf(A, 0)
  //   xx11 Q = SELt(A, B)
  //   Efective PS
  //   0000
  //   1ft0
  //   t0t0
  //   f0f0
  //   CS Select
  //   000
  //   001
  //   010
  //   011
  //   100
  //   101
  //   110
  //   111
  //   Efective CS
  //   0
  //   1
  //   Cy
  //   (reserved)
  //   /T
  //   T
  //   /A15
  //   A15
endmodule

module RegPC1 (
  input  CLK,
  input  RESET,
  input  nWR_PC,
  input  BR,
  input  [15:0] IN,
  output [15:0] PC_OUT
);

  wire CLK_WRPC, d_latch_1_q, ic_74x163_1_tc, ic_74x163_2_tc, ic_74x163_3_tc, not_1_out, not_2_out;
  wire [3:0] ic_74x163_1_q1;
  wire [7:4] ic_74x163_2_q1;
  wire [11:8] ic_74x163_3_q1;
  wire [15:0] ic_74x3257_1_a1;
  wire [15:12] ic_74x163_4_q1;

  not not_1 (not_1_out, BR);
  IC_74x163 ic_74x163_1 (
    .Q1(ic_74x163_1_q1[0]), .Q2(ic_74x163_1_q1[1]), .Q3(ic_74x163_1_q1[2]), .Q4(ic_74x163_1_q1[3]),
    .TC(ic_74x163_1_tc), .nLD(not_1_out), .CEP(not_1_out), .CET(not_1_out), .D1(IN[0]), .CLK(CLK_WRPC),
    .D2(IN[1]), .D3(IN[2]), .D4(IN[3]), .nCLR(RESET));
  not not_2 (not_2_out, CLK);
  D_Latch d_latch_1 (.Q(d_latch_1_q), .D(nWR_PC), .LE(not_2_out));  // open: R, SET, CLR
  IC_74x163 ic_74x163_2 (
    .Q1(ic_74x163_2_q1[4]), .Q2(ic_74x163_2_q1[5]), .Q3(ic_74x163_2_q1[6]), .Q4(ic_74x163_2_q1[7]),
    .TC(ic_74x163_2_tc), .nLD(not_1_out), .CEP(not_1_out), .CET(ic_74x163_1_tc), .D1(IN[4]), .CLK(CLK_WRPC),
    .D2(IN[5]), .D3(IN[6]), .D4(IN[7]), .nCLR(RESET));
  IC_74x3257 ic_74x3257_1 (
    .A1(ic_74x3257_1_a1[0]), .A2(ic_74x3257_1_a1[1]), .A3(ic_74x3257_1_a1[2]), .A4(ic_74x3257_1_a1[3]),
    .B2_1(IN[0]), .B1_2(ic_74x163_1_q1[1]), .B2_2(IN[1]), .B1_3(ic_74x163_1_q1[2]), .B2_3(IN[2]),
    .B1_4(ic_74x163_1_q1[3]), .B2_4(IN[3]), .S(BR), .nOE(1'b0), .B1_1(ic_74x163_1_q1[0]));
  IC_74x3257 ic_74x3257_2 (
    .A1(ic_74x3257_1_a1[4]), .A2(ic_74x3257_1_a1[5]), .A3(ic_74x3257_1_a1[6]), .A4(ic_74x3257_1_a1[7]),
    .B2_1(IN[4]), .B1_2(ic_74x163_2_q1[5]), .B2_2(IN[5]), .B1_3(ic_74x163_2_q1[6]), .B2_3(IN[6]),
    .B1_4(ic_74x163_2_q1[7]), .B2_4(IN[7]), .S(BR), .nOE(1'b0), .B1_1(ic_74x163_2_q1[4]));
  nor nor_1 (CLK_WRPC, d_latch_1_q, not_2_out);
  IC_74x163 ic_74x163_3 (
    .Q1(ic_74x163_3_q1[8]), .Q2(ic_74x163_3_q1[9]), .Q3(ic_74x163_3_q1[10]), .Q4(ic_74x163_3_q1[11]),
    .TC(ic_74x163_3_tc), .nLD(not_1_out), .CEP(not_1_out), .CET(ic_74x163_2_tc), .D1(IN[8]), .CLK(CLK_WRPC),
    .D2(IN[9]), .D3(IN[10]), .D4(IN[11]), .nCLR(RESET));
  IC_74x163 ic_74x163_4 (
    .Q1(ic_74x163_4_q1[12]), .Q2(ic_74x163_4_q1[13]), .Q3(ic_74x163_4_q1[14]), .Q4(ic_74x163_4_q1[15]),
    .nLD(not_1_out), .CEP(not_1_out), .CET(ic_74x163_3_tc), .D1(IN[12]), .CLK(CLK_WRPC), .D2(IN[13]),
    .D3(IN[14]), .D4(IN[15]), .nCLR(RESET));  // open: TC
  IC_74x3257 ic_74x3257_3 (
    .A1(ic_74x3257_1_a1[8]), .A2(ic_74x3257_1_a1[9]), .A3(ic_74x3257_1_a1[10]), .A4(ic_74x3257_1_a1[11]),
    .B2_1(IN[8]), .B1_2(ic_74x163_3_q1[9]), .B2_2(IN[9]), .B1_3(ic_74x163_3_q1[10]), .B2_3(IN[10]),
    .B1_4(ic_74x163_3_q1[11]), .B2_4(IN[11]), .S(BR), .nOE(1'b0), .B1_1(ic_74x163_3_q1[8]));
  IC_74x3257 ic_74x3257_4 (
    .A1(ic_74x3257_1_a1[12]), .A2(ic_74x3257_1_a1[13]), .A3(ic_74x3257_1_a1[14]), .A4(ic_74x3257_1_a1[15]),
    .B2_1(IN[12]), .B1_2(ic_74x163_4_q1[13]), .B2_2(IN[13]), .B1_3(ic_74x163_4_q1[14]), .B2_3(IN[14]),
    .B1_4(ic_74x163_4_q1[15]), .B2_4(IN[15]), .S(BR), .nOE(1'b0), .B1_1(ic_74x163_4_q1[12]));
  IC_74x273 PC (
    .Q1(PC_OUT[0]), .Q2(PC_OUT[1]), .Q3(PC_OUT[2]), .Q4(PC_OUT[3]), .Q5(PC_OUT[4]), .Q6(PC_OUT[5]),
    .Q7(PC_OUT[6]), .Q8(PC_OUT[7]), .D1(ic_74x3257_1_a1[0]), .D2(ic_74x3257_1_a1[1]),
    .D3(ic_74x3257_1_a1[2]), .D4(ic_74x3257_1_a1[3]), .D5(ic_74x3257_1_a1[4]), .D6(ic_74x3257_1_a1[5]),
    .D7(ic_74x3257_1_a1[6]), .D8(ic_74x3257_1_a1[7]), .CLK(CLK_WRPC), .nMR(RESET));  // open: Probe
  IC_74x273 PC_2 (
    .Q1(PC_OUT[8]), .Q2(PC_OUT[9]), .Q3(PC_OUT[10]), .Q4(PC_OUT[11]), .Q5(PC_OUT[12]), .Q6(PC_OUT[13]),
    .Q7(PC_OUT[14]), .Q8(PC_OUT[15]), .D1(ic_74x3257_1_a1[8]), .D2(ic_74x3257_1_a1[9]),
    .D3(ic_74x3257_1_a1[10]), .D4(ic_74x3257_1_a1[11]), .D5(ic_74x3257_1_a1[12]), .D6(ic_74x3257_1_a1[13]),
    .D7(ic_74x3257_1_a1[14]), .D8(ic_74x3257_1_a1[15]), .CLK(CLK_WRPC), .nMR(RESET));  // open: Probe

  // Other names for the same wires on the sheet: BRANCH = BR; CLR_n = RESET
endmodule

module RegPCV (
  input  CLK,
  input  RESET,
  input  nWR_PC,
  input  nWR_PMAR,
  input  BR,
  input  [15:0] IN,
  output [15:0] PC_OUT
);

  wire CLK_WRPC, CLK_WRPMAR, d_latch_1_q, d_latch_2_q, ic_74283_1_cout, ic_74283_2_cout, ic_74283_3_cout,
       nOE_PMAR, not_1_out;
  wire [3:0] ic_74283_1_y1;
  wire [7:4] ic_74283_2_y1;
  wire [11:8] ic_74283_3_y1;
  wire [15:0] ic_74x3257_1_a1, PC_q1;
  wire [15:12] ic_74283_4_y1;

  IC_74x273 PC (
    .Q1(PC_q1[0]), .Q2(PC_q1[1]), .Q3(PC_q1[2]), .Q4(PC_q1[3]), .Q5(PC_q1[4]), .Q6(PC_q1[5]), .Q7(PC_q1[6]),
    .Q8(PC_q1[7]), .D1(ic_74x3257_1_a1[0]), .D2(ic_74x3257_1_a1[1]), .D3(ic_74x3257_1_a1[2]),
    .D4(ic_74x3257_1_a1[3]), .D5(ic_74x3257_1_a1[4]), .D6(ic_74x3257_1_a1[5]), .D7(ic_74x3257_1_a1[6]),
    .D8(ic_74x3257_1_a1[7]), .CLK(CLK_WRPC), .nMR(RESET));  // open: Probe
  IC_74x273 PC_2 (
    .Q1(PC_q1[8]), .Q2(PC_q1[9]), .Q3(PC_q1[10]), .Q4(PC_q1[11]), .Q5(PC_q1[12]), .Q6(PC_q1[13]),
    .Q7(PC_q1[14]), .Q8(PC_q1[15]), .D1(ic_74x3257_1_a1[8]), .D2(ic_74x3257_1_a1[9]),
    .D3(ic_74x3257_1_a1[10]), .D4(ic_74x3257_1_a1[11]), .D5(ic_74x3257_1_a1[12]), .D6(ic_74x3257_1_a1[13]),
    .D7(ic_74x3257_1_a1[14]), .D8(ic_74x3257_1_a1[15]), .CLK(CLK_WRPC), .nMR(RESET));  // open: Probe
  logi7400ic_IC_74x574 PMAR (
    .Q2(PC_OUT[1]), .Q3(PC_OUT[2]), .Q4(PC_OUT[3]), .Q5(PC_OUT[4]), .Q6(PC_OUT[5]), .Q7(PC_OUT[6]),
    .Q8(PC_OUT[7]), .Q1(PC_OUT[0]), .D2(IN[1]), .D3(IN[2]), .D4(IN[3]), .D5(IN[4]), .D6(IN[5]), .D7(IN[6]),
    .D8(IN[7]), .CLK(CLK_WRPMAR), .nOE(nOE_PMAR), .D1(IN[0]));  // open: Probe
  logi7400ic_IC_74x574 PMAR_2 (
    .Q2(PC_OUT[9]), .Q3(PC_OUT[10]), .Q4(PC_OUT[11]), .Q5(PC_OUT[12]), .Q6(PC_OUT[13]), .Q7(PC_OUT[14]),
    .Q8(PC_OUT[15]), .Q1(PC_OUT[8]), .D2(IN[9]), .D3(IN[10]), .D4(IN[11]), .D5(IN[12]), .D6(IN[13]),
    .D7(IN[14]), .D8(IN[15]), .CLK(CLK_WRPMAR), .nOE(nOE_PMAR), .D1(IN[8]));  // open: Probe
  IC_74283 ic_74283_1 (
    .Y2(ic_74283_1_y1[1]), .Y3(ic_74283_1_y1[2]), .Y4(ic_74283_1_y1[3]), .Y1(ic_74283_1_y1[0]),
    .COUT(ic_74283_1_cout), .A3(PC_q1[2]), .A4(PC_q1[3]), .B1(1'b0), .B2(1'b0), .A1(PC_q1[0]), .B3(1'b0),
    .B4(1'b0), .CIN(1'b1), .A2(PC_q1[1]));
  IC_74283 ic_74283_2 (
    .Y2(ic_74283_2_y1[5]), .Y3(ic_74283_2_y1[6]), .Y4(ic_74283_2_y1[7]), .Y1(ic_74283_2_y1[4]),
    .COUT(ic_74283_2_cout), .A3(PC_q1[6]), .A4(PC_q1[7]), .B1(1'b0), .B2(1'b0), .A1(PC_q1[4]), .B3(1'b0),
    .B4(1'b0), .CIN(ic_74283_1_cout), .A2(PC_q1[5]));
  IC_74x3257 ic_74x3257_1 (
    .A1(ic_74x3257_1_a1[0]), .A2(ic_74x3257_1_a1[1]), .A3(ic_74x3257_1_a1[2]), .A4(ic_74x3257_1_a1[3]),
    .B2_1(IN[0]), .B1_2(ic_74283_1_y1[1]), .B2_2(IN[1]), .B1_3(ic_74283_1_y1[2]), .B2_3(IN[2]),
    .B1_4(ic_74283_1_y1[3]), .B2_4(IN[3]), .S(BR), .nOE(1'b0), .B1_1(ic_74283_1_y1[0]));
  not not_1 (not_1_out, CLK);
  IC_74283 ic_74283_3 (
    .Y2(ic_74283_3_y1[9]), .Y3(ic_74283_3_y1[10]), .Y4(ic_74283_3_y1[11]), .Y1(ic_74283_3_y1[8]),
    .COUT(ic_74283_3_cout), .A3(PC_q1[10]), .A4(PC_q1[11]), .B1(1'b0), .B2(1'b0), .A1(PC_q1[8]), .B3(1'b0),
    .B4(1'b0), .CIN(ic_74283_2_cout), .A2(PC_q1[9]));
  IC_74x3257 ic_74x3257_2 (
    .A1(ic_74x3257_1_a1[4]), .A2(ic_74x3257_1_a1[5]), .A3(ic_74x3257_1_a1[6]), .A4(ic_74x3257_1_a1[7]),
    .B2_1(IN[4]), .B1_2(ic_74283_2_y1[5]), .B2_2(IN[5]), .B1_3(ic_74283_2_y1[6]), .B2_3(IN[6]),
    .B1_4(ic_74283_2_y1[7]), .B2_4(IN[7]), .S(BR), .nOE(1'b0), .B1_1(ic_74283_2_y1[4]));
  D_Latch d_latch_1 (.Q(d_latch_1_q), .D(nWR_PC), .LE(not_1_out));  // open: R, SET, CLR
  D_Latch d_latch_2 (.Q(d_latch_2_q), .D(nWR_PMAR), .LE(not_1_out));  // open: R, SET, CLR
  D_Flip_Flop d_flip_flop_1 (.Q(nOE_PMAR), .D(nWR_PMAR), .CLK(CLK));  // open: R, SET, CLR
  nor nor_1 (CLK_WRPC, d_latch_1_q, not_1_out);
  nor nor_2 (CLK_WRPMAR, d_latch_2_q, not_1_out);
  IC_74283 ic_74283_4 (
    .Y2(ic_74283_4_y1[13]), .Y3(ic_74283_4_y1[14]), .Y4(ic_74283_4_y1[15]), .Y1(ic_74283_4_y1[12]),
    .A3(PC_q1[14]), .A4(PC_q1[15]), .B1(1'b0), .B2(1'b0), .A1(PC_q1[12]), .B3(1'b0), .B4(1'b0),
    .CIN(ic_74283_3_cout), .A2(PC_q1[13]));  // open: COUT
  IC_74x3257 ic_74x3257_3 (
    .A1(ic_74x3257_1_a1[8]), .A2(ic_74x3257_1_a1[9]), .A3(ic_74x3257_1_a1[10]), .A4(ic_74x3257_1_a1[11]),
    .B2_1(IN[8]), .B1_2(ic_74283_3_y1[9]), .B2_2(IN[9]), .B1_3(ic_74283_3_y1[10]), .B2_3(IN[10]),
    .B1_4(ic_74283_3_y1[11]), .B2_4(IN[11]), .S(BR), .nOE(1'b0), .B1_1(ic_74283_3_y1[8]));
  IC_74x3257 ic_74x3257_4 (
    .A1(ic_74x3257_1_a1[12]), .A2(ic_74x3257_1_a1[13]), .A3(ic_74x3257_1_a1[14]), .A4(ic_74x3257_1_a1[15]),
    .B2_1(IN[12]), .B1_2(ic_74283_4_y1[13]), .B2_2(IN[13]), .B1_3(ic_74283_4_y1[14]), .B2_3(IN[14]),
    .B1_4(ic_74283_4_y1[15]), .B2_4(IN[15]), .S(BR), .nOE(1'b0), .B1_1(ic_74283_4_y1[12]));
  IC_74x3345 ic_74x3345_1 (
    .A3(PC_OUT[2]), .A4(PC_OUT[3]), .A5(PC_OUT[4]), .A6(PC_OUT[5]), .A7(PC_OUT[6]), .A8(PC_OUT[7]),
    .A1(PC_OUT[0]), .A2(PC_OUT[1]), .B3(PC_q1[2]), .B4(PC_q1[3]), .B5(PC_q1[4]), .B6(PC_q1[5]),
    .B7(PC_q1[6]), .B8(PC_q1[7]), .OE(nOE_PMAR), .nOE(1'b1), .B1(PC_q1[0]), .B2(PC_q1[1]));
  IC_74x3345 ic_74x3345_2 (
    .A3(PC_OUT[10]), .A4(PC_OUT[11]), .A5(PC_OUT[12]), .A6(PC_OUT[13]), .A7(PC_OUT[14]), .A8(PC_OUT[15]),
    .A1(PC_OUT[8]), .A2(PC_OUT[9]), .B3(PC_q1[10]), .B4(PC_q1[11]), .B5(PC_q1[12]), .B6(PC_q1[13]),
    .B7(PC_q1[14]), .B8(PC_q1[15]), .OE(nOE_PMAR), .nOE(1'b1), .B1(PC_q1[8]), .B2(PC_q1[9]));

  // Other names for the same wires on the sheet: BRANCH = BR; CLR_n = RESET
endmodule

module Prova (
  input  [1:0] M,
  input  [4:0] I,
  output [3:0] PF,
  output [3:0] PT,
  output [2:0] C,
  output [1:0] G,
  output SH,
  output CM,
  output B0,
  output B1,
  output M0,
  output M1
);

  wire and_1_out, and_2_out, and_3_out, and_4_out, and_5_out, and_6_out, and_7_out, and_8_out, and_9_out,
       and_10_out, and_11_out, and_12_out, and_13_out, and_14_out, and_15_out, and_16_out, and_17_out,
       and_18_out, and_19_out, and_20_out, and_21_out, and_22_out, and_23_out, and_24_out, and_25_out,
       and_26_out, and_27_out, and_28_out, and_29_out, and_30_out, and_31_out, and_32_out, and_33_out,
       and_34_out, and_35_out, and_36_out, and_37_out, and_38_out, and_39_out, and_40_out, and_41_out,
       and_42_out, and_43_out, and_44_out, and_45_out, and_46_out, and_47_out, and_48_out, and_49_out,
       and_50_out, and_51_out, and_52_out, and_53_out, and_54_out, and_55_out, and_56_out, and_57_out,
       and_58_out, and_59_out, and_60_out, and_61_out, and_62_out, and_63_out, and_64_out, and_65_out,
       and_66_out, and_67_out, and_68_out, and_69_out, and_70_out, and_71_out, and_72_out, and_73_out,
       and_74_out, and_75_out, and_76_out, and_77_out, and_78_out, and_79_out, or_1_out, or_2_out, or_3_out,
       or_4_out, or_5_out, or_6_out, or_7_out, or_8_out, or_9_out, or_10_out, or_11_out, or_12_out,
       or_13_out, or_14_out;

  and and_1 (and_1_out, ~M[1], ~M[0], ~I[3], ~I[1]);  // AND_Gate
  and and_2 (and_2_out, ~I[4], ~I[3]);  // AND_Gate
  and and_3 (and_3_out, ~I[4], ~I[2]);  // AND_Gate
  and and_4 (and_4_out, ~I[4], ~I[1], I[0]);  // AND_Gate
  and and_5 (and_5_out, M[0], ~I[4]);  // AND_Gate
  and and_6 (and_6_out, M[0], I[3], ~I[2]);  // AND_Gate
  and and_7 (and_7_out, M[1], I[3], I[2], ~I[1]);  // AND_Gate
  and and_8 (and_8_out, M[1], I[4], I[3], I[1]);
  and and_9 (and_9_out, ~M[0], ~I[4], ~I[3], I[2], ~I[1], I[0]);  // AND_Gate
  and and_10 (and_10_out, ~I[4], I[3], I[2], I[1]);  // AND_Gate
  and and_11 (and_11_out, ~M[1], M[0], I[2], I[0]);  // AND_Gate
  and and_12 (and_12_out, M[0], I[4]);
  and and_13 (and_13_out, M[1], ~M[0], ~I[3]);  // AND_Gate
  and and_14 (and_14_out, M[1], I[4], ~I[2], ~I[1]);  // AND_Gate
  or or_1 (or_1_out, M[1], I[4], ~I[3], ~I[2], I[0]);  // OR_Gate
  or or_2 (or_2_out, M[1], M[0], ~I[3], ~I[2], ~I[1]);  // OR_Gate
  or or_3 (or_3_out, M[1], M[0], ~I[4], ~I[1]);  // OR_Gate
  or or_4 (or_4_out, ~I[4], ~I[3], I[2], ~I[1]);  // OR_Gate
  or or_5 (or_5_out, M[0], ~I[4], ~I[3], ~I[2], I[1]);  // OR_Gate
  or or_6 (or_6_out, M[1], ~M[0], ~I[3], I[2]);  // OR_Gate
  or or_7 (or_7_out, ~M[1], ~I[3], ~I[2], I[1], ~I[0]);  // OR_Gate
  and and_15 (and_15_out, ~M[1], ~I[4], ~I[3], I[2], ~I[1], I[0]);  // AND_Gate
  and and_16 (and_16_out, ~M[1], ~I[4], I[3], I[2], I[1]);  // AND_Gate
  and and_17 (and_17_out, ~M[1], M[0], ~I[4], ~I[2]);  // AND_Gate
  and and_18 (and_18_out, M[1], I[3], I[2], ~I[1], I[0]);  // AND_Gate
  and and_19 (and_19_out, M[1], I[4], I[3], I[2], ~I[1]);  // AND_Gate
  and and_20 (and_20_out, ~M[1], ~M[0], ~I[3], ~I[1]);  // AND_Gate
  and and_21 (and_21_out, ~I[4], ~I[3]);  // AND_Gate
  and and_22 (and_22_out, ~I[4], ~I[2]);  // AND_Gate
  and and_23 (and_23_out, ~I[4], ~I[1], ~I[0]);  // AND_Gate
  and and_24 (and_24_out, M[0], ~I[4]);  // AND_Gate
  and and_25 (and_25_out, M[0], I[3], ~I[2]);  // AND_Gate
  and and_26 (and_26_out, M[1], I[3], I[2], ~I[1]);  // AND_Gate
  and and_27 (and_27_out, M[1], I[4], I[3], I[1]);
  and and_28 (and_28_out, ~M[0], ~I[4], ~I[3], I[2], ~I[1], I[0]);  // AND_Gate
  and and_29 (and_29_out, ~I[4], I[3], I[2], I[1]);  // AND_Gate
  and and_30 (and_30_out, ~M[1], M[0], ~I[3]);  // AND_Gate
  and and_31 (and_31_out, ~M[1], M[0], I[2], I[0]);  // AND_Gate
  and and_32 (and_32_out, M[0], I[4], I[2]);
  and and_33 (and_33_out, M[1], ~M[0], ~I[3]);  // AND_Gate
  and and_34 (and_34_out, M[1], I[4], ~I[2], ~I[1]);  // AND_Gate
  or or_8 (or_8_out, M[0], ~I[3], ~I[2], I[1], ~I[0]);  // OR_Gate
  or or_9 (or_9_out, M[1], M[0], ~I[3], ~I[2], ~I[1]);  // OR_Gate
  or or_10 (or_10_out, M[1], M[0], ~I[4], ~I[1]);  // OR_Gate
  or or_11 (or_11_out, ~I[4], ~I[3], I[2], ~I[1]);  // OR_Gate
  or or_12 (or_12_out, M[0], ~I[4], ~I[3], ~I[2], I[1]);  // OR_Gate
  or or_13 (or_13_out, M[1], ~M[0], I[4], I[2]);  // OR_Gate
  or or_14 (or_14_out, M[1], ~M[0], I[4], I[0]);  // OR_Gate
  and and_35 (and_35_out, ~M[1], ~I[4], ~I[3], I[2], ~I[1], I[0]);  // AND_Gate
  and and_36 (and_36_out, ~M[1], ~I[4], I[3], I[2], I[1]);  // AND_Gate
  and and_37 (and_37_out, ~M[1], M[0], ~I[4], ~I[2]);  // AND_Gate
  and and_38 (and_38_out, M[1], I[3], I[2], ~I[1], I[0]);  // AND_Gate
  and and_39 (and_39_out, M[1], I[4], I[3], I[2], ~I[1]);  // AND_Gate
  and and_40 (and_40_out, ~I[4], ~I[3], I[2], ~I[1], I[0]);  // AND_Gate
  and and_41 (and_41_out, ~M[1], ~I[4], I[3], ~I[2], ~I[1], I[0]);  // AND_Gate
  and and_42 (and_42_out, ~M[1], ~I[4], I[3], ~I[2], I[1], ~I[0]);  // AND_Gate
  and and_43 (and_43_out, ~M[1], ~I[4], I[3], ~I[2], ~I[1], I[0]);  // AND_Gate
  and and_44 (and_44_out, ~M[1], ~M[0], I[4], ~I[3], I[1]);  // AND_Gate
  and and_45 (and_45_out, ~M[0], I[4], I[3], I[2], ~I[1], I[0]);  // AND_Gate
  and and_46 (and_46_out, M[0], ~I[2], ~I[1], I[0]);  // AND_Gate
  and and_47 (and_47_out, M[0], ~I[4], I[1], ~I[0]);  // AND_Gate
  and and_48 (and_48_out, ~M[1], ~I[4], I[3], I[1], ~I[0]);  // AND_Gate
  and and_49 (and_49_out, ~M[1], ~M[0], I[4], ~I[3], I[1], I[0]);  // AND_Gate
  and and_50 (and_50_out, ~M[0], I[4], I[3], I[2], ~I[1], I[0]);  // AND_Gate
  and and_51 (and_51_out, M[0], ~I[2], ~I[1], I[0]);  // AND_Gate
  and and_52 (and_52_out, M[0], ~I[3], I[0]);  // AND_Gate
  and and_53 (and_53_out, M[0], ~I[3], I[1]);  // AND_Gate
  and and_54 (and_54_out, M[0], I[4], I[2]);
  and and_55 (and_55_out, M[1], ~I[3]);  // AND_Gate
  and and_56 (and_56_out, M[1], ~I[4], I[2], I[1]);  // AND_Gate
  and and_57 (and_57_out, M[1], I[4], ~I[2], ~I[1]);  // AND_Gate
  and and_58 (and_58_out, M[0], ~I[4], ~I[2]);  // AND_Gate
  and and_59 (and_59_out, M[1], ~I[4], I[2], ~I[1], I[0]);  // AND_Gate
  and and_60 (and_60_out, M[1], I[4], I[3], I[2], ~I[1]);  // AND_Gate
  and and_61 (and_61_out, ~M[1], ~M[0], ~I[4], I[3], ~I[2], ~I[1]);  // AND_Gate
  and and_62 (and_62_out, ~M[1], ~M[0], ~I[4], I[3], ~I[2], ~I[0]);  // AND_Gate
  and and_63 (and_63_out, ~M[1], M[0], ~I[4], ~I[2], ~I[1]);  // AND_Gate
  and and_64 (and_64_out, M[1], I[4], I[3], I[2], ~I[1]);  // AND_Gate
  and and_65 (and_65_out, ~M[1], ~M[0], I[4], ~I[3], ~I[2], ~I[1], ~I[0]);  // AND_Gate
  and and_66 (and_66_out, M[0], I[4], I[3], I[2], ~I[1], ~I[0]);  // AND_Gate
  and and_67 (and_67_out, M[0], I[4], I[3], I[2], I[1], I[0]);
  and and_68 (and_68_out, ~M[1], ~M[0], I[4], ~I[3], ~I[2], ~I[1], ~I[0]);  // AND_Gate
  and and_69 (and_69_out, M[0], I[4], I[3], I[2], I[0]);
  and and_70 (and_70_out, ~M[1], ~I[4], ~I[3], I[2], ~I[1], I[0]);  // AND_Gate
  and and_71 (and_71_out, ~M[1], I[3], I[2], I[1]);  // AND_Gate
  and and_72 (and_72_out, ~M[1], I[4], I[1]);  // AND_Gate
  and and_73 (and_73_out, ~M[1], I[4], I[3], I[2]);  // AND_Gate
  and and_74 (and_74_out, ~M[1], M[0]);  // AND_Gate
  and and_75 (and_75_out, M[1], ~M[0], ~I[3]);  // AND_Gate
  and and_76 (and_76_out, M[1], ~M[0], I[2], ~I[1], I[0]);  // AND_Gate
  and and_77 (and_77_out, M[1], ~M[0], ~I[4], I[2], I[1]);  // AND_Gate
  and and_78 (and_78_out, M[1], I[4], ~I[2]);  // AND_Gate
  and and_79 (and_79_out, M[1], I[4], ~I[1]);  // AND_Gate
  or or_15 (PF[3], and_1_out, and_2_out, and_3_out, and_4_out, and_5_out, and_6_out, and_7_out, and_8_out);
  or or_16 (PF[2], and_9_out, and_10_out, and_11_out, and_12_out, and_13_out, and_14_out);
  and and_80 (PF[1], or_1_out, or_2_out, or_3_out, or_4_out, or_5_out, or_6_out, or_7_out);
  or or_17 (PF[0], and_15_out, and_16_out, and_17_out, and_18_out, and_19_out);
  or or_18 (PT[3], and_20_out, and_21_out, and_22_out, and_23_out, and_24_out, and_25_out, and_26_out, and_27_out);
  or or_19 (PT[2], and_28_out, and_29_out, and_30_out, and_31_out, and_32_out, and_33_out, and_34_out);
  and and_81 (PT[1], or_8_out, or_9_out, or_10_out, or_11_out, or_12_out, or_13_out, or_14_out);
  or or_20 (PT[0], and_35_out, and_36_out, and_37_out, and_38_out, and_39_out);
  or or_21 (C[2], and_40_out, and_41_out, and_42_out);
  or or_22 (C[1], and_43_out, and_44_out, and_45_out, and_46_out, and_47_out);
  or or_23 (C[0], and_48_out, and_49_out, and_50_out, and_51_out);
  or or_24 (G[1], and_52_out, and_53_out, and_54_out, and_55_out, and_56_out, and_57_out);
  or or_25 (G[0], and_58_out, and_59_out, and_60_out);
  or or_26 (SH, and_61_out, and_62_out);
  or or_27 (CM, and_63_out, and_64_out);
  or or_28 (B0, and_65_out, and_66_out, and_67_out);
  or or_29 (B1, and_68_out, and_69_out);
  or or_30 (M0, and_70_out, and_71_out, and_72_out, and_73_out, and_74_out);
  or or_31 (M1, and_75_out, and_76_out, and_77_out, and_78_out, and_79_out);
endmodule

module Prova1 (
  input  [4:0] I,
  output SE
);

  or or_1 (SE, ~I[0], I[1]);  // OR_Gate
endmodule

module BUG (
  input  a,
  input  b,
  input  c,
  input  d,
  input  e,
  input  f,
  input  g,
  input  h,
  output x
);

  wire and_1_out;

  and and_1 (and_1_out, c, d);
  or or_1 (x, a, ~b, and_1_out, e, f, g, h);  // OR_Gate
endmodule

module main (
  input  [1:0] M,
  input  [4:0] I,
  output SE,
  output P0,
  output P1,
  output P2,
  output P3,
  output C0,
  output C1,
  output C2,
  output G0,
  output G1,
  output SH,
  output CM,
  output B0,
  output B1,
  output N0,
  output N1
);

  wire and_1_out, and_2_out, and_3_out, and_4_out;

  and and_1 (and_1_out, ~M[0], ~I[2]);  // AND_Gate
  and and_2 (and_2_out, ~I[2], I[0]);  // AND_Gate
  and and_3 (and_3_out, I[4], I[2]);
  and and_4 (and_4_out, M[0], ~I[4]);  // AND_Gate
  or or_1 (SE, and_1_out, ~I[3], and_2_out, I[1], and_3_out, and_4_out, M[1]);  // OR_Gate

  assign B0 = 1'b0;
  assign B1 = 1'b0;
  assign C0 = 1'b0;
  assign C1 = 1'b0;
  assign C2 = 1'b0;
  assign CM = 1'b0;
  assign G0 = 1'b0;
  assign G1 = 1'b0;
  assign N0 = 1'b0;
  assign N1 = 1'b0;
  assign P0 = 1'b0;
  assign P1 = 1'b0;
  assign P2 = 1'b0;
  assign P3 = 1'b0;
  assign SH = 1'b0;
endmodule

module prova (
  input  [1:0] M,
  input  [4:0] I,
  output [3:0] PF,
  output [3:0] PT,
  output [2:0] C,
  output [1:0] G,
  output SH,
  output CM,
  output B0,
  output B1,
  output M0,
  output M1
);

  wire and_1_out, and_2_out, and_3_out, and_4_out, and_5_out, and_6_out, and_7_out, and_8_out, and_9_out,
       and_10_out, and_11_out, and_12_out, and_13_out, and_14_out, and_15_out, and_16_out, and_17_out,
       and_18_out, and_19_out, and_20_out, and_21_out, and_22_out, and_23_out, and_24_out, and_25_out,
       and_26_out, and_27_out, and_28_out, and_29_out, and_30_out, and_31_out, and_32_out, and_33_out,
       and_34_out, and_35_out, and_36_out, and_37_out, and_38_out, and_39_out, and_40_out, and_41_out,
       and_42_out, and_43_out, and_44_out, and_45_out, and_46_out, and_47_out, and_48_out, and_49_out,
       and_50_out, and_51_out, and_52_out, and_53_out, and_54_out, and_55_out, and_56_out, and_57_out,
       and_58_out, and_59_out, and_60_out, and_61_out, and_62_out, and_63_out, and_64_out, and_65_out,
       and_66_out, and_67_out, and_68_out, and_69_out, and_70_out, and_71_out, and_72_out, and_73_out,
       and_74_out, and_75_out, and_76_out, and_77_out, and_78_out, and_79_out, or_1_out, or_2_out, or_3_out,
       or_4_out, or_5_out, or_6_out, or_7_out, or_8_out, or_9_out, or_10_out, or_11_out, or_12_out,
       or_13_out, or_14_out;

  and and_1 (and_1_out, ~M[1], ~M[0], ~I[3], ~I[1]);  // AND_Gate
  and and_2 (and_2_out, ~I[4], ~I[3]);  // AND_Gate
  and and_3 (and_3_out, ~I[4], ~I[2]);  // AND_Gate
  and and_4 (and_4_out, ~I[4], ~I[1], I[0]);  // AND_Gate
  and and_5 (and_5_out, M[0], ~I[4]);  // AND_Gate
  and and_6 (and_6_out, M[0], I[3], ~I[2]);  // AND_Gate
  and and_7 (and_7_out, M[1], I[3], I[2], ~I[1]);  // AND_Gate
  and and_8 (and_8_out, M[1], I[4], I[3], I[1]);
  and and_9 (and_9_out, ~M[0], ~I[4], ~I[3], I[2], ~I[1], I[0]);  // AND_Gate
  and and_10 (and_10_out, ~I[4], I[3], I[2], I[1]);  // AND_Gate
  and and_11 (and_11_out, ~M[1], M[0], I[2], I[0]);  // AND_Gate
  and and_12 (and_12_out, M[0], I[4]);
  and and_13 (and_13_out, M[1], ~M[0], ~I[3]);  // AND_Gate
  and and_14 (and_14_out, M[1], I[4], ~I[2], ~I[1]);  // AND_Gate
  or or_1 (or_1_out, M[1], I[4], ~I[3], ~I[2], I[0]);  // OR_Gate
  or or_2 (or_2_out, M[1], M[0], ~I[3], ~I[2], ~I[1]);  // OR_Gate
  or or_3 (or_3_out, M[1], M[0], ~I[4], ~I[1]);  // OR_Gate
  or or_4 (or_4_out, ~I[4], ~I[3], I[2], ~I[1]);  // OR_Gate
  or or_5 (or_5_out, M[0], ~I[4], ~I[3], ~I[2], I[1]);  // OR_Gate
  or or_6 (or_6_out, M[1], ~M[0], ~I[3], I[2]);  // OR_Gate
  or or_7 (or_7_out, ~M[1], ~I[3], ~I[2], I[1], ~I[0]);  // OR_Gate
  and and_15 (and_15_out, ~M[1], ~I[4], ~I[3], I[2], ~I[1], I[0]);  // AND_Gate
  and and_16 (and_16_out, ~M[1], ~I[4], I[3], I[2], I[1]);  // AND_Gate
  and and_17 (and_17_out, ~M[1], M[0], ~I[4], ~I[2]);  // AND_Gate
  and and_18 (and_18_out, M[1], I[3], I[2], ~I[1], I[0]);  // AND_Gate
  and and_19 (and_19_out, M[1], I[4], I[3], I[2], ~I[1]);  // AND_Gate
  and and_20 (and_20_out, ~M[1], ~M[0], ~I[3], ~I[1]);  // AND_Gate
  and and_21 (and_21_out, ~I[4], ~I[3]);  // AND_Gate
  and and_22 (and_22_out, ~I[4], ~I[2]);  // AND_Gate
  and and_23 (and_23_out, ~I[4], ~I[1], ~I[0]);  // AND_Gate
  and and_24 (and_24_out, M[0], ~I[4]);  // AND_Gate
  and and_25 (and_25_out, M[0], I[3], ~I[2]);  // AND_Gate
  and and_26 (and_26_out, M[1], I[3], I[2], ~I[1]);  // AND_Gate
  and and_27 (and_27_out, M[1], I[4], I[3], I[1]);
  and and_28 (and_28_out, ~M[0], ~I[4], ~I[3], I[2], ~I[1], I[0]);  // AND_Gate
  and and_29 (and_29_out, ~I[4], I[3], I[2], I[1]);  // AND_Gate
  and and_30 (and_30_out, ~M[1], M[0], ~I[3]);  // AND_Gate
  and and_31 (and_31_out, ~M[1], M[0], I[2], I[0]);  // AND_Gate
  and and_32 (and_32_out, M[0], I[4], I[2]);
  and and_33 (and_33_out, M[1], ~M[0], ~I[3]);  // AND_Gate
  and and_34 (and_34_out, M[1], I[4], ~I[2], ~I[1]);  // AND_Gate
  or or_8 (or_8_out, M[0], ~I[3], ~I[2], I[1], ~I[0]);  // OR_Gate
  or or_9 (or_9_out, M[1], M[0], ~I[3], ~I[2], ~I[1]);  // OR_Gate
  or or_10 (or_10_out, M[1], M[0], ~I[4], ~I[1]);  // OR_Gate
  or or_11 (or_11_out, ~I[4], ~I[3], I[2], ~I[1]);  // OR_Gate
  or or_12 (or_12_out, M[0], ~I[4], ~I[3], ~I[2], I[1]);  // OR_Gate
  or or_13 (or_13_out, M[1], ~M[0], I[4], I[2]);  // OR_Gate
  or or_14 (or_14_out, M[1], ~M[0], I[4], I[0]);  // OR_Gate
  and and_35 (and_35_out, ~M[1], ~I[4], ~I[3], I[2], ~I[1], I[0]);  // AND_Gate
  and and_36 (and_36_out, ~M[1], ~I[4], I[3], I[2], I[1]);  // AND_Gate
  and and_37 (and_37_out, ~M[1], M[0], ~I[4], ~I[2]);  // AND_Gate
  and and_38 (and_38_out, M[1], I[3], I[2], ~I[1], I[0]);  // AND_Gate
  and and_39 (and_39_out, M[1], I[4], I[3], I[2], ~I[1]);  // AND_Gate
  and and_40 (and_40_out, ~I[4], ~I[3], I[2], ~I[1], I[0]);  // AND_Gate
  and and_41 (and_41_out, ~M[1], ~I[4], I[3], ~I[2], ~I[1], I[0]);  // AND_Gate
  and and_42 (and_42_out, ~M[1], ~I[4], I[3], ~I[2], I[1], ~I[0]);  // AND_Gate
  and and_43 (and_43_out, ~M[1], ~I[4], I[3], ~I[2], ~I[1], I[0]);  // AND_Gate
  and and_44 (and_44_out, ~M[1], ~M[0], I[4], ~I[3], I[1]);  // AND_Gate
  and and_45 (and_45_out, ~M[0], I[4], I[3], I[2], ~I[1], I[0]);  // AND_Gate
  and and_46 (and_46_out, M[0], ~I[2], ~I[1], I[0]);  // AND_Gate
  and and_47 (and_47_out, M[0], ~I[4], I[1], ~I[0]);  // AND_Gate
  and and_48 (and_48_out, ~M[1], ~I[4], I[3], I[1], ~I[0]);  // AND_Gate
  and and_49 (and_49_out, ~M[1], ~M[0], I[4], ~I[3], I[1], I[0]);  // AND_Gate
  and and_50 (and_50_out, ~M[0], I[4], I[3], I[2], ~I[1], I[0]);  // AND_Gate
  and and_51 (and_51_out, M[0], ~I[2], ~I[1], I[0]);  // AND_Gate
  and and_52 (and_52_out, M[0], ~I[3], I[0]);  // AND_Gate
  and and_53 (and_53_out, M[0], ~I[3], I[1]);  // AND_Gate
  and and_54 (and_54_out, M[0], I[4], I[2]);
  and and_55 (and_55_out, M[1], ~I[3]);  // AND_Gate
  and and_56 (and_56_out, M[1], ~I[4], I[2], I[1]);  // AND_Gate
  and and_57 (and_57_out, M[1], I[4], ~I[2], ~I[1]);  // AND_Gate
  and and_58 (and_58_out, M[0], ~I[4], ~I[2]);  // AND_Gate
  and and_59 (and_59_out, M[1], ~I[4], I[2], ~I[1], I[0]);  // AND_Gate
  and and_60 (and_60_out, M[1], I[4], I[3], I[2], ~I[1]);  // AND_Gate
  and and_61 (and_61_out, ~M[1], ~M[0], ~I[4], I[3], ~I[2], ~I[1]);  // AND_Gate
  and and_62 (and_62_out, ~M[1], ~M[0], ~I[4], I[3], ~I[2], ~I[0]);  // AND_Gate
  and and_63 (and_63_out, ~M[1], M[0], ~I[4], ~I[2], ~I[1]);  // AND_Gate
  and and_64 (and_64_out, M[1], I[4], I[3], I[2], ~I[1]);  // AND_Gate
  and and_65 (and_65_out, ~M[1], ~M[0], I[4], ~I[3], ~I[2], ~I[1], ~I[0]);  // AND_Gate
  and and_66 (and_66_out, M[0], I[4], I[3], I[2], ~I[1], ~I[0]);  // AND_Gate
  and and_67 (and_67_out, M[0], I[4], I[3], I[2], I[1], I[0]);
  and and_68 (and_68_out, ~M[1], ~M[0], I[4], ~I[3], ~I[2], ~I[1], ~I[0]);  // AND_Gate
  and and_69 (and_69_out, M[0], I[4], I[3], I[2], I[0]);
  and and_70 (and_70_out, ~M[1], ~I[4], ~I[3], I[2], ~I[1], I[0]);  // AND_Gate
  and and_71 (and_71_out, ~M[1], I[3], I[2], I[1]);  // AND_Gate
  and and_72 (and_72_out, ~M[1], I[4], I[1]);  // AND_Gate
  and and_73 (and_73_out, ~M[1], I[4], I[3], I[2]);  // AND_Gate
  and and_74 (and_74_out, ~M[1], M[0]);  // AND_Gate
  and and_75 (and_75_out, M[1], ~M[0], ~I[3]);  // AND_Gate
  and and_76 (and_76_out, M[1], ~M[0], I[2], ~I[1], I[0]);  // AND_Gate
  and and_77 (and_77_out, M[1], ~M[0], ~I[4], I[2], I[1]);  // AND_Gate
  and and_78 (and_78_out, M[1], I[4], ~I[2]);  // AND_Gate
  and and_79 (and_79_out, M[1], I[4], ~I[1]);  // AND_Gate
  or or_15 (PF[3], and_1_out, and_2_out, and_3_out, and_4_out, and_5_out, and_6_out, and_7_out, and_8_out);
  or or_16 (PF[2], and_9_out, and_10_out, and_11_out, and_12_out, and_13_out, and_14_out);
  and and_80 (PF[1], or_1_out, or_2_out, or_3_out, or_4_out, or_5_out, or_6_out, or_7_out);
  or or_17 (PF[0], and_15_out, and_16_out, and_17_out, and_18_out, and_19_out);
  or or_18 (PT[3], and_20_out, and_21_out, and_22_out, and_23_out, and_24_out, and_25_out, and_26_out, and_27_out);
  or or_19 (PT[2], and_28_out, and_29_out, and_30_out, and_31_out, and_32_out, and_33_out, and_34_out);
  and and_81 (PT[1], or_8_out, or_9_out, or_10_out, or_11_out, or_12_out, or_13_out, or_14_out);
  or or_20 (PT[0], and_35_out, and_36_out, and_37_out, and_38_out, and_39_out);
  or or_21 (C[2], and_40_out, and_41_out, and_42_out);
  or or_22 (C[1], and_43_out, and_44_out, and_45_out, and_46_out, and_47_out);
  or or_23 (C[0], and_48_out, and_49_out, and_50_out, and_51_out);
  or or_24 (G[1], and_52_out, and_53_out, and_54_out, and_55_out, and_56_out, and_57_out);
  or or_25 (G[0], and_58_out, and_59_out, and_60_out);
  or or_26 (SH, and_61_out, and_62_out);
  or or_27 (CM, and_63_out, and_64_out);
  or or_28 (B0, and_65_out, and_66_out, and_67_out);
  or or_29 (B1, and_68_out, and_69_out);
  or or_30 (M0, and_70_out, and_71_out, and_72_out, and_73_out, and_74_out);
  or or_31 (M1, and_75_out, and_76_out, and_77_out, and_78_out, and_79_out);
endmodule

// Imm
module ImmDecoder1 (
  input  nRESET,
  input  CLK,
  input  nOE,
  input  [15:0] IR,
  output [15:0] IMM_OUT
);

  wire and_1_out, and_2_out, and_3_out, and_4_out, and_5_out, and_6_out, B0_n, B1_n, B2_n, B3_n, B4_n, B5_n,
       B6_n, B7, B7_n, C0, C3_n, IR12_n, PFIX_Reg_2_q4, PFIX_Reg_2_r4, pull_resistor_1_node;
  wire [15:5] P_Imm_q1, PFIX_Reg_y1;

  and and_1 (and_1_out, B7, IR[11], IR[12]);
  and and_2 (and_2_out, B7, IR12_n, IR[10]);
  and and_3 (and_3_out, B5_n, B6_n, B7_n);
  and and_4 (and_4_out, B7, IR[12]);
  and and_5 (and_5_out, IR[13], C0, IR[5]);
  and and_6 (and_6_out, B2_n, B3_n, B4_n);
  IC_74x541 P_Imm (
    .Q1(P_Imm_q1[5]), .Q2(P_Imm_q1[6]), .Q3(P_Imm_q1[7]), .Q4(P_Imm_q1[8]), .Q5(P_Imm_q1[9]),
    .Q6(P_Imm_q1[10]), .Q7(P_Imm_q1[11]), .Q8(P_Imm_q1[15]), .I1(IR[0]), .I2(IR[1]), .I3(IR[2]), .I4(IR[3]),
    .I5(IR[4]), .I6(IR[5]), .I7(1'b0), .I8(1'b0), .nOE1(B7_n), .nOE2(IR12_n));
  IC_74x541 I2_Imm (
    .Q1(P_Imm_q1[5]), .Q2(P_Imm_q1[6]), .Q3(P_Imm_q1[7]), .Q4(P_Imm_q1[8]), .Q5(P_Imm_q1[9]),
    .Q6(P_Imm_q1[10]), .Q7(P_Imm_q1[11]), .Q8(P_Imm_q1[15]), .I1(and_2_out), .I2(and_2_out), .I3(and_2_out),
    .I4(and_2_out), .I5(and_2_out), .I6(and_2_out), .I7(and_2_out), .I8(and_2_out), .nOE1(and_3_out),
    .nOE2(and_4_out));
  IC_74x541 I1_Imm (
    .Q1(P_Imm_q1[5]), .Q2(P_Imm_q1[6]), .Q3(P_Imm_q1[7]), .Q4(P_Imm_q1[8]), .Q5(P_Imm_q1[9]),
    .Q6(P_Imm_q1[10]), .Q7(P_Imm_q1[11]), .Q8(P_Imm_q1[15]), .I1(IR[3]), .I2(IR[4]), .I3(IR[5]),
    .I4(and_5_out), .I5(and_5_out), .I6(and_5_out), .I7(and_5_out), .I8(and_5_out), .nOE1(and_6_out),
    .nOE2(1'b0));
  IC_74x541 J_Imm (
    .Q1(P_Imm_q1[5]), .Q2(P_Imm_q1[6]), .Q3(P_Imm_q1[7]), .Q4(P_Imm_q1[8]), .Q5(P_Imm_q1[9]),
    .Q6(P_Imm_q1[10]), .Q7(P_Imm_q1[11]), .Q8(P_Imm_q1[15]), .I1(IR[2]), .I2(IR[3]), .I3(IR[4]), .I4(IR[5]),
    .I5(IR[5]), .I6(IR[5]), .I7(IR[5]), .I8(IR[5]), .nOE1(B1_n), .nOE2(C3_n));
  Pull_Resistor pull_resistor_1 (.node(pull_resistor_1_node));
  IC_74273 PFIX_Reg (
    .Y2(PFIX_Reg_y1[6]), .Y3(PFIX_Reg_y1[7]), .Y1(PFIX_Reg_y1[5]), .Y4(PFIX_Reg_y1[8]), .Y5(PFIX_Reg_y1[9]),
    .Y6(PFIX_Reg_y1[10]), .Y7(PFIX_Reg_y1[11]), .Y8(PFIX_Reg_y1[12]), .D2(IR[7]), .D3(IR[8]), .D1(IR[6]),
    .D4(IR[9]), .D5(IR[10]), .D6(P_Imm_q1[5]), .D7(P_Imm_q1[6]), .D8(P_Imm_q1[7]), .CLK(CLK), .CLR(nRESET));
  IC_74175 PFIX_Reg_2 (
    .Q2(PFIX_Reg_y1[14]), .Q3(PFIX_Reg_y1[15]), .Q1(PFIX_Reg_y1[13]), .Q4(PFIX_Reg_2_q4), .R4(PFIX_Reg_2_r4),
    .D2(P_Imm_q1[9]), .D3(P_Imm_q1[10]), .D1(P_Imm_q1[8]), .D4(and_1_out), .CLK(CLK), .CLR(nRESET));  // open: R2, R3, R1
  nor nor_1 (C0, IR[11], IR[12]);
  nand nand_1 (C3_n, IR[11], IR[12]);
  not not_1 (IR12_n, IR[12]);
  IC_74138 ic_74138_1 (
    .Y0(B0_n), .Y1(B1_n), .Y2(B2_n), .Y3(B3_n), .Y4(B4_n), .Y5(B5_n), .Y6(B6_n), .Y7(B7_n), .A2(IR[15]),
    .A0(IR[13]), .OE1(1'b0), .OE2(1'b0), .OE3(1'b1), .A1(IR[14]));
  and and_7 (B7, IR[13], IR[14], IR[15]);
  IC_74x541 ic_74x541_1 (
    .Q1(IMM_OUT[0]), .Q2(IMM_OUT[1]), .Q3(IMM_OUT[2]), .Q4(IMM_OUT[3]), .Q5(IMM_OUT[4]), .Q6(IMM_OUT[5]),
    .Q7(IMM_OUT[6]), .Q8(IMM_OUT[7]), .I1(IR[6]), .I2(IR[7]), .I3(IR[8]), .I4(IR[9]), .I5(IR[10]),
    .I6(PFIX_Reg_y1[5]), .I7(PFIX_Reg_y1[6]), .I8(PFIX_Reg_y1[7]), .nOE1(PFIX_Reg_2_r4), .nOE2(nOE));
  IC_74x541 ic_74x541_2 (
    .Q1(IMM_OUT[8]), .Q2(IMM_OUT[9]), .Q3(IMM_OUT[10]), .Q4(IMM_OUT[11]), .Q5(IMM_OUT[12]), .Q6(IMM_OUT[13]),
    .Q7(IMM_OUT[14]), .Q8(IMM_OUT[15]), .I1(PFIX_Reg_y1[8]), .I2(PFIX_Reg_y1[9]), .I3(PFIX_Reg_y1[10]),
    .I4(PFIX_Reg_y1[11]), .I5(PFIX_Reg_y1[12]), .I6(PFIX_Reg_y1[13]), .I7(PFIX_Reg_y1[14]),
    .I8(PFIX_Reg_y1[15]), .nOE1(PFIX_Reg_2_r4), .nOE2(nOE));
  IC_74x541 ic_74x541_3 (
    .Q1(IMM_OUT[0]), .Q2(IMM_OUT[1]), .Q3(IMM_OUT[2]), .Q4(IMM_OUT[3]), .Q5(IMM_OUT[4]), .Q6(IMM_OUT[5]),
    .Q7(IMM_OUT[6]), .Q8(IMM_OUT[7]), .I1(IR[6]), .I2(IR[7]), .I3(IR[8]), .I4(IR[9]), .I5(IR[10]),
    .I6(P_Imm_q1[5]), .I7(P_Imm_q1[6]), .I8(P_Imm_q1[7]), .nOE1(PFIX_Reg_2_q4), .nOE2(nOE));
  IC_74x541 ic_74x541_4 (
    .Q1(IMM_OUT[8]), .Q2(IMM_OUT[9]), .Q3(IMM_OUT[10]), .Q4(IMM_OUT[11]), .Q5(IMM_OUT[12]), .Q6(IMM_OUT[13]),
    .Q7(IMM_OUT[14]), .Q8(IMM_OUT[15]), .I1(P_Imm_q1[8]), .I2(P_Imm_q1[9]), .I3(P_Imm_q1[10]),
    .I4(P_Imm_q1[11]), .I5(P_Imm_q1[15]), .I6(P_Imm_q1[15]), .I7(P_Imm_q1[15]), .I8(P_Imm_q1[15]),
    .nOE1(PFIX_Reg_2_q4), .nOE2(nOE));

  // Other names for the same wires on the sheet: CLR_n = nRESET; OE_n = nOE
endmodule
// Register File
module Registers541 (
  input  nCLK,
  input  nWR_RD,
  input  nRD_TO_A,
  input  nRS_TO_A,
  input  nRN_TO_B,
  input  [15:0] IN,
  input  [2:0] RD,
  input  [2:0] RS,
  input  [2:0] RN,
  output [15:0] REG_A,
  output [15:0] REG_B
);

  wire ic_74x573_1_q1, ic_74x573_1_q2, ic_74x573_1_q3, ic_74x573_1_q4, ic_74x573_1_q5, ic_74x573_1_q6,
       ic_74x573_1_q7, ic_74x573_1_q8, RWriteEn_y0, RWriteEn_y1, RWriteEn_y2, RWriteEn_y3, RWriteEn_y4,
       RWriteEn_y5, RWriteEn_y6, RWriteEn_y7, sR0_1A_n, sR0_2A_n, sR0_B_n, sR1_1A_n, sR1_2A_n, sR1_B_n,
       sR2_1A_n, sR2_2A_n, sR2_B_n, sR3_1A_n, sR3_2A_n, sR3_B_n, sR4_1A_n, sR4_2A_n, sR4_B_n, sR5_1A_n,
       sR5_2A_n, sR5_B_n, sR6_1A_n, sR6_2A_n, sR6_B_n, sR7_1A_n, sR7_2A_n, sR7_B_n, WR_R0, WR_R1, WR_R2,
       WR_R3, WR_R4, WR_R5, WR_R6, WR_R7;
  wire [15:0] R0_q1, R1_q1, R2_q1, R3_q1, R4_q1, R5_q1, R6_q1, R7_q1;

  IC_74x273 R0 (
    .Q1(R0_q1[0]), .Q2(R0_q1[1]), .Q3(R0_q1[2]), .Q4(R0_q1[3]), .Q5(R0_q1[4]), .Q6(R0_q1[5]), .Q7(R0_q1[6]),
    .Q8(R0_q1[7]), .D1(IN[0]), .D2(IN[1]), .D3(IN[2]), .D4(IN[3]), .D5(IN[4]), .D6(IN[5]), .D7(IN[6]),
    .D8(IN[7]), .CLK(WR_R0), .nMR(1'b1));  // open: Probe
  IC_74x273 R0_2 (
    .Q1(R0_q1[8]), .Q2(R0_q1[9]), .Q3(R0_q1[10]), .Q4(R0_q1[11]), .Q5(R0_q1[12]), .Q6(R0_q1[13]),
    .Q7(R0_q1[14]), .Q8(R0_q1[15]), .D1(IN[8]), .D2(IN[9]), .D3(IN[10]), .D4(IN[11]), .D5(IN[12]),
    .D6(IN[13]), .D7(IN[14]), .D8(IN[15]), .CLK(WR_R0), .nMR(1'b1));  // open: Probe
  IC_74x273 R1 (
    .Q1(R1_q1[0]), .Q2(R1_q1[1]), .Q3(R1_q1[2]), .Q4(R1_q1[3]), .Q5(R1_q1[4]), .Q6(R1_q1[5]), .Q7(R1_q1[6]),
    .Q8(R1_q1[7]), .D1(IN[0]), .D2(IN[1]), .D3(IN[2]), .D4(IN[3]), .D5(IN[4]), .D6(IN[5]), .D7(IN[6]),
    .D8(IN[7]), .CLK(WR_R1), .nMR(1'b1));  // open: Probe
  IC_74x273 R1_2 (
    .Q1(R1_q1[8]), .Q2(R1_q1[9]), .Q3(R1_q1[10]), .Q4(R1_q1[11]), .Q5(R1_q1[12]), .Q6(R1_q1[13]),
    .Q7(R1_q1[14]), .Q8(R1_q1[15]), .D1(IN[8]), .D2(IN[9]), .D3(IN[10]), .D4(IN[11]), .D5(IN[12]),
    .D6(IN[13]), .D7(IN[14]), .D8(IN[15]), .CLK(WR_R1), .nMR(1'b1));  // open: Probe
  IC_74x273 R2 (
    .Q1(R2_q1[0]), .Q2(R2_q1[1]), .Q3(R2_q1[2]), .Q4(R2_q1[3]), .Q5(R2_q1[4]), .Q6(R2_q1[5]), .Q7(R2_q1[6]),
    .Q8(R2_q1[7]), .D1(IN[0]), .D2(IN[1]), .D3(IN[2]), .D4(IN[3]), .D5(IN[4]), .D6(IN[5]), .D7(IN[6]),
    .D8(IN[7]), .CLK(WR_R2), .nMR(1'b1));  // open: Probe
  IC_74x273 R2_2 (
    .Q1(R2_q1[8]), .Q2(R2_q1[9]), .Q3(R2_q1[10]), .Q4(R2_q1[11]), .Q5(R2_q1[12]), .Q6(R2_q1[13]),
    .Q7(R2_q1[14]), .Q8(R2_q1[15]), .D1(IN[8]), .D2(IN[9]), .D3(IN[10]), .D4(IN[11]), .D5(IN[12]),
    .D6(IN[13]), .D7(IN[14]), .D8(IN[15]), .CLK(WR_R2), .nMR(1'b1));  // open: Probe
  IC_74x273 R3 (
    .Q1(R3_q1[0]), .Q2(R3_q1[1]), .Q3(R3_q1[2]), .Q4(R3_q1[3]), .Q5(R3_q1[4]), .Q6(R3_q1[5]), .Q7(R3_q1[6]),
    .Q8(R3_q1[7]), .D1(IN[0]), .D2(IN[1]), .D3(IN[2]), .D4(IN[3]), .D5(IN[4]), .D6(IN[5]), .D7(IN[6]),
    .D8(IN[7]), .CLK(WR_R3), .nMR(1'b1));  // open: Probe
  IC_74x273 R3_2 (
    .Q1(R3_q1[8]), .Q2(R3_q1[9]), .Q3(R3_q1[10]), .Q4(R3_q1[11]), .Q5(R3_q1[12]), .Q6(R3_q1[13]),
    .Q7(R3_q1[14]), .Q8(R3_q1[15]), .D1(IN[8]), .D2(IN[9]), .D3(IN[10]), .D4(IN[11]), .D5(IN[12]),
    .D6(IN[13]), .D7(IN[14]), .D8(IN[15]), .CLK(WR_R3), .nMR(1'b1));  // open: Probe
  IC_74x541 RD_A (
    .Q1(REG_A[0]), .Q2(REG_A[1]), .Q3(REG_A[2]), .Q4(REG_A[3]), .Q5(REG_A[4]), .Q6(REG_A[5]), .Q7(REG_A[6]),
    .Q8(REG_A[7]), .I1(R0_q1[0]), .I2(R0_q1[1]), .I3(R0_q1[2]), .I4(R0_q1[3]), .I5(R0_q1[4]), .I6(R0_q1[5]),
    .I7(R0_q1[6]), .I8(R0_q1[7]), .nOE1(nRD_TO_A), .nOE2(sR0_1A_n));
  IC_74x541 RD_A_2 (
    .Q1(REG_A[8]), .Q2(REG_A[9]), .Q3(REG_A[10]), .Q4(REG_A[11]), .Q5(REG_A[12]), .Q6(REG_A[13]),
    .Q7(REG_A[14]), .Q8(REG_A[15]), .I1(R0_q1[8]), .I2(R0_q1[9]), .I3(R0_q1[10]), .I4(R0_q1[11]),
    .I5(R0_q1[12]), .I6(R0_q1[13]), .I7(R0_q1[14]), .I8(R0_q1[15]), .nOE1(nRD_TO_A), .nOE2(sR0_1A_n));
  IC_74x541 RD_A_3 (
    .Q1(REG_A[0]), .Q2(REG_A[1]), .Q3(REG_A[2]), .Q4(REG_A[3]), .Q5(REG_A[4]), .Q6(REG_A[5]), .Q7(REG_A[6]),
    .Q8(REG_A[7]), .I1(R1_q1[0]), .I2(R1_q1[1]), .I3(R1_q1[2]), .I4(R1_q1[3]), .I5(R1_q1[4]), .I6(R1_q1[5]),
    .I7(R1_q1[6]), .I8(R1_q1[7]), .nOE1(nRD_TO_A), .nOE2(sR1_1A_n));
  IC_74x541 RD_A_4 (
    .Q1(REG_A[8]), .Q2(REG_A[9]), .Q3(REG_A[10]), .Q4(REG_A[11]), .Q5(REG_A[12]), .Q6(REG_A[13]),
    .Q7(REG_A[14]), .Q8(REG_A[15]), .I1(R1_q1[8]), .I2(R1_q1[9]), .I3(R1_q1[10]), .I4(R1_q1[11]),
    .I5(R1_q1[12]), .I6(R1_q1[13]), .I7(R1_q1[14]), .I8(R1_q1[15]), .nOE1(nRD_TO_A), .nOE2(sR1_1A_n));
  IC_74x541 RD_A_5 (
    .Q1(REG_A[0]), .Q2(REG_A[1]), .Q3(REG_A[2]), .Q4(REG_A[3]), .Q5(REG_A[4]), .Q6(REG_A[5]), .Q7(REG_A[6]),
    .Q8(REG_A[7]), .I1(R2_q1[0]), .I2(R2_q1[1]), .I3(R2_q1[2]), .I4(R2_q1[3]), .I5(R2_q1[4]), .I6(R2_q1[5]),
    .I7(R2_q1[6]), .I8(R2_q1[7]), .nOE1(nRD_TO_A), .nOE2(sR2_1A_n));
  IC_74x541 RD_A_6 (
    .Q1(REG_A[8]), .Q2(REG_A[9]), .Q3(REG_A[10]), .Q4(REG_A[11]), .Q5(REG_A[12]), .Q6(REG_A[13]),
    .Q7(REG_A[14]), .Q8(REG_A[15]), .I1(R2_q1[8]), .I2(R2_q1[9]), .I3(R2_q1[10]), .I4(R2_q1[11]),
    .I5(R2_q1[12]), .I6(R2_q1[13]), .I7(R2_q1[14]), .I8(R2_q1[15]), .nOE1(nRD_TO_A), .nOE2(sR2_1A_n));
  IC_74x541 RD_A_7 (
    .Q1(REG_A[0]), .Q2(REG_A[1]), .Q3(REG_A[2]), .Q4(REG_A[3]), .Q5(REG_A[4]), .Q6(REG_A[5]), .Q7(REG_A[6]),
    .Q8(REG_A[7]), .I1(R3_q1[0]), .I2(R3_q1[1]), .I3(R3_q1[2]), .I4(R3_q1[3]), .I5(R3_q1[4]), .I6(R3_q1[5]),
    .I7(R3_q1[6]), .I8(R3_q1[7]), .nOE1(nRD_TO_A), .nOE2(sR3_1A_n));
  IC_74x541 RD_A_8 (
    .Q1(REG_A[8]), .Q2(REG_A[9]), .Q3(REG_A[10]), .Q4(REG_A[11]), .Q5(REG_A[12]), .Q6(REG_A[13]),
    .Q7(REG_A[14]), .Q8(REG_A[15]), .I1(R3_q1[8]), .I2(R3_q1[9]), .I3(R3_q1[10]), .I4(R3_q1[11]),
    .I5(R3_q1[12]), .I6(R3_q1[13]), .I7(R3_q1[14]), .I8(R3_q1[15]), .nOE1(nRD_TO_A), .nOE2(sR3_1A_n));
  IC_74x138 RWriteEn (
    .Y0(RWriteEn_y0), .Y1(RWriteEn_y1), .Y2(RWriteEn_y2), .Y3(RWriteEn_y3), .Y4(RWriteEn_y4),
    .Y5(RWriteEn_y5), .Y6(RWriteEn_y6), .Y7(RWriteEn_y7), .A(RD[0]), .B(RD[1]), .C(RD[2]), .nG2A(nWR_RD),
    .nG2B(1'b0), .G1(1'b1));
  IC_74x138 RDSelA (
    .Y0(sR0_1A_n), .Y1(sR1_1A_n), .Y2(sR2_1A_n), .Y3(sR3_1A_n), .Y4(sR4_1A_n), .Y5(sR5_1A_n), .Y6(sR6_1A_n),
    .Y7(sR7_1A_n), .A(RD[0]), .B(RD[1]), .C(RD[2]), .nG2A(1'b0), .nG2B(1'b0), .G1(1'b1));
  IC_74x138 RSSelA (
    .Y0(sR0_2A_n), .Y1(sR1_2A_n), .Y2(sR2_2A_n), .Y3(sR3_2A_n), .Y4(sR4_2A_n), .Y5(sR5_2A_n), .Y6(sR6_2A_n),
    .Y7(sR7_2A_n), .A(RS[0]), .B(RS[1]), .C(RS[2]), .nG2A(1'b0), .nG2B(1'b0), .G1(1'b1));
  IC_74x138 RNEnB (
    .Y0(sR0_B_n), .Y1(sR1_B_n), .Y2(sR2_B_n), .Y3(sR3_B_n), .Y4(sR4_B_n), .Y5(sR5_B_n), .Y6(sR6_B_n),
    .Y7(sR7_B_n), .A(RN[0]), .B(RN[1]), .C(RN[2]), .nG2A(1'b0), .nG2B(1'b0), .G1(1'b1));
  IC_74x541 RS_A (
    .Q1(REG_A[0]), .Q2(REG_A[1]), .Q3(REG_A[2]), .Q4(REG_A[3]), .Q5(REG_A[4]), .Q6(REG_A[5]), .Q7(REG_A[6]),
    .Q8(REG_A[7]), .I1(R0_q1[0]), .I2(R0_q1[1]), .I3(R0_q1[2]), .I4(R0_q1[3]), .I5(R0_q1[4]), .I6(R0_q1[5]),
    .I7(R0_q1[6]), .I8(R0_q1[7]), .nOE1(nRS_TO_A), .nOE2(sR0_2A_n));
  IC_74x541 RS_A_2 (
    .Q1(REG_A[8]), .Q2(REG_A[9]), .Q3(REG_A[10]), .Q4(REG_A[11]), .Q5(REG_A[12]), .Q6(REG_A[13]),
    .Q7(REG_A[14]), .Q8(REG_A[15]), .I1(R0_q1[8]), .I2(R0_q1[9]), .I3(R0_q1[10]), .I4(R0_q1[11]),
    .I5(R0_q1[12]), .I6(R0_q1[13]), .I7(R0_q1[14]), .I8(R0_q1[15]), .nOE1(nRS_TO_A), .nOE2(sR0_2A_n));
  IC_74x541 RS_A_3 (
    .Q1(REG_A[0]), .Q2(REG_A[1]), .Q3(REG_A[2]), .Q4(REG_A[3]), .Q5(REG_A[4]), .Q6(REG_A[5]), .Q7(REG_A[6]),
    .Q8(REG_A[7]), .I1(R1_q1[0]), .I2(R1_q1[1]), .I3(R1_q1[2]), .I4(R1_q1[3]), .I5(R1_q1[4]), .I6(R1_q1[5]),
    .I7(R1_q1[6]), .I8(R1_q1[7]), .nOE1(nRS_TO_A), .nOE2(sR1_2A_n));
  IC_74x541 RS_A_4 (
    .Q1(REG_A[8]), .Q2(REG_A[9]), .Q3(REG_A[10]), .Q4(REG_A[11]), .Q5(REG_A[12]), .Q6(REG_A[13]),
    .Q7(REG_A[14]), .Q8(REG_A[15]), .I1(R1_q1[8]), .I2(R1_q1[9]), .I3(R1_q1[10]), .I4(R1_q1[11]),
    .I5(R1_q1[12]), .I6(R1_q1[13]), .I7(R1_q1[14]), .I8(R1_q1[15]), .nOE1(nRS_TO_A), .nOE2(sR1_2A_n));
  IC_74x541 RS_A_5 (
    .Q1(REG_A[0]), .Q2(REG_A[1]), .Q3(REG_A[2]), .Q4(REG_A[3]), .Q5(REG_A[4]), .Q6(REG_A[5]), .Q7(REG_A[6]),
    .Q8(REG_A[7]), .I1(R2_q1[0]), .I2(R2_q1[1]), .I3(R2_q1[2]), .I4(R2_q1[3]), .I5(R2_q1[4]), .I6(R2_q1[5]),
    .I7(R2_q1[6]), .I8(R2_q1[7]), .nOE1(nRS_TO_A), .nOE2(sR2_2A_n));
  IC_74x541 RS_A_6 (
    .Q1(REG_A[8]), .Q2(REG_A[9]), .Q3(REG_A[10]), .Q4(REG_A[11]), .Q5(REG_A[12]), .Q6(REG_A[13]),
    .Q7(REG_A[14]), .Q8(REG_A[15]), .I1(R2_q1[8]), .I2(R2_q1[9]), .I3(R2_q1[10]), .I4(R2_q1[11]),
    .I5(R2_q1[12]), .I6(R2_q1[13]), .I7(R2_q1[14]), .I8(R2_q1[15]), .nOE1(nRS_TO_A), .nOE2(sR2_2A_n));
  IC_74x541 RS_A_7 (
    .Q1(REG_A[0]), .Q2(REG_A[1]), .Q3(REG_A[2]), .Q4(REG_A[3]), .Q5(REG_A[4]), .Q6(REG_A[5]), .Q7(REG_A[6]),
    .Q8(REG_A[7]), .I1(R3_q1[0]), .I2(R3_q1[1]), .I3(R3_q1[2]), .I4(R3_q1[3]), .I5(R3_q1[4]), .I6(R3_q1[5]),
    .I7(R3_q1[6]), .I8(R3_q1[7]), .nOE1(nRS_TO_A), .nOE2(sR3_2A_n));
  IC_74x541 RS_A_8 (
    .Q1(REG_A[8]), .Q2(REG_A[9]), .Q3(REG_A[10]), .Q4(REG_A[11]), .Q5(REG_A[12]), .Q6(REG_A[13]),
    .Q7(REG_A[14]), .Q8(REG_A[15]), .I1(R3_q1[8]), .I2(R3_q1[9]), .I3(R3_q1[10]), .I4(R3_q1[11]),
    .I5(R3_q1[12]), .I6(R3_q1[13]), .I7(R3_q1[14]), .I8(R3_q1[15]), .nOE1(nRS_TO_A), .nOE2(sR3_2A_n));
  IC_74x573 ic_74x573_1 (
    .Q2(ic_74x573_1_q2), .Q3(ic_74x573_1_q3), .Q4(ic_74x573_1_q4), .Q5(ic_74x573_1_q5), .Q6(ic_74x573_1_q6),
    .Q7(ic_74x573_1_q7), .Q8(ic_74x573_1_q8), .Q1(ic_74x573_1_q1), .D2(RWriteEn_y1), .D3(RWriteEn_y2),
    .D4(RWriteEn_y3), .D5(RWriteEn_y4), .D6(RWriteEn_y5), .D7(RWriteEn_y6), .D8(RWriteEn_y7), .LE(nCLK),
    .nOE(1'b0), .D1(RWriteEn_y0));  // open: Probe
  nor nor_1 (WR_R0, nCLK, ic_74x573_1_q1);
  nor nor_2 (WR_R1, nCLK, ic_74x573_1_q2);
  nor nor_3 (WR_R2, nCLK, ic_74x573_1_q3);
  nor nor_4 (WR_R3, nCLK, ic_74x573_1_q4);
  nor nor_5 (WR_R4, nCLK, ic_74x573_1_q5);
  nor nor_6 (WR_R5, nCLK, ic_74x573_1_q6);
  nor nor_7 (WR_R6, nCLK, ic_74x573_1_q7);
  nor nor_8 (WR_R7, nCLK, ic_74x573_1_q8);
  IC_74x541 RN_B (
    .Q1(REG_B[0]), .Q2(REG_B[1]), .Q3(REG_B[2]), .Q4(REG_B[3]), .Q5(REG_B[4]), .Q6(REG_B[5]), .Q7(REG_B[6]),
    .Q8(REG_B[7]), .I1(R0_q1[0]), .I2(R0_q1[1]), .I3(R0_q1[2]), .I4(R0_q1[3]), .I5(R0_q1[4]), .I6(R0_q1[5]),
    .I7(R0_q1[6]), .I8(R0_q1[7]), .nOE1(nRN_TO_B), .nOE2(sR0_B_n));
  IC_74x541 RN_B_2 (
    .Q1(REG_B[8]), .Q2(REG_B[9]), .Q3(REG_B[10]), .Q4(REG_B[11]), .Q5(REG_B[12]), .Q6(REG_B[13]),
    .Q7(REG_B[14]), .Q8(REG_B[15]), .I1(R0_q1[8]), .I2(R0_q1[9]), .I3(R0_q1[10]), .I4(R0_q1[11]),
    .I5(R0_q1[12]), .I6(R0_q1[13]), .I7(R0_q1[14]), .I8(R0_q1[15]), .nOE1(nRN_TO_B), .nOE2(sR0_B_n));
  IC_74x541 RN_B_3 (
    .Q1(REG_B[0]), .Q2(REG_B[1]), .Q3(REG_B[2]), .Q4(REG_B[3]), .Q5(REG_B[4]), .Q6(REG_B[5]), .Q7(REG_B[6]),
    .Q8(REG_B[7]), .I1(R1_q1[0]), .I2(R1_q1[1]), .I3(R1_q1[2]), .I4(R1_q1[3]), .I5(R1_q1[4]), .I6(R1_q1[5]),
    .I7(R1_q1[6]), .I8(R1_q1[7]), .nOE1(nRN_TO_B), .nOE2(sR1_B_n));
  IC_74x541 RN_B_4 (
    .Q1(REG_B[8]), .Q2(REG_B[9]), .Q3(REG_B[10]), .Q4(REG_B[11]), .Q5(REG_B[12]), .Q6(REG_B[13]),
    .Q7(REG_B[14]), .Q8(REG_B[15]), .I1(R1_q1[8]), .I2(R1_q1[9]), .I3(R1_q1[10]), .I4(R1_q1[11]),
    .I5(R1_q1[12]), .I6(R1_q1[13]), .I7(R1_q1[14]), .I8(R1_q1[15]), .nOE1(nRN_TO_B), .nOE2(sR1_B_n));
  IC_74x541 RN_B_5 (
    .Q1(REG_B[0]), .Q2(REG_B[1]), .Q3(REG_B[2]), .Q4(REG_B[3]), .Q5(REG_B[4]), .Q6(REG_B[5]), .Q7(REG_B[6]),
    .Q8(REG_B[7]), .I1(R2_q1[0]), .I2(R2_q1[1]), .I3(R2_q1[2]), .I4(R2_q1[3]), .I5(R2_q1[4]), .I6(R2_q1[5]),
    .I7(R2_q1[6]), .I8(R2_q1[7]), .nOE1(nRN_TO_B), .nOE2(sR2_B_n));
  IC_74x541 RN_B_6 (
    .Q1(REG_B[8]), .Q2(REG_B[9]), .Q3(REG_B[10]), .Q4(REG_B[11]), .Q5(REG_B[12]), .Q6(REG_B[13]),
    .Q7(REG_B[14]), .Q8(REG_B[15]), .I1(R2_q1[8]), .I2(R2_q1[9]), .I3(R2_q1[10]), .I4(R2_q1[11]),
    .I5(R2_q1[12]), .I6(R2_q1[13]), .I7(R2_q1[14]), .I8(R2_q1[15]), .nOE1(nRN_TO_B), .nOE2(sR2_B_n));
  IC_74x541 RN_B_7 (
    .Q1(REG_B[0]), .Q2(REG_B[1]), .Q3(REG_B[2]), .Q4(REG_B[3]), .Q5(REG_B[4]), .Q6(REG_B[5]), .Q7(REG_B[6]),
    .Q8(REG_B[7]), .I1(R3_q1[0]), .I2(R3_q1[1]), .I3(R3_q1[2]), .I4(R3_q1[3]), .I5(R3_q1[4]), .I6(R3_q1[5]),
    .I7(R3_q1[6]), .I8(R3_q1[7]), .nOE1(nRN_TO_B), .nOE2(sR3_B_n));
  IC_74x541 RN_B_8 (
    .Q1(REG_B[8]), .Q2(REG_B[9]), .Q3(REG_B[10]), .Q4(REG_B[11]), .Q5(REG_B[12]), .Q6(REG_B[13]),
    .Q7(REG_B[14]), .Q8(REG_B[15]), .I1(R3_q1[8]), .I2(R3_q1[9]), .I3(R3_q1[10]), .I4(R3_q1[11]),
    .I5(R3_q1[12]), .I6(R3_q1[13]), .I7(R3_q1[14]), .I8(R3_q1[15]), .nOE1(nRN_TO_B), .nOE2(sR3_B_n));
  IC_74x273 R4 (
    .Q1(R4_q1[0]), .Q2(R4_q1[1]), .Q3(R4_q1[2]), .Q4(R4_q1[3]), .Q5(R4_q1[4]), .Q6(R4_q1[5]), .Q7(R4_q1[6]),
    .Q8(R4_q1[7]), .D1(IN[0]), .D2(IN[1]), .D3(IN[2]), .D4(IN[3]), .D5(IN[4]), .D6(IN[5]), .D7(IN[6]),
    .D8(IN[7]), .CLK(WR_R4), .nMR(1'b1));  // open: Probe
  IC_74x273 R4_2 (
    .Q1(R4_q1[8]), .Q2(R4_q1[9]), .Q3(R4_q1[10]), .Q4(R4_q1[11]), .Q5(R4_q1[12]), .Q6(R4_q1[13]),
    .Q7(R4_q1[14]), .Q8(R4_q1[15]), .D1(IN[8]), .D2(IN[9]), .D3(IN[10]), .D4(IN[11]), .D5(IN[12]),
    .D6(IN[13]), .D7(IN[14]), .D8(IN[15]), .CLK(WR_R4), .nMR(1'b1));  // open: Probe
  IC_74x273 R5 (
    .Q1(R5_q1[0]), .Q2(R5_q1[1]), .Q3(R5_q1[2]), .Q4(R5_q1[3]), .Q5(R5_q1[4]), .Q6(R5_q1[5]), .Q7(R5_q1[6]),
    .Q8(R5_q1[7]), .D1(IN[0]), .D2(IN[1]), .D3(IN[2]), .D4(IN[3]), .D5(IN[4]), .D6(IN[5]), .D7(IN[6]),
    .D8(IN[7]), .CLK(WR_R5), .nMR(1'b1));  // open: Probe
  IC_74x273 R5_2 (
    .Q1(R5_q1[8]), .Q2(R5_q1[9]), .Q3(R5_q1[10]), .Q4(R5_q1[11]), .Q5(R5_q1[12]), .Q6(R5_q1[13]),
    .Q7(R5_q1[14]), .Q8(R5_q1[15]), .D1(IN[8]), .D2(IN[9]), .D3(IN[10]), .D4(IN[11]), .D5(IN[12]),
    .D6(IN[13]), .D7(IN[14]), .D8(IN[15]), .CLK(WR_R5), .nMR(1'b1));  // open: Probe
  IC_74x273 R6 (
    .Q1(R6_q1[0]), .Q2(R6_q1[1]), .Q3(R6_q1[2]), .Q4(R6_q1[3]), .Q5(R6_q1[4]), .Q6(R6_q1[5]), .Q7(R6_q1[6]),
    .Q8(R6_q1[7]), .D1(IN[0]), .D2(IN[1]), .D3(IN[2]), .D4(IN[3]), .D5(IN[4]), .D6(IN[5]), .D7(IN[6]),
    .D8(IN[7]), .CLK(WR_R6), .nMR(1'b1));  // open: Probe
  IC_74x273 R6_2 (
    .Q1(R6_q1[8]), .Q2(R6_q1[9]), .Q3(R6_q1[10]), .Q4(R6_q1[11]), .Q5(R6_q1[12]), .Q6(R6_q1[13]),
    .Q7(R6_q1[14]), .Q8(R6_q1[15]), .D1(IN[8]), .D2(IN[9]), .D3(IN[10]), .D4(IN[11]), .D5(IN[12]),
    .D6(IN[13]), .D7(IN[14]), .D8(IN[15]), .CLK(WR_R6), .nMR(1'b1));  // open: Probe
  IC_74x273 R7 (
    .Q1(R7_q1[0]), .Q2(R7_q1[1]), .Q3(R7_q1[2]), .Q4(R7_q1[3]), .Q5(R7_q1[4]), .Q6(R7_q1[5]), .Q7(R7_q1[6]),
    .Q8(R7_q1[7]), .D1(IN[0]), .D2(IN[1]), .D3(IN[2]), .D4(IN[3]), .D5(IN[4]), .D6(IN[5]), .D7(IN[6]),
    .D8(IN[7]), .CLK(WR_R7), .nMR(1'b1));  // open: Probe
  IC_74x273 R7_2 (
    .Q1(R7_q1[8]), .Q2(R7_q1[9]), .Q3(R7_q1[10]), .Q4(R7_q1[11]), .Q5(R7_q1[12]), .Q6(R7_q1[13]),
    .Q7(R7_q1[14]), .Q8(R7_q1[15]), .D1(IN[8]), .D2(IN[9]), .D3(IN[10]), .D4(IN[11]), .D5(IN[12]),
    .D6(IN[13]), .D7(IN[14]), .D8(IN[15]), .CLK(WR_R7), .nMR(1'b1));  // open: Probe
  IC_74x541 RD_A_9 (
    .Q1(REG_A[0]), .Q2(REG_A[1]), .Q3(REG_A[2]), .Q4(REG_A[3]), .Q5(REG_A[4]), .Q6(REG_A[5]), .Q7(REG_A[6]),
    .Q8(REG_A[7]), .I1(R4_q1[0]), .I2(R4_q1[1]), .I3(R4_q1[2]), .I4(R4_q1[3]), .I5(R4_q1[4]), .I6(R4_q1[5]),
    .I7(R4_q1[6]), .I8(R4_q1[7]), .nOE1(nRD_TO_A), .nOE2(sR4_1A_n));
  IC_74x541 RD_A_10 (
    .Q1(REG_A[8]), .Q2(REG_A[9]), .Q3(REG_A[10]), .Q4(REG_A[11]), .Q5(REG_A[12]), .Q6(REG_A[13]),
    .Q7(REG_A[14]), .Q8(REG_A[15]), .I1(R4_q1[8]), .I2(R4_q1[9]), .I3(R4_q1[10]), .I4(R4_q1[11]),
    .I5(R4_q1[12]), .I6(R4_q1[13]), .I7(R4_q1[14]), .I8(R4_q1[15]), .nOE1(nRD_TO_A), .nOE2(sR4_1A_n));
  IC_74x541 RD_A_11 (
    .Q1(REG_A[0]), .Q2(REG_A[1]), .Q3(REG_A[2]), .Q4(REG_A[3]), .Q5(REG_A[4]), .Q6(REG_A[5]), .Q7(REG_A[6]),
    .Q8(REG_A[7]), .I1(R5_q1[0]), .I2(R5_q1[1]), .I3(R5_q1[2]), .I4(R5_q1[3]), .I5(R5_q1[4]), .I6(R5_q1[5]),
    .I7(R5_q1[6]), .I8(R5_q1[7]), .nOE1(nRD_TO_A), .nOE2(sR5_1A_n));
  IC_74x541 RD_A_12 (
    .Q1(REG_A[8]), .Q2(REG_A[9]), .Q3(REG_A[10]), .Q4(REG_A[11]), .Q5(REG_A[12]), .Q6(REG_A[13]),
    .Q7(REG_A[14]), .Q8(REG_A[15]), .I1(R5_q1[8]), .I2(R5_q1[9]), .I3(R5_q1[10]), .I4(R5_q1[11]),
    .I5(R5_q1[12]), .I6(R5_q1[13]), .I7(R5_q1[14]), .I8(R5_q1[15]), .nOE1(nRD_TO_A), .nOE2(sR5_1A_n));
  IC_74x541 RD_A_13 (
    .Q1(REG_A[0]), .Q2(REG_A[1]), .Q3(REG_A[2]), .Q4(REG_A[3]), .Q5(REG_A[4]), .Q6(REG_A[5]), .Q7(REG_A[6]),
    .Q8(REG_A[7]), .I1(R6_q1[0]), .I2(R6_q1[1]), .I3(R6_q1[2]), .I4(R6_q1[3]), .I5(R6_q1[4]), .I6(R6_q1[5]),
    .I7(R6_q1[6]), .I8(R6_q1[7]), .nOE1(nRD_TO_A), .nOE2(sR6_1A_n));
  IC_74x541 RD_A_14 (
    .Q1(REG_A[8]), .Q2(REG_A[9]), .Q3(REG_A[10]), .Q4(REG_A[11]), .Q5(REG_A[12]), .Q6(REG_A[13]),
    .Q7(REG_A[14]), .Q8(REG_A[15]), .I1(R6_q1[8]), .I2(R6_q1[9]), .I3(R6_q1[10]), .I4(R6_q1[11]),
    .I5(R6_q1[12]), .I6(R6_q1[13]), .I7(R6_q1[14]), .I8(R6_q1[15]), .nOE1(nRD_TO_A), .nOE2(sR6_1A_n));
  IC_74x541 RD_A_15 (
    .Q1(REG_A[0]), .Q2(REG_A[1]), .Q3(REG_A[2]), .Q4(REG_A[3]), .Q5(REG_A[4]), .Q6(REG_A[5]), .Q7(REG_A[6]),
    .Q8(REG_A[7]), .I1(R7_q1[0]), .I2(R7_q1[1]), .I3(R7_q1[2]), .I4(R7_q1[3]), .I5(R7_q1[4]), .I6(R7_q1[5]),
    .I7(R7_q1[6]), .I8(R7_q1[7]), .nOE1(nRD_TO_A), .nOE2(sR7_1A_n));
  IC_74x541 RD_A_16 (
    .Q1(REG_A[8]), .Q2(REG_A[9]), .Q3(REG_A[10]), .Q4(REG_A[11]), .Q5(REG_A[12]), .Q6(REG_A[13]),
    .Q7(REG_A[14]), .Q8(REG_A[15]), .I1(R7_q1[8]), .I2(R7_q1[9]), .I3(R7_q1[10]), .I4(R7_q1[11]),
    .I5(R7_q1[12]), .I6(R7_q1[13]), .I7(R7_q1[14]), .I8(R7_q1[15]), .nOE1(nRD_TO_A), .nOE2(sR7_1A_n));
  IC_74x541 RS_A_9 (
    .Q1(REG_A[0]), .Q2(REG_A[1]), .Q3(REG_A[2]), .Q4(REG_A[3]), .Q5(REG_A[4]), .Q6(REG_A[5]), .Q7(REG_A[6]),
    .Q8(REG_A[7]), .I1(R4_q1[0]), .I2(R4_q1[1]), .I3(R4_q1[2]), .I4(R4_q1[3]), .I5(R4_q1[4]), .I6(R4_q1[5]),
    .I7(R4_q1[6]), .I8(R4_q1[7]), .nOE1(nRS_TO_A), .nOE2(sR4_2A_n));
  IC_74x541 RS_A_10 (
    .Q1(REG_A[8]), .Q2(REG_A[9]), .Q3(REG_A[10]), .Q4(REG_A[11]), .Q5(REG_A[12]), .Q6(REG_A[13]),
    .Q7(REG_A[14]), .Q8(REG_A[15]), .I1(R4_q1[8]), .I2(R4_q1[9]), .I3(R4_q1[10]), .I4(R4_q1[11]),
    .I5(R4_q1[12]), .I6(R4_q1[13]), .I7(R4_q1[14]), .I8(R4_q1[15]), .nOE1(nRS_TO_A), .nOE2(sR4_2A_n));
  IC_74x541 RS_A_11 (
    .Q1(REG_A[0]), .Q2(REG_A[1]), .Q3(REG_A[2]), .Q4(REG_A[3]), .Q5(REG_A[4]), .Q6(REG_A[5]), .Q7(REG_A[6]),
    .Q8(REG_A[7]), .I1(R5_q1[0]), .I2(R5_q1[1]), .I3(R5_q1[2]), .I4(R5_q1[3]), .I5(R5_q1[4]), .I6(R5_q1[5]),
    .I7(R5_q1[6]), .I8(R5_q1[7]), .nOE1(nRS_TO_A), .nOE2(sR5_2A_n));
  IC_74x541 RS_A_12 (
    .Q1(REG_A[8]), .Q2(REG_A[9]), .Q3(REG_A[10]), .Q4(REG_A[11]), .Q5(REG_A[12]), .Q6(REG_A[13]),
    .Q7(REG_A[14]), .Q8(REG_A[15]), .I1(R5_q1[8]), .I2(R5_q1[9]), .I3(R5_q1[10]), .I4(R5_q1[11]),
    .I5(R5_q1[12]), .I6(R5_q1[13]), .I7(R5_q1[14]), .I8(R5_q1[15]), .nOE1(nRS_TO_A), .nOE2(sR5_2A_n));
  IC_74x541 RS_A_13 (
    .Q1(REG_A[0]), .Q2(REG_A[1]), .Q3(REG_A[2]), .Q4(REG_A[3]), .Q5(REG_A[4]), .Q6(REG_A[5]), .Q7(REG_A[6]),
    .Q8(REG_A[7]), .I1(R6_q1[0]), .I2(R6_q1[1]), .I3(R6_q1[2]), .I4(R6_q1[3]), .I5(R6_q1[4]), .I6(R6_q1[5]),
    .I7(R6_q1[6]), .I8(R6_q1[7]), .nOE1(nRS_TO_A), .nOE2(sR6_2A_n));
  IC_74x541 RS_A_14 (
    .Q1(REG_A[8]), .Q2(REG_A[9]), .Q3(REG_A[10]), .Q4(REG_A[11]), .Q5(REG_A[12]), .Q6(REG_A[13]),
    .Q7(REG_A[14]), .Q8(REG_A[15]), .I1(R6_q1[8]), .I2(R6_q1[9]), .I3(R6_q1[10]), .I4(R6_q1[11]),
    .I5(R6_q1[12]), .I6(R6_q1[13]), .I7(R6_q1[14]), .I8(R6_q1[15]), .nOE1(nRS_TO_A), .nOE2(sR6_2A_n));
  IC_74x541 RS_A_15 (
    .Q1(REG_A[0]), .Q2(REG_A[1]), .Q3(REG_A[2]), .Q4(REG_A[3]), .Q5(REG_A[4]), .Q6(REG_A[5]), .Q7(REG_A[6]),
    .Q8(REG_A[7]), .I1(R7_q1[0]), .I2(R7_q1[1]), .I3(R7_q1[2]), .I4(R7_q1[3]), .I5(R7_q1[4]), .I6(R7_q1[5]),
    .I7(R7_q1[6]), .I8(R7_q1[7]), .nOE1(nRS_TO_A), .nOE2(sR7_2A_n));
  IC_74x541 RS_A_16 (
    .Q1(REG_A[8]), .Q2(REG_A[9]), .Q3(REG_A[10]), .Q4(REG_A[11]), .Q5(REG_A[12]), .Q6(REG_A[13]),
    .Q7(REG_A[14]), .Q8(REG_A[15]), .I1(R7_q1[8]), .I2(R7_q1[9]), .I3(R7_q1[10]), .I4(R7_q1[11]),
    .I5(R7_q1[12]), .I6(R7_q1[13]), .I7(R7_q1[14]), .I8(R7_q1[15]), .nOE1(nRS_TO_A), .nOE2(sR7_2A_n));
  IC_74x541 RN_B_9 (
    .Q1(REG_B[0]), .Q2(REG_B[1]), .Q3(REG_B[2]), .Q4(REG_B[3]), .Q5(REG_B[4]), .Q6(REG_B[5]), .Q7(REG_B[6]),
    .Q8(REG_B[7]), .I1(R4_q1[0]), .I2(R4_q1[1]), .I3(R4_q1[2]), .I4(R4_q1[3]), .I5(R4_q1[4]), .I6(R4_q1[5]),
    .I7(R4_q1[6]), .I8(R4_q1[7]), .nOE1(nRN_TO_B), .nOE2(sR4_B_n));
  IC_74x541 RN_B_10 (
    .Q1(REG_B[8]), .Q2(REG_B[9]), .Q3(REG_B[10]), .Q4(REG_B[11]), .Q5(REG_B[12]), .Q6(REG_B[13]),
    .Q7(REG_B[14]), .Q8(REG_B[15]), .I1(R4_q1[8]), .I2(R4_q1[9]), .I3(R4_q1[10]), .I4(R4_q1[11]),
    .I5(R4_q1[12]), .I6(R4_q1[13]), .I7(R4_q1[14]), .I8(R4_q1[15]), .nOE1(nRN_TO_B), .nOE2(sR4_B_n));
  IC_74x541 RN_B_11 (
    .Q1(REG_B[0]), .Q2(REG_B[1]), .Q3(REG_B[2]), .Q4(REG_B[3]), .Q5(REG_B[4]), .Q6(REG_B[5]), .Q7(REG_B[6]),
    .Q8(REG_B[7]), .I1(R5_q1[0]), .I2(R5_q1[1]), .I3(R5_q1[2]), .I4(R5_q1[3]), .I5(R5_q1[4]), .I6(R5_q1[5]),
    .I7(R5_q1[6]), .I8(R5_q1[7]), .nOE1(nRN_TO_B), .nOE2(sR5_B_n));
  IC_74x541 RN_B_12 (
    .Q1(REG_B[8]), .Q2(REG_B[9]), .Q3(REG_B[10]), .Q4(REG_B[11]), .Q5(REG_B[12]), .Q6(REG_B[13]),
    .Q7(REG_B[14]), .Q8(REG_B[15]), .I1(R5_q1[8]), .I2(R5_q1[9]), .I3(R5_q1[10]), .I4(R5_q1[11]),
    .I5(R5_q1[12]), .I6(R5_q1[13]), .I7(R5_q1[14]), .I8(R5_q1[15]), .nOE1(nRN_TO_B), .nOE2(sR5_B_n));
  IC_74x541 RN_B_13 (
    .Q1(REG_B[0]), .Q2(REG_B[1]), .Q3(REG_B[2]), .Q4(REG_B[3]), .Q5(REG_B[4]), .Q6(REG_B[5]), .Q7(REG_B[6]),
    .Q8(REG_B[7]), .I1(R6_q1[0]), .I2(R6_q1[1]), .I3(R6_q1[2]), .I4(R6_q1[3]), .I5(R6_q1[4]), .I6(R6_q1[5]),
    .I7(R6_q1[6]), .I8(R6_q1[7]), .nOE1(nRN_TO_B), .nOE2(sR6_B_n));
  IC_74x541 RN_B_14 (
    .Q1(REG_B[8]), .Q2(REG_B[9]), .Q3(REG_B[10]), .Q4(REG_B[11]), .Q5(REG_B[12]), .Q6(REG_B[13]),
    .Q7(REG_B[14]), .Q8(REG_B[15]), .I1(R6_q1[8]), .I2(R6_q1[9]), .I3(R6_q1[10]), .I4(R6_q1[11]),
    .I5(R6_q1[12]), .I6(R6_q1[13]), .I7(R6_q1[14]), .I8(R6_q1[15]), .nOE1(nRN_TO_B), .nOE2(sR6_B_n));
  IC_74x541 RN_B_15 (
    .Q1(REG_B[0]), .Q2(REG_B[1]), .Q3(REG_B[2]), .Q4(REG_B[3]), .Q5(REG_B[4]), .Q6(REG_B[5]), .Q7(REG_B[6]),
    .Q8(REG_B[7]), .I1(R7_q1[0]), .I2(R7_q1[1]), .I3(R7_q1[2]), .I4(R7_q1[3]), .I5(R7_q1[4]), .I6(R7_q1[5]),
    .I7(R7_q1[6]), .I8(R7_q1[7]), .nOE1(nRN_TO_B), .nOE2(sR7_B_n));
  IC_74x541 RN_B_16 (
    .Q1(REG_B[8]), .Q2(REG_B[9]), .Q3(REG_B[10]), .Q4(REG_B[11]), .Q5(REG_B[12]), .Q6(REG_B[13]),
    .Q7(REG_B[14]), .Q8(REG_B[15]), .I1(R7_q1[8]), .I2(R7_q1[9]), .I3(R7_q1[10]), .I4(R7_q1[11]),
    .I5(R7_q1[12]), .I6(R7_q1[13]), .I7(R7_q1[14]), .I8(R7_q1[15]), .nOE1(nRN_TO_B), .nOE2(sR7_B_n));

  // Other names for the same wires on the sheet: RD_A_n = nRD_TO_A; RN_B_n = nRN_TO_B; RS_A_n = nRS_TO_A
endmodule

// Register File
module RegistersC3157 (
  input  nCLK,
  input  nWR_RD,
  input  nRD_TO_A,
  input  nRS_TO_A,
  input  nRN_TO_B,
  input  [15:0] IN,
  input  [2:0] RD,
  input  [2:0] RS,
  input  [2:0] RN,
  output [15:0] REG_A,
  output [15:0] REG_B
);

  wire ic_74x1g3157_1_a, ic_74x1g3157_2_a, ic_74x1g3157_3_a, ic_74x1g3157_4_a, ic_74x1g3157_5_a,
       ic_74x1g3157_6_a, ic_74x1g3157_7_a, ic_74x1g3157_8_a, ic_74x1g3157_9_a, ic_74x1g3157_10_a,
       ic_74x1g3157_11_a, ic_74x1g3157_12_a, ic_74x1g3157_13_a, ic_74x1g3157_14_a, ic_74x1g3157_15_a,
       ic_74x1g3157_16_a, ic_74x1g3157_17_a, ic_74x1g3157_18_a, ic_74x1g3157_19_a, ic_74x1g3157_20_a,
       ic_74x1g3157_21_a, ic_74x1g3157_22_a, ic_74x1g3157_23_a, ic_74x1g3157_24_a, ic_74x573_1_q1,
       ic_74x573_1_q2, ic_74x573_1_q3, ic_74x573_1_q4, ic_74x573_1_q5, ic_74x573_1_q6, ic_74x573_1_q7,
       ic_74x573_1_q8, RWriteEn_y0, RWriteEn_y1, RWriteEn_y2, RWriteEn_y3, RWriteEn_y4, RWriteEn_y5,
       RWriteEn_y6, RWriteEn_y7, sR0_1A_n, sR0_2A_n, sR0_B_n, sR1_1A_n, sR1_2A_n, sR1_B_n, sR2_1A_n,
       sR2_2A_n, sR2_B_n, sR3_1A_n, sR3_2A_n, sR3_B_n, sR4_1A_n, sR4_2A_n, sR4_B_n, sR5_1A_n, sR5_2A_n,
       sR5_B_n, sR6_1A_n, sR6_2A_n, sR6_B_n, sR7_1A_n, sR7_2A_n, sR7_B_n, WR_R0, WR_R1, WR_R2, WR_R3, WR_R4,
       WR_R5, WR_R6, WR_R7;

  IC_74x1G3157 ic_74x1g3157_1 (.A(ic_74x1g3157_1_a), .B1(nRD_TO_A), .B2(1'b1), .S(sR0_1A_n));
  IC_74x1G3157 ic_74x1g3157_2 (.A(ic_74x1g3157_2_a), .B1(nRD_TO_A), .B2(1'b1), .S(sR1_1A_n));
  IC_74x1G3157 ic_74x1g3157_3 (.A(ic_74x1g3157_3_a), .B1(nRD_TO_A), .B2(1'b1), .S(sR2_1A_n));
  IC_74x1G3157 ic_74x1g3157_4 (.A(ic_74x1g3157_4_a), .B1(nRD_TO_A), .B2(1'b1), .S(sR3_1A_n));
  logi7400ic_IC_74x574 R0_A (
    .Q2(REG_A[1]), .Q3(REG_A[2]), .Q4(REG_A[3]), .Q5(REG_A[4]), .Q6(REG_A[5]), .Q7(REG_A[6]), .Q8(REG_A[7]),
    .Q1(REG_A[0]), .D2(IN[1]), .D3(IN[2]), .D4(IN[3]), .D5(IN[4]), .D6(IN[5]), .D7(IN[6]), .D8(IN[7]),
    .CLK(WR_R0), .nOE(ic_74x1g3157_1_a), .D1(IN[0]));  // open: Probe
  logi7400ic_IC_74x574 R0_A_2 (
    .Q2(REG_A[9]), .Q3(REG_A[10]), .Q4(REG_A[11]), .Q5(REG_A[12]), .Q6(REG_A[13]), .Q7(REG_A[14]),
    .Q8(REG_A[15]), .Q1(REG_A[8]), .D2(IN[9]), .D3(IN[10]), .D4(IN[11]), .D5(IN[12]), .D6(IN[13]),
    .D7(IN[14]), .D8(IN[15]), .CLK(WR_R0), .nOE(ic_74x1g3157_1_a), .D1(IN[8]));  // open: Probe
  logi7400ic_IC_74x574 R1_A (
    .Q2(REG_A[1]), .Q3(REG_A[2]), .Q4(REG_A[3]), .Q5(REG_A[4]), .Q6(REG_A[5]), .Q7(REG_A[6]), .Q8(REG_A[7]),
    .Q1(REG_A[0]), .D2(IN[1]), .D3(IN[2]), .D4(IN[3]), .D5(IN[4]), .D6(IN[5]), .D7(IN[6]), .D8(IN[7]),
    .CLK(WR_R1), .nOE(ic_74x1g3157_2_a), .D1(IN[0]));  // open: Probe
  logi7400ic_IC_74x574 R1_A_2 (
    .Q2(REG_A[9]), .Q3(REG_A[10]), .Q4(REG_A[11]), .Q5(REG_A[12]), .Q6(REG_A[13]), .Q7(REG_A[14]),
    .Q8(REG_A[15]), .Q1(REG_A[8]), .D2(IN[9]), .D3(IN[10]), .D4(IN[11]), .D5(IN[12]), .D6(IN[13]),
    .D7(IN[14]), .D8(IN[15]), .CLK(WR_R1), .nOE(ic_74x1g3157_2_a), .D1(IN[8]));  // open: Probe
  logi7400ic_IC_74x574 R2_A (
    .Q2(REG_A[1]), .Q3(REG_A[2]), .Q4(REG_A[3]), .Q5(REG_A[4]), .Q6(REG_A[5]), .Q7(REG_A[6]), .Q8(REG_A[7]),
    .Q1(REG_A[0]), .D2(IN[1]), .D3(IN[2]), .D4(IN[3]), .D5(IN[4]), .D6(IN[5]), .D7(IN[6]), .D8(IN[7]),
    .CLK(WR_R2), .nOE(ic_74x1g3157_3_a), .D1(IN[0]));  // open: Probe
  logi7400ic_IC_74x574 R2_A_2 (
    .Q2(REG_A[9]), .Q3(REG_A[10]), .Q4(REG_A[11]), .Q5(REG_A[12]), .Q6(REG_A[13]), .Q7(REG_A[14]),
    .Q8(REG_A[15]), .Q1(REG_A[8]), .D2(IN[9]), .D3(IN[10]), .D4(IN[11]), .D5(IN[12]), .D6(IN[13]),
    .D7(IN[14]), .D8(IN[15]), .CLK(WR_R2), .nOE(ic_74x1g3157_3_a), .D1(IN[8]));  // open: Probe
  logi7400ic_IC_74x574 R3_A (
    .Q2(REG_A[1]), .Q3(REG_A[2]), .Q4(REG_A[3]), .Q5(REG_A[4]), .Q6(REG_A[5]), .Q7(REG_A[6]), .Q8(REG_A[7]),
    .Q1(REG_A[0]), .D2(IN[1]), .D3(IN[2]), .D4(IN[3]), .D5(IN[4]), .D6(IN[5]), .D7(IN[6]), .D8(IN[7]),
    .CLK(WR_R3), .nOE(ic_74x1g3157_4_a), .D1(IN[0]));  // open: Probe
  logi7400ic_IC_74x574 R3_A_2 (
    .Q2(REG_A[9]), .Q3(REG_A[10]), .Q4(REG_A[11]), .Q5(REG_A[12]), .Q6(REG_A[13]), .Q7(REG_A[14]),
    .Q8(REG_A[15]), .Q1(REG_A[8]), .D2(IN[9]), .D3(IN[10]), .D4(IN[11]), .D5(IN[12]), .D6(IN[13]),
    .D7(IN[14]), .D8(IN[15]), .CLK(WR_R3), .nOE(ic_74x1g3157_4_a), .D1(IN[8]));  // open: Probe
  IC_74x138 RWriteEn (
    .Y0(RWriteEn_y0), .Y1(RWriteEn_y1), .Y2(RWriteEn_y2), .Y3(RWriteEn_y3), .Y4(RWriteEn_y4),
    .Y5(RWriteEn_y5), .Y6(RWriteEn_y6), .Y7(RWriteEn_y7), .A(RD[0]), .B(RD[1]), .C(RD[2]), .nG2A(nWR_RD),
    .nG2B(1'b0), .G1(1'b1));
  IC_74x138 RDSelA (
    .Y0(sR0_1A_n), .Y1(sR1_1A_n), .Y2(sR2_1A_n), .Y3(sR3_1A_n), .Y4(sR4_1A_n), .Y5(sR5_1A_n), .Y6(sR6_1A_n),
    .Y7(sR7_1A_n), .A(RD[0]), .B(RD[1]), .C(RD[2]), .nG2A(1'b0), .nG2B(1'b0), .G1(1'b1));
  IC_74x138 RSSelA (
    .Y0(sR0_2A_n), .Y1(sR1_2A_n), .Y2(sR2_2A_n), .Y3(sR3_2A_n), .Y4(sR4_2A_n), .Y5(sR5_2A_n), .Y6(sR6_2A_n),
    .Y7(sR7_2A_n), .A(RS[0]), .B(RS[1]), .C(RS[2]), .nG2A(1'b0), .nG2B(1'b0), .G1(1'b1));
  IC_74x138 RNEnB (
    .Y0(sR0_B_n), .Y1(sR1_B_n), .Y2(sR2_B_n), .Y3(sR3_B_n), .Y4(sR4_B_n), .Y5(sR5_B_n), .Y6(sR6_B_n),
    .Y7(sR7_B_n), .A(RN[0]), .B(RN[1]), .C(RN[2]), .nG2A(1'b0), .nG2B(1'b0), .G1(1'b1));
  IC_74x1G3157 ic_74x1g3157_5 (.A(ic_74x1g3157_5_a), .B1(nRS_TO_A), .B2(1'b1), .S(sR0_2A_n));
  IC_74x1G3157 ic_74x1g3157_6 (.A(ic_74x1g3157_6_a), .B1(nRS_TO_A), .B2(1'b1), .S(sR1_2A_n));
  IC_74x1G3157 ic_74x1g3157_7 (.A(ic_74x1g3157_7_a), .B1(nRS_TO_A), .B2(1'b1), .S(sR2_2A_n));
  IC_74x1G3157 ic_74x1g3157_8 (.A(ic_74x1g3157_8_a), .B1(nRS_TO_A), .B2(1'b1), .S(sR3_2A_n));
  IC_74x573 ic_74x573_1 (
    .Q2(ic_74x573_1_q2), .Q3(ic_74x573_1_q3), .Q4(ic_74x573_1_q4), .Q5(ic_74x573_1_q5), .Q6(ic_74x573_1_q6),
    .Q7(ic_74x573_1_q7), .Q8(ic_74x573_1_q8), .Q1(ic_74x573_1_q1), .D2(RWriteEn_y1), .D3(RWriteEn_y2),
    .D4(RWriteEn_y3), .D5(RWriteEn_y4), .D6(RWriteEn_y5), .D7(RWriteEn_y6), .D8(RWriteEn_y7), .LE(nCLK),
    .nOE(1'b0), .D1(RWriteEn_y0));  // open: Probe
  logi7400ic_IC_74x574 R0_A_3 (
    .Q2(REG_A[1]), .Q3(REG_A[2]), .Q4(REG_A[3]), .Q5(REG_A[4]), .Q6(REG_A[5]), .Q7(REG_A[6]), .Q8(REG_A[7]),
    .Q1(REG_A[0]), .D2(IN[1]), .D3(IN[2]), .D4(IN[3]), .D5(IN[4]), .D6(IN[5]), .D7(IN[6]), .D8(IN[7]),
    .CLK(WR_R0), .nOE(ic_74x1g3157_5_a), .D1(IN[0]));  // open: Probe
  logi7400ic_IC_74x574 R0_A_4 (
    .Q2(REG_A[9]), .Q3(REG_A[10]), .Q4(REG_A[11]), .Q5(REG_A[12]), .Q6(REG_A[13]), .Q7(REG_A[14]),
    .Q8(REG_A[15]), .Q1(REG_A[8]), .D2(IN[9]), .D3(IN[10]), .D4(IN[11]), .D5(IN[12]), .D6(IN[13]),
    .D7(IN[14]), .D8(IN[15]), .CLK(WR_R0), .nOE(ic_74x1g3157_5_a), .D1(IN[8]));  // open: Probe
  logi7400ic_IC_74x574 R1_A_3 (
    .Q2(REG_A[1]), .Q3(REG_A[2]), .Q4(REG_A[3]), .Q5(REG_A[4]), .Q6(REG_A[5]), .Q7(REG_A[6]), .Q8(REG_A[7]),
    .Q1(REG_A[0]), .D2(IN[1]), .D3(IN[2]), .D4(IN[3]), .D5(IN[4]), .D6(IN[5]), .D7(IN[6]), .D8(IN[7]),
    .CLK(WR_R1), .nOE(ic_74x1g3157_6_a), .D1(IN[0]));  // open: Probe
  logi7400ic_IC_74x574 R1_A_4 (
    .Q2(REG_A[9]), .Q3(REG_A[10]), .Q4(REG_A[11]), .Q5(REG_A[12]), .Q6(REG_A[13]), .Q7(REG_A[14]),
    .Q8(REG_A[15]), .Q1(REG_A[8]), .D2(IN[9]), .D3(IN[10]), .D4(IN[11]), .D5(IN[12]), .D6(IN[13]),
    .D7(IN[14]), .D8(IN[15]), .CLK(WR_R1), .nOE(ic_74x1g3157_6_a), .D1(IN[8]));  // open: Probe
  logi7400ic_IC_74x574 R2_A_3 (
    .Q2(REG_A[1]), .Q3(REG_A[2]), .Q4(REG_A[3]), .Q5(REG_A[4]), .Q6(REG_A[5]), .Q7(REG_A[6]), .Q8(REG_A[7]),
    .Q1(REG_A[0]), .D2(IN[1]), .D3(IN[2]), .D4(IN[3]), .D5(IN[4]), .D6(IN[5]), .D7(IN[6]), .D8(IN[7]),
    .CLK(WR_R2), .nOE(ic_74x1g3157_7_a), .D1(IN[0]));  // open: Probe
  logi7400ic_IC_74x574 R2_A_4 (
    .Q2(REG_A[9]), .Q3(REG_A[10]), .Q4(REG_A[11]), .Q5(REG_A[12]), .Q6(REG_A[13]), .Q7(REG_A[14]),
    .Q8(REG_A[15]), .Q1(REG_A[8]), .D2(IN[9]), .D3(IN[10]), .D4(IN[11]), .D5(IN[12]), .D6(IN[13]),
    .D7(IN[14]), .D8(IN[15]), .CLK(WR_R2), .nOE(ic_74x1g3157_7_a), .D1(IN[8]));  // open: Probe
  logi7400ic_IC_74x574 R3_A_3 (
    .Q2(REG_A[1]), .Q3(REG_A[2]), .Q4(REG_A[3]), .Q5(REG_A[4]), .Q6(REG_A[5]), .Q7(REG_A[6]), .Q8(REG_A[7]),
    .Q1(REG_A[0]), .D2(IN[1]), .D3(IN[2]), .D4(IN[3]), .D5(IN[4]), .D6(IN[5]), .D7(IN[6]), .D8(IN[7]),
    .CLK(WR_R3), .nOE(ic_74x1g3157_8_a), .D1(IN[0]));  // open: Probe
  logi7400ic_IC_74x574 R3_A_4 (
    .Q2(REG_A[9]), .Q3(REG_A[10]), .Q4(REG_A[11]), .Q5(REG_A[12]), .Q6(REG_A[13]), .Q7(REG_A[14]),
    .Q8(REG_A[15]), .Q1(REG_A[8]), .D2(IN[9]), .D3(IN[10]), .D4(IN[11]), .D5(IN[12]), .D6(IN[13]),
    .D7(IN[14]), .D8(IN[15]), .CLK(WR_R3), .nOE(ic_74x1g3157_8_a), .D1(IN[8]));  // open: Probe
  nor nor_1 (WR_R0, nCLK, ic_74x573_1_q1);
  nor nor_2 (WR_R1, nCLK, ic_74x573_1_q2);
  nor nor_3 (WR_R2, nCLK, ic_74x573_1_q3);
  nor nor_4 (WR_R3, nCLK, ic_74x573_1_q4);
  nor nor_5 (WR_R4, nCLK, ic_74x573_1_q5);
  nor nor_6 (WR_R5, nCLK, ic_74x573_1_q6);
  nor nor_7 (WR_R6, nCLK, ic_74x573_1_q7);
  nor nor_8 (WR_R7, nCLK, ic_74x573_1_q8);
  IC_74x1G3157 ic_74x1g3157_9 (.A(ic_74x1g3157_9_a), .B1(nRN_TO_B), .B2(1'b1), .S(sR0_B_n));
  IC_74x1G3157 ic_74x1g3157_10 (.A(ic_74x1g3157_10_a), .B1(nRN_TO_B), .B2(1'b1), .S(sR1_B_n));
  IC_74x1G3157 ic_74x1g3157_11 (.A(ic_74x1g3157_11_a), .B1(nRN_TO_B), .B2(1'b1), .S(sR2_B_n));
  IC_74x1G3157 ic_74x1g3157_12 (.A(ic_74x1g3157_12_a), .B1(nRN_TO_B), .B2(1'b1), .S(sR3_B_n));
  logi7400ic_IC_74x574 RO_B (
    .Q2(REG_B[1]), .Q3(REG_B[2]), .Q4(REG_B[3]), .Q5(REG_B[4]), .Q6(REG_B[5]), .Q7(REG_B[6]), .Q8(REG_B[7]),
    .Q1(REG_B[0]), .D2(IN[1]), .D3(IN[2]), .D4(IN[3]), .D5(IN[4]), .D6(IN[5]), .D7(IN[6]), .D8(IN[7]),
    .CLK(WR_R0), .nOE(ic_74x1g3157_9_a), .D1(IN[0]));  // open: Probe
  logi7400ic_IC_74x574 R0_B (
    .Q2(REG_B[9]), .Q3(REG_B[10]), .Q4(REG_B[11]), .Q5(REG_B[12]), .Q6(REG_B[13]), .Q7(REG_B[14]),
    .Q8(REG_B[15]), .Q1(REG_B[8]), .D2(IN[9]), .D3(IN[10]), .D4(IN[11]), .D5(IN[12]), .D6(IN[13]),
    .D7(IN[14]), .D8(IN[15]), .CLK(WR_R0), .nOE(ic_74x1g3157_9_a), .D1(IN[8]));  // open: Probe
  logi7400ic_IC_74x574 R1_B (
    .Q2(REG_B[1]), .Q3(REG_B[2]), .Q4(REG_B[3]), .Q5(REG_B[4]), .Q6(REG_B[5]), .Q7(REG_B[6]), .Q8(REG_B[7]),
    .Q1(REG_B[0]), .D2(IN[1]), .D3(IN[2]), .D4(IN[3]), .D5(IN[4]), .D6(IN[5]), .D7(IN[6]), .D8(IN[7]),
    .CLK(WR_R1), .nOE(ic_74x1g3157_10_a), .D1(IN[0]));  // open: Probe
  logi7400ic_IC_74x574 R1_B_2 (
    .Q2(REG_B[9]), .Q3(REG_B[10]), .Q4(REG_B[11]), .Q5(REG_B[12]), .Q6(REG_B[13]), .Q7(REG_B[14]),
    .Q8(REG_B[15]), .Q1(REG_B[8]), .D2(IN[9]), .D3(IN[10]), .D4(IN[11]), .D5(IN[12]), .D6(IN[13]),
    .D7(IN[14]), .D8(IN[15]), .CLK(WR_R1), .nOE(ic_74x1g3157_10_a), .D1(IN[8]));  // open: Probe
  logi7400ic_IC_74x574 R2_B (
    .Q2(REG_B[1]), .Q3(REG_B[2]), .Q4(REG_B[3]), .Q5(REG_B[4]), .Q6(REG_B[5]), .Q7(REG_B[6]), .Q8(REG_B[7]),
    .Q1(REG_B[0]), .D2(IN[1]), .D3(IN[2]), .D4(IN[3]), .D5(IN[4]), .D6(IN[5]), .D7(IN[6]), .D8(IN[7]),
    .CLK(WR_R2), .nOE(ic_74x1g3157_11_a), .D1(IN[0]));  // open: Probe
  logi7400ic_IC_74x574 R2_B_2 (
    .Q2(REG_B[9]), .Q3(REG_B[10]), .Q4(REG_B[11]), .Q5(REG_B[12]), .Q6(REG_B[13]), .Q7(REG_B[14]),
    .Q8(REG_B[15]), .Q1(REG_B[8]), .D2(IN[9]), .D3(IN[10]), .D4(IN[11]), .D5(IN[12]), .D6(IN[13]),
    .D7(IN[14]), .D8(IN[15]), .CLK(WR_R2), .nOE(ic_74x1g3157_11_a), .D1(IN[8]));  // open: Probe
  logi7400ic_IC_74x574 R3_B (
    .Q2(REG_B[1]), .Q3(REG_B[2]), .Q4(REG_B[3]), .Q5(REG_B[4]), .Q6(REG_B[5]), .Q7(REG_B[6]), .Q8(REG_B[7]),
    .Q1(REG_B[0]), .D2(IN[1]), .D3(IN[2]), .D4(IN[3]), .D5(IN[4]), .D6(IN[5]), .D7(IN[6]), .D8(IN[7]),
    .CLK(WR_R3), .nOE(ic_74x1g3157_12_a), .D1(IN[0]));  // open: Probe
  logi7400ic_IC_74x574 R3_B_2 (
    .Q2(REG_B[9]), .Q3(REG_B[10]), .Q4(REG_B[11]), .Q5(REG_B[12]), .Q6(REG_B[13]), .Q7(REG_B[14]),
    .Q8(REG_B[15]), .Q1(REG_B[8]), .D2(IN[9]), .D3(IN[10]), .D4(IN[11]), .D5(IN[12]), .D6(IN[13]),
    .D7(IN[14]), .D8(IN[15]), .CLK(WR_R3), .nOE(ic_74x1g3157_12_a), .D1(IN[8]));  // open: Probe
  IC_74x1G3157 ic_74x1g3157_13 (.A(ic_74x1g3157_13_a), .B1(nRD_TO_A), .B2(1'b1), .S(sR4_1A_n));
  IC_74x1G3157 ic_74x1g3157_14 (.A(ic_74x1g3157_14_a), .B1(nRD_TO_A), .B2(1'b1), .S(sR5_1A_n));
  IC_74x1G3157 ic_74x1g3157_15 (.A(ic_74x1g3157_15_a), .B1(nRD_TO_A), .B2(1'b1), .S(sR6_1A_n));
  IC_74x1G3157 ic_74x1g3157_16 (.A(ic_74x1g3157_16_a), .B1(nRD_TO_A), .B2(1'b1), .S(sR7_1A_n));
  logi7400ic_IC_74x574 R4_A (
    .Q2(REG_A[1]), .Q3(REG_A[2]), .Q4(REG_A[3]), .Q5(REG_A[4]), .Q6(REG_A[5]), .Q7(REG_A[6]), .Q8(REG_A[7]),
    .Q1(REG_A[0]), .D2(IN[1]), .D3(IN[2]), .D4(IN[3]), .D5(IN[4]), .D6(IN[5]), .D7(IN[6]), .D8(IN[7]),
    .CLK(WR_R4), .nOE(ic_74x1g3157_13_a), .D1(IN[0]));  // open: Probe
  logi7400ic_IC_74x574 R4_A_2 (
    .Q2(REG_A[9]), .Q3(REG_A[10]), .Q4(REG_A[11]), .Q5(REG_A[12]), .Q6(REG_A[13]), .Q7(REG_A[14]),
    .Q8(REG_A[15]), .Q1(REG_A[8]), .D2(IN[9]), .D3(IN[10]), .D4(IN[11]), .D5(IN[12]), .D6(IN[13]),
    .D7(IN[14]), .D8(IN[15]), .CLK(WR_R4), .nOE(ic_74x1g3157_13_a), .D1(IN[8]));  // open: Probe
  logi7400ic_IC_74x574 R5_A (
    .Q2(REG_A[1]), .Q3(REG_A[2]), .Q4(REG_A[3]), .Q5(REG_A[4]), .Q6(REG_A[5]), .Q7(REG_A[6]), .Q8(REG_A[7]),
    .Q1(REG_A[0]), .D2(IN[1]), .D3(IN[2]), .D4(IN[3]), .D5(IN[4]), .D6(IN[5]), .D7(IN[6]), .D8(IN[7]),
    .CLK(WR_R5), .nOE(ic_74x1g3157_14_a), .D1(IN[0]));  // open: Probe
  logi7400ic_IC_74x574 R5_A_2 (
    .Q2(REG_A[9]), .Q3(REG_A[10]), .Q4(REG_A[11]), .Q5(REG_A[12]), .Q6(REG_A[13]), .Q7(REG_A[14]),
    .Q8(REG_A[15]), .Q1(REG_A[8]), .D2(IN[9]), .D3(IN[10]), .D4(IN[11]), .D5(IN[12]), .D6(IN[13]),
    .D7(IN[14]), .D8(IN[15]), .CLK(WR_R5), .nOE(ic_74x1g3157_14_a), .D1(IN[8]));  // open: Probe
  logi7400ic_IC_74x574 R6_A (
    .Q2(REG_A[1]), .Q3(REG_A[2]), .Q4(REG_A[3]), .Q5(REG_A[4]), .Q6(REG_A[5]), .Q7(REG_A[6]), .Q8(REG_A[7]),
    .Q1(REG_A[0]), .D2(IN[1]), .D3(IN[2]), .D4(IN[3]), .D5(IN[4]), .D6(IN[5]), .D7(IN[6]), .D8(IN[7]),
    .CLK(WR_R6), .nOE(ic_74x1g3157_15_a), .D1(IN[0]));  // open: Probe
  logi7400ic_IC_74x574 R6_A_2 (
    .Q2(REG_A[9]), .Q3(REG_A[10]), .Q4(REG_A[11]), .Q5(REG_A[12]), .Q6(REG_A[13]), .Q7(REG_A[14]),
    .Q8(REG_A[15]), .Q1(REG_A[8]), .D2(IN[9]), .D3(IN[10]), .D4(IN[11]), .D5(IN[12]), .D6(IN[13]),
    .D7(IN[14]), .D8(IN[15]), .CLK(WR_R6), .nOE(ic_74x1g3157_15_a), .D1(IN[8]));  // open: Probe
  logi7400ic_IC_74x574 R7_A (
    .Q2(REG_A[1]), .Q3(REG_A[2]), .Q4(REG_A[3]), .Q5(REG_A[4]), .Q6(REG_A[5]), .Q7(REG_A[6]), .Q8(REG_A[7]),
    .Q1(REG_A[0]), .D2(IN[1]), .D3(IN[2]), .D4(IN[3]), .D5(IN[4]), .D6(IN[5]), .D7(IN[6]), .D8(IN[7]),
    .CLK(WR_R7), .nOE(ic_74x1g3157_16_a), .D1(IN[0]));  // open: Probe
  logi7400ic_IC_74x574 R8_A (
    .Q2(REG_A[9]), .Q3(REG_A[10]), .Q4(REG_A[11]), .Q5(REG_A[12]), .Q6(REG_A[13]), .Q7(REG_A[14]),
    .Q8(REG_A[15]), .Q1(REG_A[8]), .D2(IN[9]), .D3(IN[10]), .D4(IN[11]), .D5(IN[12]), .D6(IN[13]),
    .D7(IN[14]), .D8(IN[15]), .CLK(WR_R7), .nOE(ic_74x1g3157_16_a), .D1(IN[8]));  // open: Probe
  IC_74x1G3157 ic_74x1g3157_17 (.A(ic_74x1g3157_17_a), .B1(nRS_TO_A), .B2(1'b1), .S(sR4_2A_n));
  IC_74x1G3157 ic_74x1g3157_18 (.A(ic_74x1g3157_18_a), .B1(nRS_TO_A), .B2(1'b1), .S(sR5_2A_n));
  IC_74x1G3157 ic_74x1g3157_19 (.A(ic_74x1g3157_19_a), .B1(nRS_TO_A), .B2(1'b1), .S(sR6_2A_n));
  IC_74x1G3157 ic_74x1g3157_20 (.A(ic_74x1g3157_20_a), .B1(nRS_TO_A), .B2(1'b1), .S(sR7_2A_n));
  logi7400ic_IC_74x574 R4_A_3 (
    .Q2(REG_A[1]), .Q3(REG_A[2]), .Q4(REG_A[3]), .Q5(REG_A[4]), .Q6(REG_A[5]), .Q7(REG_A[6]), .Q8(REG_A[7]),
    .Q1(REG_A[0]), .D2(IN[1]), .D3(IN[2]), .D4(IN[3]), .D5(IN[4]), .D6(IN[5]), .D7(IN[6]), .D8(IN[7]),
    .CLK(WR_R4), .nOE(ic_74x1g3157_17_a), .D1(IN[0]));  // open: Probe
  logi7400ic_IC_74x574 R4_A_4 (
    .Q2(REG_A[9]), .Q3(REG_A[10]), .Q4(REG_A[11]), .Q5(REG_A[12]), .Q6(REG_A[13]), .Q7(REG_A[14]),
    .Q8(REG_A[15]), .Q1(REG_A[8]), .D2(IN[9]), .D3(IN[10]), .D4(IN[11]), .D5(IN[12]), .D6(IN[13]),
    .D7(IN[14]), .D8(IN[15]), .CLK(WR_R4), .nOE(ic_74x1g3157_17_a), .D1(IN[8]));  // open: Probe
  logi7400ic_IC_74x574 R5_A_3 (
    .Q2(REG_A[1]), .Q3(REG_A[2]), .Q4(REG_A[3]), .Q5(REG_A[4]), .Q6(REG_A[5]), .Q7(REG_A[6]), .Q8(REG_A[7]),
    .Q1(REG_A[0]), .D2(IN[1]), .D3(IN[2]), .D4(IN[3]), .D5(IN[4]), .D6(IN[5]), .D7(IN[6]), .D8(IN[7]),
    .CLK(WR_R5), .nOE(ic_74x1g3157_18_a), .D1(IN[0]));  // open: Probe
  logi7400ic_IC_74x574 R5_A_4 (
    .Q2(REG_A[9]), .Q3(REG_A[10]), .Q4(REG_A[11]), .Q5(REG_A[12]), .Q6(REG_A[13]), .Q7(REG_A[14]),
    .Q8(REG_A[15]), .Q1(REG_A[8]), .D2(IN[9]), .D3(IN[10]), .D4(IN[11]), .D5(IN[12]), .D6(IN[13]),
    .D7(IN[14]), .D8(IN[15]), .CLK(WR_R5), .nOE(ic_74x1g3157_18_a), .D1(IN[8]));  // open: Probe
  logi7400ic_IC_74x574 R6_A_3 (
    .Q2(REG_A[1]), .Q3(REG_A[2]), .Q4(REG_A[3]), .Q5(REG_A[4]), .Q6(REG_A[5]), .Q7(REG_A[6]), .Q8(REG_A[7]),
    .Q1(REG_A[0]), .D2(IN[1]), .D3(IN[2]), .D4(IN[3]), .D5(IN[4]), .D6(IN[5]), .D7(IN[6]), .D8(IN[7]),
    .CLK(WR_R6), .nOE(ic_74x1g3157_19_a), .D1(IN[0]));  // open: Probe
  logi7400ic_IC_74x574 R6_A_4 (
    .Q2(REG_A[9]), .Q3(REG_A[10]), .Q4(REG_A[11]), .Q5(REG_A[12]), .Q6(REG_A[13]), .Q7(REG_A[14]),
    .Q8(REG_A[15]), .Q1(REG_A[8]), .D2(IN[9]), .D3(IN[10]), .D4(IN[11]), .D5(IN[12]), .D6(IN[13]),
    .D7(IN[14]), .D8(IN[15]), .CLK(WR_R6), .nOE(ic_74x1g3157_19_a), .D1(IN[8]));  // open: Probe
  logi7400ic_IC_74x574 R7_A_2 (
    .Q2(REG_A[1]), .Q3(REG_A[2]), .Q4(REG_A[3]), .Q5(REG_A[4]), .Q6(REG_A[5]), .Q7(REG_A[6]), .Q8(REG_A[7]),
    .Q1(REG_A[0]), .D2(IN[1]), .D3(IN[2]), .D4(IN[3]), .D5(IN[4]), .D6(IN[5]), .D7(IN[6]), .D8(IN[7]),
    .CLK(WR_R7), .nOE(ic_74x1g3157_20_a), .D1(IN[0]));  // open: Probe
  logi7400ic_IC_74x574 R8_A_2 (
    .Q2(REG_A[9]), .Q3(REG_A[10]), .Q4(REG_A[11]), .Q5(REG_A[12]), .Q6(REG_A[13]), .Q7(REG_A[14]),
    .Q8(REG_A[15]), .Q1(REG_A[8]), .D2(IN[9]), .D3(IN[10]), .D4(IN[11]), .D5(IN[12]), .D6(IN[13]),
    .D7(IN[14]), .D8(IN[15]), .CLK(WR_R7), .nOE(ic_74x1g3157_20_a), .D1(IN[8]));  // open: Probe
  IC_74x1G3157 ic_74x1g3157_21 (.A(ic_74x1g3157_21_a), .B1(nRN_TO_B), .B2(1'b1), .S(sR4_B_n));
  IC_74x1G3157 ic_74x1g3157_22 (.A(ic_74x1g3157_22_a), .B1(nRN_TO_B), .B2(1'b1), .S(sR5_B_n));
  IC_74x1G3157 ic_74x1g3157_23 (.A(ic_74x1g3157_23_a), .B1(nRN_TO_B), .B2(1'b1), .S(sR6_B_n));
  IC_74x1G3157 ic_74x1g3157_24 (.A(ic_74x1g3157_24_a), .B1(nRN_TO_B), .B2(1'b1), .S(sR7_B_n));
  logi7400ic_IC_74x574 R4_B (
    .Q2(REG_B[1]), .Q3(REG_B[2]), .Q4(REG_B[3]), .Q5(REG_B[4]), .Q6(REG_B[5]), .Q7(REG_B[6]), .Q8(REG_B[7]),
    .Q1(REG_B[0]), .D2(IN[1]), .D3(IN[2]), .D4(IN[3]), .D5(IN[4]), .D6(IN[5]), .D7(IN[6]), .D8(IN[7]),
    .CLK(WR_R4), .nOE(ic_74x1g3157_21_a), .D1(IN[0]));  // open: Probe
  logi7400ic_IC_74x574 R4_B_2 (
    .Q2(REG_B[9]), .Q3(REG_B[10]), .Q4(REG_B[11]), .Q5(REG_B[12]), .Q6(REG_B[13]), .Q7(REG_B[14]),
    .Q8(REG_B[15]), .Q1(REG_B[8]), .D2(IN[9]), .D3(IN[10]), .D4(IN[11]), .D5(IN[12]), .D6(IN[13]),
    .D7(IN[14]), .D8(IN[15]), .CLK(WR_R4), .nOE(ic_74x1g3157_21_a), .D1(IN[8]));  // open: Probe
  logi7400ic_IC_74x574 R5_B (
    .Q2(REG_B[1]), .Q3(REG_B[2]), .Q4(REG_B[3]), .Q5(REG_B[4]), .Q6(REG_B[5]), .Q7(REG_B[6]), .Q8(REG_B[7]),
    .Q1(REG_B[0]), .D2(IN[1]), .D3(IN[2]), .D4(IN[3]), .D5(IN[4]), .D6(IN[5]), .D7(IN[6]), .D8(IN[7]),
    .CLK(WR_R5), .nOE(ic_74x1g3157_22_a), .D1(IN[0]));  // open: Probe
  logi7400ic_IC_74x574 R5_B_2 (
    .Q2(REG_B[9]), .Q3(REG_B[10]), .Q4(REG_B[11]), .Q5(REG_B[12]), .Q6(REG_B[13]), .Q7(REG_B[14]),
    .Q8(REG_B[15]), .Q1(REG_B[8]), .D2(IN[9]), .D3(IN[10]), .D4(IN[11]), .D5(IN[12]), .D6(IN[13]),
    .D7(IN[14]), .D8(IN[15]), .CLK(WR_R5), .nOE(ic_74x1g3157_22_a), .D1(IN[8]));  // open: Probe
  logi7400ic_IC_74x574 R6_B (
    .Q2(REG_B[1]), .Q3(REG_B[2]), .Q4(REG_B[3]), .Q5(REG_B[4]), .Q6(REG_B[5]), .Q7(REG_B[6]), .Q8(REG_B[7]),
    .Q1(REG_B[0]), .D2(IN[1]), .D3(IN[2]), .D4(IN[3]), .D5(IN[4]), .D6(IN[5]), .D7(IN[6]), .D8(IN[7]),
    .CLK(WR_R6), .nOE(ic_74x1g3157_23_a), .D1(IN[0]));  // open: Probe
  logi7400ic_IC_74x574 R6_B_2 (
    .Q2(REG_B[9]), .Q3(REG_B[10]), .Q4(REG_B[11]), .Q5(REG_B[12]), .Q6(REG_B[13]), .Q7(REG_B[14]),
    .Q8(REG_B[15]), .Q1(REG_B[8]), .D2(IN[9]), .D3(IN[10]), .D4(IN[11]), .D5(IN[12]), .D6(IN[13]),
    .D7(IN[14]), .D8(IN[15]), .CLK(WR_R6), .nOE(ic_74x1g3157_23_a), .D1(IN[8]));  // open: Probe
  logi7400ic_IC_74x574 R7_B (
    .Q2(REG_B[1]), .Q3(REG_B[2]), .Q4(REG_B[3]), .Q5(REG_B[4]), .Q6(REG_B[5]), .Q7(REG_B[6]), .Q8(REG_B[7]),
    .Q1(REG_B[0]), .D2(IN[1]), .D3(IN[2]), .D4(IN[3]), .D5(IN[4]), .D6(IN[5]), .D7(IN[6]), .D8(IN[7]),
    .CLK(WR_R7), .nOE(ic_74x1g3157_24_a), .D1(IN[0]));  // open: Probe
  logi7400ic_IC_74x574 R8_B (
    .Q2(REG_B[9]), .Q3(REG_B[10]), .Q4(REG_B[11]), .Q5(REG_B[12]), .Q6(REG_B[13]), .Q7(REG_B[14]),
    .Q8(REG_B[15]), .Q1(REG_B[8]), .D2(IN[9]), .D3(IN[10]), .D4(IN[11]), .D5(IN[12]), .D6(IN[13]),
    .D7(IN[14]), .D8(IN[15]), .CLK(WR_R7), .nOE(ic_74x1g3157_24_a), .D1(IN[8]));  // open: Probe

  // Other names for the same wires on the sheet: RD_A_n = nRD_TO_A; RN_B_n = nRN_TO_B; RS_A_n = nRS_TO_A
endmodule

// Register File
module Registers_8_1 (
  input  nCLK,
  input  nWR_RD,
  input  nRD_TO_A,
  input  nRS_TO_A,
  input  nRN_TO_B,
  input  [15:0] IN,
  input  [2:0] RD,
  input  [2:0] RS,
  input  [2:0] RN,
  output [15:0] REG_A,
  output [15:0] REG_B
);

  wire ic_74x573_1_q1, ic_74x573_1_q2, ic_74x573_1_q3, ic_74x573_1_q4, ic_74x573_1_q5, ic_74x573_1_q6,
       ic_74x573_1_q7, ic_74x573_1_q8, R0_0, R0_1, R0_2, R0_3, R0_4, R0_5, R0_6, R0_7, R0_8, R0_9, R0_10,
       R0_11, R0_12, R0_13, R0_14, R0_15, R1_0, R1_1, R1_2, R1_3, R1_4, R1_5, R1_6, R1_7, R1_8, R1_9, R1_10,
       R1_11, R1_12, R1_13, R1_14, R1_15, R2_0, R2_1, R2_2, R2_3, R2_4, R2_5, R2_6, R2_7, R2_8, R2_9, R2_10,
       R2_11, R2_12, R2_13, R2_14, R2_15, R3_0, R3_1, R3_2, R3_3, R3_4, R3_5, R3_6, R3_7, R3_8, R3_9, R3_10,
       R3_11, R3_12, R3_13, R3_14, R3_15, R4_0, R4_1, R4_2, R4_3, R4_4, R4_5, R4_6, R4_7, R4_8, R4_9, R4_10,
       R4_11, R4_12, R4_13, R4_14, R4_15, R5_0, R5_1, R5_2, R5_3, R5_4, R5_5, R5_6, R5_7, R5_8, R5_9, R5_10,
       R5_11, R5_12, R5_13, R5_14, R5_15, R6_0, R6_1, R6_2, R6_3, R6_4, R6_5, R6_6, R6_7, R6_8, R6_9, R6_10,
       R6_11, R6_12, R6_13, R6_14, R6_15, R7_0, R7_1, R7_2, R7_3, R7_4, R7_5, R7_6, R7_7, R7_8, R7_9, R7_10,
       R7_11, R7_12, R7_13, R7_14, R7_15, RWriteEn_y0, RWriteEn_y1, RWriteEn_y2, RWriteEn_y3, RWriteEn_y4,
       RWriteEn_y5, RWriteEn_y6, RWriteEn_y7, WR_R0, WR_R1, WR_R2, WR_R3, WR_R4, WR_R5, WR_R6, WR_R7;
  wire [2:0] RD_t, RN_t, RS_t;

  IC_74x3G34 AdrBuffer (.Y3(RD_t[2]), .Y1(RD_t[0]), .Y2(RD_t[1]), .A3(RD[2]), .A1(RD[0]), .A2(RD[1]));
  IC_74x3G34 AddrBuffer (.Y3(RS_t[2]), .Y1(RS_t[0]), .Y2(RS_t[1]), .A3(RS[2]), .A1(RS[0]), .A2(RS[1]));
  IC_74x3G34 AddrBuffer_2 (.Y3(RN_t[2]), .Y1(RN_t[0]), .Y2(RN_t[1]), .A3(RN[2]), .A1(RN[0]), .A2(RN[1]));
  IC_74x273 R0 (
    .Q1(R0_0), .Q2(R0_1), .Q3(R0_2), .Q4(R0_3), .Q5(R0_4), .Q6(R0_5), .Q7(R0_6), .Q8(R0_7), .D1(IN[0]),
    .D2(IN[1]), .D3(IN[2]), .D4(IN[3]), .D5(IN[4]), .D6(IN[5]), .D7(IN[6]), .D8(IN[7]), .CLK(WR_R0),
    .nMR(1'b1));  // open: Probe
  IC_74x273 u_R0_2 (
    .Q1(R0_8), .Q2(R0_9), .Q3(R0_10), .Q4(R0_11), .Q5(R0_12), .Q6(R0_13), .Q7(R0_14), .Q8(R0_15), .D1(IN[8]),
    .D2(IN[9]), .D3(IN[10]), .D4(IN[11]), .D5(IN[12]), .D6(IN[13]), .D7(IN[14]), .D8(IN[15]), .CLK(WR_R0),
    .nMR(1'b1));  // open: Probe
  IC_74x273 R1 (
    .Q1(R1_0), .Q2(R1_1), .Q3(R1_2), .Q4(R1_3), .Q5(R1_4), .Q6(R1_5), .Q7(R1_6), .Q8(R1_7), .D1(IN[0]),
    .D2(IN[1]), .D3(IN[2]), .D4(IN[3]), .D5(IN[4]), .D6(IN[5]), .D7(IN[6]), .D8(IN[7]), .CLK(WR_R1),
    .nMR(1'b1));  // open: Probe
  IC_74x273 u_R1_2 (
    .Q1(R1_8), .Q2(R1_9), .Q3(R1_10), .Q4(R1_11), .Q5(R1_12), .Q6(R1_13), .Q7(R1_14), .Q8(R1_15), .D1(IN[8]),
    .D2(IN[9]), .D3(IN[10]), .D4(IN[11]), .D5(IN[12]), .D6(IN[13]), .D7(IN[14]), .D8(IN[15]), .CLK(WR_R1),
    .nMR(1'b1));  // open: Probe
  IC_74x273 R2 (
    .Q1(R2_0), .Q2(R2_1), .Q3(R2_2), .Q4(R2_3), .Q5(R2_4), .Q6(R2_5), .Q7(R2_6), .Q8(R2_7), .D1(IN[0]),
    .D2(IN[1]), .D3(IN[2]), .D4(IN[3]), .D5(IN[4]), .D6(IN[5]), .D7(IN[6]), .D8(IN[7]), .CLK(WR_R2),
    .nMR(1'b1));  // open: Probe
  IC_74x273 u_R2_2 (
    .Q1(R2_8), .Q2(R2_9), .Q3(R2_10), .Q4(R2_11), .Q5(R2_12), .Q6(R2_13), .Q7(R2_14), .Q8(R2_15), .D1(IN[8]),
    .D2(IN[9]), .D3(IN[10]), .D4(IN[11]), .D5(IN[12]), .D6(IN[13]), .D7(IN[14]), .D8(IN[15]), .CLK(WR_R2),
    .nMR(1'b1));  // open: Probe
  IC_74x273 R3 (
    .Q1(R3_0), .Q2(R3_1), .Q3(R3_2), .Q4(R3_3), .Q5(R3_4), .Q6(R3_5), .Q7(R3_6), .Q8(R3_7), .D1(IN[0]),
    .D2(IN[1]), .D3(IN[2]), .D4(IN[3]), .D5(IN[4]), .D6(IN[5]), .D7(IN[6]), .D8(IN[7]), .CLK(WR_R3),
    .nMR(1'b1));  // open: Probe
  IC_74x273 u_R3_2 (
    .Q1(R3_8), .Q2(R3_9), .Q3(R3_10), .Q4(R3_11), .Q5(R3_12), .Q6(R3_13), .Q7(R3_14), .Q8(R3_15), .D1(IN[8]),
    .D2(IN[9]), .D3(IN[10]), .D4(IN[11]), .D5(IN[12]), .D6(IN[13]), .D7(IN[14]), .D8(IN[15]), .CLK(WR_R3),
    .nMR(1'b1));  // open: Probe
  IC_74x138 RWriteEn (
    .Y0(RWriteEn_y0), .Y1(RWriteEn_y1), .Y2(RWriteEn_y2), .Y3(RWriteEn_y3), .Y4(RWriteEn_y4),
    .Y5(RWriteEn_y5), .Y6(RWriteEn_y6), .Y7(RWriteEn_y7), .A(RD_t[0]), .B(RD_t[1]), .C(RD_t[2]),
    .nG2A(nWR_RD), .nG2B(1'b0), .G1(1'b1));
  IC_74x273 R4 (
    .Q1(R4_0), .Q2(R4_1), .Q3(R4_2), .Q4(R4_3), .Q5(R4_4), .Q6(R4_5), .Q7(R4_6), .Q8(R4_7), .D1(IN[0]),
    .D2(IN[1]), .D3(IN[2]), .D4(IN[3]), .D5(IN[4]), .D6(IN[5]), .D7(IN[6]), .D8(IN[7]), .CLK(WR_R4),
    .nMR(1'b1));  // open: Probe
  IC_74x273 u_R4_2 (
    .Q1(R4_8), .Q2(R4_9), .Q3(R4_10), .Q4(R4_11), .Q5(R4_12), .Q6(R4_13), .Q7(R4_14), .Q8(R4_15), .D1(IN[8]),
    .D2(IN[9]), .D3(IN[10]), .D4(IN[11]), .D5(IN[12]), .D6(IN[13]), .D7(IN[14]), .D8(IN[15]), .CLK(WR_R4),
    .nMR(1'b1));  // open: Probe
  IC_74x273 R5 (
    .Q1(R5_0), .Q2(R5_1), .Q3(R5_2), .Q4(R5_3), .Q5(R5_4), .Q6(R5_5), .Q7(R5_6), .Q8(R5_7), .D1(IN[0]),
    .D2(IN[1]), .D3(IN[2]), .D4(IN[3]), .D5(IN[4]), .D6(IN[5]), .D7(IN[6]), .D8(IN[7]), .CLK(WR_R5),
    .nMR(1'b1));  // open: Probe
  IC_74x273 u_R5_2 (
    .Q1(R5_8), .Q2(R5_9), .Q3(R5_10), .Q4(R5_11), .Q5(R5_12), .Q6(R5_13), .Q7(R5_14), .Q8(R5_15), .D1(IN[8]),
    .D2(IN[9]), .D3(IN[10]), .D4(IN[11]), .D5(IN[12]), .D6(IN[13]), .D7(IN[14]), .D8(IN[15]), .CLK(WR_R5),
    .nMR(1'b1));  // open: Probe
  IC_74x273 R6 (
    .Q1(R6_0), .Q2(R6_1), .Q3(R6_2), .Q4(R6_3), .Q5(R6_4), .Q6(R6_5), .Q7(R6_6), .Q8(R6_7), .D1(IN[0]),
    .D2(IN[1]), .D3(IN[2]), .D4(IN[3]), .D5(IN[4]), .D6(IN[5]), .D7(IN[6]), .D8(IN[7]), .CLK(WR_R6),
    .nMR(1'b1));  // open: Probe
  IC_74x273 u_R6_2 (
    .Q1(R6_8), .Q2(R6_9), .Q3(R6_10), .Q4(R6_11), .Q5(R6_12), .Q6(R6_13), .Q7(R6_14), .Q8(R6_15), .D1(IN[8]),
    .D2(IN[9]), .D3(IN[10]), .D4(IN[11]), .D5(IN[12]), .D6(IN[13]), .D7(IN[14]), .D8(IN[15]), .CLK(WR_R6),
    .nMR(1'b1));  // open: Probe
  IC_74x273 R7 (
    .Q1(R7_0), .Q2(R7_1), .Q3(R7_2), .Q4(R7_3), .Q5(R7_4), .Q6(R7_5), .Q7(R7_6), .Q8(R7_7), .D1(IN[0]),
    .D2(IN[1]), .D3(IN[2]), .D4(IN[3]), .D5(IN[4]), .D6(IN[5]), .D7(IN[6]), .D8(IN[7]), .CLK(WR_R7),
    .nMR(1'b1));  // open: Probe
  IC_74x273 u_R7_2 (
    .Q1(R7_8), .Q2(R7_9), .Q3(R7_10), .Q4(R7_11), .Q5(R7_12), .Q6(R7_13), .Q7(R7_14), .Q8(R7_15), .D1(IN[8]),
    .D2(IN[9]), .D3(IN[10]), .D4(IN[11]), .D5(IN[12]), .D6(IN[13]), .D7(IN[14]), .D8(IN[15]), .CLK(WR_R7),
    .nMR(1'b1));  // open: Probe
  IC_74x573 ic_74x573_1 (
    .Q2(ic_74x573_1_q2), .Q3(ic_74x573_1_q3), .Q4(ic_74x573_1_q4), .Q5(ic_74x573_1_q5), .Q6(ic_74x573_1_q6),
    .Q7(ic_74x573_1_q7), .Q8(ic_74x573_1_q8), .Q1(ic_74x573_1_q1), .D2(RWriteEn_y1), .D3(RWriteEn_y2),
    .D4(RWriteEn_y3), .D5(RWriteEn_y4), .D6(RWriteEn_y5), .D7(RWriteEn_y6), .D8(RWriteEn_y7), .LE(nCLK),
    .nOE(1'b0), .D1(RWriteEn_y0));  // open: Probe
  nor nor_1 (WR_R0, nCLK, ic_74x573_1_q1);
  nor nor_2 (WR_R1, nCLK, ic_74x573_1_q2);
  nor nor_3 (WR_R2, nCLK, ic_74x573_1_q3);
  nor nor_4 (WR_R3, nCLK, ic_74x573_1_q4);
  nor nor_5 (WR_R4, nCLK, ic_74x573_1_q5);
  nor nor_6 (WR_R5, nCLK, ic_74x573_1_q6);
  nor nor_7 (WR_R6, nCLK, ic_74x573_1_q7);
  nor nor_8 (WR_R7, nCLK, ic_74x573_1_q8);
  IC_74x251 Bit0 (
    .Y(REG_A[0]), .I0(R0_0), .I1(R1_0), .I2(R2_0), .I3(R3_0), .I4(R4_0), .I5(R5_0), .I6(R6_0), .I7(R7_0),
    .S0(RD_t[0]), .S1(RD_t[1]), .S2(RD_t[2]), .nOE(nRD_TO_A));  // open: W
  IC_74x251 Bit1 (
    .Y(REG_A[1]), .I0(R0_1), .I1(R1_1), .I2(R2_1), .I3(R3_1), .I4(R4_1), .I5(R5_1), .I6(R6_1), .I7(R7_1),
    .S0(RD_t[0]), .S1(RD_t[1]), .S2(RD_t[2]), .nOE(nRD_TO_A));  // open: W
  IC_74x251 Bit2 (
    .Y(REG_A[2]), .I0(R0_2), .I1(R1_2), .I2(R2_2), .I3(R3_2), .I4(R4_2), .I5(R5_2), .I6(R6_2), .I7(R7_2),
    .S0(RD_t[0]), .S1(RD_t[1]), .S2(RD_t[2]), .nOE(nRD_TO_A));  // open: W
  IC_74x251 Bit3 (
    .Y(REG_A[3]), .I0(R0_3), .I1(R1_3), .I2(R2_3), .I3(R3_3), .I4(R4_3), .I5(R5_3), .I6(R6_3), .I7(R7_3),
    .S0(RD_t[0]), .S1(RD_t[1]), .S2(RD_t[2]), .nOE(nRD_TO_A));  // open: W
  IC_74x251 Bit4 (
    .Y(REG_A[4]), .I0(R0_4), .I1(R1_4), .I2(R2_4), .I3(R3_4), .I4(R4_4), .I5(R5_4), .I6(R6_4), .I7(R7_4),
    .S0(RD_t[0]), .S1(RD_t[1]), .S2(RD_t[2]), .nOE(nRD_TO_A));  // open: W
  IC_74x251 Bit5 (
    .Y(REG_A[5]), .I0(R0_5), .I1(R1_5), .I2(R2_5), .I3(R3_5), .I4(R4_5), .I5(R5_5), .I6(R6_5), .I7(R7_5),
    .S0(RD_t[0]), .S1(RD_t[1]), .S2(RD_t[2]), .nOE(nRD_TO_A));  // open: W
  IC_74x251 Bit6 (
    .Y(REG_A[6]), .I0(R0_6), .I1(R1_6), .I2(R2_6), .I3(R3_6), .I4(R4_6), .I5(R5_6), .I6(R6_6), .I7(R7_6),
    .S0(RD_t[0]), .S1(RD_t[1]), .S2(RD_t[2]), .nOE(nRD_TO_A));  // open: W
  IC_74x251 Bit7 (
    .Y(REG_A[7]), .I0(R0_7), .I1(R1_7), .I2(R2_7), .I3(R3_7), .I4(R4_7), .I5(R5_7), .I6(R6_7), .I7(R7_7),
    .S0(RD_t[0]), .S1(RD_t[1]), .S2(RD_t[2]), .nOE(nRD_TO_A));  // open: W
  IC_74x251 Bit0_2 (
    .Y(REG_A[0]), .I0(R0_0), .I1(R1_0), .I2(R2_0), .I3(R3_0), .I4(R4_0), .I5(R5_0), .I6(R6_0), .I7(R7_0),
    .S0(RS_t[0]), .S1(RS_t[1]), .S2(RS_t[2]), .nOE(nRS_TO_A));  // open: W
  IC_74x251 Bit1_2 (
    .Y(REG_A[1]), .I0(R0_1), .I1(R1_1), .I2(R2_1), .I3(R3_1), .I4(R4_1), .I5(R5_1), .I6(R6_1), .I7(R7_1),
    .S0(RS_t[0]), .S1(RS_t[1]), .S2(RS_t[2]), .nOE(nRS_TO_A));  // open: W
  IC_74x251 Bit2_2 (
    .Y(REG_A[2]), .I0(R0_2), .I1(R1_2), .I2(R2_2), .I3(R3_2), .I4(R4_2), .I5(R5_2), .I6(R6_2), .I7(R7_2),
    .S0(RS_t[0]), .S1(RS_t[1]), .S2(RS_t[2]), .nOE(nRS_TO_A));  // open: W
  IC_74x251 Bit3_2 (
    .Y(REG_A[3]), .I0(R0_3), .I1(R1_3), .I2(R2_3), .I3(R3_3), .I4(R4_3), .I5(R5_3), .I6(R6_3), .I7(R7_3),
    .S0(RS_t[0]), .S1(RS_t[1]), .S2(RS_t[2]), .nOE(nRS_TO_A));  // open: W
  IC_74x251 Bit4_2 (
    .Y(REG_A[4]), .I0(R0_4), .I1(R1_4), .I2(R2_4), .I3(R3_4), .I4(R4_4), .I5(R5_4), .I6(R6_4), .I7(R7_4),
    .S0(RS_t[0]), .S1(RS_t[1]), .S2(RS_t[2]), .nOE(nRS_TO_A));  // open: W
  IC_74x251 Bit5_2 (
    .Y(REG_A[5]), .I0(R0_5), .I1(R1_5), .I2(R2_5), .I3(R3_5), .I4(R4_5), .I5(R5_5), .I6(R6_5), .I7(R7_5),
    .S0(RS_t[0]), .S1(RS_t[1]), .S2(RS_t[2]), .nOE(nRS_TO_A));  // open: W
  IC_74x251 Bit6_2 (
    .Y(REG_A[6]), .I0(R0_6), .I1(R1_6), .I2(R2_6), .I3(R3_6), .I4(R4_6), .I5(R5_6), .I6(R6_6), .I7(R7_6),
    .S0(RS_t[0]), .S1(RS_t[1]), .S2(RS_t[2]), .nOE(nRS_TO_A));  // open: W
  IC_74x251 Bit7_2 (
    .Y(REG_A[7]), .I0(R0_7), .I1(R1_7), .I2(R2_7), .I3(R3_7), .I4(R4_7), .I5(R5_7), .I6(R6_7), .I7(R7_7),
    .S0(RS_t[0]), .S1(RS_t[1]), .S2(RS_t[2]), .nOE(nRS_TO_A));  // open: W
  IC_74x251 Bit0_3 (
    .Y(REG_B[0]), .I0(R0_0), .I1(R1_0), .I2(R2_0), .I3(R3_0), .I4(R4_0), .I5(R5_0), .I6(R6_0), .I7(R7_0),
    .S0(RN_t[0]), .S1(RN_t[1]), .S2(RN_t[2]), .nOE(nRN_TO_B));  // open: W
  IC_74x251 Bit1_3 (
    .Y(REG_B[1]), .I0(R0_1), .I1(R1_1), .I2(R2_1), .I3(R3_1), .I4(R4_1), .I5(R5_1), .I6(R6_1), .I7(R7_1),
    .S0(RN_t[0]), .S1(RN_t[1]), .S2(RN_t[2]), .nOE(nRN_TO_B));  // open: W
  IC_74x251 Bit2_3 (
    .Y(REG_B[2]), .I0(R0_2), .I1(R1_2), .I2(R2_2), .I3(R3_2), .I4(R4_2), .I5(R5_2), .I6(R6_2), .I7(R7_2),
    .S0(RN_t[0]), .S1(RN_t[1]), .S2(RN_t[2]), .nOE(nRN_TO_B));  // open: W
  IC_74x251 Bit3_3 (
    .Y(REG_B[3]), .I0(R0_3), .I1(R1_3), .I2(R2_3), .I3(R3_3), .I4(R4_3), .I5(R5_3), .I6(R6_3), .I7(R7_3),
    .S0(RN_t[0]), .S1(RN_t[1]), .S2(RN_t[2]), .nOE(nRN_TO_B));  // open: W
  IC_74x251 Bit4_3 (
    .Y(REG_B[4]), .I0(R0_4), .I1(R1_4), .I2(R2_4), .I3(R3_4), .I4(R4_4), .I5(R5_4), .I6(R6_4), .I7(R7_4),
    .S0(RN_t[0]), .S1(RN_t[1]), .S2(RN_t[2]), .nOE(nRN_TO_B));  // open: W
  IC_74x251 Bit5_3 (
    .Y(REG_B[5]), .I0(R0_5), .I1(R1_5), .I2(R2_5), .I3(R3_5), .I4(R4_5), .I5(R5_5), .I6(R6_5), .I7(R7_5),
    .S0(RN_t[0]), .S1(RN_t[1]), .S2(RN_t[2]), .nOE(nRN_TO_B));  // open: W
  IC_74x251 Bit6_3 (
    .Y(REG_B[6]), .I0(R0_6), .I1(R1_6), .I2(R2_6), .I3(R3_6), .I4(R4_6), .I5(R5_6), .I6(R6_6), .I7(R7_6),
    .S0(RN_t[0]), .S1(RN_t[1]), .S2(RN_t[2]), .nOE(nRN_TO_B));  // open: W
  IC_74x251 Bit7_3 (
    .Y(REG_B[7]), .I0(R0_7), .I1(R1_7), .I2(R2_7), .I3(R3_7), .I4(R4_7), .I5(R5_7), .I6(R6_7), .I7(R7_7),
    .S0(RN_t[0]), .S1(RN_t[1]), .S2(RN_t[2]), .nOE(nRN_TO_B));  // open: W
  IC_74x251 Bit8 (
    .Y(REG_A[8]), .I0(R0_8), .I1(R1_8), .I2(R2_8), .I3(R3_8), .I4(R4_8), .I5(R5_8), .I6(R6_8), .I7(R7_8),
    .S0(RD_t[0]), .S1(RD_t[1]), .S2(RD_t[2]), .nOE(nRD_TO_A));  // open: W
  IC_74x251 Bit9 (
    .Y(REG_A[9]), .I0(R0_9), .I1(R1_9), .I2(R2_9), .I3(R3_9), .I4(R4_9), .I5(R5_9), .I6(R6_9), .I7(R7_9),
    .S0(RD_t[0]), .S1(RD_t[1]), .S2(RD_t[2]), .nOE(nRD_TO_A));  // open: W
  IC_74x251 Bit10 (
    .Y(REG_A[10]), .I0(R0_10), .I1(R1_10), .I2(R2_10), .I3(R3_10), .I4(R4_10), .I5(R5_10), .I6(R6_10),
    .I7(R7_10), .S0(RD_t[0]), .S1(RD_t[1]), .S2(RD_t[2]), .nOE(nRD_TO_A));  // open: W
  IC_74x251 Bit11 (
    .Y(REG_A[11]), .I0(R0_11), .I1(R1_11), .I2(R2_11), .I3(R3_11), .I4(R4_11), .I5(R5_11), .I6(R6_11),
    .I7(R7_11), .S0(RD_t[0]), .S1(RD_t[1]), .S2(RD_t[2]), .nOE(nRD_TO_A));  // open: W
  IC_74x251 Bit12 (
    .Y(REG_A[12]), .I0(R0_12), .I1(R1_12), .I2(R2_12), .I3(R3_12), .I4(R4_12), .I5(R5_12), .I6(R6_12),
    .I7(R7_12), .S0(RD_t[0]), .S1(RD_t[1]), .S2(RD_t[2]), .nOE(nRD_TO_A));  // open: W
  IC_74x251 Bit13 (
    .Y(REG_A[13]), .I0(R0_13), .I1(R1_13), .I2(R2_13), .I3(R3_13), .I4(R4_13), .I5(R5_13), .I6(R6_13),
    .I7(R7_13), .S0(RD_t[0]), .S1(RD_t[1]), .S2(RD_t[2]), .nOE(nRD_TO_A));  // open: W
  IC_74x251 Bit14 (
    .Y(REG_A[14]), .I0(R0_14), .I1(R1_14), .I2(R2_14), .I3(R3_14), .I4(R4_14), .I5(R5_14), .I6(R6_14),
    .I7(R7_14), .S0(RD_t[0]), .S1(RD_t[1]), .S2(RD_t[2]), .nOE(nRD_TO_A));  // open: W
  IC_74x251 Bit15 (
    .Y(REG_A[15]), .I0(R0_15), .I1(R1_15), .I2(R2_15), .I3(R3_15), .I4(R4_15), .I5(R5_15), .I6(R6_15),
    .I7(R7_15), .S0(RD_t[0]), .S1(RD_t[1]), .S2(RD_t[2]), .nOE(nRD_TO_A));  // open: W
  IC_74x251 Bit8_2 (
    .Y(REG_A[8]), .I0(R0_8), .I1(R1_8), .I2(R2_8), .I3(R3_8), .I4(R4_8), .I5(R5_8), .I6(R6_8), .I7(R7_8),
    .S0(RS_t[0]), .S1(RS_t[1]), .S2(RS_t[2]), .nOE(nRS_TO_A));  // open: W
  IC_74x251 Bit9_2 (
    .Y(REG_A[9]), .I0(R0_9), .I1(R1_9), .I2(R2_9), .I3(R3_9), .I4(R4_9), .I5(R5_9), .I6(R6_9), .I7(R7_9),
    .S0(RS_t[0]), .S1(RS_t[1]), .S2(RS_t[2]), .nOE(nRS_TO_A));  // open: W
  IC_74x251 Bit10_2 (
    .Y(REG_A[10]), .I0(R0_10), .I1(R1_10), .I2(R2_10), .I3(R3_10), .I4(R4_10), .I5(R5_10), .I6(R6_10),
    .I7(R7_10), .S0(RS_t[0]), .S1(RS_t[1]), .S2(RS_t[2]), .nOE(nRS_TO_A));  // open: W
  IC_74x251 Bit11_2 (
    .Y(REG_A[11]), .I0(R0_11), .I1(R1_11), .I2(R2_11), .I3(R3_11), .I4(R4_11), .I5(R5_11), .I6(R6_11),
    .I7(R7_11), .S0(RS_t[0]), .S1(RS_t[1]), .S2(RS_t[2]), .nOE(nRS_TO_A));  // open: W
  IC_74x251 Bit12_2 (
    .Y(REG_A[12]), .I0(R0_12), .I1(R1_12), .I2(R2_12), .I3(R3_12), .I4(R4_12), .I5(R5_12), .I6(R6_12),
    .I7(R7_12), .S0(RS_t[0]), .S1(RS_t[1]), .S2(RS_t[2]), .nOE(nRS_TO_A));  // open: W
  IC_74x251 Bit13_2 (
    .Y(REG_A[13]), .I0(R0_13), .I1(R1_13), .I2(R2_13), .I3(R3_13), .I4(R4_13), .I5(R5_13), .I6(R6_13),
    .I7(R7_13), .S0(RS_t[0]), .S1(RS_t[1]), .S2(RS_t[2]), .nOE(nRS_TO_A));  // open: W
  IC_74x251 Bit14_2 (
    .Y(REG_A[14]), .I0(R0_14), .I1(R1_14), .I2(R2_14), .I3(R3_14), .I4(R4_14), .I5(R5_14), .I6(R6_14),
    .I7(R7_14), .S0(RS_t[0]), .S1(RS_t[1]), .S2(RS_t[2]), .nOE(nRS_TO_A));  // open: W
  IC_74x251 Bit15_2 (
    .Y(REG_A[15]), .I0(R0_15), .I1(R1_15), .I2(R2_15), .I3(R3_15), .I4(R4_15), .I5(R5_15), .I6(R6_15),
    .I7(R7_15), .S0(RS_t[0]), .S1(RS_t[1]), .S2(RS_t[2]), .nOE(nRS_TO_A));  // open: W
  IC_74x251 Bit8_3 (
    .Y(REG_B[8]), .I0(R0_8), .I1(R1_8), .I2(R2_8), .I3(R3_8), .I4(R4_8), .I5(R5_8), .I6(R6_8), .I7(R7_8),
    .S0(RN_t[0]), .S1(RN_t[1]), .S2(RN_t[2]), .nOE(nRN_TO_B));  // open: W
  IC_74x251 Bit9_3 (
    .Y(REG_B[9]), .I0(R0_9), .I1(R1_9), .I2(R2_9), .I3(R3_9), .I4(R4_9), .I5(R5_9), .I6(R6_9), .I7(R7_9),
    .S0(RN_t[0]), .S1(RN_t[1]), .S2(RN_t[2]), .nOE(nRN_TO_B));  // open: W
  IC_74x251 Bit10_3 (
    .Y(REG_B[10]), .I0(R0_10), .I1(R1_10), .I2(R2_10), .I3(R3_10), .I4(R4_10), .I5(R5_10), .I6(R6_10),
    .I7(R7_10), .S0(RN_t[0]), .S1(RN_t[1]), .S2(RN_t[2]), .nOE(nRN_TO_B));  // open: W
  IC_74x251 Bit11_3 (
    .Y(REG_B[11]), .I0(R0_11), .I1(R1_11), .I2(R2_11), .I3(R3_11), .I4(R4_11), .I5(R5_11), .I6(R6_11),
    .I7(R7_11), .S0(RN_t[0]), .S1(RN_t[1]), .S2(RN_t[2]), .nOE(nRN_TO_B));  // open: W
  IC_74x251 Bit12_3 (
    .Y(REG_B[12]), .I0(R0_12), .I1(R1_12), .I2(R2_12), .I3(R3_12), .I4(R4_12), .I5(R5_12), .I6(R6_12),
    .I7(R7_12), .S0(RN_t[0]), .S1(RN_t[1]), .S2(RN_t[2]), .nOE(nRN_TO_B));  // open: W
  IC_74x251 Bit13_3 (
    .Y(REG_B[13]), .I0(R0_13), .I1(R1_13), .I2(R2_13), .I3(R3_13), .I4(R4_13), .I5(R5_13), .I6(R6_13),
    .I7(R7_13), .S0(RN_t[0]), .S1(RN_t[1]), .S2(RN_t[2]), .nOE(nRN_TO_B));  // open: W
  IC_74x251 Bit14_3 (
    .Y(REG_B[14]), .I0(R0_14), .I1(R1_14), .I2(R2_14), .I3(R3_14), .I4(R4_14), .I5(R5_14), .I6(R6_14),
    .I7(R7_14), .S0(RN_t[0]), .S1(RN_t[1]), .S2(RN_t[2]), .nOE(nRN_TO_B));  // open: W
  IC_74x251 Bit15_3 (
    .Y(REG_B[15]), .I0(R0_15), .I1(R1_15), .I2(R2_15), .I3(R3_15), .I4(R4_15), .I5(R5_15), .I6(R6_15),
    .I7(R7_15), .S0(RN_t[0]), .S1(RN_t[1]), .S2(RN_t[2]), .nOE(nRN_TO_B));  // open: W

  // Other names for the same wires on the sheet: RD_A_n = nRD_TO_A; RN_B_n = nRN_TO_B; RS_A_n = nRS_TO_A
endmodule

// Imm
module ImmDecoderV (
  input  nRESET,
  input  CLK,
  input  nOE,
  input  [15:0] IR,
  output [15:0] IMM_OUT
);

  wire Im_2_out, Im_out, J_out, P_out, PFIX_Reg_2_q4, Type_I1_a, Type_I2_a, Zero_Sign_Ext_y1,
       Zero_Sign_Ext_y2;
  wire [11:5] Type_P_q1;
  wire [15:5] PFIX_Reg_q1;

  nand P (P_out, IR[13], IR[14], IR[15]);
  nand Im (Im_out, IR[11], IR[12], 1'b1);
  or J (J_out, IR[14], IR[15]);
  IC_74x153 Zero_Sign_Ext (
    .Y1(Zero_Sign_Ext_y1), .Y2(Zero_Sign_Ext_y2), .C1_0(1'b0), .C1_1(1'b0), .C1_2(IR[10]), .C1_3(1'b0),
    .C2_0(1'b0), .C2_1(1'b0), .C2_2(IR[2]), .C2_3(1'b0), .A(IR[12]), .B(IR[13]), .nG1(1'b0), .nG2(IR[11]));
  or Im_2 (Im_2_out, P_out, Im_out);
  IC_74x3251 Type_I2 (
    .A(Type_I2_a), .B1(1'b1), .B2(1'b1), .B3(1'b1), .B4(1'b1), .B5(1'b1), .B6(1'b0), .B7(1'b0), .B8(1'b1),
    .S0(IR[13]), .S1(IR[14]), .S2(IR[15]), .nOE(1'b0));
  IC_74x3251 Type_I1 (
    .A(Type_I1_a), .B1(1'b1), .B2(1'b1), .B3(1'b0), .B4(1'b0), .B5(1'b0), .B6(1'b1), .B7(1'b1), .B8(1'b1),
    .S0(IR[13]), .S1(IR[14]), .S2(IR[15]), .nOE(1'b0));
  IC_74x541 Type_P (
    .Q1(Type_P_q1[5]), .Q2(Type_P_q1[6]), .Q3(Type_P_q1[7]), .Q4(Type_P_q1[8]), .Q5(Type_P_q1[9]),
    .Q6(Type_P_q1[10]), .Q7(Type_P_q1[11]), .I1(IR[0]), .I2(IR[1]), .I3(IR[2]), .I4(IR[3]), .I5(IR[4]),
    .I6(IR[5]), .I7(1'b0), .I8(1'b0), .nOE1(1'b0), .nOE2(P_out));  // open: Q8
  IC_74x541 Type_I2_2 (
    .Q1(Type_P_q1[5]), .Q2(Type_P_q1[6]), .Q3(Type_P_q1[7]), .Q4(Type_P_q1[8]), .Q5(Type_P_q1[9]),
    .Q6(Type_P_q1[10]), .Q7(Type_P_q1[11]), .I1(Zero_Sign_Ext_y1), .I2(Zero_Sign_Ext_y1),
    .I3(Zero_Sign_Ext_y1), .I4(Zero_Sign_Ext_y1), .I5(Zero_Sign_Ext_y1), .I6(Zero_Sign_Ext_y1),
    .I7(Zero_Sign_Ext_y1), .I8(1'b0), .nOE1(1'b0), .nOE2(Type_I2_a));  // open: Q8
  IC_74x541 Type_I1_2 (
    .Q1(Type_P_q1[5]), .Q2(Type_P_q1[6]), .Q3(Type_P_q1[7]), .Q4(Type_P_q1[8]), .Q5(Type_P_q1[9]),
    .Q6(Type_P_q1[10]), .Q7(Type_P_q1[11]), .I1(IR[0]), .I2(IR[1]), .I3(IR[2]), .I4(Zero_Sign_Ext_y2),
    .I5(Zero_Sign_Ext_y2), .I6(Zero_Sign_Ext_y2), .I7(Zero_Sign_Ext_y2), .I8(1'b0), .nOE1(1'b0),
    .nOE2(Type_I1_a));  // open: Q8
  IC_74x541 Type_J (
    .Q1(Type_P_q1[5]), .Q2(Type_P_q1[6]), .Q3(Type_P_q1[7]), .Q4(Type_P_q1[8]), .Q5(Type_P_q1[9]),
    .Q6(Type_P_q1[10]), .Q7(Type_P_q1[11]), .I1(IR[0]), .I2(IR[1]), .I3(IR[2]), .I4(IR[3]), .I5(IR[3]),
    .I6(IR[3]), .I7(IR[3]), .I8(1'b0), .nOE1(1'b0), .nOE2(J_out));  // open: Q8
  // IC_74x11244 ic_74x11244_1: pin names not known
  IC_74x273 PFIX_Reg (
    .Q1(PFIX_Reg_q1[5]), .Q2(PFIX_Reg_q1[6]), .Q3(PFIX_Reg_q1[7]), .Q4(PFIX_Reg_q1[8]), .Q5(PFIX_Reg_q1[9]),
    .Q6(PFIX_Reg_q1[10]), .Q7(PFIX_Reg_q1[11]), .Q8(PFIX_Reg_q1[12]), .D1(IR[6]), .D2(IR[7]), .D3(IR[8]),
    .D4(IR[9]), .D5(IR[10]), .D6(Type_P_q1[5]), .D7(Type_P_q1[6]), .D8(Type_P_q1[7]), .CLK(CLK), .nMR(nRESET));  // open: Probe
  IC_74175 PFIX_Reg_2 (
    .Q2(PFIX_Reg_q1[14]), .Q3(PFIX_Reg_q1[15]), .Q1(PFIX_Reg_q1[13]), .Q4(PFIX_Reg_2_q4), .D2(Type_P_q1[9]),
    .D3(Type_P_q1[10]), .D1(Type_P_q1[8]), .D4(Im_2_out), .CLK(CLK), .CLR(nRESET));  // open: R2, R3, R4, R1
  // IC_74x241 ic_74x241_1: pin names not known
  IC_74x257 _0__3 (
    .Y1(IMM_OUT[0]), .Y2(IMM_OUT[1]), .Y3(IMM_OUT[2]), .Y4(IMM_OUT[3]), .I1_0(IR[6]), .I2_0(IR[6]),
    .I1_1(IR[7]), .I2_1(IR[7]), .I1_2(IR[8]), .I2_2(IR[8]), .I1_3(IR[9]), .I2_3(IR[9]), .nA_B(PFIX_Reg_2_q4),
    .nOE(nOE));
  IC_74x257 _4__7 (
    .Y1(IMM_OUT[4]), .Y2(IMM_OUT[5]), .Y3(IMM_OUT[6]), .Y4(IMM_OUT[7]), .I1_0(IR[10]), .I2_0(IR[10]),
    .I1_1(PFIX_Reg_q1[5]), .I2_1(Type_P_q1[5]), .I1_2(PFIX_Reg_q1[6]), .I2_2(Type_P_q1[6]),
    .I1_3(PFIX_Reg_q1[7]), .I2_3(Type_P_q1[7]), .nA_B(PFIX_Reg_2_q4), .nOE(nOE));
  IC_74x257 _8__11 (
    .Y1(IMM_OUT[8]), .Y2(IMM_OUT[9]), .Y3(IMM_OUT[10]), .Y4(IMM_OUT[11]), .I1_0(PFIX_Reg_q1[8]),
    .I2_0(Type_P_q1[8]), .I1_1(PFIX_Reg_q1[9]), .I2_1(Type_P_q1[9]), .I1_2(PFIX_Reg_q1[10]),
    .I2_2(Type_P_q1[10]), .I1_3(PFIX_Reg_q1[11]), .I2_3(Type_P_q1[11]), .nA_B(PFIX_Reg_2_q4), .nOE(nOE));
  IC_74x257 _12__15 (
    .Y1(IMM_OUT[12]), .Y2(IMM_OUT[13]), .Y3(IMM_OUT[14]), .Y4(IMM_OUT[15]), .I1_0(PFIX_Reg_q1[12]),
    .I2_0(Type_P_q1[11]), .I1_1(PFIX_Reg_q1[13]), .I2_1(Type_P_q1[11]), .I1_2(PFIX_Reg_q1[14]),
    .I2_2(Type_P_q1[11]), .I1_3(PFIX_Reg_q1[15]), .I2_3(Type_P_q1[11]), .nA_B(PFIX_Reg_2_q4), .nOE(nOE));

  // Other names for the same wires on the sheet: CLR_n = nRESET; OE_n = nOE
endmodule

// Imm
module ImmDecoderVBo (
  input  nRESET,
  input  CLK,
  input  nOE,
  input  [15:0] IR,
  output [15:0] IMM_OUT
);

  wire and_1_out, PFIX_Reg_2_q4, PFIX_Reg_2_r4, Type_I1_y, Type_I2_y, Type_P__Type_J_y1, Type_P__Type_J_y2,
       Zero_Sign_Ext_y1, Zero_Sign_Ext_y2;
  wire [11:5] Type_P_a1;
  wire [15:5] PFIX_Reg_q1;

  IC_74x153 Zero_Sign_Ext (
    .Y1(Zero_Sign_Ext_y1), .Y2(Zero_Sign_Ext_y2), .C1_0(1'b0), .C1_1(1'b0), .C1_2(IR[10]), .C1_3(1'b0),
    .C2_0(1'b0), .C2_1(1'b0), .C2_2(IR[2]), .C2_3(1'b0), .A(IR[12]), .B(IR[13]), .nG1(1'b0), .nG2(IR[11]));
  IC_74x153 Type_P__Type_J (
    .Y1(Type_P__Type_J_y1), .Y2(Type_P__Type_J_y2), .C1_0(1'b0), .C1_1(1'b0), .C1_2(1'b0), .C1_3(IR[13]),
    .C2_0(1'b1), .C2_1(1'b0), .C2_2(1'b0), .C2_3(1'b0), .A(IR[14]), .B(IR[15]), .nG1(1'b0), .nG2(1'b0));
  IC_74x151 Type_I2 (
    .Y(Type_I2_y), .D1(1'b0), .D2(1'b0), .D3(1'b0), .D4(1'b0), .D5(1'b1), .D6(1'b1), .D7(1'b0), .A(IR[13]),
    .B(IR[14]), .C(IR[15]), .nG(1'b0), .D0(1'b0));  // open: W
  IC_74x151 Type_I1 (
    .Y(Type_I1_y), .D1(1'b0), .D2(1'b1), .D3(1'b1), .D4(1'b1), .D5(1'b0), .D6(1'b0), .D7(1'b0), .A(IR[13]),
    .B(IR[14]), .C(IR[15]), .nG(1'b0), .D0(1'b0));  // open: W
  and and_1 (and_1_out, IR[11], IR[12], Type_P__Type_J_y1);
  IC_74x3345 Type_P (
    .A3(Type_P_a1[7]), .A4(Type_P_a1[8]), .A5(Type_P_a1[9]), .A6(Type_P_a1[10]), .A7(Type_P_a1[11]),
    .A1(Type_P_a1[5]), .A2(Type_P_a1[6]), .B3(IR[2]), .B4(IR[3]), .B5(IR[4]), .B6(IR[5]), .B7(1'b0),
    .B8(1'b0), .OE(Type_P__Type_J_y1), .nOE(1'b1), .B1(IR[0]), .B2(IR[1]));  // open: A8
  IC_74x3345 Type_I2_2 (
    .A3(Type_P_a1[7]), .A4(Type_P_a1[8]), .A5(Type_P_a1[9]), .A6(Type_P_a1[10]), .A7(Type_P_a1[11]),
    .A1(Type_P_a1[5]), .A2(Type_P_a1[6]), .B3(Zero_Sign_Ext_y1), .B4(Zero_Sign_Ext_y1),
    .B5(Zero_Sign_Ext_y1), .B6(Zero_Sign_Ext_y1), .B7(Zero_Sign_Ext_y1), .B8(1'b0), .OE(Type_I2_y),
    .nOE(1'b1), .B1(Zero_Sign_Ext_y1), .B2(Zero_Sign_Ext_y1));  // open: A8
  IC_74x3345 Type_I1_2 (
    .A3(Type_P_a1[7]), .A4(Type_P_a1[8]), .A5(Type_P_a1[9]), .A6(Type_P_a1[10]), .A7(Type_P_a1[11]),
    .A1(Type_P_a1[5]), .A2(Type_P_a1[6]), .B3(IR[2]), .B4(Zero_Sign_Ext_y2), .B5(Zero_Sign_Ext_y2),
    .B6(Zero_Sign_Ext_y2), .B7(Zero_Sign_Ext_y2), .B8(1'b0), .OE(Type_I1_y), .nOE(1'b1), .B1(IR[0]),
    .B2(IR[1]));  // open: A8
  IC_74x3345 Type_J (
    .A3(Type_P_a1[7]), .A4(Type_P_a1[8]), .A5(Type_P_a1[9]), .A6(Type_P_a1[10]), .A7(Type_P_a1[11]),
    .A1(Type_P_a1[5]), .A2(Type_P_a1[6]), .B3(IR[2]), .B4(IR[3]), .B5(IR[3]), .B6(IR[3]), .B7(IR[3]),
    .B8(1'b0), .OE(Type_P__Type_J_y2), .nOE(1'b1), .B1(IR[0]), .B2(IR[1]));  // open: A8
  IC_74x273 PFIX_Reg (
    .Q1(PFIX_Reg_q1[5]), .Q2(PFIX_Reg_q1[6]), .Q3(PFIX_Reg_q1[7]), .Q4(PFIX_Reg_q1[8]), .Q5(PFIX_Reg_q1[9]),
    .Q6(PFIX_Reg_q1[10]), .Q7(PFIX_Reg_q1[11]), .Q8(PFIX_Reg_q1[12]), .D1(IR[6]), .D2(IR[7]), .D3(IR[8]),
    .D4(IR[9]), .D5(IR[10]), .D6(Type_P_a1[5]), .D7(Type_P_a1[6]), .D8(Type_P_a1[7]), .CLK(CLK), .nMR(nRESET));  // open: Probe
  IC_74175 PFIX_Reg_2 (
    .Q2(PFIX_Reg_q1[14]), .Q3(PFIX_Reg_q1[15]), .Q1(PFIX_Reg_q1[13]), .Q4(PFIX_Reg_2_q4), .R4(PFIX_Reg_2_r4),
    .D2(Type_P_a1[9]), .D3(Type_P_a1[10]), .D1(Type_P_a1[8]), .D4(and_1_out), .CLK(CLK), .CLR(nRESET));  // open: R2, R3, R1
  IC_74x541 IMM (
    .Q1(IMM_OUT[0]), .Q2(IMM_OUT[1]), .Q3(IMM_OUT[2]), .Q4(IMM_OUT[3]), .Q5(IMM_OUT[4]), .Q6(IMM_OUT[5]),
    .Q7(IMM_OUT[6]), .Q8(IMM_OUT[7]), .I1(IR[6]), .I2(IR[7]), .I3(IR[8]), .I4(IR[9]), .I5(IR[10]),
    .I6(PFIX_Reg_q1[5]), .I7(PFIX_Reg_q1[6]), .I8(PFIX_Reg_q1[7]), .nOE1(PFIX_Reg_2_r4), .nOE2(nOE));
  IC_74x541 IMM_2 (
    .Q1(IMM_OUT[8]), .Q2(IMM_OUT[9]), .Q3(IMM_OUT[10]), .Q4(IMM_OUT[11]), .Q5(IMM_OUT[12]), .Q6(IMM_OUT[13]),
    .Q7(IMM_OUT[14]), .Q8(IMM_OUT[15]), .I1(PFIX_Reg_q1[8]), .I2(PFIX_Reg_q1[9]), .I3(PFIX_Reg_q1[10]),
    .I4(PFIX_Reg_q1[11]), .I5(PFIX_Reg_q1[12]), .I6(PFIX_Reg_q1[13]), .I7(PFIX_Reg_q1[14]),
    .I8(PFIX_Reg_q1[15]), .nOE1(PFIX_Reg_2_r4), .nOE2(nOE));
  IC_74x541 IMM_3 (
    .Q1(IMM_OUT[0]), .Q2(IMM_OUT[1]), .Q3(IMM_OUT[2]), .Q4(IMM_OUT[3]), .Q5(IMM_OUT[4]), .Q6(IMM_OUT[5]),
    .Q7(IMM_OUT[6]), .Q8(IMM_OUT[7]), .I1(IR[6]), .I2(IR[7]), .I3(IR[8]), .I4(IR[9]), .I5(IR[10]),
    .I6(Type_P_a1[5]), .I7(Type_P_a1[6]), .I8(Type_P_a1[7]), .nOE1(PFIX_Reg_2_q4), .nOE2(nOE));
  IC_74x541 IMM_4 (
    .Q1(IMM_OUT[8]), .Q2(IMM_OUT[9]), .Q3(IMM_OUT[10]), .Q4(IMM_OUT[11]), .Q5(IMM_OUT[12]), .Q6(IMM_OUT[13]),
    .Q7(IMM_OUT[14]), .Q8(IMM_OUT[15]), .I1(Type_P_a1[8]), .I2(Type_P_a1[9]), .I3(Type_P_a1[10]),
    .I4(Type_P_a1[11]), .I5(Type_P_a1[11]), .I6(Type_P_a1[11]), .I7(Type_P_a1[11]), .I8(Type_P_a1[11]),
    .nOE1(PFIX_Reg_2_q4), .nOE2(nOE));

  // Other names for the same wires on the sheet: CLR_n = nRESET; OE_n = nOE
endmodule

// SWAP - MEM - EXT
module SRAM1 (
  input  RESET,
  input  CLK,
  input  cpWRMAR,
  input  WRMAR,
  input  nExt,
  input  SEx,
  input  ISw,
  input  OSh,
  input  nIE,
  input  nOE,
  input  [15:0] A_BUS_IN,
  input  [15:0] Q_BUS_IN,
  output [15:0] Q_BUS_OUT
);

  wire Addr0, and_1_out, and_2_out, and_3_out, and_4_out, and_5_out, and_6_out, CE0_n, CE1_n, CE_a1, CE_a2,
       ic_74x1g3157_1_a, ic_74x1g3157_2_a, ic_74x74half_1_r1, ic_74x3257_1_a1, ISwap, MemCy2_q1, MemCy2_q2,
       MemCy2_q3, MemCy2_q4, MemCy2_q6, MemCy2_q8, MOE_n, MWE_n, OExt_n, or_1_out, OShift, SExt, undriven;
  wire [7:0] ic_74x32571_1_b1_1, ic_74x32571_1_b2_1;
  wire [14:0] MAR_q2;

  // IC_74x257 ic_74x257_1: pin names not known
  IC_74x273 MemCy2 (
    .Q1(MemCy2_q1), .Q2(MemCy2_q2), .Q3(MemCy2_q3), .Q4(MemCy2_q4), .Q6(MemCy2_q6), .Q8(MemCy2_q8),
    .D1(nExt), .D2(SEx), .D3(ISw), .D4(OSh), .D6(WRMAR), .D8(ic_74x3257_1_a1), .CLK(CLK), .nMR(RESET));  // open: Probe, Q5, Q7, D5, D7
  IC_74x32571 ic_74x32571_1 (
    .B1_2(ic_74x32571_1_b1_1[1]), .B1_3(ic_74x32571_1_b1_1[2]), .B1_4(ic_74x32571_1_b1_1[3]),
    .B2_1(ic_74x32571_1_b2_1[0]), .B2_2(ic_74x32571_1_b2_1[1]), .B2_3(ic_74x32571_1_b2_1[2]),
    .B2_4(ic_74x32571_1_b2_1[3]), .B1_1(ic_74x32571_1_b1_1[0]), .S(ISwap), .nOE(nIE), .A1(A_BUS_IN[0]),
    .A2(A_BUS_IN[1]), .A3(A_BUS_IN[2]), .A4(A_BUS_IN[3]));
  IC_74x32571 ic_74x32571_2 (
    .B1_2(ic_74x32571_1_b1_1[5]), .B1_3(ic_74x32571_1_b1_1[6]), .B1_4(ic_74x32571_1_b1_1[7]),
    .B2_1(ic_74x32571_1_b2_1[4]), .B2_2(ic_74x32571_1_b2_1[5]), .B2_3(ic_74x32571_1_b2_1[6]),
    .B2_4(ic_74x32571_1_b2_1[7]), .B1_1(ic_74x32571_1_b1_1[4]), .S(ISwap), .nOE(nIE), .A1(A_BUS_IN[4]),
    .A2(A_BUS_IN[5]), .A3(A_BUS_IN[6]), .A4(A_BUS_IN[7]));
  IC_74x32571 ic_74x32571_3 (
    .B1_2(ic_74x32571_1_b2_1[1]), .B1_3(ic_74x32571_1_b2_1[2]), .B1_4(ic_74x32571_1_b2_1[3]),
    .B2_1(ic_74x32571_1_b1_1[0]), .B2_2(ic_74x32571_1_b1_1[1]), .B2_3(ic_74x32571_1_b1_1[2]),
    .B2_4(ic_74x32571_1_b1_1[3]), .B1_1(ic_74x32571_1_b2_1[0]), .S(ISwap), .nOE(nIE), .A1(A_BUS_IN[8]),
    .A2(A_BUS_IN[9]), .A3(A_BUS_IN[10]), .A4(A_BUS_IN[11]));
  IC_74x32571 ic_74x32571_4 (
    .B1_2(ic_74x32571_1_b2_1[5]), .B1_3(ic_74x32571_1_b2_1[6]), .B1_4(ic_74x32571_1_b2_1[7]),
    .B2_1(ic_74x32571_1_b1_1[4]), .B2_2(ic_74x32571_1_b1_1[5]), .B2_3(ic_74x32571_1_b1_1[6]),
    .B2_4(ic_74x32571_1_b1_1[7]), .B1_1(ic_74x32571_1_b2_1[4]), .S(ISwap), .nOE(nIE), .A1(A_BUS_IN[12]),
    .A2(A_BUS_IN[13]), .A3(A_BUS_IN[14]), .A4(A_BUS_IN[15]));
  IC_74x273 MAR (
    .Q1(Addr0), .Q2(MAR_q2[0]), .Q3(MAR_q2[1]), .Q4(MAR_q2[2]), .Q5(MAR_q2[3]), .Q6(MAR_q2[4]),
    .Q7(MAR_q2[5]), .Q8(MAR_q2[6]), .D1(Q_BUS_IN[0]), .D2(Q_BUS_IN[1]), .D3(Q_BUS_IN[2]), .D4(Q_BUS_IN[3]),
    .D5(Q_BUS_IN[4]), .D6(Q_BUS_IN[5]), .D7(Q_BUS_IN[6]), .D8(Q_BUS_IN[7]), .CLK(cpWRMAR), .nMR(1'b1));  // open: Probe
  IC_74x273 MAR_2 (
    .Q1(MAR_q2[7]), .Q2(MAR_q2[8]), .Q3(MAR_q2[9]), .Q4(MAR_q2[10]), .Q5(MAR_q2[11]), .Q6(MAR_q2[12]),
    .Q7(MAR_q2[13]), .Q8(MAR_q2[14]), .D1(Q_BUS_IN[8]), .D2(Q_BUS_IN[9]), .D3(Q_BUS_IN[10]),
    .D4(Q_BUS_IN[11]), .D5(Q_BUS_IN[12]), .D6(Q_BUS_IN[13]), .D7(Q_BUS_IN[14]), .D8(Q_BUS_IN[15]),
    .CLK(cpWRMAR), .nMR(1'b1));  // open: Probe
  and and_1 (and_1_out, MemCy2_q3, Addr0);
  and and_2 (and_2_out, Addr0, MemCy2_q4);
  IC_74x3253 CE (
    .A1(CE_a1), .A2(CE_a2), .B1_1(1'b0), .B1_2(1'b0), .B1_3(1'b0), .B1_4(1'b1), .B2_1(1'b0), .B2_2(1'b0),
    .B2_3(1'b1), .B2_4(1'b0), .S0(Addr0), .S1(MemCy2_q3), .nOE1(1'b0), .nOE2(1'b0));
  IC_74x1G3157 ic_74x1g3157_1 (
    .A(ic_74x1g3157_1_a), .B1(ic_74x32571_1_b1_1[7]), .B2(ic_74x32571_1_b2_1[7]), .S(OShift));
  IC_74x1G3157 ic_74x1g3157_2 (.A(ic_74x1g3157_2_a), .B1(1'b0), .B2(ic_74x1g3157_1_a), .S(SExt));
  and and_3 (and_3_out, ~MOE_n, MWE_n, ~CE0_n);  // AND_Gate
  and and_4 (and_4_out, ~CE0_n, ~MWE_n);  // AND_Gate
  and and_5 (and_5_out, ~MOE_n, MWE_n, ~CE1_n);  // AND_Gate
  and and_6 (and_6_out, ~CE1_n, ~MWE_n);  // AND_Gate
  RAM #(.addrWidth(15), .databus("bidir"), .trigger("low")) Low_Byte (
    .addr(MAR_q2), .data(ic_74x32571_1_b1_1));  // open: we, oe, clk
  RAM #(.addrWidth(15), .databus("bidir"), .trigger("low")) High_Byte (
    .addr(MAR_q2), .data(ic_74x32571_1_b2_1));  // open: we, oe, clk
  IC_74x3257 CtrlSel (
    .A1(OExt_n), .A2(SExt), .A3(ISwap), .A4(OShift), .B2_1(MemCy2_q1), .B1_2(SEx), .B2_2(MemCy2_q2),
    .B1_3(ISw), .B2_3(and_1_out), .B1_4(OSh), .B2_4(and_2_out), .S(MemCy2_q6), .nOE(1'b0), .B1_1(nExt));
  IC_74x1G3157 ic_74x1g3157_3 (.A(MWE_n), .B1(1'b1), .B2(ic_74x3257_1_a1), .S(MemCy2_q8));
  IC_74x3257 ic_74x3257_1 (
    .A1(ic_74x3257_1_a1), .A2(MOE_n), .A3(CE0_n), .A4(CE1_n), .B2_1(nIE), .B1_2(1'b1), .B2_2(nOE),
    .B1_3(1'b1), .B2_3(CE_a1), .B1_4(1'b1), .B2_4(CE_a2), .S(MemCy2_q6), .nOE(1'b0), .B1_1(1'b1));
  IC_74x3257 ic_74x3257_2 (
    .A1(Q_BUS_OUT[0]), .A2(Q_BUS_OUT[1]), .A3(Q_BUS_OUT[2]), .A4(Q_BUS_OUT[3]), .B2_1(ic_74x32571_1_b2_1[0]),
    .B1_2(ic_74x32571_1_b1_1[1]), .B2_2(ic_74x32571_1_b2_1[1]), .B1_3(ic_74x32571_1_b1_1[2]),
    .B2_3(ic_74x32571_1_b2_1[2]), .B1_4(ic_74x32571_1_b1_1[3]), .B2_4(ic_74x32571_1_b2_1[3]), .S(OShift),
    .nOE(nOE), .B1_1(ic_74x32571_1_b1_1[0]));
  IC_74x3257 ic_74x3257_3 (
    .A1(Q_BUS_OUT[4]), .A2(Q_BUS_OUT[5]), .A3(Q_BUS_OUT[6]), .A4(Q_BUS_OUT[7]), .B2_1(ic_74x32571_1_b2_1[4]),
    .B1_2(ic_74x32571_1_b1_1[5]), .B2_2(ic_74x32571_1_b2_1[5]), .B1_3(ic_74x32571_1_b1_1[6]),
    .B2_3(ic_74x32571_1_b2_1[6]), .B1_4(ic_74x32571_1_b1_1[7]), .B2_4(ic_74x32571_1_b2_1[7]), .S(OShift),
    .nOE(nOE), .B1_1(ic_74x32571_1_b1_1[4]));
  IC_74x3257 ic_74x3257_4 (
    .A1(Q_BUS_OUT[8]), .A2(Q_BUS_OUT[9]), .A3(Q_BUS_OUT[10]), .A4(Q_BUS_OUT[11]),
    .B2_1(ic_74x32571_1_b2_1[0]), .B1_2(ic_74x1g3157_2_a), .B2_2(ic_74x32571_1_b2_1[1]),
    .B1_3(ic_74x1g3157_2_a), .B2_3(ic_74x32571_1_b2_1[2]), .B1_4(ic_74x1g3157_2_a),
    .B2_4(ic_74x32571_1_b2_1[3]), .S(OExt_n), .nOE(nOE), .B1_1(ic_74x1g3157_2_a));
  IC_74x3257 ic_74x3257_5 (
    .A1(Q_BUS_OUT[12]), .A2(Q_BUS_OUT[13]), .A3(Q_BUS_OUT[14]), .A4(Q_BUS_OUT[15]),
    .B2_1(ic_74x32571_1_b2_1[4]), .B1_2(ic_74x1g3157_2_a), .B2_2(ic_74x32571_1_b2_1[5]),
    .B1_3(ic_74x1g3157_2_a), .B2_3(ic_74x32571_1_b2_1[6]), .B1_4(ic_74x1g3157_2_a),
    .B2_4(ic_74x32571_1_b2_1[7]), .S(OExt_n), .nOE(nOE), .B1_1(ic_74x1g3157_2_a));
  IC_74x74half ic_74x74half_1 (
    .R1(ic_74x74half_1_r1), .CLK1(CLK), .CLR1(1'b1), .SET1(1'b1), .D1(undriven));  // open: Q1
  or or_1 (or_1_out, ic_74x74half_1_r1, undriven);

  // Other names for the same wires on the sheet: CLK_WRMAR = cpWRMAR; CLR_n = RESET; IE_n = nIE; MEM = WRMAR;
  //   OE_n = nOE

  // Notes on the sheet:
  //   Operation
  //   ---------
  //   ST.W
  //   ST.B
  //   LD.W
  //   LD.SB
  //   LD.ZB
  //   SWAPB
  //   SEXT
  //   ZEXT
  //   ASR8
  //   LSR8
  //   LSL8
  //           CYCLE 1
  //   Mem nIE nOE nEx SEx ISw OSh
  //   ---------------------------
  //    1   1   1   x   x   0   x 
  //    1   1   1   x   x   1   x
  //    1   1   1   1   x   0   0
  //    1   1   1   0   1   0   1
  //    1   1   1   0   0   0   1
  //    0   0   0   1   x   1   0
  //    0   0   0   0   1   0   0
  //    0   0   0   0   0   0   0
  //    0   0   0   0   1   0   1
  //    0   0   0   0   0   0   1
  //    0   0   0   0   0   1   0
  //            CYCLE 2
  //   Mem nIE nOE nEx SEx ISw OSh
  //   ---------------------------
  //    0   0   1   x   x   x   x 
  //    0   0   1   x   x   x   x
  //    0   1   0   x   x   x   x
  //    0   1   0   x   x   x   x
  //    0   1   0   x   x   x   x
  //    -   -   -   -   -   -   -
  //    -   -   -   -   -   -   -
  //    -   -   -   -   -   -   -
  //    -   -   -   -   -   -   -
  //    -   -   -   -   -   -   -
  //    -   -   -   -   -   -   -
endmodule

module SRAMV (
  input  CLK,
  input  cpWRMAR,
  input  nIE,
  input  nOE,
  input  Wrd,
  input  SEx,
  input  nST,
  input  nLD,
  input  [15:0] A_BUS_IN,
  input  [15:0] Q_BUS_IN,
  output [15:0] Q_BUS_OUT
);

  wire Addr0, and_1_out, and_2_out, and_3_out, and_4_out, CE0_n, CE1_n, ic_74x1g3157_1_a, ic_74x1g3157_2_a,
       ic_74x74half_1_r1, ISwap, MWE_n, Oext_n, OSwap;
  wire [7:0] High_Byte_data, Low_Byte_data;
  wire [14:0] MAR_q2;

  IC_74x153 ic_74x153_1 (
    .Y1(ISwap), .Y2(OSwap), .C1_0(1'b0), .C1_1(Addr0), .C1_2(1'b0), .C1_3(1'b0), .C2_0(1'b0), .C2_1(1'b0),
    .C2_2(Addr0), .C2_3(1'b0), .A(nLD), .B(nIE), .nG1(Wrd), .nG2(Wrd));
  IC_74x273 MAR (
    .Q1(Addr0), .Q2(MAR_q2[0]), .Q3(MAR_q2[1]), .Q4(MAR_q2[2]), .Q5(MAR_q2[3]), .Q6(MAR_q2[4]),
    .Q7(MAR_q2[5]), .Q8(MAR_q2[6]), .D1(Q_BUS_IN[0]), .D2(Q_BUS_IN[1]), .D3(Q_BUS_IN[2]), .D4(Q_BUS_IN[3]),
    .D5(Q_BUS_IN[4]), .D6(Q_BUS_IN[5]), .D7(Q_BUS_IN[6]), .D8(Q_BUS_IN[7]), .CLK(cpWRMAR), .nMR(1'b1));  // open: Probe
  IC_74x273 MAR_2 (
    .Q1(MAR_q2[7]), .Q2(MAR_q2[8]), .Q3(MAR_q2[9]), .Q4(MAR_q2[10]), .Q5(MAR_q2[11]), .Q6(MAR_q2[12]),
    .Q7(MAR_q2[13]), .Q8(MAR_q2[14]), .D1(Q_BUS_IN[8]), .D2(Q_BUS_IN[9]), .D3(Q_BUS_IN[10]),
    .D4(Q_BUS_IN[11]), .D5(Q_BUS_IN[12]), .D6(Q_BUS_IN[13]), .D7(Q_BUS_IN[14]), .D8(Q_BUS_IN[15]),
    .CLK(cpWRMAR), .nMR(1'b1));  // open: Probe
  IC_74x153 ic_74x153_2 (
    .Y1(CE0_n), .Y2(CE1_n), .C1_0(1'b0), .C1_1(1'b1), .C1_2(1'b0), .C1_3(1'b0), .C2_0(1'b1), .C2_1(1'b0),
    .C2_2(1'b0), .C2_3(1'b0), .A(Addr0), .B(nST), .nG1(Wrd), .nG2(Wrd));
  or or_1 (Oext_n, nLD, Wrd);
  IC_74x74half ic_74x74half_1 (.R1(ic_74x74half_1_r1), .CLK1(CLK), .CLR1(1'b1), .SET1(1'b1), .D1(nST));  // open: Q1
  or or_2 (MWE_n, nST, ic_74x74half_1_r1);
  RAM #(.addrWidth(15), .databus("bidir"), .trigger("low")) Low_Byte (
    .addr(MAR_q2), .data(Low_Byte_data));  // open: we, oe, clk
  and and_1 (and_1_out, ~nLD, MWE_n, ~CE0_n);  // AND_Gate
  and and_2 (and_2_out, ~CE0_n, ~MWE_n);  // AND_Gate
  RAM #(.addrWidth(15), .databus("bidir"), .trigger("low")) High_Byte (
    .addr(MAR_q2), .data(High_Byte_data));  // open: we, oe, clk
  and and_3 (and_3_out, ~nLD, MWE_n, ~CE1_n);  // AND_Gate
  and and_4 (and_4_out, ~CE1_n, ~MWE_n);  // AND_Gate
  IC_74x32571 ic_74x32571_1 (
    .B1_2(Low_Byte_data[1]), .B1_3(Low_Byte_data[2]), .B1_4(Low_Byte_data[3]), .B2_1(High_Byte_data[0]),
    .B2_2(High_Byte_data[1]), .B2_3(High_Byte_data[2]), .B2_4(High_Byte_data[3]), .B1_1(Low_Byte_data[0]),
    .S(ISwap), .nOE(nIE), .A1(A_BUS_IN[0]), .A2(A_BUS_IN[1]), .A3(A_BUS_IN[2]), .A4(A_BUS_IN[3]));
  IC_74x32571 ic_74x32571_2 (
    .B1_2(Low_Byte_data[5]), .B1_3(Low_Byte_data[6]), .B1_4(Low_Byte_data[7]), .B2_1(High_Byte_data[4]),
    .B2_2(High_Byte_data[5]), .B2_3(High_Byte_data[6]), .B2_4(High_Byte_data[7]), .B1_1(Low_Byte_data[4]),
    .S(ISwap), .nOE(nIE), .A1(A_BUS_IN[4]), .A2(A_BUS_IN[5]), .A3(A_BUS_IN[6]), .A4(A_BUS_IN[7]));
  IC_74x32571 ic_74x32571_3 (
    .B1_2(High_Byte_data[1]), .B1_3(High_Byte_data[2]), .B1_4(High_Byte_data[3]), .B2_1(Low_Byte_data[0]),
    .B2_2(Low_Byte_data[1]), .B2_3(Low_Byte_data[2]), .B2_4(Low_Byte_data[3]), .B1_1(High_Byte_data[0]),
    .S(ISwap), .nOE(nIE), .A1(A_BUS_IN[8]), .A2(A_BUS_IN[9]), .A3(A_BUS_IN[10]), .A4(A_BUS_IN[11]));
  IC_74x32571 ic_74x32571_4 (
    .B1_2(High_Byte_data[5]), .B1_3(High_Byte_data[6]), .B1_4(High_Byte_data[7]), .B2_1(Low_Byte_data[4]),
    .B2_2(Low_Byte_data[5]), .B2_3(Low_Byte_data[6]), .B2_4(Low_Byte_data[7]), .B1_1(High_Byte_data[4]),
    .S(ISwap), .nOE(nIE), .A1(A_BUS_IN[12]), .A2(A_BUS_IN[13]), .A3(A_BUS_IN[14]), .A4(A_BUS_IN[15]));
  // IC_74x257 ic_74x257_1: pin names not known
  IC_74x1G3157 ic_74x1g3157_1 (.A(ic_74x1g3157_1_a), .B1(Low_Byte_data[7]), .B2(High_Byte_data[7]), .S(OSwap));
  IC_74x1G3157 ic_74x1g3157_2 (.A(ic_74x1g3157_2_a), .B1(ic_74x1g3157_1_a), .B2(1'b0), .S(SEx));
  IC_74x3257 ic_74x3257_1 (
    .A1(Q_BUS_OUT[0]), .A2(Q_BUS_OUT[1]), .A3(Q_BUS_OUT[2]), .A4(Q_BUS_OUT[3]), .B2_1(High_Byte_data[0]),
    .B1_2(Low_Byte_data[1]), .B2_2(High_Byte_data[1]), .B1_3(Low_Byte_data[2]), .B2_3(High_Byte_data[2]),
    .B1_4(Low_Byte_data[3]), .B2_4(High_Byte_data[3]), .S(OSwap), .nOE(nOE), .B1_1(Low_Byte_data[0]));
  IC_74x3257 ic_74x3257_2 (
    .A1(Q_BUS_OUT[4]), .A2(Q_BUS_OUT[5]), .A3(Q_BUS_OUT[6]), .A4(Q_BUS_OUT[7]), .B2_1(High_Byte_data[4]),
    .B1_2(Low_Byte_data[5]), .B2_2(High_Byte_data[5]), .B1_3(Low_Byte_data[6]), .B2_3(High_Byte_data[6]),
    .B1_4(Low_Byte_data[7]), .B2_4(High_Byte_data[7]), .S(OSwap), .nOE(nOE), .B1_1(Low_Byte_data[4]));
  IC_74x3257 ic_74x3257_3 (
    .A1(Q_BUS_OUT[8]), .A2(Q_BUS_OUT[9]), .A3(Q_BUS_OUT[10]), .A4(Q_BUS_OUT[11]), .B2_1(High_Byte_data[0]),
    .B1_2(ic_74x1g3157_2_a), .B2_2(High_Byte_data[1]), .B1_3(ic_74x1g3157_2_a), .B2_3(High_Byte_data[2]),
    .B1_4(ic_74x1g3157_2_a), .B2_4(High_Byte_data[3]), .S(Oext_n), .nOE(nOE), .B1_1(ic_74x1g3157_2_a));
  IC_74x3257 ic_74x3257_4 (
    .A1(Q_BUS_OUT[12]), .A2(Q_BUS_OUT[13]), .A3(Q_BUS_OUT[14]), .A4(Q_BUS_OUT[15]), .B2_1(High_Byte_data[4]),
    .B1_2(ic_74x1g3157_2_a), .B2_2(High_Byte_data[5]), .B1_3(ic_74x1g3157_2_a), .B2_3(High_Byte_data[6]),
    .B1_4(ic_74x1g3157_2_a), .B2_4(High_Byte_data[7]), .S(Oext_n), .nOE(nOE), .B1_1(ic_74x1g3157_2_a));

  // Other names for the same wires on the sheet: CLK_WRMAR = cpWRMAR; IE_n = nIE; MOE_n = nLD; nMemLD = nLD;
  //   nMemST = nST; OE_n = nOE; SExt = SEx; Word = Wrd

  // Notes on the sheet:
  //   Operation
  //   ---------
  //   ST.W
  //   ST.B
  //   LD.W
  //   LD.SB
  //   LD.ZB
  //   SWAPB
  //   SEXT
  //   ZEXT
  //   nIE nOE Wrd SEx nST nLD 
  //   -----------------------
  //    0   1   1   x   0   1
  //    0   1   0   x   0   1
  //    1   0   1   x   1   0
  //    1   0   0   1   1   0
  //    1   0   0   0   1   0
  //    0   0   0   x   1   1
  //    0   0   0   1   1   1
  //    0   0   0   0   1   1
endmodule
// Register File
module Registers_541 (
  input  nCLK,
  input  nWR_RD,
  input  nRD_TO_A,
  input  nRS_TO_A,
  input  nRN_TO_B,
  input  [15:0] IN,
  input  [2:0] RD,
  input  [2:0] RS,
  input  [2:0] RN,
  output [15:0] REG_A,
  output [15:0] REG_B
);

  wire ic_74x573_1_q1, ic_74x573_1_q2, ic_74x573_1_q3, ic_74x573_1_q4, ic_74x573_1_q5, ic_74x573_1_q6,
       ic_74x573_1_q7, ic_74x573_1_q8, nRD_0, nRD_1, nRD_2, nRD_3, nRD_4, nRD_5, nRD_6, nRD_7, nRN_0, nRN_1,
       nRN_2, nRN_3, nRN_4, nRN_5, nRN_6, nRN_7, nRS_0, nRS_1, nRS_2, nRS_3, nRS_4, nRS_5, nRS_6, nRS_7,
       RWriteEn_y0, RWriteEn_y1, RWriteEn_y2, RWriteEn_y3, RWriteEn_y4, RWriteEn_y5, RWriteEn_y6,
       RWriteEn_y7, WR_R0, WR_R1, WR_R2, WR_R3, WR_R4, WR_R5, WR_R6, WR_R7;
  wire [15:0] R0_A_3_q1, R0_A_q1, RO_B_q1;

  logi7400ic_IC_74x574 R0_A (
    .Q2(R0_A_q1[1]), .Q3(R0_A_q1[2]), .Q4(R0_A_q1[3]), .Q5(R0_A_q1[4]), .Q6(R0_A_q1[5]), .Q7(R0_A_q1[6]),
    .Q8(R0_A_q1[7]), .Q1(R0_A_q1[0]), .D2(IN[1]), .D3(IN[2]), .D4(IN[3]), .D5(IN[4]), .D6(IN[5]), .D7(IN[6]),
    .D8(IN[7]), .CLK(WR_R0), .nOE(nRD_0), .D1(IN[0]));  // open: Probe
  logi7400ic_IC_74x574 R0_A_2 (
    .Q2(R0_A_q1[9]), .Q3(R0_A_q1[10]), .Q4(R0_A_q1[11]), .Q5(R0_A_q1[12]), .Q6(R0_A_q1[13]),
    .Q7(R0_A_q1[14]), .Q8(R0_A_q1[15]), .Q1(R0_A_q1[8]), .D2(IN[9]), .D3(IN[10]), .D4(IN[11]), .D5(IN[12]),
    .D6(IN[13]), .D7(IN[14]), .D8(IN[15]), .CLK(WR_R0), .nOE(nRD_0), .D1(IN[8]));  // open: Probe
  logi7400ic_IC_74x574 R1_A (
    .Q2(R0_A_q1[1]), .Q3(R0_A_q1[2]), .Q4(R0_A_q1[3]), .Q5(R0_A_q1[4]), .Q6(R0_A_q1[5]), .Q7(R0_A_q1[6]),
    .Q8(R0_A_q1[7]), .Q1(R0_A_q1[0]), .D2(IN[1]), .D3(IN[2]), .D4(IN[3]), .D5(IN[4]), .D6(IN[5]), .D7(IN[6]),
    .D8(IN[7]), .CLK(WR_R1), .nOE(nRD_1), .D1(IN[0]));  // open: Probe
  logi7400ic_IC_74x574 R1_A_2 (
    .Q2(R0_A_q1[9]), .Q3(R0_A_q1[10]), .Q4(R0_A_q1[11]), .Q5(R0_A_q1[12]), .Q6(R0_A_q1[13]),
    .Q7(R0_A_q1[14]), .Q8(R0_A_q1[15]), .Q1(R0_A_q1[8]), .D2(IN[9]), .D3(IN[10]), .D4(IN[11]), .D5(IN[12]),
    .D6(IN[13]), .D7(IN[14]), .D8(IN[15]), .CLK(WR_R1), .nOE(nRD_1), .D1(IN[8]));  // open: Probe
  logi7400ic_IC_74x574 R2_A (
    .Q2(R0_A_q1[1]), .Q3(R0_A_q1[2]), .Q4(R0_A_q1[3]), .Q5(R0_A_q1[4]), .Q6(R0_A_q1[5]), .Q7(R0_A_q1[6]),
    .Q8(R0_A_q1[7]), .Q1(R0_A_q1[0]), .D2(IN[1]), .D3(IN[2]), .D4(IN[3]), .D5(IN[4]), .D6(IN[5]), .D7(IN[6]),
    .D8(IN[7]), .CLK(WR_R2), .nOE(nRD_2), .D1(IN[0]));  // open: Probe
  logi7400ic_IC_74x574 R2_A_2 (
    .Q2(R0_A_q1[9]), .Q3(R0_A_q1[10]), .Q4(R0_A_q1[11]), .Q5(R0_A_q1[12]), .Q6(R0_A_q1[13]),
    .Q7(R0_A_q1[14]), .Q8(R0_A_q1[15]), .Q1(R0_A_q1[8]), .D2(IN[9]), .D3(IN[10]), .D4(IN[11]), .D5(IN[12]),
    .D6(IN[13]), .D7(IN[14]), .D8(IN[15]), .CLK(WR_R2), .nOE(nRD_2), .D1(IN[8]));  // open: Probe
  logi7400ic_IC_74x574 R3_A (
    .Q2(R0_A_q1[1]), .Q3(R0_A_q1[2]), .Q4(R0_A_q1[3]), .Q5(R0_A_q1[4]), .Q6(R0_A_q1[5]), .Q7(R0_A_q1[6]),
    .Q8(R0_A_q1[7]), .Q1(R0_A_q1[0]), .D2(IN[1]), .D3(IN[2]), .D4(IN[3]), .D5(IN[4]), .D6(IN[5]), .D7(IN[6]),
    .D8(IN[7]), .CLK(WR_R3), .nOE(nRD_3), .D1(IN[0]));  // open: Probe
  logi7400ic_IC_74x574 R3_A_2 (
    .Q2(R0_A_q1[9]), .Q3(R0_A_q1[10]), .Q4(R0_A_q1[11]), .Q5(R0_A_q1[12]), .Q6(R0_A_q1[13]),
    .Q7(R0_A_q1[14]), .Q8(R0_A_q1[15]), .Q1(R0_A_q1[8]), .D2(IN[9]), .D3(IN[10]), .D4(IN[11]), .D5(IN[12]),
    .D6(IN[13]), .D7(IN[14]), .D8(IN[15]), .CLK(WR_R3), .nOE(nRD_3), .D1(IN[8]));  // open: Probe
  logi7400ic_IC_74x574 R0_A_3 (
    .Q2(R0_A_3_q1[1]), .Q3(R0_A_3_q1[2]), .Q4(R0_A_3_q1[3]), .Q5(R0_A_3_q1[4]), .Q6(R0_A_3_q1[5]),
    .Q7(R0_A_3_q1[6]), .Q8(R0_A_3_q1[7]), .Q1(R0_A_3_q1[0]), .D2(IN[1]), .D3(IN[2]), .D4(IN[3]), .D5(IN[4]),
    .D6(IN[5]), .D7(IN[6]), .D8(IN[7]), .CLK(WR_R0), .nOE(nRS_0), .D1(IN[0]));  // open: Probe
  logi7400ic_IC_74x574 R0_A_4 (
    .Q2(R0_A_3_q1[9]), .Q3(R0_A_3_q1[10]), .Q4(R0_A_3_q1[11]), .Q5(R0_A_3_q1[12]), .Q6(R0_A_3_q1[13]),
    .Q7(R0_A_3_q1[14]), .Q8(R0_A_3_q1[15]), .Q1(R0_A_3_q1[8]), .D2(IN[9]), .D3(IN[10]), .D4(IN[11]),
    .D5(IN[12]), .D6(IN[13]), .D7(IN[14]), .D8(IN[15]), .CLK(WR_R0), .nOE(nRS_0), .D1(IN[8]));  // open: Probe
  logi7400ic_IC_74x574 R1_A_3 (
    .Q2(R0_A_3_q1[1]), .Q3(R0_A_3_q1[2]), .Q4(R0_A_3_q1[3]), .Q5(R0_A_3_q1[4]), .Q6(R0_A_3_q1[5]),
    .Q7(R0_A_3_q1[6]), .Q8(R0_A_3_q1[7]), .Q1(R0_A_3_q1[0]), .D2(IN[1]), .D3(IN[2]), .D4(IN[3]), .D5(IN[4]),
    .D6(IN[5]), .D7(IN[6]), .D8(IN[7]), .CLK(WR_R1), .nOE(nRS_1), .D1(IN[0]));  // open: Probe
  logi7400ic_IC_74x574 R1_A_4 (
    .Q2(R0_A_3_q1[9]), .Q3(R0_A_3_q1[10]), .Q4(R0_A_3_q1[11]), .Q5(R0_A_3_q1[12]), .Q6(R0_A_3_q1[13]),
    .Q7(R0_A_3_q1[14]), .Q8(R0_A_3_q1[15]), .Q1(R0_A_3_q1[8]), .D2(IN[9]), .D3(IN[10]), .D4(IN[11]),
    .D5(IN[12]), .D6(IN[13]), .D7(IN[14]), .D8(IN[15]), .CLK(WR_R1), .nOE(nRS_1), .D1(IN[8]));  // open: Probe
  logi7400ic_IC_74x574 R2_A_3 (
    .Q2(R0_A_3_q1[1]), .Q3(R0_A_3_q1[2]), .Q4(R0_A_3_q1[3]), .Q5(R0_A_3_q1[4]), .Q6(R0_A_3_q1[5]),
    .Q7(R0_A_3_q1[6]), .Q8(R0_A_3_q1[7]), .Q1(R0_A_3_q1[0]), .D2(IN[1]), .D3(IN[2]), .D4(IN[3]), .D5(IN[4]),
    .D6(IN[5]), .D7(IN[6]), .D8(IN[7]), .CLK(WR_R2), .nOE(nRS_2), .D1(IN[0]));  // open: Probe
  logi7400ic_IC_74x574 R2_A_4 (
    .Q2(R0_A_3_q1[9]), .Q3(R0_A_3_q1[10]), .Q4(R0_A_3_q1[11]), .Q5(R0_A_3_q1[12]), .Q6(R0_A_3_q1[13]),
    .Q7(R0_A_3_q1[14]), .Q8(R0_A_3_q1[15]), .Q1(R0_A_3_q1[8]), .D2(IN[9]), .D3(IN[10]), .D4(IN[11]),
    .D5(IN[12]), .D6(IN[13]), .D7(IN[14]), .D8(IN[15]), .CLK(WR_R2), .nOE(nRS_2), .D1(IN[8]));  // open: Probe
  logi7400ic_IC_74x574 R3_A_3 (
    .Q2(R0_A_3_q1[1]), .Q3(R0_A_3_q1[2]), .Q4(R0_A_3_q1[3]), .Q5(R0_A_3_q1[4]), .Q6(R0_A_3_q1[5]),
    .Q7(R0_A_3_q1[6]), .Q8(R0_A_3_q1[7]), .Q1(R0_A_3_q1[0]), .D2(IN[1]), .D3(IN[2]), .D4(IN[3]), .D5(IN[4]),
    .D6(IN[5]), .D7(IN[6]), .D8(IN[7]), .CLK(WR_R3), .nOE(nRS_3), .D1(IN[0]));  // open: Probe
  logi7400ic_IC_74x574 R3_A_4 (
    .Q2(R0_A_3_q1[9]), .Q3(R0_A_3_q1[10]), .Q4(R0_A_3_q1[11]), .Q5(R0_A_3_q1[12]), .Q6(R0_A_3_q1[13]),
    .Q7(R0_A_3_q1[14]), .Q8(R0_A_3_q1[15]), .Q1(R0_A_3_q1[8]), .D2(IN[9]), .D3(IN[10]), .D4(IN[11]),
    .D5(IN[12]), .D6(IN[13]), .D7(IN[14]), .D8(IN[15]), .CLK(WR_R3), .nOE(nRS_3), .D1(IN[8]));  // open: Probe
  IC_74x138 RWriteEn (
    .Y0(RWriteEn_y0), .Y1(RWriteEn_y1), .Y2(RWriteEn_y2), .Y3(RWriteEn_y3), .Y4(RWriteEn_y4),
    .Y5(RWriteEn_y5), .Y6(RWriteEn_y6), .Y7(RWriteEn_y7), .A(RD[0]), .B(RD[1]), .C(RD[2]), .nG2A(nWR_RD),
    .nG2B(1'b0), .G1(1'b1));
  IC_74x138 RDSelA (
    .Y0(nRD_0), .Y1(nRD_1), .Y2(nRD_2), .Y3(nRD_3), .Y4(nRD_4), .Y5(nRD_5), .Y6(nRD_6), .Y7(nRD_7),
    .A(RD[0]), .B(RD[1]), .C(RD[2]), .nG2A(1'b0), .nG2B(1'b0), .G1(1'b1));
  IC_74x138 RSSelA (
    .Y0(nRS_0), .Y1(nRS_1), .Y2(nRS_2), .Y3(nRS_3), .Y4(nRS_4), .Y5(nRS_5), .Y6(nRS_6), .Y7(nRS_7),
    .A(RS[0]), .B(RS[1]), .C(RS[2]), .nG2A(1'b0), .nG2B(1'b0), .G1(1'b1));
  IC_74x138 RNEnB (
    .Y0(nRN_0), .Y1(nRN_1), .Y2(nRN_2), .Y3(nRN_3), .Y4(nRN_4), .Y5(nRN_5), .Y6(nRN_6), .Y7(nRN_7),
    .A(RN[0]), .B(RN[1]), .C(RN[2]), .nG2A(1'b0), .nG2B(1'b0), .G1(1'b1));
  IC_74x573 ic_74x573_1 (
    .Q2(ic_74x573_1_q2), .Q3(ic_74x573_1_q3), .Q4(ic_74x573_1_q4), .Q5(ic_74x573_1_q5), .Q6(ic_74x573_1_q6),
    .Q7(ic_74x573_1_q7), .Q8(ic_74x573_1_q8), .Q1(ic_74x573_1_q1), .D2(RWriteEn_y1), .D3(RWriteEn_y2),
    .D4(RWriteEn_y3), .D5(RWriteEn_y4), .D6(RWriteEn_y5), .D7(RWriteEn_y6), .D8(RWriteEn_y7), .LE(nCLK),
    .nOE(1'b0), .D1(RWriteEn_y0));  // open: Probe
  nor nor_1 (WR_R0, nCLK, ic_74x573_1_q1);
  nor nor_2 (WR_R1, nCLK, ic_74x573_1_q2);
  nor nor_3 (WR_R2, nCLK, ic_74x573_1_q3);
  nor nor_4 (WR_R3, nCLK, ic_74x573_1_q4);
  nor nor_5 (WR_R4, nCLK, ic_74x573_1_q5);
  nor nor_6 (WR_R5, nCLK, ic_74x573_1_q6);
  nor nor_7 (WR_R6, nCLK, ic_74x573_1_q7);
  nor nor_8 (WR_R7, nCLK, ic_74x573_1_q8);
  logi7400ic_IC_74x574 RO_B (
    .Q2(RO_B_q1[1]), .Q3(RO_B_q1[2]), .Q4(RO_B_q1[3]), .Q5(RO_B_q1[4]), .Q6(RO_B_q1[5]), .Q7(RO_B_q1[6]),
    .Q8(RO_B_q1[7]), .Q1(RO_B_q1[0]), .D2(IN[1]), .D3(IN[2]), .D4(IN[3]), .D5(IN[4]), .D6(IN[5]), .D7(IN[6]),
    .D8(IN[7]), .CLK(WR_R0), .nOE(nRN_0), .D1(IN[0]));  // open: Probe
  logi7400ic_IC_74x574 R0_B (
    .Q2(RO_B_q1[9]), .Q3(RO_B_q1[10]), .Q4(RO_B_q1[11]), .Q5(RO_B_q1[12]), .Q6(RO_B_q1[13]),
    .Q7(RO_B_q1[14]), .Q8(RO_B_q1[15]), .Q1(RO_B_q1[8]), .D2(IN[9]), .D3(IN[10]), .D4(IN[11]), .D5(IN[12]),
    .D6(IN[13]), .D7(IN[14]), .D8(IN[15]), .CLK(WR_R0), .nOE(nRN_0), .D1(IN[8]));  // open: Probe
  logi7400ic_IC_74x574 R1_B (
    .Q2(RO_B_q1[1]), .Q3(RO_B_q1[2]), .Q4(RO_B_q1[3]), .Q5(RO_B_q1[4]), .Q6(RO_B_q1[5]), .Q7(RO_B_q1[6]),
    .Q8(RO_B_q1[7]), .Q1(RO_B_q1[0]), .D2(IN[1]), .D3(IN[2]), .D4(IN[3]), .D5(IN[4]), .D6(IN[5]), .D7(IN[6]),
    .D8(IN[7]), .CLK(WR_R1), .nOE(nRN_1), .D1(IN[0]));  // open: Probe
  logi7400ic_IC_74x574 R1_B_2 (
    .Q2(RO_B_q1[9]), .Q3(RO_B_q1[10]), .Q4(RO_B_q1[11]), .Q5(RO_B_q1[12]), .Q6(RO_B_q1[13]),
    .Q7(RO_B_q1[14]), .Q8(RO_B_q1[15]), .Q1(RO_B_q1[8]), .D2(IN[9]), .D3(IN[10]), .D4(IN[11]), .D5(IN[12]),
    .D6(IN[13]), .D7(IN[14]), .D8(IN[15]), .CLK(WR_R1), .nOE(nRN_1), .D1(IN[8]));  // open: Probe
  logi7400ic_IC_74x574 R2_B (
    .Q2(RO_B_q1[1]), .Q3(RO_B_q1[2]), .Q4(RO_B_q1[3]), .Q5(RO_B_q1[4]), .Q6(RO_B_q1[5]), .Q7(RO_B_q1[6]),
    .Q8(RO_B_q1[7]), .Q1(RO_B_q1[0]), .D2(IN[1]), .D3(IN[2]), .D4(IN[3]), .D5(IN[4]), .D6(IN[5]), .D7(IN[6]),
    .D8(IN[7]), .CLK(WR_R2), .nOE(nRN_2), .D1(IN[0]));  // open: Probe
  logi7400ic_IC_74x574 R2_B_2 (
    .Q2(RO_B_q1[9]), .Q3(RO_B_q1[10]), .Q4(RO_B_q1[11]), .Q5(RO_B_q1[12]), .Q6(RO_B_q1[13]),
    .Q7(RO_B_q1[14]), .Q8(RO_B_q1[15]), .Q1(RO_B_q1[8]), .D2(IN[9]), .D3(IN[10]), .D4(IN[11]), .D5(IN[12]),
    .D6(IN[13]), .D7(IN[14]), .D8(IN[15]), .CLK(WR_R2), .nOE(nRN_2), .D1(IN[8]));  // open: Probe
  logi7400ic_IC_74x574 R3_B (
    .Q2(RO_B_q1[1]), .Q3(RO_B_q1[2]), .Q4(RO_B_q1[3]), .Q5(RO_B_q1[4]), .Q6(RO_B_q1[5]), .Q7(RO_B_q1[6]),
    .Q8(RO_B_q1[7]), .Q1(RO_B_q1[0]), .D2(IN[1]), .D3(IN[2]), .D4(IN[3]), .D5(IN[4]), .D6(IN[5]), .D7(IN[6]),
    .D8(IN[7]), .CLK(WR_R3), .nOE(nRN_3), .D1(IN[0]));  // open: Probe
  logi7400ic_IC_74x574 R3_B_2 (
    .Q2(RO_B_q1[9]), .Q3(RO_B_q1[10]), .Q4(RO_B_q1[11]), .Q5(RO_B_q1[12]), .Q6(RO_B_q1[13]),
    .Q7(RO_B_q1[14]), .Q8(RO_B_q1[15]), .Q1(RO_B_q1[8]), .D2(IN[9]), .D3(IN[10]), .D4(IN[11]), .D5(IN[12]),
    .D6(IN[13]), .D7(IN[14]), .D8(IN[15]), .CLK(WR_R3), .nOE(nRN_3), .D1(IN[8]));  // open: Probe
  logi7400ic_IC_74x574 R4_A (
    .Q2(R0_A_q1[1]), .Q3(R0_A_q1[2]), .Q4(R0_A_q1[3]), .Q5(R0_A_q1[4]), .Q6(R0_A_q1[5]), .Q7(R0_A_q1[6]),
    .Q8(R0_A_q1[7]), .Q1(R0_A_q1[0]), .D2(IN[1]), .D3(IN[2]), .D4(IN[3]), .D5(IN[4]), .D6(IN[5]), .D7(IN[6]),
    .D8(IN[7]), .CLK(WR_R4), .nOE(nRD_4), .D1(IN[0]));  // open: Probe
  logi7400ic_IC_74x574 R4_A_2 (
    .Q2(R0_A_q1[9]), .Q3(R0_A_q1[10]), .Q4(R0_A_q1[11]), .Q5(R0_A_q1[12]), .Q6(R0_A_q1[13]),
    .Q7(R0_A_q1[14]), .Q8(R0_A_q1[15]), .Q1(R0_A_q1[8]), .D2(IN[9]), .D3(IN[10]), .D4(IN[11]), .D5(IN[12]),
    .D6(IN[13]), .D7(IN[14]), .D8(IN[15]), .CLK(WR_R4), .nOE(nRD_4), .D1(IN[8]));  // open: Probe
  logi7400ic_IC_74x574 R5_A (
    .Q2(R0_A_q1[1]), .Q3(R0_A_q1[2]), .Q4(R0_A_q1[3]), .Q5(R0_A_q1[4]), .Q6(R0_A_q1[5]), .Q7(R0_A_q1[6]),
    .Q8(R0_A_q1[7]), .Q1(R0_A_q1[0]), .D2(IN[1]), .D3(IN[2]), .D4(IN[3]), .D5(IN[4]), .D6(IN[5]), .D7(IN[6]),
    .D8(IN[7]), .CLK(WR_R5), .nOE(nRD_5), .D1(IN[0]));  // open: Probe
  logi7400ic_IC_74x574 R5_A_2 (
    .Q2(R0_A_q1[9]), .Q3(R0_A_q1[10]), .Q4(R0_A_q1[11]), .Q5(R0_A_q1[12]), .Q6(R0_A_q1[13]),
    .Q7(R0_A_q1[14]), .Q8(R0_A_q1[15]), .Q1(R0_A_q1[8]), .D2(IN[9]), .D3(IN[10]), .D4(IN[11]), .D5(IN[12]),
    .D6(IN[13]), .D7(IN[14]), .D8(IN[15]), .CLK(WR_R5), .nOE(nRD_5), .D1(IN[8]));  // open: Probe
  logi7400ic_IC_74x574 R6_A (
    .Q2(R0_A_q1[1]), .Q3(R0_A_q1[2]), .Q4(R0_A_q1[3]), .Q5(R0_A_q1[4]), .Q6(R0_A_q1[5]), .Q7(R0_A_q1[6]),
    .Q8(R0_A_q1[7]), .Q1(R0_A_q1[0]), .D2(IN[1]), .D3(IN[2]), .D4(IN[3]), .D5(IN[4]), .D6(IN[5]), .D7(IN[6]),
    .D8(IN[7]), .CLK(WR_R6), .nOE(nRD_6), .D1(IN[0]));  // open: Probe
  logi7400ic_IC_74x574 R6_A_2 (
    .Q2(R0_A_q1[9]), .Q3(R0_A_q1[10]), .Q4(R0_A_q1[11]), .Q5(R0_A_q1[12]), .Q6(R0_A_q1[13]),
    .Q7(R0_A_q1[14]), .Q8(R0_A_q1[15]), .Q1(R0_A_q1[8]), .D2(IN[9]), .D3(IN[10]), .D4(IN[11]), .D5(IN[12]),
    .D6(IN[13]), .D7(IN[14]), .D8(IN[15]), .CLK(WR_R6), .nOE(nRD_6), .D1(IN[8]));  // open: Probe
  logi7400ic_IC_74x574 R7_A (
    .Q2(R0_A_q1[1]), .Q3(R0_A_q1[2]), .Q4(R0_A_q1[3]), .Q5(R0_A_q1[4]), .Q6(R0_A_q1[5]), .Q7(R0_A_q1[6]),
    .Q8(R0_A_q1[7]), .Q1(R0_A_q1[0]), .D2(IN[1]), .D3(IN[2]), .D4(IN[3]), .D5(IN[4]), .D6(IN[5]), .D7(IN[6]),
    .D8(IN[7]), .CLK(WR_R7), .nOE(nRD_7), .D1(IN[0]));  // open: Probe
  logi7400ic_IC_74x574 R8_A (
    .Q2(R0_A_q1[9]), .Q3(R0_A_q1[10]), .Q4(R0_A_q1[11]), .Q5(R0_A_q1[12]), .Q6(R0_A_q1[13]),
    .Q7(R0_A_q1[14]), .Q8(R0_A_q1[15]), .Q1(R0_A_q1[8]), .D2(IN[9]), .D3(IN[10]), .D4(IN[11]), .D5(IN[12]),
    .D6(IN[13]), .D7(IN[14]), .D8(IN[15]), .CLK(WR_R7), .nOE(nRD_7), .D1(IN[8]));  // open: Probe
  IC_74x541 RD_A (
    .Q1(REG_A[0]), .Q2(REG_A[1]), .Q3(REG_A[2]), .Q4(REG_A[3]), .Q5(REG_A[4]), .Q6(REG_A[5]), .Q7(REG_A[6]),
    .Q8(REG_A[7]), .I1(R0_A_q1[0]), .I2(R0_A_q1[1]), .I3(R0_A_q1[2]), .I4(R0_A_q1[3]), .I5(R0_A_q1[4]),
    .I6(R0_A_q1[5]), .I7(R0_A_q1[6]), .I8(R0_A_q1[7]), .nOE1(1'b0), .nOE2(nRD_TO_A));
  IC_74x541 RD_A_2 (
    .Q1(REG_A[8]), .Q2(REG_A[9]), .Q3(REG_A[10]), .Q4(REG_A[11]), .Q5(REG_A[12]), .Q6(REG_A[13]),
    .Q7(REG_A[14]), .Q8(REG_A[15]), .I1(R0_A_q1[8]), .I2(R0_A_q1[9]), .I3(R0_A_q1[10]), .I4(R0_A_q1[11]),
    .I5(R0_A_q1[12]), .I6(R0_A_q1[13]), .I7(R0_A_q1[14]), .I8(R0_A_q1[15]), .nOE1(1'b0), .nOE2(nRD_TO_A));
  logi7400ic_IC_74x574 R4_A_3 (
    .Q2(R0_A_3_q1[1]), .Q3(R0_A_3_q1[2]), .Q4(R0_A_3_q1[3]), .Q5(R0_A_3_q1[4]), .Q6(R0_A_3_q1[5]),
    .Q7(R0_A_3_q1[6]), .Q8(R0_A_3_q1[7]), .Q1(R0_A_3_q1[0]), .D2(IN[1]), .D3(IN[2]), .D4(IN[3]), .D5(IN[4]),
    .D6(IN[5]), .D7(IN[6]), .D8(IN[7]), .CLK(WR_R4), .nOE(nRS_4), .D1(IN[0]));  // open: Probe
  logi7400ic_IC_74x574 R4_A_4 (
    .Q2(R0_A_3_q1[9]), .Q3(R0_A_3_q1[10]), .Q4(R0_A_3_q1[11]), .Q5(R0_A_3_q1[12]), .Q6(R0_A_3_q1[13]),
    .Q7(R0_A_3_q1[14]), .Q8(R0_A_3_q1[15]), .Q1(R0_A_3_q1[8]), .D2(IN[9]), .D3(IN[10]), .D4(IN[11]),
    .D5(IN[12]), .D6(IN[13]), .D7(IN[14]), .D8(IN[15]), .CLK(WR_R4), .nOE(nRS_4), .D1(IN[8]));  // open: Probe
  logi7400ic_IC_74x574 R5_A_3 (
    .Q2(R0_A_3_q1[1]), .Q3(R0_A_3_q1[2]), .Q4(R0_A_3_q1[3]), .Q5(R0_A_3_q1[4]), .Q6(R0_A_3_q1[5]),
    .Q7(R0_A_3_q1[6]), .Q8(R0_A_3_q1[7]), .Q1(R0_A_3_q1[0]), .D2(IN[1]), .D3(IN[2]), .D4(IN[3]), .D5(IN[4]),
    .D6(IN[5]), .D7(IN[6]), .D8(IN[7]), .CLK(WR_R5), .nOE(nRS_5), .D1(IN[0]));  // open: Probe
  logi7400ic_IC_74x574 R5_A_4 (
    .Q2(R0_A_3_q1[9]), .Q3(R0_A_3_q1[10]), .Q4(R0_A_3_q1[11]), .Q5(R0_A_3_q1[12]), .Q6(R0_A_3_q1[13]),
    .Q7(R0_A_3_q1[14]), .Q8(R0_A_3_q1[15]), .Q1(R0_A_3_q1[8]), .D2(IN[9]), .D3(IN[10]), .D4(IN[11]),
    .D5(IN[12]), .D6(IN[13]), .D7(IN[14]), .D8(IN[15]), .CLK(WR_R5), .nOE(nRS_5), .D1(IN[8]));  // open: Probe
  logi7400ic_IC_74x574 R6_A_3 (
    .Q2(R0_A_3_q1[1]), .Q3(R0_A_3_q1[2]), .Q4(R0_A_3_q1[3]), .Q5(R0_A_3_q1[4]), .Q6(R0_A_3_q1[5]),
    .Q7(R0_A_3_q1[6]), .Q8(R0_A_3_q1[7]), .Q1(R0_A_3_q1[0]), .D2(IN[1]), .D3(IN[2]), .D4(IN[3]), .D5(IN[4]),
    .D6(IN[5]), .D7(IN[6]), .D8(IN[7]), .CLK(WR_R6), .nOE(nRS_6), .D1(IN[0]));  // open: Probe
  logi7400ic_IC_74x574 R6_A_4 (
    .Q2(R0_A_3_q1[9]), .Q3(R0_A_3_q1[10]), .Q4(R0_A_3_q1[11]), .Q5(R0_A_3_q1[12]), .Q6(R0_A_3_q1[13]),
    .Q7(R0_A_3_q1[14]), .Q8(R0_A_3_q1[15]), .Q1(R0_A_3_q1[8]), .D2(IN[9]), .D3(IN[10]), .D4(IN[11]),
    .D5(IN[12]), .D6(IN[13]), .D7(IN[14]), .D8(IN[15]), .CLK(WR_R6), .nOE(nRS_6), .D1(IN[8]));  // open: Probe
  logi7400ic_IC_74x574 R7_A_2 (
    .Q2(R0_A_3_q1[1]), .Q3(R0_A_3_q1[2]), .Q4(R0_A_3_q1[3]), .Q5(R0_A_3_q1[4]), .Q6(R0_A_3_q1[5]),
    .Q7(R0_A_3_q1[6]), .Q8(R0_A_3_q1[7]), .Q1(R0_A_3_q1[0]), .D2(IN[1]), .D3(IN[2]), .D4(IN[3]), .D5(IN[4]),
    .D6(IN[5]), .D7(IN[6]), .D8(IN[7]), .CLK(WR_R7), .nOE(nRS_7), .D1(IN[0]));  // open: Probe
  logi7400ic_IC_74x574 R8_A_2 (
    .Q2(R0_A_3_q1[9]), .Q3(R0_A_3_q1[10]), .Q4(R0_A_3_q1[11]), .Q5(R0_A_3_q1[12]), .Q6(R0_A_3_q1[13]),
    .Q7(R0_A_3_q1[14]), .Q8(R0_A_3_q1[15]), .Q1(R0_A_3_q1[8]), .D2(IN[9]), .D3(IN[10]), .D4(IN[11]),
    .D5(IN[12]), .D6(IN[13]), .D7(IN[14]), .D8(IN[15]), .CLK(WR_R7), .nOE(nRS_7), .D1(IN[8]));  // open: Probe
  IC_74x541 RS_A (
    .Q1(REG_A[0]), .Q2(REG_A[1]), .Q3(REG_A[2]), .Q4(REG_A[3]), .Q5(REG_A[4]), .Q6(REG_A[5]), .Q7(REG_A[6]),
    .Q8(REG_A[7]), .I1(R0_A_3_q1[0]), .I2(R0_A_3_q1[1]), .I3(R0_A_3_q1[2]), .I4(R0_A_3_q1[3]),
    .I5(R0_A_3_q1[4]), .I6(R0_A_3_q1[5]), .I7(R0_A_3_q1[6]), .I8(R0_A_3_q1[7]), .nOE1(1'b0), .nOE2(nRS_TO_A));
  IC_74x541 RS_A_2 (
    .Q1(REG_A[8]), .Q2(REG_A[9]), .Q3(REG_A[10]), .Q4(REG_A[11]), .Q5(REG_A[12]), .Q6(REG_A[13]),
    .Q7(REG_A[14]), .Q8(REG_A[15]), .I1(R0_A_3_q1[8]), .I2(R0_A_3_q1[9]), .I3(R0_A_3_q1[10]),
    .I4(R0_A_3_q1[11]), .I5(R0_A_3_q1[12]), .I6(R0_A_3_q1[13]), .I7(R0_A_3_q1[14]), .I8(R0_A_3_q1[15]),
    .nOE1(1'b0), .nOE2(nRS_TO_A));
  logi7400ic_IC_74x574 R4_B (
    .Q2(RO_B_q1[1]), .Q3(RO_B_q1[2]), .Q4(RO_B_q1[3]), .Q5(RO_B_q1[4]), .Q6(RO_B_q1[5]), .Q7(RO_B_q1[6]),
    .Q8(RO_B_q1[7]), .Q1(RO_B_q1[0]), .D2(IN[1]), .D3(IN[2]), .D4(IN[3]), .D5(IN[4]), .D6(IN[5]), .D7(IN[6]),
    .D8(IN[7]), .CLK(WR_R4), .nOE(nRN_4), .D1(IN[0]));  // open: Probe
  logi7400ic_IC_74x574 R4_B_2 (
    .Q2(RO_B_q1[9]), .Q3(RO_B_q1[10]), .Q4(RO_B_q1[11]), .Q5(RO_B_q1[12]), .Q6(RO_B_q1[13]),
    .Q7(RO_B_q1[14]), .Q8(RO_B_q1[15]), .Q1(RO_B_q1[8]), .D2(IN[9]), .D3(IN[10]), .D4(IN[11]), .D5(IN[12]),
    .D6(IN[13]), .D7(IN[14]), .D8(IN[15]), .CLK(WR_R4), .nOE(nRN_4), .D1(IN[8]));  // open: Probe
  logi7400ic_IC_74x574 R5_B (
    .Q2(RO_B_q1[1]), .Q3(RO_B_q1[2]), .Q4(RO_B_q1[3]), .Q5(RO_B_q1[4]), .Q6(RO_B_q1[5]), .Q7(RO_B_q1[6]),
    .Q8(RO_B_q1[7]), .Q1(RO_B_q1[0]), .D2(IN[1]), .D3(IN[2]), .D4(IN[3]), .D5(IN[4]), .D6(IN[5]), .D7(IN[6]),
    .D8(IN[7]), .CLK(WR_R5), .nOE(nRN_5), .D1(IN[0]));  // open: Probe
  logi7400ic_IC_74x574 R5_B_2 (
    .Q2(RO_B_q1[9]), .Q3(RO_B_q1[10]), .Q4(RO_B_q1[11]), .Q5(RO_B_q1[12]), .Q6(RO_B_q1[13]),
    .Q7(RO_B_q1[14]), .Q8(RO_B_q1[15]), .Q1(RO_B_q1[8]), .D2(IN[9]), .D3(IN[10]), .D4(IN[11]), .D5(IN[12]),
    .D6(IN[13]), .D7(IN[14]), .D8(IN[15]), .CLK(WR_R5), .nOE(nRN_5), .D1(IN[8]));  // open: Probe
  logi7400ic_IC_74x574 R6_B (
    .Q2(RO_B_q1[1]), .Q3(RO_B_q1[2]), .Q4(RO_B_q1[3]), .Q5(RO_B_q1[4]), .Q6(RO_B_q1[5]), .Q7(RO_B_q1[6]),
    .Q8(RO_B_q1[7]), .Q1(RO_B_q1[0]), .D2(IN[1]), .D3(IN[2]), .D4(IN[3]), .D5(IN[4]), .D6(IN[5]), .D7(IN[6]),
    .D8(IN[7]), .CLK(WR_R6), .nOE(nRN_6), .D1(IN[0]));  // open: Probe
  logi7400ic_IC_74x574 R6_B_2 (
    .Q2(RO_B_q1[9]), .Q3(RO_B_q1[10]), .Q4(RO_B_q1[11]), .Q5(RO_B_q1[12]), .Q6(RO_B_q1[13]),
    .Q7(RO_B_q1[14]), .Q8(RO_B_q1[15]), .Q1(RO_B_q1[8]), .D2(IN[9]), .D3(IN[10]), .D4(IN[11]), .D5(IN[12]),
    .D6(IN[13]), .D7(IN[14]), .D8(IN[15]), .CLK(WR_R6), .nOE(nRN_6), .D1(IN[8]));  // open: Probe
  logi7400ic_IC_74x574 R7_B (
    .Q2(RO_B_q1[1]), .Q3(RO_B_q1[2]), .Q4(RO_B_q1[3]), .Q5(RO_B_q1[4]), .Q6(RO_B_q1[5]), .Q7(RO_B_q1[6]),
    .Q8(RO_B_q1[7]), .Q1(RO_B_q1[0]), .D2(IN[1]), .D3(IN[2]), .D4(IN[3]), .D5(IN[4]), .D6(IN[5]), .D7(IN[6]),
    .D8(IN[7]), .CLK(WR_R7), .nOE(nRN_7), .D1(IN[0]));  // open: Probe
  logi7400ic_IC_74x574 R8_B (
    .Q2(RO_B_q1[9]), .Q3(RO_B_q1[10]), .Q4(RO_B_q1[11]), .Q5(RO_B_q1[12]), .Q6(RO_B_q1[13]),
    .Q7(RO_B_q1[14]), .Q8(RO_B_q1[15]), .Q1(RO_B_q1[8]), .D2(IN[9]), .D3(IN[10]), .D4(IN[11]), .D5(IN[12]),
    .D6(IN[13]), .D7(IN[14]), .D8(IN[15]), .CLK(WR_R7), .nOE(nRN_7), .D1(IN[8]));  // open: Probe
  IC_74x541 RN_B (
    .Q1(REG_B[0]), .Q2(REG_B[1]), .Q3(REG_B[2]), .Q4(REG_B[3]), .Q5(REG_B[4]), .Q6(REG_B[5]), .Q7(REG_B[6]),
    .Q8(REG_B[7]), .I1(RO_B_q1[0]), .I2(RO_B_q1[1]), .I3(RO_B_q1[2]), .I4(RO_B_q1[3]), .I5(RO_B_q1[4]),
    .I6(RO_B_q1[5]), .I7(RO_B_q1[6]), .I8(RO_B_q1[7]), .nOE1(1'b0), .nOE2(nRN_TO_B));
  IC_74x541 RN_B_2 (
    .Q1(REG_B[8]), .Q2(REG_B[9]), .Q3(REG_B[10]), .Q4(REG_B[11]), .Q5(REG_B[12]), .Q6(REG_B[13]),
    .Q7(REG_B[14]), .Q8(REG_B[15]), .I1(RO_B_q1[8]), .I2(RO_B_q1[9]), .I3(RO_B_q1[10]), .I4(RO_B_q1[11]),
    .I5(RO_B_q1[12]), .I6(RO_B_q1[13]), .I7(RO_B_q1[14]), .I8(RO_B_q1[15]), .nOE1(1'b0), .nOE2(nRN_TO_B));

  // Other names for the same wires on the sheet: nRD_A = nRD_TO_A; nRN_B = nRN_TO_B; nRS_A = nRS_TO_A
endmodule

// ALU
module ALUV (
  input  PS0f,
  input  PS1f,
  input  PS2f,
  input  PS3f,
  input  PS0t,
  input  PS1t,
  input  PS2t,
  input  PS3t,
  input  CS0,
  input  CS1,
  input  CS2,
  input  Z,
  input  GS0,
  input  GS1,
  input  SHR,
  input  [15:0] A,
  input  [15:0] B,
  input  C,
  input  T,
  input  [2:0] CC,
  input  CMP,
  input  BR0,
  input  BR1,
  output [15:0] Q,
  output ALU_Z,
  output ALU_C,
  output ALU_T,
  output ALU_nBR
);

  wire A15, alucore_1_p8, alucore_1_p9, and_1_out, and_2_out, buffer_4_out, buffer_6_out, C_t, CS_Select_a,
       F, nA15, nand_1_out, not_1_out, not_5_out, not_6_out, T_t, xnor_1_out, xor_1_out, Zero_Detect_2_y1,
       Zero_Detect_2_y2, Zero_Detect_2_y3, Zero_Detect_3_y, Zero_Detect_y1, Zero_Detect_y2, Zero_Detect_y3;
  wire [2:0] ic_74x257_1_y1;
  wire [3:0] PS_Select_a1;

  not not_1 (not_1_out, Z);
  buf buffer_1 (A15, A[15]);
  not not_2 (nA15, A[15]);
  buf buffer_2 (C_t, C);
  buf buffer_3 (T_t, T);
  not not_3 (F, T);
  IC_74x3257 PS_Select (
    .A1(PS_Select_a1[0]), .A2(PS_Select_a1[1]), .A3(PS_Select_a1[2]), .A4(PS_Select_a1[3]), .B2_1(PS0t),
    .B1_2(PS1f), .B2_2(PS1t), .B1_3(PS2f), .B2_3(PS2t), .B1_4(PS3f), .B2_4(PS3t), .S(T_t), .nOE(1'b0),
    .B1_1(PS0f));
  IC_74x3251 CS_Select (
    .A(CS_Select_a), .B1(1'b0), .B2(1'b1), .B3(F), .B4(T_t), .B5(nA15), .B6(A15), .B7(C_t), .B8(C_t),
    .S0(CS0), .S1(CS1), .S2(CS2), .nOE(1'b0));
  nand nand_1 (nand_1_out, CS2, CS1, not_1_out);
  IC_74x3253 BR_Select (
    .A1(ALU_nBR), .B1_1(1'b0), .B1_2(F), .B1_3(T_t), .B1_4(1'b1), .B2_1(1'b0), .B2_2(1'b0), .B2_3(1'b0),
    .B2_4(1'b0), .S0(BR0), .S1(BR1), .nOE1(1'b0), .nOE2(1'b0));  // open: A2
  // ALUCore alucore_1: pin names not known; wires that end beside it: PS_Select_a1, CS_Select_a, {GS1, GS0}, SHR, A, B, Q, alucore_1_p8, alucore_1_p9
  xor xor_1 (xor_1_out, alucore_1_p8, alucore_1_p9);
  xnor xnor_1 (xnor_1_out, Q[15], xor_1_out);
  IC_74x27 Zero_Detect (
    .Y2(Zero_Detect_y2), .Y3(Zero_Detect_y3), .Y1(Zero_Detect_y1), .A2(Q[3]), .B2(Q[4]), .C2(Q[5]),
    .A3(Q[6]), .B3(Q[7]), .C3(Q[8]), .A1(Q[0]), .B1(Q[1]), .C1(Q[2]));
  IC_74x27 Zero_Detect_2 (
    .Y2(Zero_Detect_2_y2), .Y3(Zero_Detect_2_y3), .Y1(Zero_Detect_2_y1), .A2(Q[12]), .B2(Q[13]), .C2(Q[14]),
    .A3(Q[15]), .B3(1'b0), .C3(1'b0), .A1(Q[9]), .B1(Q[10]), .C1(Q[11]));
  IC_74x257 ic_74x257_1 (
    .Y1(ic_74x257_1_y1[0]), .Y2(ic_74x257_1_y1[1]), .Y3(ic_74x257_1_y1[2]), .I1_0(1'b0), .I2_0(CC[0]),
    .I1_1(1'b0), .I2_1(CC[1]), .I1_2(1'b0), .I2_2(CC[2]), .I1_3(1'b0), .I2_3(1'b0), .nA_B(CMP), .nOE(1'b0));  // open: Y4
  IC_74x30 Zero_Detect_3 (
    .Y(Zero_Detect_3_y), .C(Zero_Detect_y2), .D(Zero_Detect_y3), .E(Zero_Detect_2_y1), .F(Zero_Detect_2_y2),
    .G(Zero_Detect_2_y3), .A(nand_1_out), .H(1'b1), .B(Zero_Detect_y1));
  not not_4 (ALU_Z, Zero_Detect_3_y);
  buf buffer_4 (buffer_4_out, Zero_Detect_3_y);
  buf buffer_5 (ALU_C, alucore_1_p8);
  not not_5 (not_5_out, alucore_1_p8);
  buf buffer_6 (buffer_6_out, xnor_1_out);
  not not_6 (not_6_out, xnor_1_out);
  and and_1 (and_1_out, alucore_1_p8, Zero_Detect_3_y);
  and and_2 (and_2_out, xnor_1_out, Zero_Detect_3_y);
  IC_74x3251 CondCode (
    .A(ALU_T), .B1(ALU_Z), .B2(buffer_4_out), .B3(ALU_C), .B4(not_5_out), .B5(buffer_6_out), .B6(not_6_out),
    .B7(and_1_out), .B8(and_2_out), .S0(ic_74x257_1_y1[0]), .S1(ic_74x257_1_y1[1]), .S2(ic_74x257_1_y1[2]),
    .nOE(1'b0));

  // Notes on the sheet:
  //   BR Select
  //   (Branch)
  //   --------
  //   00 (never)
  //   01 (if T)
  //   10 (if F)
  //   11 (always)
  //   T    PS Select
  //   --  ---------
  //   1    PS0t...PS3t
  //   0    PS0f...PS3f
  //   CS Select
  //   (GSSel)
  //   --------
  //   000
  //   001
  //   010
  //   011
  //   100
  //   101
  //   11x
  //   Efective
  //   /BR
  //   -------
  //   0
  //   /T
  //   T
  //   1
  //   Efective
  //   CS
  //   -------
  //   0
  //   1
  //   /T
  //   T
  //   /A15
  //   A15
  //   Cy
  //   Conditon 
  //   Code (CC)
  //   ---------
  //   000 (EQ)
  //   001 (NE)
  //   010 (UGE)
  //   011 (ULT)
  //   100 (GE)
  //   101 (LT)
  //   110 (UGT)
  //   111 (GT)
  //   Logic 
  //   Function (T)
  //   ------------
  //   Z
  //   /Z
  //   C
  //   /C
  //   S == V
  //   S != V
  //   C AND /Z
  //   (S==V) AND /Z
endmodule

// Register File
module Registers1 (
  input  nCLK,
  input  [2:0] RQ,
  input  nWR,
  input  [2:0] RA,
  input  nR_TO_A,
  input  [2:0] RB,
  input  nR_TO_B,
  input  [15:0] IN,
  output [15:0] REG_B,
  output [15:0] REG_A
);

  wire ic_74x573_1_q1, ic_74x573_1_q2, ic_74x573_1_q3, ic_74x573_1_q4, ic_74x573_1_q5, ic_74x573_1_q6,
       ic_74x573_1_q7, ic_74x573_1_q8, nRA_0, nRA_1, nRA_2, nRA_3, nRA_4, nRA_5, nRA_6, nRA_7, nRB_0, nRB_1,
       nRB_2, nRB_3, nRB_4, nRB_5, nRB_6, nRB_7, RWriteEn_y0, RWriteEn_y1, RWriteEn_y2, RWriteEn_y3,
       RWriteEn_y4, RWriteEn_y5, RWriteEn_y6, RWriteEn_y7, WR_R0, WR_R1, WR_R2, WR_R3, WR_R4, WR_R5, WR_R6,
       WR_R7;
  wire [15:0] R0_A_q1, RO_B_q1;

  logi7400ic_IC_74x574 R0_A (
    .Q2(R0_A_q1[1]), .Q3(R0_A_q1[2]), .Q4(R0_A_q1[3]), .Q5(R0_A_q1[4]), .Q6(R0_A_q1[5]), .Q7(R0_A_q1[6]),
    .Q8(R0_A_q1[7]), .Q1(R0_A_q1[0]), .D2(IN[1]), .D3(IN[2]), .D4(IN[3]), .D5(IN[4]), .D6(IN[5]), .D7(IN[6]),
    .D8(IN[7]), .CLK(WR_R0), .nOE(nRA_0), .D1(IN[0]));  // open: Probe
  logi7400ic_IC_74x574 R0_A_2 (
    .Q2(R0_A_q1[9]), .Q3(R0_A_q1[10]), .Q4(R0_A_q1[11]), .Q5(R0_A_q1[12]), .Q6(R0_A_q1[13]),
    .Q7(R0_A_q1[14]), .Q8(R0_A_q1[15]), .Q1(R0_A_q1[8]), .D2(IN[9]), .D3(IN[10]), .D4(IN[11]), .D5(IN[12]),
    .D6(IN[13]), .D7(IN[14]), .D8(IN[15]), .CLK(WR_R0), .nOE(nRA_0), .D1(IN[8]));  // open: Probe
  logi7400ic_IC_74x574 R1_A (
    .Q2(R0_A_q1[1]), .Q3(R0_A_q1[2]), .Q4(R0_A_q1[3]), .Q5(R0_A_q1[4]), .Q6(R0_A_q1[5]), .Q7(R0_A_q1[6]),
    .Q8(R0_A_q1[7]), .Q1(R0_A_q1[0]), .D2(IN[1]), .D3(IN[2]), .D4(IN[3]), .D5(IN[4]), .D6(IN[5]), .D7(IN[6]),
    .D8(IN[7]), .CLK(WR_R1), .nOE(nRA_1), .D1(IN[0]));  // open: Probe
  logi7400ic_IC_74x574 R1_A_2 (
    .Q2(R0_A_q1[9]), .Q3(R0_A_q1[10]), .Q4(R0_A_q1[11]), .Q5(R0_A_q1[12]), .Q6(R0_A_q1[13]),
    .Q7(R0_A_q1[14]), .Q8(R0_A_q1[15]), .Q1(R0_A_q1[8]), .D2(IN[9]), .D3(IN[10]), .D4(IN[11]), .D5(IN[12]),
    .D6(IN[13]), .D7(IN[14]), .D8(IN[15]), .CLK(WR_R1), .nOE(nRA_1), .D1(IN[8]));  // open: Probe
  logi7400ic_IC_74x574 R2_A (
    .Q2(R0_A_q1[1]), .Q3(R0_A_q1[2]), .Q4(R0_A_q1[3]), .Q5(R0_A_q1[4]), .Q6(R0_A_q1[5]), .Q7(R0_A_q1[6]),
    .Q8(R0_A_q1[7]), .Q1(R0_A_q1[0]), .D2(IN[1]), .D3(IN[2]), .D4(IN[3]), .D5(IN[4]), .D6(IN[5]), .D7(IN[6]),
    .D8(IN[7]), .CLK(WR_R2), .nOE(nRA_2), .D1(IN[0]));  // open: Probe
  logi7400ic_IC_74x574 R2_A_2 (
    .Q2(R0_A_q1[9]), .Q3(R0_A_q1[10]), .Q4(R0_A_q1[11]), .Q5(R0_A_q1[12]), .Q6(R0_A_q1[13]),
    .Q7(R0_A_q1[14]), .Q8(R0_A_q1[15]), .Q1(R0_A_q1[8]), .D2(IN[9]), .D3(IN[10]), .D4(IN[11]), .D5(IN[12]),
    .D6(IN[13]), .D7(IN[14]), .D8(IN[15]), .CLK(WR_R2), .nOE(nRA_2), .D1(IN[8]));  // open: Probe
  logi7400ic_IC_74x574 R3_A (
    .Q2(R0_A_q1[1]), .Q3(R0_A_q1[2]), .Q4(R0_A_q1[3]), .Q5(R0_A_q1[4]), .Q6(R0_A_q1[5]), .Q7(R0_A_q1[6]),
    .Q8(R0_A_q1[7]), .Q1(R0_A_q1[0]), .D2(IN[1]), .D3(IN[2]), .D4(IN[3]), .D5(IN[4]), .D6(IN[5]), .D7(IN[6]),
    .D8(IN[7]), .CLK(WR_R3), .nOE(nRA_3), .D1(IN[0]));  // open: Probe
  logi7400ic_IC_74x574 R3_A_2 (
    .Q2(R0_A_q1[9]), .Q3(R0_A_q1[10]), .Q4(R0_A_q1[11]), .Q5(R0_A_q1[12]), .Q6(R0_A_q1[13]),
    .Q7(R0_A_q1[14]), .Q8(R0_A_q1[15]), .Q1(R0_A_q1[8]), .D2(IN[9]), .D3(IN[10]), .D4(IN[11]), .D5(IN[12]),
    .D6(IN[13]), .D7(IN[14]), .D8(IN[15]), .CLK(WR_R3), .nOE(nRA_3), .D1(IN[8]));  // open: Probe
  logi7400ic_IC_74x574 RO_B (
    .Q2(RO_B_q1[1]), .Q3(RO_B_q1[2]), .Q4(RO_B_q1[3]), .Q5(RO_B_q1[4]), .Q6(RO_B_q1[5]), .Q7(RO_B_q1[6]),
    .Q8(RO_B_q1[7]), .Q1(RO_B_q1[0]), .D2(IN[1]), .D3(IN[2]), .D4(IN[3]), .D5(IN[4]), .D6(IN[5]), .D7(IN[6]),
    .D8(IN[7]), .CLK(WR_R0), .nOE(nRB_0), .D1(IN[0]));  // open: Probe
  logi7400ic_IC_74x574 R0_B (
    .Q2(RO_B_q1[9]), .Q3(RO_B_q1[10]), .Q4(RO_B_q1[11]), .Q5(RO_B_q1[12]), .Q6(RO_B_q1[13]),
    .Q7(RO_B_q1[14]), .Q8(RO_B_q1[15]), .Q1(RO_B_q1[8]), .D2(IN[9]), .D3(IN[10]), .D4(IN[11]), .D5(IN[12]),
    .D6(IN[13]), .D7(IN[14]), .D8(IN[15]), .CLK(WR_R0), .nOE(nRB_0), .D1(IN[8]));  // open: Probe
  logi7400ic_IC_74x574 R1_B (
    .Q2(RO_B_q1[1]), .Q3(RO_B_q1[2]), .Q4(RO_B_q1[3]), .Q5(RO_B_q1[4]), .Q6(RO_B_q1[5]), .Q7(RO_B_q1[6]),
    .Q8(RO_B_q1[7]), .Q1(RO_B_q1[0]), .D2(IN[1]), .D3(IN[2]), .D4(IN[3]), .D5(IN[4]), .D6(IN[5]), .D7(IN[6]),
    .D8(IN[7]), .CLK(WR_R1), .nOE(nRB_1), .D1(IN[0]));  // open: Probe
  logi7400ic_IC_74x574 R1_B_2 (
    .Q2(RO_B_q1[9]), .Q3(RO_B_q1[10]), .Q4(RO_B_q1[11]), .Q5(RO_B_q1[12]), .Q6(RO_B_q1[13]),
    .Q7(RO_B_q1[14]), .Q8(RO_B_q1[15]), .Q1(RO_B_q1[8]), .D2(IN[9]), .D3(IN[10]), .D4(IN[11]), .D5(IN[12]),
    .D6(IN[13]), .D7(IN[14]), .D8(IN[15]), .CLK(WR_R1), .nOE(nRB_1), .D1(IN[8]));  // open: Probe
  logi7400ic_IC_74x574 R2_B (
    .Q2(RO_B_q1[1]), .Q3(RO_B_q1[2]), .Q4(RO_B_q1[3]), .Q5(RO_B_q1[4]), .Q6(RO_B_q1[5]), .Q7(RO_B_q1[6]),
    .Q8(RO_B_q1[7]), .Q1(RO_B_q1[0]), .D2(IN[1]), .D3(IN[2]), .D4(IN[3]), .D5(IN[4]), .D6(IN[5]), .D7(IN[6]),
    .D8(IN[7]), .CLK(WR_R2), .nOE(nRB_2), .D1(IN[0]));  // open: Probe
  logi7400ic_IC_74x574 R2_B_2 (
    .Q2(RO_B_q1[9]), .Q3(RO_B_q1[10]), .Q4(RO_B_q1[11]), .Q5(RO_B_q1[12]), .Q6(RO_B_q1[13]),
    .Q7(RO_B_q1[14]), .Q8(RO_B_q1[15]), .Q1(RO_B_q1[8]), .D2(IN[9]), .D3(IN[10]), .D4(IN[11]), .D5(IN[12]),
    .D6(IN[13]), .D7(IN[14]), .D8(IN[15]), .CLK(WR_R2), .nOE(nRB_2), .D1(IN[8]));  // open: Probe
  logi7400ic_IC_74x574 R3_B (
    .Q2(RO_B_q1[1]), .Q3(RO_B_q1[2]), .Q4(RO_B_q1[3]), .Q5(RO_B_q1[4]), .Q6(RO_B_q1[5]), .Q7(RO_B_q1[6]),
    .Q8(RO_B_q1[7]), .Q1(RO_B_q1[0]), .D2(IN[1]), .D3(IN[2]), .D4(IN[3]), .D5(IN[4]), .D6(IN[5]), .D7(IN[6]),
    .D8(IN[7]), .CLK(WR_R3), .nOE(nRB_3), .D1(IN[0]));  // open: Probe
  logi7400ic_IC_74x574 R3_B_2 (
    .Q2(RO_B_q1[9]), .Q3(RO_B_q1[10]), .Q4(RO_B_q1[11]), .Q5(RO_B_q1[12]), .Q6(RO_B_q1[13]),
    .Q7(RO_B_q1[14]), .Q8(RO_B_q1[15]), .Q1(RO_B_q1[8]), .D2(IN[9]), .D3(IN[10]), .D4(IN[11]), .D5(IN[12]),
    .D6(IN[13]), .D7(IN[14]), .D8(IN[15]), .CLK(WR_R3), .nOE(nRB_3), .D1(IN[8]));  // open: Probe
  IC_74x138 RWriteEn (
    .Y0(RWriteEn_y0), .Y1(RWriteEn_y1), .Y2(RWriteEn_y2), .Y3(RWriteEn_y3), .Y4(RWriteEn_y4),
    .Y5(RWriteEn_y5), .Y6(RWriteEn_y6), .Y7(RWriteEn_y7), .A(RQ[0]), .B(RQ[1]), .C(RQ[2]), .nG2A(nWR),
    .nG2B(1'b0), .G1(1'b1));
  IC_74x138 RSelA (
    .Y0(nRA_0), .Y1(nRA_1), .Y2(nRA_2), .Y3(nRA_3), .Y4(nRA_4), .Y5(nRA_5), .Y6(nRA_6), .Y7(nRA_7),
    .A(RA[0]), .B(RA[1]), .C(RA[2]), .nG2A(1'b0), .nG2B(1'b0), .G1(1'b1));
  IC_74x138 RSelB (
    .Y0(nRB_0), .Y1(nRB_1), .Y2(nRB_2), .Y3(nRB_3), .Y4(nRB_4), .Y5(nRB_5), .Y6(nRB_6), .Y7(nRB_7),
    .A(RB[0]), .B(RB[1]), .C(RB[2]), .nG2A(1'b0), .nG2B(1'b0), .G1(1'b1));
  IC_74x573 ic_74x573_1 (
    .Q2(ic_74x573_1_q2), .Q3(ic_74x573_1_q3), .Q4(ic_74x573_1_q4), .Q5(ic_74x573_1_q5), .Q6(ic_74x573_1_q6),
    .Q7(ic_74x573_1_q7), .Q8(ic_74x573_1_q8), .Q1(ic_74x573_1_q1), .D2(RWriteEn_y1), .D3(RWriteEn_y2),
    .D4(RWriteEn_y3), .D5(RWriteEn_y4), .D6(RWriteEn_y5), .D7(RWriteEn_y6), .D8(RWriteEn_y7), .LE(nCLK),
    .nOE(1'b0), .D1(RWriteEn_y0));  // open: Probe
  nor nor_1 (WR_R0, nCLK, ic_74x573_1_q1);
  nor nor_2 (WR_R1, nCLK, ic_74x573_1_q2);
  nor nor_3 (WR_R2, nCLK, ic_74x573_1_q3);
  nor nor_4 (WR_R3, nCLK, ic_74x573_1_q4);
  nor nor_5 (WR_R4, nCLK, ic_74x573_1_q5);
  nor nor_6 (WR_R5, nCLK, ic_74x573_1_q6);
  nor nor_7 (WR_R6, nCLK, ic_74x573_1_q7);
  nor nor_8 (WR_R7, nCLK, ic_74x573_1_q8);
  logi7400ic_IC_74x574 R4_A (
    .Q2(R0_A_q1[1]), .Q3(R0_A_q1[2]), .Q4(R0_A_q1[3]), .Q5(R0_A_q1[4]), .Q6(R0_A_q1[5]), .Q7(R0_A_q1[6]),
    .Q8(R0_A_q1[7]), .Q1(R0_A_q1[0]), .D2(IN[1]), .D3(IN[2]), .D4(IN[3]), .D5(IN[4]), .D6(IN[5]), .D7(IN[6]),
    .D8(IN[7]), .CLK(WR_R4), .nOE(nRA_4), .D1(IN[0]));  // open: Probe
  logi7400ic_IC_74x574 R4_A_2 (
    .Q2(R0_A_q1[9]), .Q3(R0_A_q1[10]), .Q4(R0_A_q1[11]), .Q5(R0_A_q1[12]), .Q6(R0_A_q1[13]),
    .Q7(R0_A_q1[14]), .Q8(R0_A_q1[15]), .Q1(R0_A_q1[8]), .D2(IN[9]), .D3(IN[10]), .D4(IN[11]), .D5(IN[12]),
    .D6(IN[13]), .D7(IN[14]), .D8(IN[15]), .CLK(WR_R4), .nOE(nRA_4), .D1(IN[8]));  // open: Probe
  logi7400ic_IC_74x574 R5_A (
    .Q2(R0_A_q1[1]), .Q3(R0_A_q1[2]), .Q4(R0_A_q1[3]), .Q5(R0_A_q1[4]), .Q6(R0_A_q1[5]), .Q7(R0_A_q1[6]),
    .Q8(R0_A_q1[7]), .Q1(R0_A_q1[0]), .D2(IN[1]), .D3(IN[2]), .D4(IN[3]), .D5(IN[4]), .D6(IN[5]), .D7(IN[6]),
    .D8(IN[7]), .CLK(WR_R5), .nOE(nRA_5), .D1(IN[0]));  // open: Probe
  logi7400ic_IC_74x574 R5_A_2 (
    .Q2(R0_A_q1[9]), .Q3(R0_A_q1[10]), .Q4(R0_A_q1[11]), .Q5(R0_A_q1[12]), .Q6(R0_A_q1[13]),
    .Q7(R0_A_q1[14]), .Q8(R0_A_q1[15]), .Q1(R0_A_q1[8]), .D2(IN[9]), .D3(IN[10]), .D4(IN[11]), .D5(IN[12]),
    .D6(IN[13]), .D7(IN[14]), .D8(IN[15]), .CLK(WR_R5), .nOE(nRA_5), .D1(IN[8]));  // open: Probe
  logi7400ic_IC_74x574 R6_A (
    .Q2(R0_A_q1[1]), .Q3(R0_A_q1[2]), .Q4(R0_A_q1[3]), .Q5(R0_A_q1[4]), .Q6(R0_A_q1[5]), .Q7(R0_A_q1[6]),
    .Q8(R0_A_q1[7]), .Q1(R0_A_q1[0]), .D2(IN[1]), .D3(IN[2]), .D4(IN[3]), .D5(IN[4]), .D6(IN[5]), .D7(IN[6]),
    .D8(IN[7]), .CLK(WR_R6), .nOE(nRA_6), .D1(IN[0]));  // open: Probe
  logi7400ic_IC_74x574 R6_A_2 (
    .Q2(R0_A_q1[9]), .Q3(R0_A_q1[10]), .Q4(R0_A_q1[11]), .Q5(R0_A_q1[12]), .Q6(R0_A_q1[13]),
    .Q7(R0_A_q1[14]), .Q8(R0_A_q1[15]), .Q1(R0_A_q1[8]), .D2(IN[9]), .D3(IN[10]), .D4(IN[11]), .D5(IN[12]),
    .D6(IN[13]), .D7(IN[14]), .D8(IN[15]), .CLK(WR_R6), .nOE(nRA_6), .D1(IN[8]));  // open: Probe
  logi7400ic_IC_74x574 R7_A (
    .Q2(R0_A_q1[1]), .Q3(R0_A_q1[2]), .Q4(R0_A_q1[3]), .Q5(R0_A_q1[4]), .Q6(R0_A_q1[5]), .Q7(R0_A_q1[6]),
    .Q8(R0_A_q1[7]), .Q1(R0_A_q1[0]), .D2(IN[1]), .D3(IN[2]), .D4(IN[3]), .D5(IN[4]), .D6(IN[5]), .D7(IN[6]),
    .D8(IN[7]), .CLK(WR_R7), .nOE(nRA_7), .D1(IN[0]));  // open: Probe
  logi7400ic_IC_74x574 R8_A (
    .Q2(R0_A_q1[9]), .Q3(R0_A_q1[10]), .Q4(R0_A_q1[11]), .Q5(R0_A_q1[12]), .Q6(R0_A_q1[13]),
    .Q7(R0_A_q1[14]), .Q8(R0_A_q1[15]), .Q1(R0_A_q1[8]), .D2(IN[9]), .D3(IN[10]), .D4(IN[11]), .D5(IN[12]),
    .D6(IN[13]), .D7(IN[14]), .D8(IN[15]), .CLK(WR_R7), .nOE(nRA_7), .D1(IN[8]));  // open: Probe
  IC_74x541 R_A (
    .Q1(REG_A[0]), .Q2(REG_A[1]), .Q3(REG_A[2]), .Q4(REG_A[3]), .Q5(REG_A[4]), .Q6(REG_A[5]), .Q7(REG_A[6]),
    .Q8(REG_A[7]), .I1(R0_A_q1[0]), .I2(R0_A_q1[1]), .I3(R0_A_q1[2]), .I4(R0_A_q1[3]), .I5(R0_A_q1[4]),
    .I6(R0_A_q1[5]), .I7(R0_A_q1[6]), .I8(R0_A_q1[7]), .nOE1(1'b0), .nOE2(nR_TO_A));
  IC_74x541 R_A_2 (
    .Q1(REG_A[8]), .Q2(REG_A[9]), .Q3(REG_A[10]), .Q4(REG_A[11]), .Q5(REG_A[12]), .Q6(REG_A[13]),
    .Q7(REG_A[14]), .Q8(REG_A[15]), .I1(R0_A_q1[8]), .I2(R0_A_q1[9]), .I3(R0_A_q1[10]), .I4(R0_A_q1[11]),
    .I5(R0_A_q1[12]), .I6(R0_A_q1[13]), .I7(R0_A_q1[14]), .I8(R0_A_q1[15]), .nOE1(1'b0), .nOE2(nR_TO_A));
  logi7400ic_IC_74x574 R4_B (
    .Q2(RO_B_q1[1]), .Q3(RO_B_q1[2]), .Q4(RO_B_q1[3]), .Q5(RO_B_q1[4]), .Q6(RO_B_q1[5]), .Q7(RO_B_q1[6]),
    .Q8(RO_B_q1[7]), .Q1(RO_B_q1[0]), .D2(IN[1]), .D3(IN[2]), .D4(IN[3]), .D5(IN[4]), .D6(IN[5]), .D7(IN[6]),
    .D8(IN[7]), .CLK(WR_R4), .nOE(nRB_4), .D1(IN[0]));  // open: Probe
  logi7400ic_IC_74x574 R4_B_2 (
    .Q2(RO_B_q1[9]), .Q3(RO_B_q1[10]), .Q4(RO_B_q1[11]), .Q5(RO_B_q1[12]), .Q6(RO_B_q1[13]),
    .Q7(RO_B_q1[14]), .Q8(RO_B_q1[15]), .Q1(RO_B_q1[8]), .D2(IN[9]), .D3(IN[10]), .D4(IN[11]), .D5(IN[12]),
    .D6(IN[13]), .D7(IN[14]), .D8(IN[15]), .CLK(WR_R4), .nOE(nRB_4), .D1(IN[8]));  // open: Probe
  logi7400ic_IC_74x574 R5_B (
    .Q2(RO_B_q1[1]), .Q3(RO_B_q1[2]), .Q4(RO_B_q1[3]), .Q5(RO_B_q1[4]), .Q6(RO_B_q1[5]), .Q7(RO_B_q1[6]),
    .Q8(RO_B_q1[7]), .Q1(RO_B_q1[0]), .D2(IN[1]), .D3(IN[2]), .D4(IN[3]), .D5(IN[4]), .D6(IN[5]), .D7(IN[6]),
    .D8(IN[7]), .CLK(WR_R5), .nOE(nRB_5), .D1(IN[0]));  // open: Probe
  logi7400ic_IC_74x574 R5_B_2 (
    .Q2(RO_B_q1[9]), .Q3(RO_B_q1[10]), .Q4(RO_B_q1[11]), .Q5(RO_B_q1[12]), .Q6(RO_B_q1[13]),
    .Q7(RO_B_q1[14]), .Q8(RO_B_q1[15]), .Q1(RO_B_q1[8]), .D2(IN[9]), .D3(IN[10]), .D4(IN[11]), .D5(IN[12]),
    .D6(IN[13]), .D7(IN[14]), .D8(IN[15]), .CLK(WR_R5), .nOE(nRB_5), .D1(IN[8]));  // open: Probe
  logi7400ic_IC_74x574 R6_B (
    .Q2(RO_B_q1[1]), .Q3(RO_B_q1[2]), .Q4(RO_B_q1[3]), .Q5(RO_B_q1[4]), .Q6(RO_B_q1[5]), .Q7(RO_B_q1[6]),
    .Q8(RO_B_q1[7]), .Q1(RO_B_q1[0]), .D2(IN[1]), .D3(IN[2]), .D4(IN[3]), .D5(IN[4]), .D6(IN[5]), .D7(IN[6]),
    .D8(IN[7]), .CLK(WR_R6), .nOE(nRB_6), .D1(IN[0]));  // open: Probe
  logi7400ic_IC_74x574 R6_B_2 (
    .Q2(RO_B_q1[9]), .Q3(RO_B_q1[10]), .Q4(RO_B_q1[11]), .Q5(RO_B_q1[12]), .Q6(RO_B_q1[13]),
    .Q7(RO_B_q1[14]), .Q8(RO_B_q1[15]), .Q1(RO_B_q1[8]), .D2(IN[9]), .D3(IN[10]), .D4(IN[11]), .D5(IN[12]),
    .D6(IN[13]), .D7(IN[14]), .D8(IN[15]), .CLK(WR_R6), .nOE(nRB_6), .D1(IN[8]));  // open: Probe
  logi7400ic_IC_74x574 R7_B (
    .Q2(RO_B_q1[1]), .Q3(RO_B_q1[2]), .Q4(RO_B_q1[3]), .Q5(RO_B_q1[4]), .Q6(RO_B_q1[5]), .Q7(RO_B_q1[6]),
    .Q8(RO_B_q1[7]), .Q1(RO_B_q1[0]), .D2(IN[1]), .D3(IN[2]), .D4(IN[3]), .D5(IN[4]), .D6(IN[5]), .D7(IN[6]),
    .D8(IN[7]), .CLK(WR_R7), .nOE(nRB_7), .D1(IN[0]));  // open: Probe
  logi7400ic_IC_74x574 R8_B (
    .Q2(RO_B_q1[9]), .Q3(RO_B_q1[10]), .Q4(RO_B_q1[11]), .Q5(RO_B_q1[12]), .Q6(RO_B_q1[13]),
    .Q7(RO_B_q1[14]), .Q8(RO_B_q1[15]), .Q1(RO_B_q1[8]), .D2(IN[9]), .D3(IN[10]), .D4(IN[11]), .D5(IN[12]),
    .D6(IN[13]), .D7(IN[14]), .D8(IN[15]), .CLK(WR_R7), .nOE(nRB_7), .D1(IN[8]));  // open: Probe
  IC_74x541 R_B (
    .Q1(REG_B[0]), .Q2(REG_B[1]), .Q3(REG_B[2]), .Q4(REG_B[3]), .Q5(REG_B[4]), .Q6(REG_B[5]), .Q7(REG_B[6]),
    .Q8(REG_B[7]), .I1(RO_B_q1[0]), .I2(RO_B_q1[1]), .I3(RO_B_q1[2]), .I4(RO_B_q1[3]), .I5(RO_B_q1[4]),
    .I6(RO_B_q1[5]), .I7(RO_B_q1[6]), .I8(RO_B_q1[7]), .nOE1(1'b0), .nOE2(nR_TO_B));
  IC_74x541 R_B_2 (
    .Q1(REG_B[8]), .Q2(REG_B[9]), .Q3(REG_B[10]), .Q4(REG_B[11]), .Q5(REG_B[12]), .Q6(REG_B[13]),
    .Q7(REG_B[14]), .Q8(REG_B[15]), .I1(RO_B_q1[8]), .I2(RO_B_q1[9]), .I3(RO_B_q1[10]), .I4(RO_B_q1[11]),
    .I5(RO_B_q1[12]), .I6(RO_B_q1[13]), .I7(RO_B_q1[14]), .I8(RO_B_q1[15]), .nOE1(1'b0), .nOE2(nR_TO_B));

  // Other names for the same wires on the sheet: nQ_R = nWR; nR_A = nR_TO_A; nR_B = nR_TO_B
endmodule

// ALU
module ALU1 (
  input  PS0,
  input  PS1,
  input  PS2,
  input  PS3,
  input  CS0,
  input  CS1,
  input  CS2,
  input  Z,
  input  GS0,
  input  GS1,
  input  SHR,
  input  [15:0] A,
  input  [15:0] B,
  input  C,
  input  T,
  input  SL0,
  input  SL1,
  input  [2:0] CC,
  input  CMP,
  input  BR0,
  input  BR1,
  output [15:0] Q,
  output ALU_Z,
  output ALU_C,
  output ALU_T,
  output ALU_nBR
);

  wire A15, ALUCore_C, ALUCore_Cx, ALUCore_nZ, ALUCore_S, and_1_out, and_2_out, buffer_4_out, buffer_6_out,
       C_t, CS_Select_a, F, nA15, nand_1_out, not_1_out, not_5_out, not_6_out, T_t, xnor_1_out, xor_1_out,
       Zero_Detect_2_y1, Zero_Detect_2_y2, Zero_Detect_2_y3, Zero_Detect_y1, Zero_Detect_y2, Zero_Detect_y3;
  wire [2:0] ic_74x257_1_y1;
  wire [14:0] alucore_1_p7;

  not not_1 (not_1_out, Z);
  buf buffer_1 (A15, A[15]);
  not not_2 (nA15, A[15]);
  buf buffer_2 (C_t, C);
  buf buffer_3 (T_t, T);
  not not_3 (F, T);
  IC_74x3251 CS_Select (
    .A(CS_Select_a), .B1(1'b0), .B2(1'b1), .B3(nA15), .B4(A15), .B5(C_t), .B6(C_t), .B7(C_t), .B8(C_t),
    .S0(CS0), .S1(CS1), .S2(CS2), .nOE(1'b0));
  nand nand_1 (nand_1_out, CS2, not_1_out);
  IC_74x3253 BR_Select (
    .A1(ALU_nBR), .B1_1(1'b0), .B1_2(F), .B1_3(T_t), .B1_4(1'b1), .B2_1(1'b0), .B2_2(1'b0), .B2_3(1'b0),
    .B2_4(1'b0), .S0(BR0), .S1(BR1), .nOE1(1'b0), .nOE2(1'b0));  // open: A2
  // ALUCore alucore_1: pin names not known; wires that end beside it: {PS3, PS2, PS1, PS0}, CS_Select_a, {GS1, GS0}, SHR, A, B, {ALUCore_S, alucore_1_p7}, ALUCore_C, ALUCore_Cx
  xor xor_1 (xor_1_out, ALUCore_C, ALUCore_Cx);
  ALUSel alusel_1 (.Q(Q), .T(T_t), .nT(F), .SL0(SL0), .SL1(SL1), .A({ALUCore_S, alucore_1_p7}), .B(B));  // open: nOE
  xnor xnor_1 (xnor_1_out, ALUCore_S, xor_1_out);
  IC_74x257 ic_74x257_1 (
    .Y1(ic_74x257_1_y1[0]), .Y2(ic_74x257_1_y1[1]), .Y3(ic_74x257_1_y1[2]), .I1_0(1'b0), .I2_0(CC[0]),
    .I1_1(1'b0), .I2_1(CC[1]), .I1_2(1'b0), .I2_2(CC[2]), .I1_3(1'b0), .I2_3(1'b0), .nA_B(CMP), .nOE(1'b0));  // open: Y4
  IC_74x27 Zero_Detect (
    .Y2(Zero_Detect_y2), .Y3(Zero_Detect_y3), .Y1(Zero_Detect_y1), .A2(alucore_1_p7[3]),
    .B2(alucore_1_p7[4]), .C2(alucore_1_p7[5]), .A3(alucore_1_p7[6]), .B3(alucore_1_p7[7]),
    .C3(alucore_1_p7[8]), .A1(alucore_1_p7[0]), .B1(alucore_1_p7[1]), .C1(alucore_1_p7[2]));
  IC_74x27 Zero_Detect_2 (
    .Y2(Zero_Detect_2_y2), .Y3(Zero_Detect_2_y3), .Y1(Zero_Detect_2_y1), .A2(alucore_1_p7[12]),
    .B2(alucore_1_p7[13]), .C2(alucore_1_p7[14]), .A3(ALUCore_S), .B3(1'b0), .C3(1'b0), .A1(alucore_1_p7[9]),
    .B1(alucore_1_p7[10]), .C1(alucore_1_p7[11]));
  not not_4 (ALU_Z, ALUCore_nZ);
  buf buffer_4 (buffer_4_out, ALUCore_nZ);
  buf buffer_5 (ALU_C, ALUCore_C);
  not not_5 (not_5_out, ALUCore_C);
  buf buffer_6 (buffer_6_out, xnor_1_out);
  not not_6 (not_6_out, xnor_1_out);
  and and_1 (and_1_out, ALUCore_C, ALUCore_nZ);
  and and_2 (and_2_out, xnor_1_out, ALUCore_nZ);
  IC_74x30 Zero_Detect_3 (
    .Y(ALUCore_nZ), .C(Zero_Detect_y2), .D(Zero_Detect_y3), .E(Zero_Detect_2_y1), .F(Zero_Detect_2_y2),
    .G(Zero_Detect_2_y3), .A(nand_1_out), .H(1'b1), .B(Zero_Detect_y1));
  IC_74x3251 CondCode (
    .A(ALU_T), .B1(ALU_Z), .B2(buffer_4_out), .B3(ALU_C), .B4(not_5_out), .B5(buffer_6_out), .B6(not_6_out),
    .B7(and_1_out), .B8(and_2_out), .S0(ic_74x257_1_y1[0]), .S1(ic_74x257_1_y1[1]), .S2(ic_74x257_1_y1[2]),
    .nOE(1'b0));

  // Notes on the sheet:
  //   BR Select
  //   (Branch)
  //   --------
  //   00 (never)
  //   01 (if T)
  //   10 (if F)
  //   11 (always)
  //   T    PS Select
  //   --  ---------
  //   1    PS0t...PS3t
  //   0    PS0f...PS3f
  //   CS Select
  //   (GSSel)
  //   --------
  //   000
  //   001
  //   010
  //   011
  //   1xx
  //   Efective
  //   /BR
  //   -------
  //   0
  //   /T
  //   T
  //   1
  //   Efective
  //   CS
  //   -------
  //   0
  //   1
  //   /A15
  //   A15
  //   Cy
  //   Conditon 
  //   Code (CC)
  //   ---------
  //   000 (EQ)
  //   001 (NE)
  //   010 (UGE)
  //   011 (ULT)
  //   100 (GE)
  //   101 (LT)
  //   110 (UGT)
  //   111 (GT)
  //   Logic 
  //   Function (T)
  //   ------------
  //   Z
  //   /Z
  //   C
  //   /C
  //   S == V
  //   S != V
  //   C AND /Z
  //   (S==V) AND /Z
endmodule

// SR
module RegSRV (
  input  cpWR,
  input  Zin,
  input  Cin,
  input  Tin,
  output SR_Z,
  output SR_C,
  output SR_T
);

  IC_74x273 ic_74x273_1 (
    .Q1(SR_Z), .Q2(SR_C), .Q3(SR_T), .D1(Zin), .D2(Cin), .D3(Tin), .D4(1'b0), .D5(1'b0), .D6(1'b0),
    .D7(1'b0), .D8(1'b0), .CLK(cpWR), .nMR(1'b1));  // open: Probe, Q4, Q5, Q6, Q7, Q8

  // Other names for the same wires on the sheet: CLK_WR = cpWR
endmodule

module Signals (
);


  // Notes on the sheet:
  //   Function
  //   -----------
  //   SELECT 0
  //   SELECT 1
  //   SELECT A
  //   SELECT B
  //   OR A, B
  //   AND A, B
  //   XOR A, B
  //   NOT A
  //   ADD A, B
  //   ADDC A, B
  //   SUB A, B
  //   SUBC A, B
  //   NEG A
  //   SEXTW A
  //   LSR A
  //   LSRC A
  //   ASR A
  //   INC A
  //   DEC A
  //   A+2
  //   A-2 
  //   (other functions are possible)
  //   CS Select
  //   (GSSel)
  //   --------
  //   000
  //   001
  //   010
  //   011
  //   1xx
  //   BR Select
  //   (Branch)
  //   --------
  //   00 (never)
  //   01 (if T)
  //   10 (if F)
  //   11 (always)
  //   Function    A  B   SL  
  //   ---------------------------
  //   SELECT A    A  x   00
  //   SELT A, 0   A  x   01
  //   SETT        1  x   01
  //   SELF A, 0   A  x   10
  //   SETF        1  x   10
  //   SEL A, B    A  B   11
  //   Efective
  //   CS
  //   -------
  //   0
  //   1
  //   /A15
  //   A15
  //   Cy
  //   PS
  //   -------------
  //   0000 (0x0)
  //   0000 (0x0)
  //   1010 (A)
  //   1100 (B)
  //   1110 (A OR B)
  //   1000 (A AND B)
  //   0110 (A XOR B)
  //   0101 (/A)
  //   0110 (A XOR B)
  //   0110 (A XOR B)
  //   1001 (A XOR /B)
  //   1001 (A XOR /B)
  //   0101 (/A)
  //   1111 (0xffff)
  //   1010 (A)
  //   1010 (A)
  //   1010 (A)
  //   1010 (A)
  //   0101 (/A)
  //   1010 (A)
  //   0101 (/A)
  //   Efective
  //   BR
  //   -------
  //   0
  //   T
  //   /T
  //   1
  //   GS
  //   -----------
  //   00 (0x0)
  //   00 (0x0)
  //   00 (0x0)
  //   00 (0x0)
  //   00 (0x0)
  //   00 (0x0)
  //   00 (0x0)
  //   00 (0x0)
  //   10 (A AND B)
  //   10 (A AND B)
  //   01 (A AND /B)
  //   01 (A AND /B)
  //   00 (0x0)
  //   00 (0x0)
  //   00 (0x0)
  //   00 (0x0)
  //   00 (0x0)
  //   00 (0x0)
  //   11 (A)
  //   00 (0x0)
  //   11 (A)
  //   Operation
  //   ---------
  //   ST.W
  //   ST.B
  //   LD.W
  //   LD.SB
  //   LD.ZB
  //   PASTHR
  //   SEXT
  //   ZEXT
  //   ASR8
  //   LSR8
  //   LSL8
  //   Hi Z
  //           CYCLE 1
  //   Mem nIE nOE ISh OSh nEx SEx
  //   ---------------------------
  //    1   1   1   0   x   x   x 
  //    1   1   1   1   x   x   x
  //    1   1   1   0   0   1   x
  //    1   1   1   0   1   0   1
  //    1   1   1   0   1   0   0
  //    0   0   0   0   0   1   x
  //    0   0   0   0   0   0   1
  //    0   0   0   0   0   0   0
  //    0   0   0   0   1   0   1
  //    0   0   0   0   1   0   0
  //    0   0   0   1   0   1   x
  //    0   1   1   x   x   x   x
  //   Operation
  //   ---------
  //   ST.W
  //   ST.B
  //   LD.W
  //   LD.SB
  //   LD.ZB
  //   PASTHR
  //   SEXT
  //   ZEXT
  //   ASR8
  //   LSR8
  //   LSL8
  //   Hi Z
  //   P2
  //   ---
  //   0
  //   0
  //   0
  //   0
  //   0
  //   0
  //   0
  //   0
  //   0
  //   0
  //   0
  //   0
  //   0
  //   0
  //   0
  //   0
  //   0
  //   0
  //   0
  //   1
  //   1
  //   SHR
  //   ---
  //   0
  //   0
  //   0
  //   0
  //   0
  //   0
  //   0
  //   0
  //   0
  //   0
  //   0
  //   0
  //   0
  //   0
  //   1
  //   1
  //   1
  //   0
  //   0
  //   0
  //   0
  //           CYCLE 1
  //   Mem  IE  OE ISh OSh  Ex SEx
  //   ---------------------------
  //    1   0   0   0   x   x   x 
  //    1   0   0   1   x   x   x
  //    1   0   0   0   0   0   x
  //    1   0   0   0   1   1   1
  //    1   0   0   0   1   1   0
  //    0   1   1   0   0   0   x
  //    0   1   1   0   0   1   1
  //    0   1   1   0   0   1   0
  //    0   1   1   0   1   1   1
  //    0   1   1   0   1   1   0
  //    0   1   1   1   0   0   x
  //    0   0   0   x   x   x   x
  //   CS
  //   --------
  //   0
  //   1
  //   0
  //   0
  //   0
  //   0
  //   0
  //   0
  //   0
  //   Prev Carry
  //   1
  //   Prev Carry
  //   1
  //   /A15
  //   0
  //   Prev Carry
  //   A15
  //   1
  //   0
  //   0
  //   0
  //            CYCLE 2
  //   Mem nIE nOE ISh OSh nEx SEx
  //   ---------------------------
  //    0   0   1   x   x   x   x 
  //    0   0   1   x   x   x   x
  //    0   1   0   x   x   x   x
  //    0   1   0   x   x   x   x
  //    0   1   0   x   x   x   x
  //    -   -   -   -   -   -   -
  //    -   -   -   -   -   -   -
  //    -   -   -   -   -   -   -
  //    -   -   -   -   -   -   -
  //    -   -   -   -   -   -   -
  //    -   -   -   -   -   -   -
  //    -   -   -   -   -   -   -
  //            CYCLE 2
  //   Mem  IE  OE ISh OSh  Ex SEx
  //   ---------------------------
  //    0   1   0   x   x   x   x 
  //    0   1   0   x   x   x   x
  //    0   0   1   x   x   x   x
  //    0   0   1   x   x   x   x
  //    0   0   1   x   x   x   x
  //    -   -   -   -   -   -   -
  //    -   -   -   -   -   -   -
  //    -   -   -   -   -   -   -
  //    -   -   -   -   -   -   -
  //    -   -   -   -   -   -   -
  //    -   -   -   -   -   -   -
  //    -   -   -   -   -   -   -
endmodule

// Inst Decoder
module InstDecoder1 (
  input  nRESET,
  input  CLK,
  input  [15:0] IRin,
  output IR_RA,
  output CTRL_PS0,
  output CTRL_PS1,
  output CTRL_PS2,
  output CTRL_PS3,
  output CTRL_GS0,
  output CTRL_GS1,
  output CTRL_CS0,
  output CTRL_CS1,
  output CTRL_CS2,
  output CTRL_SL0,
  output CTRL_SL1,
  output CTRL_BR0,
  output CTRL_BR1,
  output CTRL_SHR,
  output CTRL_CMP,
  output CTRL_P2,
  output CTRL_SH1,
  output CTRL_A_M,
  output CTRL_SHL8,
  output CTRL_SHR8,
  output CTRL_EXT,
  output CTRL_SEXT,
  output CTRL_R_A,
  output CTRL_SP_A,
  output CTRL_PC_A,
  output CTRL_R_B,
  output CTRL_K_B,
  output CTRL_ALU_Q,
  output CTRL_M_Q,
  output CTRL_D_Q,
  output CTRL_WRRD,
  output CTRL_WRSP,
  output CTRL_WRSR,
  output CTRL_WRMAR,
  output CTRL_WRPMAR,
  output CTRL_HLT,
  output CTRL_END,
  output [6:0] MIR
);

  wire Mir_Reg_2_q1, Mir_Reg_2_q2, Mir_Reg_2_q3, Mir_Reg_2_q4, Mir_Reg_2_q5, Mir_Reg_2_q6, Mir_Reg_2_q7,
       Mir_Reg_2_q8, MIRSel_q1, MIRSel_r1, pla_all_1_a_m, pla_all_1_aluq, pla_all_1_d_q, pla_all_1_ext,
       pla_all_1_k_b, pla_all_1_m_q, pla_all_1_nxt, pla_all_1_pc_a, pla_all_1_r_a, pla_all_1_r_b,
       pla_all_1_sp_a, Type_I1__I2__P_a, Type_I1_Sel_a, Type_J_a, Type_R2_a, Type_R3_a, undriven_2;
  wire [3:0] pla_all_1_next, undriven;
  wire [6:0] Type_Mir_a1;
  wire [7:0] Mir_Reg_2_probe;

  IC_74x3251 Type_R2 (
    .A(Type_R2_a), .B1(IRin[15]), .B2(1'b1), .B3(1'b1), .B4(1'b1), .B5(1'b1), .B6(1'b1), .B7(1'b1),
    .B8(1'b1), .S0(IRin[12]), .S1(IRin[13]), .S2(IRin[14]), .nOE(1'b0));
  IC_74x3251 Type_R3 (
    .A(Type_R3_a), .B1(1'b1), .B2(IRin[15]), .B3(IRin[15]), .B4(1'b1), .B5(1'b1), .B6(1'b1), .B7(1'b1),
    .B8(1'b1), .S0(IRin[12]), .S1(IRin[13]), .S2(IRin[14]), .nOE(1'b0));
  IC_74x3251 Type_J (
    .A(Type_J_a), .B1(1'b1), .B2(1'b1), .B3(1'b1), .B4(IRin[15]), .B5(1'b1), .B6(1'b1), .B7(1'b1), .B8(1'b1),
    .S0(IRin[12]), .S1(IRin[13]), .S2(IRin[14]), .nOE(1'b0));
  IC_74x3251 Type_I1__I2__P (
    .A(Type_I1__I2__P_a), .B1(1'b1), .B2(1'b0), .B3(1'b0), .B4(1'b0), .B5(1'b0), .B6(1'b0), .B7(1'b0),
    .B8(1'b0), .S0(IRin[14]), .S1(IRin[15]), .S2(1'b0), .nOE(1'b0));
  IC_74x3251 Type_I1_Sel (
    .A(Type_I1_Sel_a), .B1(1'b1), .B2(1'b1), .B3(1'b0), .B4(1'b0), .B5(1'b0), .B6(1'b1), .B7(1'b1),
    .B8(1'b1), .S0(IRin[13]), .S1(IRin[14]), .S2(IRin[15]), .nOE(1'b0));
  IC_74x74half MIRSel (.R1(MIRSel_r1), .Q1(MIRSel_q1), .CLK1(CLK), .CLR1(1'b1), .SET1(nRESET), .D1(CTRL_END));
  IC_74x541 Type_R2_2 (
    .Q1(MIR[0]), .Q2(MIR[1]), .Q3(MIR[2]), .Q4(MIR[3]), .Q5(MIR[4]), .Q6(MIR[5]), .Q7(MIR[6]), .I1(IRin[0]),
    .I2(IRin[1]), .I3(IRin[2]), .I4(IRin[3]), .I5(IRin[4]), .I6(1'b0), .I7(1'b0), .I8(1'b0),
    .nOE1(Type_R2_a), .nOE2(MIRSel_r1));  // open: Q8
  IC_74x541 Type_R3_2 (
    .Q1(MIR[0]), .Q2(MIR[1]), .Q3(MIR[2]), .Q4(MIR[3]), .Q5(MIR[4]), .Q6(MIR[5]), .Q7(MIR[6]), .I1(IRin[0]),
    .I2(IRin[1]), .I3(IRin[11]), .I4(IRin[12]), .I5(IRin[13]), .I6(1'b1), .I7(1'b0), .I8(1'b0),
    .nOE1(Type_R3_a), .nOE2(MIRSel_r1));  // open: Q8
  IC_74x541 Type_J_2 (
    .Q1(MIR[0]), .Q2(MIR[1]), .Q3(MIR[2]), .Q4(MIR[3]), .Q5(MIR[4]), .Q6(MIR[5]), .Q7(MIR[6]), .I1(IRin[9]),
    .I2(IRin[10]), .I3(IRin[11]), .I4(IRin[12]), .I5(IRin[13]), .I6(1'b1), .I7(1'b0), .I8(1'b0),
    .nOE1(Type_J_a), .nOE2(MIRSel_r1));  // open: Q8
  IC_74x541 Type_I1__I2__P_2 (
    .Q1(MIR[0]), .Q2(MIR[1]), .Q3(MIR[2]), .Q4(MIR[3]), .Q5(MIR[4]), .Q6(MIR[5]), .Q7(MIR[6]), .I1(IRin[11]),
    .I2(IRin[12]), .I3(IRin[13]), .I4(IRin[14]), .I5(IRin[15]), .I6(1'b0), .I7(1'b1), .I8(1'b0),
    .nOE1(Type_I1__I2__P_a), .nOE2(MIRSel_r1));  // open: Q8
  logi7400ic_IC_74x574 MIR_Reg (
    .Q2(MIR[1]), .Q3(MIR[2]), .Q4(MIR[3]), .Q5(MIR[4]), .Q6(MIR[5]), .Q7(MIR[6]), .Q1(MIR[0]),
    .D2(pla_all_1_next[1]), .D3(pla_all_1_next[2]), .D4(pla_all_1_next[3]), .D5(1'b0), .D6(1'b1), .D7(1'b1),
    .D8(1'b0), .CLK(CLK), .nOE(MIRSel_q1), .D1(pla_all_1_next[0]));  // open: Probe, Q8
  IC_74x1G3157 RA (.A(IR_RA), .B1(Type_I1_Sel_a), .B2(1'b0), .S(MIRSel_r1));
  PLA_ALL pla_all_1 (
    .M(MIR[6:5]), .I(MIR[4:0]), .PF({CTRL_PS3, CTRL_PS2, CTRL_PS1, CTRL_PS0}), .GS({CTRL_GS1, CTRL_GS0}),
    .CS({CTRL_CS2, CTRL_CS1, CTRL_CS0}), .SL({CTRL_SL1, CTRL_SL0}), .BR({CTRL_BR1, CTRL_BR0}),
    .SHR(CTRL_SHR), .CMP(CTRL_CMP), .P2(CTRL_P2), .SH1(CTRL_SH1), .A_M(pla_all_1_a_m), .SHL8(CTRL_SHL8),
    .SHR8(CTRL_SHR8), .EXT(pla_all_1_ext), .SEXT(CTRL_SEXT), .R_A(pla_all_1_r_a), .SP_A(pla_all_1_sp_a),
    .PC_A(pla_all_1_pc_a), .R_B(pla_all_1_r_b), .K_B(pla_all_1_k_b), .ALUQ(pla_all_1_aluq),
    .M_Q(pla_all_1_m_q), .D_Q(pla_all_1_d_q), .WRRD(CTRL_WRRD), .WRSP(CTRL_WRSP), .WRSR(CTRL_WRSR),
    .WMAR(CTRL_WRMAR), .WPMAR(CTRL_WRPMAR), .HLT(CTRL_HLT), .NXT(pla_all_1_nxt), .NEXT(pla_all_1_next));
  not not_1 (CTRL_END, pla_all_1_nxt);
  not not_2 (CTRL_A_M, pla_all_1_a_m);
  not not_3 (CTRL_EXT, pla_all_1_ext);
  not not_4 (CTRL_R_A, pla_all_1_r_a);
  not not_5 (CTRL_SP_A, pla_all_1_sp_a);
  not not_6 (CTRL_PC_A, pla_all_1_pc_a);
  not not_7 (CTRL_R_B, pla_all_1_r_b);
  not not_8 (CTRL_K_B, pla_all_1_k_b);
  not not_9 (CTRL_ALU_Q, pla_all_1_aluq);
  not not_10 (CTRL_M_Q, pla_all_1_m_q);
  not not_11 (CTRL_D_Q, pla_all_1_d_q);
  IC_74x273 Mir_Reg_2 (
    .Probe(Mir_Reg_2_probe), .Q1(Mir_Reg_2_q1), .Q2(Mir_Reg_2_q2), .Q3(Mir_Reg_2_q3), .Q4(Mir_Reg_2_q4),
    .Q5(Mir_Reg_2_q5), .Q6(Mir_Reg_2_q6), .Q7(Mir_Reg_2_q7), .Q8(Mir_Reg_2_q8), .D1(undriven[0]),
    .D2(undriven[1]), .D3(undriven[2]), .D4(undriven[3]), .D5(1'b0), .D6(1'b1), .D7(1'b1), .D8(undriven_2),
    .CLK(CLK), .nMR(nRESET));
  IC_74x3345 Type_Mir (
    .A3(Type_Mir_a1[2]), .A4(Type_Mir_a1[3]), .A5(Type_Mir_a1[4]), .A6(Type_Mir_a1[5]), .A7(Type_Mir_a1[6]),
    .A1(Type_Mir_a1[0]), .A2(Type_Mir_a1[1]), .B3(Mir_Reg_2_q3), .B4(Mir_Reg_2_q4), .B5(Mir_Reg_2_q5),
    .B6(Mir_Reg_2_q6), .B7(Mir_Reg_2_q7), .B8(1'b0), .OE(Mir_Reg_2_q8), .nOE(1'b1), .B1(Mir_Reg_2_q1),
    .B2(Mir_Reg_2_q2));  // open: A8

  // Other names for the same wires on the sheet: CLR_n = nRESET; IR0 = IRin[0]; IR1 = IRin[1]; IR2 = IRin[2];
  //   IR3 = IRin[3]; IR4 = IRin[4]; IR9 = IRin[9]; IR10 = IRin[10]; IR11 = IRin[11]; IR12 = IRin[12]; IR13 = IRin[13];
  //   IR14 = IRin[14]; IR15 = IRin[15]

  // Notes on the sheet:
  //   Note: 
  //   From the Immediate Decoder
endmodule

// 74x574 DFF
module IC_74x574 (
  input  D1,
  input  D2,
  input  D3,
  input  D4,
  input  D5,
  input  D6,
  input  D7,
  input  D8,
  input  CLK,
  input  nOE,
  output Q1,
  output Q2,
  output Q3,
  output Q4,
  output Q5,
  output Q6,
  output Q7,
  output Q8,
  output [7:0] Probe
);

  wire not_1_out;

  D_Flip_Flop d_ff_1 (.D(D1), .clk(CLK), .Q(Probe[0]));  // open: Qn, preset, reset
  D_Flip_Flop d_ff_2 (.D(D2), .clk(CLK), .Q(Probe[1]));  // open: Qn, preset, reset
  D_Flip_Flop d_ff_3 (.D(D3), .clk(CLK), .Q(Probe[2]));  // open: Qn, preset, reset
  D_Flip_Flop d_ff_4 (.D(D4), .clk(CLK), .Q(Probe[3]));  // open: Qn, preset, reset
  D_Flip_Flop d_ff_5 (.D(D5), .clk(CLK), .Q(Probe[4]));  // open: Qn, preset, reset
  D_Flip_Flop d_ff_6 (.D(D6), .clk(CLK), .Q(Probe[5]));  // open: Qn, preset, reset
  D_Flip_Flop d_ff_7 (.D(D7), .clk(CLK), .Q(Probe[6]));  // open: Qn, preset, reset
  D_Flip_Flop d_ff_8 (.D(D8), .clk(CLK), .Q(Probe[7]));  // open: Qn, preset, reset
  not not_1 (not_1_out, nOE);
  assign Q1 = not_1_out ? Probe[0] : 1'bz;  // Controlled_Buffer controlled_buffer_1
  assign Q2 = not_1_out ? Probe[1] : 1'bz;  // Controlled_Buffer controlled_buffer_2
  assign Q3 = not_1_out ? Probe[2] : 1'bz;  // Controlled_Buffer controlled_buffer_3
  assign Q4 = not_1_out ? Probe[3] : 1'bz;  // Controlled_Buffer controlled_buffer_4
  assign Q5 = not_1_out ? Probe[4] : 1'bz;  // Controlled_Buffer controlled_buffer_5
  assign Q6 = not_1_out ? Probe[5] : 1'bz;  // Controlled_Buffer controlled_buffer_6
  assign Q7 = not_1_out ? Probe[6] : 1'bz;  // Controlled_Buffer controlled_buffer_7
  assign Q8 = not_1_out ? Probe[7] : 1'bz;  // Controlled_Buffer controlled_buffer_8
endmodule
