// Logisim project logi7400ic.circ as structural Verilog: 75 circuits, main circuit README
module README (
);

  IC_7400 ic_7400_1 ();  // open: Y3, Y4, Y1, Y2, A3, A4, B1, B2, A1, B3, B4, A2
  IC_7414 ic_7414_1 ();  // open: Y3, Y4, Y5, Y6, Y1, Y2, A3, A4, A5, A6, A1, A2
  IC_7473 ic_7473_1 ();  // open: Q2, R2, Q1, R1, K1, CLR1, J2, CLK2, J1, K2, CLR2, CLK1
  IC_74109 ic_74109_1 ();  // open: R1, Q2, R2, Q1, CLK1, K1, CLR1, SET2, SET1, J2, CLK2, K2, CLR2, J1
  IC_74157 ic_74157_1 ();  // open: Y2, Y3, Y4, Y1, A2, B2, A3, B3, A4, A1, B4, S0, OE, B1
  IC_74374 ic_74374_1 ();  // open: Y2, Y3, Y1, Y4, Y5, Y6, Y7, Y8, D2, D3, D1, D4, D5, D6, D7, D8, CLK, OE
  IC_74x573 ic_74x573_1 ();  // open: Probe, Q2, Q3, Q4, Q5, Q6, Q7, Q8, Q1, D2, D3, D4, D5, D6, D7, D8, LE, nOE, D1
  IC_74x563 ic_74x563_1 ();  // open: Probe, Q2, Q3, Q4, Q5, Q6, Q7, Q8, Q1, D2, D3, D4, D5, D6, D7, D8, LE, nOE, D1
  IC_7402 ic_7402_1 ();  // open: Y3, Y4, Y1, Y2, A3, A4, B1, B2, A1, B3, B4, A2
  IC_7420 ic_7420_1 ();  // open: Y2, Y1, B1, B2, C1, A1, C2, D1, D2, A2
  IC_7474 ic_7474_1 ();  // open: R1, Q2, R2, Q1, CLK1, CLR1, SET2, D2, SET1, CLK2, CLR2, D1
  IC_74112 ic_74112_1 ();  // open: R1, Q2, R2, Q1, CLK1, K1, CLR1, SET2, SET1, J2, CLK2, K2, CLR2, J1
  IC_74161 ic_74161_1 ();  // open: Q1, Q2, Q3, Q4, TC, LE, CEP, CET, D1, CLK, D2, D3, D4, CLR
  IC_74377 ic_74377_1 ();  // open: Y2, Y3, Y1, Y4, Y5, Y6, Y7, Y8, D2, D3, D1, D4, D5, D6, D7, D8, CLK, CE
  IC_74x574 ic_74x574_1 ();  // open: Probe, Q2, Q3, Q4, Q5, Q6, Q7, Q8, Q1, D2, D3, D4, D5, D6, D7, D8, CLK, nOE, D1
  IC_74x273 ic_74x273_1 ();  // open: Probe, Q1, Q2, Q3, Q4, Q5, Q6, Q7, Q8, D1, D2, D3, D4, D5, D6, D7, D8, CLK, nMR
  IC_7403 ic_7403_1 ();  // open: Y3, Y4, Y1, Y2, A3, A4, B1, B2, A1, B3, B4, A2
  IC_7421 ic_7421_1 ();  // open: Y2, Y1, B1, B2, C1, A1, C2, D1, D2, A2
  IC_7475 ic_7475_1 ();  // open: Q2, R2, Q3, R3, Q1, Q4, R4, R1, D2, LE12, D3, D1, D4, LE34
  IC_74132 ic_74132_1 ();  // open: Y3, Y4, Y1, Y2, A3, A4, B1, B2, A1, B3, B4, A2
  IC_74163 ic_74163_1 ();  // open: Q1, Q2, Q3, Q4, TC, nPE, CEP, CET, D1, CLK, D2, D3, D4, nSR
  IC_7404 ic_7404_1 ();  // open: Y3, Y4, Y5, Y6, Y1, Y2, A3, A4, A5, A6, A1, A2
  IC_7427 ic_7427_1 ();  // open: Y3, Y1, Y2, A3, B1, B2, B3, A1, C1, C2, C3, A2
  IC_7476 ic_7476_1 ();  // open: R1, Q2, R2, Q1, CLK1, K1, CLR1, SET2, SET1, J2, CLK2, K2, CLR2, J1
  IC_74173 ic_74173_1 ();  // open: Q2, Q3, Q1, Q4, D2, D3, D1, D4, CLK, CE1, CE2, CLR, OE1, OE2
  IC_74x153 ic_74x153_1 ();  // open: Y1, Y2, C1_0, C1_1, C1_2, C1_3, C2_0, C2_1, C2_2, C2_3, A, B, nG1, nG2
  IC_74x151 ic_74x151_1 ();  // open: Y, W, D1, D2, D3, D4, D5, D6, D7, A, B, C, nG, D0
  IC_7405 ic_7405_1 ();  // open: Y3, Y4, Y5, Y6, Y1, Y2, A3, A4, A5, A6, A1, A2
  IC_7430 ic_7430_1 ();  // open: Y, C, D, E, F, G, A, H, B
  IC_7485 ic_7485_1 ();  // open: YLT, YEQ, YGT, A3, A4, B1, B2, A1, B3, B4, CLT, CEQ, CGT, A2
  IC_74138 ic_74138_1 ();  // open: Y0, Y1, Y2, Y3, Y4, Y5, Y6, Y7, A2, A0, OE1, OE2, OE3, A1
  IC_74x253 ic_74x253_1 ();  // open: Y1, Y2, I_n_0, I1_1, I1_2, I1_3, I2_0, I2_1, I2_2, I2_3, S0, S1, nOE1, nOE2
  IC_74x251 ic_74x251_1 ();  // open: Y, W, I0, I1, I2, I3, I4, I5, I6, I7, S0, S1, S2, nOE
  IC_74x161 ic_74x161_1 ();  // open: Q1, Q2, Q3, Q4, TC, nLD, CEP, CET, D1, CLK, D2, D3, D4, nCLR
  IC_7408 ic_7408_1 ();  // open: Y3, Y4, Y1, Y2, A3, A4, B1, B2, A1, B3, B4, A2
  IC_7432 ic_7432_1 ();  // open: Y3, Y4, Y1, Y2, A3, A4, B1, B2, A1, B3, B4, A2
  IC_7486 ic_7486_1 ();  // open: Y3, Y4, Y1, Y2, A3, A4, B1, B2, A1, B3, B4, A2
  IC_74139 ic_74139_1 ();  // open: Y1, Y2, Y3, Z0, Z1, Z2, Z3, Y0, OEA, A0, B0, B1, OEB, A1
  IC_74175 ic_74175_1 ();  // open: Q2, R2, Q3, R3, Q1, Q4, R4, R1, D2, D3, D1, D4, CLK, CLR
  IC_74x3253 ic_74x3253_1 ();  // open: A1, A2, B1_1, B1_2, B1_3, B1_4, B2_1, B2_2, B2_3, B2_4, S0, S1, nOE1, nOE2
  IC_74x3251 ic_74x3251_1 ();  // open: A, B1, B2, B3, B4, B5, B6, B7, B8, S0, S1, S2, nOE
  IC_74x163 ic_74x163_1 ();  // open: Q1, Q2, Q3, Q4, TC, nLD, CEP, CET, D1, CLK, D2, D3, D4, nCLR
  IC_74147 ic_74147_1 ();  // open: Y1, Y2, Y3, Y4, D3, D4, D5, D6, D7, D1, D8, D9, D2
  IC_74238 ic_74238_1 ();  // open: Y0, Y1, Y2, Y3, Y4, Y5, Y6, Y7, A2, A0, OE1, OE2, OE3, A1
  IC_7410 ic_7410_1 ();  // open: Y3, Y1, Y2, A3, B1, B2, B3, A1, C1, C2, C3, A2
  IC_7442 ic_7442_1 ();  // open: Y2, Y3, Y4, Y5, Y6, Y7, Y8, Y0, Y9, Y1, D1, D2, D3, D4
  IC_7493 ic_7493_1 ();  // open: Q2, Q3, Q4, Q1, CLR1, CLR2, CLK0, CLK1
  IC_74107 ic_74107_1 ();  // open: Q2, R2, Q1, R1, K1, CLR1, J2, CLK2, J1, K2, CLR2, CLK1
  IC_74151 ic_74151_1 ();  // open: Y, W, C, D, E, A, F, G, J, S0, S1, S2, nOE, B
  IC_74244 ic_74244_1 ();  // open: Y3, Y4, Z1, Y1, Z2, Z3, Z4, Y2, A3, A4, OEA, B1, A1, B2, B3, B4, OEB, A2
  IC_74x74half ic_74x74half_1 ();  // open: R1, Q1, CLK1, CLR1, SET1, D1
  IC_7411 ic_7411_1 ();  // open: Y3, Y1, Y2, A3, B1, B2, B3, A1, C1, C2, C3, A2
  IC_7451 ic_7451_1 ();  // open: Y1, Y2, C1, D1, E1, F1, A2, A1, B2, C2, D2, B1
  IC_74153 ic_74153_1 ();  // open: Y1, Y2, C1, D1, A2, A1, B2, C2, D2, S0, S1, OE1, OE2, B1
  IC_74273 ic_74273_1 ();  // open: Y2, Y3, Y1, Y4, Y5, Y6, Y7, Y8, D2, D3, D1, D4, D5, D6, D7, D8, CLK, CLR
  IC_74x241 ic_74x241_1 ();  // open: Y3, Y4, Z1, Z2, Z3, Z4, Y1, Y2, A3, A4, nOEA, B1, B2, B3, B4, A1, OEB, A2
  IC_74x3G34 ic_74x3g34_1 ();  // open: Y3, Y1, Y2, A3, A1, A2
  IC_74283 ic_74283_1 ();  // open: Y2, Y3, Y4, Y1, COUT, A3, A4, B1, B2, A1, B3, B4, CIN, A2
  IC_74x541 ic_74x541_1 ();  // open: Q1, Q2, Q3, Q4, Q5, Q6, Q7, Q8, I1, I2, I3, I4, I5, I6, I7, I8, nOE1, nOE2
  IC_74x11244 ic_74x11244_1 ();  // open: Y1_3, Y1_4, Y2_1, Y2_2, Y2_3, Y2_4, Y1_1, Y1_2, A1_3, A1_4, nOE1, A2_1, A2_2, A2_3, A2_4, A1_1, nOE2, A1_2
  IC_74x238 ic_74x238_1 ();  // open: Y0, Y1, Y2, Y3, Y4, Y5, Y6, Y7, A, B, C, nG2A, nG2B, G1
  IC_74x283 ic_74x283_1 ();  // open: Y1, Y2, Y3, Y4, COUT, A1, A2, A3, A4, B1, B2, B3, B4, CIN
  IC_74x3345 ic_74x3345_1 ();  // open: A3, A4, A5, A6, A7, A8, A1, A2, B3, B4, B5, B6, B7, B8, OE, nOE, B1, B2
  IC_74x138 ic_74x138_1 ();  // open: Y0, Y1, Y2, Y3, Y4, Y5, Y6, Y7, A, B, C, nG2A, nG2B, G1
  IC_74x3257 ic_74x3257_1 ();  // open: A1, A2, A3, A4, B2_1, B1_2, B2_2, B1_3, B2_3, B1_4, B2_4, S, nOE, B1_1
  IC_74x20 ic_74x20_1 ();  // open: Y2, Y1, D1, A2, B2, C2, D2, A1, B1, C1
  IC_74x257 ic_74x257_1 ();  // open: Y1, Y2, Y3, Y4, I1_0, I2_0, I1_1, I2_1, I1_2, I2_2, I1_3, I2_3, nA_B, nOE
  IC_74x1G3157 ic_74x1g3157_1 ();  // open: A, B1, B2, S
  IC_74x27 ic_74x27_1 ();  // open: Y2, Y3, Y1, A2, B2, C2, A3, B3, C3, A1, B1, C1
  IC_74x32571 ic_74x32571_1 ();  // open: B1_2, B1_3, B1_4, B2_1, B2_2, B2_3, B2_4, B1_1, S, nOE, A1, A2, A3, A4

  // Notes on the sheet:
  //   Logisim 7400 series integrated circuits library
  //   Copyright (C) 2015 - 2018 by Stefan Rothe
  //   This library is licenced under the GNU Lesser General Public Licence version 3.
endmodule

module IC_7400 (
  input  A1,
  input  A2,
  input  A3,
  input  A4,
  input  B1,
  input  B2,
  input  B3,
  input  B4,
  output Y1,
  output Y2,
  output Y3,
  output Y4
);

  nand nand_1 (Y1, A1, B1);
  nand nand_2 (Y2, A2, B2);
  nand nand_3 (Y3, A3, B3);
  nand nand_4 (Y4, A4, B4);
endmodule

module IC_7402 (
  input  A1,
  input  A2,
  input  A3,
  input  A4,
  input  B1,
  input  B2,
  input  B3,
  input  B4,
  output Y1,
  output Y2,
  output Y3,
  output Y4
);

  nor nor_1 (Y1, A1, B1);
  nor nor_2 (Y2, A2, B2);
  nor nor_3 (Y3, A3, B3);
  nor nor_4 (Y4, A4, B4);
endmodule

module IC_7403 (
  input  A1,
  input  A2,
  input  A3,
  input  A4,
  input  B1,
  input  B2,
  input  B3,
  input  B4,
  output Y1,
  output Y2,
  output Y3,
  output Y4
);

  wire and_1_out, and_2_out, and_3_out, and_4_out;

  assign Y1 = and_1_out ? 1'b0 : 1'bz;  // Controlled_Buffer controlled_buffer_1
  and and_1 (and_1_out, A1, B1);
  assign Y2 = and_2_out ? 1'b0 : 1'bz;  // Controlled_Buffer controlled_buffer_2
  and and_2 (and_2_out, A2, B2);
  assign Y3 = and_3_out ? 1'b0 : 1'bz;  // Controlled_Buffer controlled_buffer_3
  and and_3 (and_3_out, A3, B3);
  assign Y4 = and_4_out ? 1'b0 : 1'bz;  // Controlled_Buffer controlled_buffer_4
  and and_4 (and_4_out, A4, B4);
endmodule

module IC_7404 (
  input  A1,
  input  A2,
  input  A3,
  input  A4,
  input  A5,
  input  A6,
  output Y1,
  output Y2,
  output Y3,
  output Y4,
  output Y5,
  output Y6
);

  not not_1 (Y1, A1);
  not not_2 (Y2, A2);
  not not_3 (Y3, A3);
  not not_4 (Y4, A4);
  not not_5 (Y5, A5);
  not not_6 (Y6, A6);
endmodule

module IC_7405 (
  input  A1,
  input  A2,
  input  A3,
  input  A4,
  input  A5,
  input  A6,
  output Y1,
  output Y2,
  output Y3,
  output Y4,
  output Y5,
  output Y6
);

  assign Y1 = A1 ? 1'b0 : 1'bz;  // Controlled_Buffer controlled_buffer_1
  assign Y2 = A2 ? 1'b0 : 1'bz;  // Controlled_Buffer controlled_buffer_2
  assign Y3 = A3 ? 1'b0 : 1'bz;  // Controlled_Buffer controlled_buffer_3
  assign Y4 = A4 ? 1'b0 : 1'bz;  // Controlled_Buffer controlled_buffer_4
  assign Y5 = A5 ? 1'b0 : 1'bz;  // Controlled_Buffer controlled_buffer_5
  assign Y6 = A6 ? 1'b0 : 1'bz;  // Controlled_Buffer controlled_buffer_6
endmodule

module IC_7408 (
  input  A1,
  input  A2,
  input  A3,
  input  A4,
  input  B1,
  input  B2,
  input  B3,
  input  B4,
  output Y1,
  output Y2,
  output Y3,
  output Y4
);

  and and_1 (Y1, A1, B1);
  and and_2 (Y2, A2, B2);
  and and_3 (Y3, A3, B3);
  and and_4 (Y4, A4, B4);
endmodule

module IC_7410 (
  input  A1,
  input  A2,
  input  A3,
  input  B1,
  input  B2,
  input  B3,
  input  C1,
  input  C2,
  input  C3,
  output Y1,
  output Y2,
  output Y3
);

  nand nand_1 (Y1, A1, B1, C1);
  nand nand_2 (Y2, A2, B2, C2);
  nand nand_3 (Y3, A3, B3, C3);
endmodule

module IC_7411 (
  input  A1,
  input  A2,
  input  A3,
  input  B1,
  input  B2,
  input  B3,
  input  C1,
  input  C2,
  input  C3,
  output Y1,
  output Y2,
  output Y3
);

  and and_1 (Y1, A1, B1, C1);
  and and_2 (Y2, A2, B2, C2);
  and and_3 (Y3, A3, B3, C3);
endmodule

module IC_7414 (
  input  A1,
  input  A2,
  input  A3,
  input  A4,
  input  A5,
  input  A6,
  output Y1,
  output Y2,
  output Y3,
  output Y4,
  output Y5,
  output Y6
);

  not not_1 (Y1, A1);
  not not_2 (Y2, A2);
  not not_3 (Y3, A3);
  not not_4 (Y4, A4);
  not not_5 (Y5, A5);
  not not_6 (Y6, A6);
endmodule

module IC_7420 (
  input  A1,
  input  A2,
  input  B1,
  input  B2,
  input  C1,
  input  C2,
  input  D1,
  input  D2,
  output Y1,
  output Y2
);

  nand nand_1 (Y1, A1, B1, C1, D1);
  nand nand_2 (Y2, A2, B2, C2, D2);
endmodule

// 74x20 NAND
module IC_74x20 (
  input  A1,
  input  B1,
  input  C1,
  input  D1,
  input  A2,
  input  B2,
  input  C2,
  input  D2,
  output Y1,
  output Y2
);

  nand nand_1 (Y1, A1, B1, C1, D1);
  nand nand_2 (Y2, A2, B2, C2, D2);
endmodule

module IC_7421 (
  input  A1,
  input  A2,
  input  B1,
  input  B2,
  input  C1,
  input  C2,
  input  D1,
  input  D2,
  output Y1,
  output Y2
);

  and and_1 (Y1, A1, B1, C1, D1);
  and and_2 (Y2, A2, B2, C2, D2);
endmodule

module IC_7427 (
  input  A1,
  input  A2,
  input  A3,
  input  B1,
  input  B2,
  input  B3,
  input  C1,
  input  C2,
  input  C3,
  output Y1,
  output Y2,
  output Y3
);

  nor nor_1 (Y1, A1, B1, C1);
  nor nor_2 (Y2, A2, B2, C2);
  nor nor_3 (Y3, A3, B3, C3);
endmodule

// 74x27 NOR
module IC_74x27 (
  input  A1,
  input  B1,
  input  C1,
  input  A2,
  input  B2,
  input  C2,
  input  A3,
  input  B3,
  input  C3,
  output Y1,
  output Y2,
  output Y3
);

  nor nor_1 (Y1, A1, B1, C1);
  nor nor_2 (Y2, A2, B2, C2);
  nor nor_3 (Y3, A3, B3, C3);
endmodule

module IC_7430 (
  input  A,
  input  B,
  input  C,
  input  D,
  input  E,
  input  F,
  input  G,
  input  H,
  output Y
);

  nand nand_1 (Y, A, B, C, D, E, F, G, H);
endmodule

// 74x30 NAND
module IC_74x30 (
  input  A,
  input  B,
  input  C,
  input  D,
  input  E,
  input  F,
  input  G,
  input  H,
  output Y
);

  nand nand_1 (Y, A, B, C, D, E, F, G, H);
endmodule

module IC_7432 (
  input  A1,
  input  A2,
  input  A3,
  input  A4,
  input  B1,
  input  B2,
  input  B3,
  input  B4,
  output Y1,
  output Y2,
  output Y3,
  output Y4
);

  or or_1 (Y1, A1, B1);
  or or_2 (Y2, A2, B2);
  or or_3 (Y3, A3, B3);
  or or_4 (Y4, A4, B4);
endmodule

module IC_7442 (
  input  D1,
  input  D2,
  input  D3,
  input  D4,
  output Y0,
  output Y1,
  output Y2,
  output Y3,
  output Y4,
  output Y5,
  output Y6,
  output Y7,
  output Y8,
  output Y9
);

  wire nand_1_out, nand_2_out, nand_3_out, nand_4_out, nand_5_out, nand_6_out, nand_7_out, not_1_out,
       not_2_out, not_3_out, not_4_out, not_5_out, not_6_out, not_7_out, not_8_out;

  not not_1 (not_1_out, D1);
  not not_2 (not_2_out, D2);
  not not_3 (not_3_out, D3);
  not not_4 (not_4_out, D4);
  not not_5 (not_5_out, not_1_out);
  not not_6 (not_6_out, not_2_out);
  not not_7 (not_7_out, not_3_out);
  not not_8 (not_8_out, not_4_out);
  nand nand_1 (nand_1_out, not_1_out, not_2_out);
  nand nand_2 (nand_2_out, not_5_out, not_2_out);
  nand nand_3 (nand_3_out, not_1_out, not_6_out);
  nand nand_4 (nand_4_out, not_5_out, not_6_out);
  nand nand_5 (nand_5_out, not_3_out, not_4_out);
  nand nand_6 (nand_6_out, not_7_out, not_4_out);
  nand nand_7 (nand_7_out, not_3_out, not_8_out);
  nand nand_8 (Y0, ~nand_1_out, ~nand_5_out);  // NAND_Gate
  nand nand_9 (Y1, ~nand_2_out, ~nand_5_out);  // NAND_Gate
  nand nand_10 (Y2, ~nand_3_out, ~nand_5_out);  // NAND_Gate
  nand nand_11 (Y3, ~nand_4_out, ~nand_5_out);  // NAND_Gate
  nand nand_12 (Y4, ~nand_1_out, ~nand_6_out);  // NAND_Gate
  nand nand_13 (Y5, ~nand_2_out, ~nand_6_out);  // NAND_Gate
  nand nand_14 (Y6, ~nand_3_out, ~nand_6_out);  // NAND_Gate
  nand nand_15 (Y7, ~nand_4_out, ~nand_6_out);  // NAND_Gate
  nand nand_16 (Y8, ~nand_1_out, ~nand_7_out);  // NAND_Gate
  nand nand_17 (Y9, ~nand_2_out, ~nand_7_out);  // NAND_Gate
endmodule

module IC_7451 (
  input  A1,
  input  B1,
  input  C1,
  input  D1,
  input  E1,
  input  F1,
  input  A2,
  input  B2,
  input  C2,
  input  D2,
  output Y1,
  output Y2
);

  wire and_1_out, and_2_out, and_3_out, and_4_out;

  and and_1 (and_1_out, A1, B1, C1);
  and and_2 (and_2_out, D1, E1, F1);
  and and_3 (and_3_out, A2, B2);
  and and_4 (and_4_out, C2, D2);
  nor nor_1 (Y1, and_1_out, and_2_out);
  nor nor_2 (Y2, and_3_out, and_4_out);
endmodule

module IC_7473 (
  input  J1,
  input  CLK1,
  input  K1,
  input  CLR1,
  input  J2,
  input  CLK2,
  input  K2,
  input  CLR2,
  output Q1,
  output R1,
  output Q2,
  output R2
);

  wire not_1_out, not_2_out, not_3_out, not_4_out;

  not not_1 (not_1_out, CLK1);
  not not_2 (not_2_out, CLR1);
  not not_3 (not_3_out, CLK2);
  not not_4 (not_4_out, CLR2);
  JK_Flip_Flop jk_flip_flop_1 (.R(R1), .Q(Q1), .CLR(not_2_out), .CLK(not_1_out), .K(K1), .J(J1));  // open: SET
  JK_Flip_Flop jk_flip_flop_2 (.R(R2), .Q(Q2), .CLR(not_4_out), .CLK(not_3_out), .K(K2), .J(J2));  // open: SET
endmodule

module IC_7474 (
  input  SET1,
  input  D1,
  input  CLK1,
  input  CLR1,
  input  SET2,
  input  D2,
  input  CLK2,
  input  CLR2,
  output Q1,
  output R1,
  output Q2,
  output R2
);

  wire not_1_out, not_2_out, not_3_out, not_4_out;

  not not_1 (not_1_out, SET1);
  D_Flip_Flop d_flip_flop_1 (.Q(Q1), .R(R1), .SET(not_1_out), .CLR(not_2_out), .D(D1), .CLK(CLK1));
  not not_2 (not_2_out, CLR1);
  not not_3 (not_3_out, SET2);
  D_Flip_Flop d_flip_flop_2 (.Q(Q2), .R(R2), .SET(not_3_out), .CLR(not_4_out), .D(D2), .CLK(CLK2));
  not not_4 (not_4_out, CLR2);
endmodule

// 74x74 DFF
module IC_74x74half (
  input  SET1,
  input  D1,
  input  CLK1,
  input  CLR1,
  output Q1,
  output R1
);

  wire not_1_out, not_2_out;

  not not_1 (not_1_out, SET1);
  D_Flip_Flop_part #(.enable("true")) d_ff_1 (
    .D(D1), .clk(CLK1), .Q(Q1), .Qn(R1), .preset(not_1_out), .reset(not_2_out));
  not not_2 (not_2_out, CLR1);
endmodule

module IC_7475 (
  input  D1,
  input  D2,
  input  LE12,
  input  D3,
  input  D4,
  input  LE34,
  output Q1,
  output R1,
  output Q2,
  output R2,
  output Q3,
  output R3,
  output Q4,
  output R4
);

  D_Latch d_latch_1 (.Q(Q1), .R(R1), .D(D1), .LE(LE12));  // open: SET, CLR
  D_Latch d_latch_2 (.Q(Q2), .R(R2), .D(D2), .LE(LE12));  // open: SET, CLR
  D_Latch d_latch_3 (.Q(Q3), .R(R3), .D(D3), .LE(LE34));  // open: SET, CLR
  D_Latch d_latch_4 (.Q(Q4), .R(R4), .D(D4), .LE(LE34));  // open: SET, CLR
endmodule

module IC_7476 (
  input  SET1,
  input  J1,
  input  CLK1,
  input  K1,
  input  CLR1,
  input  SET2,
  input  J2,
  input  CLK2,
  input  K2,
  input  CLR2,
  output Q1,
  output R1,
  output Q2,
  output R2
);

  wire not_1_out, not_2_out, not_3_out, not_4_out, not_5_out, not_6_out;

  not not_1 (not_1_out, SET1);
  not not_2 (not_2_out, CLK1);
  not not_3 (not_3_out, CLR1);
  not not_4 (not_4_out, SET2);
  not not_5 (not_5_out, CLK2);
  not not_6 (not_6_out, CLR2);
  JK_Flip_Flop jk_flip_flop_1 (.R(R1), .Q(Q1), .CLR(not_3_out), .SET(not_1_out), .CLK(not_2_out), .K(K1), .J(J1));
  JK_Flip_Flop jk_flip_flop_2 (.R(R2), .Q(Q2), .CLR(not_6_out), .SET(not_4_out), .CLK(not_5_out), .K(K2), .J(J2));
endmodule

module IC_7485 (
  input  A1,
  input  A2,
  input  A3,
  input  A4,
  input  B1,
  input  B2,
  input  B3,
  input  B4,
  input  CLT,
  input  CEQ,
  input  CGT,
  output YLT,
  output YEQ,
  output YGT
);

  wire and_1_out, and_2_out, and_3_out, and_4_out, and_5_out, and_6_out, and_7_out, and_8_out, and_9_out,
       and_10_out, and_11_out, and_12_out, and_13_out, and_14_out, and_16_out, and_17_out, and_18_out,
       and_19_out, and_20_out, and_21_out, nand_1_out, nand_2_out, nand_3_out, nand_4_out, nor_1_out,
       nor_2_out, nor_3_out, nor_4_out;

  nand nand_1 (nand_1_out, A4, B4);
  nand nand_2 (nand_2_out, A3, B3);
  nand nand_3 (nand_3_out, A2, B2);
  nand nand_4 (nand_4_out, A1, B1);
  and and_1 (and_1_out, A4, nand_1_out);
  and and_2 (and_2_out, nand_1_out, B4);
  and and_3 (and_3_out, A3, nand_2_out);
  and and_4 (and_4_out, nand_2_out, B3);
  and and_5 (and_5_out, A2, nand_3_out);
  and and_6 (and_6_out, nand_3_out, B2);
  and and_7 (and_7_out, A1, nand_4_out);
  and and_8 (and_8_out, nand_4_out, B1);
  nor nor_1 (nor_1_out, and_1_out, and_2_out);
  nor nor_2 (nor_2_out, and_3_out, and_4_out);
  nor nor_3 (nor_3_out, and_5_out, and_6_out);
  nor nor_4 (nor_4_out, and_7_out, and_8_out);
  and and_9 (and_9_out, B4, nand_1_out);
  and and_10 (and_10_out, B3, nand_2_out, nor_1_out);
  and and_11 (and_11_out, B2, nand_3_out, nor_1_out, nor_2_out);
  and and_12 (and_12_out, B1, nand_4_out, nor_1_out, nor_2_out, nor_3_out);
  and and_13 (and_13_out, nor_1_out, nor_2_out, nor_3_out, nor_4_out, CLT);
  and and_14 (and_14_out, nor_1_out, nor_2_out, nor_3_out, nor_4_out, CEQ);
  and and_15 (YEQ, nor_1_out, nor_2_out, CEQ, nor_3_out, nor_4_out);
  and and_16 (and_16_out, CEQ, nor_4_out, nor_3_out, nor_2_out, nor_1_out);
  and and_17 (and_17_out, CGT, nor_4_out, nor_3_out, nor_2_out, nor_1_out);
  and and_18 (and_18_out, nor_3_out, nor_2_out, nor_1_out, nand_4_out, A1);
  and and_19 (and_19_out, nor_2_out, nor_1_out, nand_3_out, A2);
  and and_20 (and_20_out, nor_1_out, nand_2_out, A3);
  and and_21 (and_21_out, nand_1_out, A4);
  nor nor_5 (YGT, and_9_out, and_10_out, and_11_out, and_12_out, and_13_out, and_14_out);
  nor nor_6 (YLT, and_16_out, and_17_out, and_18_out, and_19_out, and_20_out, and_21_out);
endmodule

module IC_7486 (
  input  A1,
  input  A2,
  input  A3,
  input  A4,
  input  B1,
  input  B2,
  input  B3,
  input  B4,
  output Y1,
  output Y2,
  output Y3,
  output Y4
);

  xor xor_1 (Y1, A1, B1);
  xor xor_2 (Y2, A2, B2);
  xor xor_3 (Y3, A3, B3);
  xor xor_4 (Y4, A4, B4);
endmodule

module IC_7493 (
  input  CLK0,
  input  CLK1,
  input  CLR1,
  input  CLR2,
  output Q1,
  output Q2,
  output Q3,
  output Q4
);

  wire and_1_out, d_flip_flop_1_r, d_flip_flop_2_r, d_flip_flop_3_r, d_flip_flop_4_r, not_1_out, not_2_out,
       not_3_out, not_4_out;

  not not_1 (not_1_out, CLK0);
  not not_2 (not_2_out, CLK1);
  and and_1 (and_1_out, CLR1, CLR2);
  not not_3 (not_3_out, Q2);
  not not_4 (not_4_out, Q3);
  D_Flip_Flop d_flip_flop_1 (
    .Q(Q1), .R(d_flip_flop_1_r), .CLR(and_1_out), .D(d_flip_flop_1_r), .CLK(not_1_out));  // open: SET
  D_Flip_Flop d_flip_flop_2 (
    .Q(Q2), .R(d_flip_flop_2_r), .CLR(and_1_out), .D(d_flip_flop_2_r), .CLK(not_2_out));  // open: SET
  D_Flip_Flop d_flip_flop_3 (
    .Q(Q3), .R(d_flip_flop_3_r), .CLR(and_1_out), .D(d_flip_flop_3_r), .CLK(not_3_out));  // open: SET
  D_Flip_Flop d_flip_flop_4 (.Q(Q4), .R(d_flip_flop_4_r), .D(d_flip_flop_4_r), .CLK(not_4_out));  // open: SET, CLR
endmodule

module IC_74107 (
  input  J1,
  input  CLK1,
  input  K1,
  input  CLR1,
  input  J2,
  input  CLK2,
  input  K2,
  input  CLR2,
  output Q1,
  output R1,
  output Q2,
  output R2
);

  wire not_1_out, not_2_out, not_3_out, not_4_out;

  not not_1 (not_1_out, K1);
  not not_2 (not_2_out, CLR1);
  not not_3 (not_3_out, K2);
  not not_4 (not_4_out, CLR2);
  JK_Flip_Flop jk_flip_flop_1 (.R(R1), .Q(Q1), .CLR(not_2_out), .CLK(CLK1), .K(not_1_out), .J(J1));  // open: SET
  JK_Flip_Flop jk_flip_flop_2 (.R(R2), .Q(Q2), .CLR(not_4_out), .CLK(CLK2), .K(not_3_out), .J(J2));  // open: SET
endmodule

module IC_74109 (
  input  SET1,
  input  J1,
  input  CLK1,
  input  K1,
  input  CLR1,
  input  SET2,
  input  J2,
  input  CLK2,
  input  K2,
  input  CLR2,
  output Q1,
  output R1,
  output Q2,
  output R2
);

  wire not_1_out, not_2_out, not_3_out, not_4_out, not_5_out, not_6_out;

  not not_1 (not_1_out, SET1);
  not not_2 (not_2_out, K1);
  not not_3 (not_3_out, CLR1);
  not not_4 (not_4_out, SET2);
  not not_5 (not_5_out, K2);
  not not_6 (not_6_out, CLR2);
  JK_Flip_Flop jk_flip_flop_1 (.R(R1), .Q(Q1), .CLR(not_3_out), .SET(not_1_out), .CLK(CLK1), .K(not_2_out), .J(J1));
  JK_Flip_Flop jk_flip_flop_2 (.R(R2), .Q(Q2), .CLR(not_6_out), .SET(not_4_out), .CLK(CLK2), .K(not_5_out), .J(J2));
endmodule

module IC_74112 (
  input  SET1,
  input  J1,
  input  CLK1,
  input  K1,
  input  CLR1,
  input  SET2,
  input  J2,
  input  CLK2,
  input  K2,
  input  CLR2,
  output Q1,
  output R1,
  output Q2,
  output R2
);

  wire not_1_out, not_2_out, not_3_out, not_4_out, not_5_out, not_6_out;

  not not_1 (not_1_out, SET1);
  not not_2 (not_2_out, CLK1);
  not not_3 (not_3_out, CLR1);
  not not_4 (not_4_out, SET2);
  not not_5 (not_5_out, CLK2);
  not not_6 (not_6_out, CLR2);
  JK_Flip_Flop jk_flip_flop_1 (.R(R1), .Q(Q1), .CLR(not_3_out), .SET(not_1_out), .CLK(not_2_out), .K(K1), .J(J1));
  JK_Flip_Flop jk_flip_flop_2 (.R(R2), .Q(Q2), .CLR(not_6_out), .SET(not_4_out), .CLK(not_5_out), .K(K2), .J(J2));
endmodule

module IC_74132 (
  input  A1,
  input  A2,
  input  A3,
  input  A4,
  input  B1,
  input  B2,
  input  B3,
  input  B4,
  output Y1,
  output Y2,
  output Y3,
  output Y4
);

  nand nand_1 (Y1, A1, B1);
  nand nand_2 (Y2, A2, B2);
  nand nand_3 (Y3, A3, B3);
  nand nand_4 (Y4, A4, B4);
endmodule

module IC_74138 (
  input  A0,
  input  A1,
  input  A2,
  input  OE1,
  input  OE2,
  input  OE3,
  output Y0,
  output Y1,
  output Y2,
  output Y3,
  output Y4,
  output Y5,
  output Y6,
  output Y7
);

  wire and_1_out, not_1_out, not_2_out, not_3_out, not_4_out, not_5_out;

  not not_1 (not_1_out, A0);
  not not_2 (not_2_out, A1);
  not not_3 (not_3_out, A2);
  not not_4 (not_4_out, OE1);
  not not_5 (not_5_out, OE2);
  and and_1 (and_1_out, not_4_out, not_5_out, OE3);
  nand nand_1 (Y0, not_1_out, not_2_out, not_3_out, and_1_out);
  nand nand_2 (Y1, A0, not_2_out, not_3_out, and_1_out);
  nand nand_3 (Y2, not_1_out, A1, not_3_out, and_1_out);
  nand nand_4 (Y3, A0, A1, not_3_out, and_1_out);
  nand nand_5 (Y4, not_1_out, not_2_out, A2, and_1_out);
  nand nand_6 (Y5, A0, not_2_out, A2, and_1_out);
  nand nand_7 (Y6, not_1_out, A1, A2, and_1_out);
  nand nand_8 (Y7, A0, A1, A2, and_1_out);
endmodule

// 74x138 3:8
module IC_74x138 (
  input  A,
  input  B,
  input  C,
  input  nG2A,
  input  nG2B,
  input  G1,
  output Y0,
  output Y1,
  output Y2,
  output Y3,
  output Y4,
  output Y5,
  output Y6,
  output Y7
);

  wire and_1_out, decoder_1_out0, decoder_1_out1, decoder_1_out2, decoder_1_out3, decoder_1_out4,
       decoder_1_out5, decoder_1_out6, decoder_1_out7;

  and and_1 (and_1_out, ~nG2A, ~nG2B, G1);  // AND_Gate
  Decoder #(.select(3)) decoder_1 (
    .out0(decoder_1_out0), .out1(decoder_1_out1), .out2(decoder_1_out2), .out3(decoder_1_out3),
    .out4(decoder_1_out4), .out5(decoder_1_out5), .out6(decoder_1_out6), .out7(decoder_1_out7),
    .sel({C, B, A}), .en(and_1_out));
  not not_1 (Y0, decoder_1_out0);
  not not_2 (Y1, decoder_1_out1);
  not not_3 (Y2, decoder_1_out2);
  not not_4 (Y3, decoder_1_out3);
  not not_5 (Y4, decoder_1_out4);
  not not_6 (Y5, decoder_1_out5);
  not not_7 (Y6, decoder_1_out6);
  not not_8 (Y7, decoder_1_out7);
endmodule

module IC_74139 (
  input  A0,
  input  A1,
  input  OEA,
  input  B0,
  input  B1,
  input  OEB,
  output Y0,
  output Y1,
  output Y2,
  output Y3,
  output Z0,
  output Z1,
  output Z2,
  output Z3
);

  wire not_1_out, not_2_out, not_3_out, not_4_out, not_5_out, not_6_out;

  not not_1 (not_1_out, A0);
  not not_2 (not_2_out, A1);
  not not_3 (not_3_out, OEA);
  not not_4 (not_4_out, B0);
  not not_5 (not_5_out, B1);
  not not_6 (not_6_out, OEB);
  nand nand_1 (Y0, not_1_out, not_2_out, not_3_out);
  nand nand_2 (Y1, A0, not_2_out, not_3_out);
  nand nand_3 (Y2, not_1_out, A1, not_3_out);
  nand nand_4 (Y3, A0, A1, not_3_out);
  nand nand_5 (Z0, not_4_out, not_5_out, not_6_out);
  nand nand_6 (Z1, B0, not_5_out, not_6_out);
  nand nand_7 (Z2, not_4_out, B1, not_6_out);
  nand nand_8 (Z3, B0, B1, not_6_out);
endmodule

module IC_74147 (
  input  D1,
  input  D2,
  input  D3,
  input  D4,
  input  D5,
  input  D6,
  input  D7,
  input  D8,
  input  D9,
  output Y1,
  output Y2,
  output Y3,
  output Y4
);

  wire and_1_out, and_2_out, and_3_out, and_4_out, and_5_out, and_6_out, and_7_out, and_8_out, and_9_out,
       and_10_out, and_11_out, and_12_out, buffer_1_out, nor_1_out, not_1_out, not_2_out, not_3_out,
       not_4_out, not_5_out, not_6_out, not_7_out, not_8_out, not_9_out, not_10_out, not_11_out, not_12_out,
       not_13_out;

  not not_1 (not_1_out, D1);
  not not_2 (not_2_out, D2);
  not not_3 (not_3_out, D3);
  not not_4 (not_4_out, D4);
  not not_5 (not_5_out, D5);
  not not_6 (not_6_out, D6);
  not not_7 (not_7_out, D7);
  not not_8 (not_8_out, D8);
  not not_9 (not_9_out, D9);
  not not_10 (not_10_out, not_2_out);
  not not_11 (not_11_out, not_4_out);
  not not_12 (not_12_out, not_5_out);
  not not_13 (not_13_out, not_6_out);
  nor nor_1 (nor_1_out, not_8_out, not_9_out);
  and and_1 (and_1_out, not_1_out, not_10_out, not_11_out, not_13_out, nor_1_out);
  and and_2 (and_2_out, not_3_out, not_11_out, not_13_out, nor_1_out);
  and and_3 (and_3_out, not_5_out, not_13_out, nor_1_out);
  and and_4 (and_4_out, not_7_out, nor_1_out);
  buf buffer_1 (buffer_1_out, not_9_out);
  and and_5 (and_5_out, not_2_out, not_11_out, not_12_out, nor_1_out);
  and and_6 (and_6_out, not_3_out, not_11_out, not_12_out, nor_1_out);
  and and_7 (and_7_out, not_6_out, nor_1_out);
  and and_8 (and_8_out, not_7_out, nor_1_out);
  and and_9 (and_9_out, not_4_out, nor_1_out);
  and and_10 (and_10_out, not_5_out, nor_1_out);
  and and_11 (and_11_out, not_6_out, nor_1_out);
  and and_12 (and_12_out, not_7_out, nor_1_out);
  nor nor_2 (Y1, and_1_out, and_2_out, and_3_out, and_4_out, buffer_1_out);
  nor nor_3 (Y2, and_5_out, and_6_out, and_7_out, and_8_out);
  nor nor_4 (Y3, and_9_out, and_10_out, and_11_out, and_12_out);
  nor nor_5 (Y4, not_8_out, not_9_out);
endmodule

module IC_74151 (
  input  A,
  input  B,
  input  C,
  input  D,
  input  E,
  input  F,
  input  G,
  input  J,
  input  S0,
  input  S1,
  input  S2,
  input  nOE,
  output Y,
  output W
);

  wire and_1_out, and_2_out, and_3_out, and_4_out, and_5_out, and_6_out, and_7_out, and_8_out, not_1_out,
       not_2_out, not_3_out, not_4_out;

  not not_1 (not_1_out, S0);
  not not_2 (not_2_out, S1);
  not not_3 (not_3_out, nOE);
  not not_4 (not_4_out, S2);
  and and_1 (and_1_out, A, not_3_out, not_1_out, not_2_out, not_4_out);
  and and_2 (and_2_out, B, not_3_out, S0, not_2_out, not_4_out);
  and and_3 (and_3_out, C, not_3_out, not_1_out, S1, not_4_out);
  and and_4 (and_4_out, D, not_3_out, S0, S1, not_4_out);
  and and_5 (and_5_out, E, not_3_out, not_1_out, not_2_out, S2);
  and and_6 (and_6_out, F, not_3_out, S0, not_2_out, S2);
  and and_7 (and_7_out, G, not_3_out, not_1_out, S1, S2);
  and and_8 (and_8_out, J, not_3_out, S0, S1, S2);
  or or_1 (Y, and_1_out, and_2_out, and_3_out, and_4_out, and_5_out, and_6_out, and_7_out, and_8_out);
  not not_5 (W, Y);
endmodule

// 74x151 8:1
module IC_74x151 (
  input  D0,
  input  D1,
  input  D2,
  input  D3,
  input  D4,
  input  D5,
  input  D6,
  input  D7,
  input  A,
  input  B,
  input  C,
  input  nG,
  output Y,
  output W
);

  wire not_1_out;

  not not_1 (not_1_out, nG);
  Multiplexer #(.select(3)) multiplexer_1 (
    .in0(D0), .in1(D1), .in2(D2), .in3(D3), .in4(D4), .in5(D5), .in6(D6), .in7(D7), .out(Y), .sel({C, B, A}),
    .en(not_1_out));
  not not_2 (W, Y);
endmodule

module IC_74153 (
  input  A1,
  input  B1,
  input  C1,
  input  D1,
  input  A2,
  input  B2,
  input  C2,
  input  D2,
  input  S0,
  input  S1,
  input  OE1,
  input  OE2,
  output Y1,
  output Y2
);

  wire and_1_out, and_2_out, and_3_out, and_4_out, and_5_out, and_6_out, and_7_out, and_8_out, not_1_out,
       not_2_out, not_3_out, not_4_out;

  not not_1 (not_1_out, S0);
  not not_2 (not_2_out, S1);
  not not_3 (not_3_out, OE1);
  not not_4 (not_4_out, OE2);
  and and_1 (and_1_out, A1, not_3_out, not_1_out, not_2_out);
  and and_2 (and_2_out, B1, not_3_out, S0, not_2_out);
  and and_3 (and_3_out, C1, not_3_out, not_1_out, S1);
  and and_4 (and_4_out, D1, not_3_out, S0, S1);
  and and_5 (and_5_out, A2, not_4_out, not_1_out, not_2_out);
  and and_6 (and_6_out, B2, not_4_out, S0, not_2_out);
  and and_7 (and_7_out, C2, not_4_out, not_1_out, S1);
  and and_8 (and_8_out, D2, not_4_out, S0, S1);
  or or_1 (Y1, and_1_out, and_2_out, and_3_out, and_4_out);
  or or_2 (Y2, and_5_out, and_6_out, and_7_out, and_8_out);
endmodule

// 74x153 4:1
module IC_74x153 (
  input  C1_0,
  input  C1_1,
  input  C1_2,
  input  C1_3,
  input  C2_0,
  input  C2_1,
  input  C2_2,
  input  C2_3,
  input  A,
  input  B,
  input  nG1,
  input  nG2,
  output Y1,
  output Y2
);

  wire not_1_out, not_2_out;

  not not_1 (not_1_out, nG1);
  not not_2 (not_2_out, nG2);
  Multiplexer #(.select(2)) multiplexer_1 (
    .in0(C1_0), .in1(C1_1), .in2(C1_2), .in3(C1_3), .out(Y1), .sel({B, A}), .en(not_1_out));
  Multiplexer #(.select(2)) multiplexer_2 (
    .in0(C2_0), .in1(C2_1), .in2(C2_2), .in3(C2_3), .out(Y2), .sel({B, A}), .en(not_2_out));
endmodule

module IC_74157 (
  input  A1,
  input  B1,
  input  A2,
  input  B2,
  input  A3,
  input  B3,
  input  A4,
  input  B4,
  input  S0,
  input  OE,
  output Y1,
  output Y2,
  output Y3,
  output Y4
);

  wire and_1_out, and_2_out, and_3_out, and_4_out, and_5_out, and_6_out, and_7_out, and_8_out, not_1_out,
       not_2_out;

  not not_1 (not_1_out, S0);
  not not_2 (not_2_out, OE);
  and and_1 (and_1_out, A1, not_1_out, not_2_out);
  and and_2 (and_2_out, B1, S0, not_2_out);
  and and_3 (and_3_out, A2, not_1_out, not_2_out);
  and and_4 (and_4_out, B2, S0, not_2_out);
  and and_5 (and_5_out, A3, not_1_out, not_2_out);
  and and_6 (and_6_out, B3, S0, not_2_out);
  and and_7 (and_7_out, A4, not_1_out, not_2_out);
  and and_8 (and_8_out, B4, S0, not_2_out);
  or or_1 (Y1, and_1_out, and_2_out);
  or or_2 (Y2, and_3_out, and_4_out);
  or or_3 (Y3, and_5_out, and_6_out);
  or or_4 (Y4, and_7_out, and_8_out);
endmodule

module IC_74161 (
  input  CLK,
  input  CLR,
  input  LE,
  input  CEP,
  input  CET,
  input  D1,
  input  D2,
  input  D3,
  input  D4,
  output Q1,
  output Q2,
  output Q3,
  output Q4,
  output TC
);

  wire and_1_out, and_2_out, and_3_out, and_4_out, and_5_out, and_6_out, and_7_out, and_8_out, and_9_out,
       and_10_out, and_11_out, and_12_out, not_1_out, not_2_out, not_3_out, or_1_out, or_2_out, or_3_out,
       or_4_out, xor_1_out, xor_2_out, xor_3_out, xor_4_out;

  not not_1 (not_1_out, CLK);
  not not_2 (not_2_out, CLR);
  and and_1 (and_1_out, LE, CEP, CET);
  not not_3 (not_3_out, LE);
  and and_2 (and_2_out, D1, not_3_out);
  and and_3 (and_3_out, Q1, LE);
  and and_4 (and_4_out, D2, not_3_out);
  and and_5 (and_5_out, Q2, LE);
  and and_6 (and_6_out, Q1, and_1_out);
  and and_7 (and_7_out, D3, not_3_out);
  and and_8 (and_8_out, Q3, LE);
  and and_9 (and_9_out, Q2, Q1, and_1_out);
  and and_10 (and_10_out, D4, not_3_out);
  and and_11 (and_11_out, Q4, LE);
  and and_12 (and_12_out, Q3, Q2, Q1, and_1_out);
  xor xor_1 (xor_1_out, and_3_out, and_1_out);
  xor xor_2 (xor_2_out, and_5_out, and_6_out);
  xor xor_3 (xor_3_out, and_8_out, and_9_out);
  xor xor_4 (xor_4_out, and_11_out, and_12_out);
  or or_1 (or_1_out, and_2_out, xor_1_out);
  or or_2 (or_2_out, and_4_out, xor_2_out);
  or or_3 (or_3_out, and_7_out, xor_3_out);
  or or_4 (or_4_out, and_10_out, xor_4_out);
  D_Flip_Flop d_flip_flop_1 (.Q(Q1), .CLR(not_2_out), .D(or_1_out), .CLK(not_1_out));  // open: R, SET
  D_Flip_Flop d_flip_flop_2 (.Q(Q2), .CLR(not_2_out), .D(or_2_out), .CLK(not_1_out));  // open: R, SET
  D_Flip_Flop d_flip_flop_3 (.Q(Q3), .CLR(not_2_out), .D(or_3_out), .CLK(not_1_out));  // open: R, SET
  D_Flip_Flop d_flip_flop_4 (.Q(Q4), .CLR(not_2_out), .D(or_4_out), .CLK(not_1_out));  // open: R, SET
  and and_13 (TC, Q4, Q3, Q2, Q1, CET);
endmodule

// 74x161
module IC_74x161 (
  input  CLK,
  input  nCLR,
  input  nLD,
  input  CEP,
  input  CET,
  input  D1,
  input  D2,
  input  D3,
  input  D4,
  output Q1,
  output Q2,
  output Q3,
  output Q4,
  output TC
);

  wire and_1_out, and_2_out, and_3_out, and_4_out, and_5_out, and_6_out, and_7_out, and_8_out, and_9_out,
       and_10_out, and_11_out, and_12_out, not_1_out, not_2_out, or_1_out, or_2_out, or_3_out, or_4_out,
       xor_1_out, xor_2_out, xor_3_out, xor_4_out;

  not not_1 (not_1_out, nCLR);
  and and_1 (and_1_out, nLD, CEP, CET);
  not not_2 (not_2_out, nLD);
  and and_2 (and_2_out, D1, not_2_out);
  and and_3 (and_3_out, Q1, nLD);
  and and_4 (and_4_out, D2, not_2_out);
  and and_5 (and_5_out, Q2, nLD);
  and and_6 (and_6_out, Q1, and_1_out);
  and and_7 (and_7_out, D3, not_2_out);
  and and_8 (and_8_out, Q3, nLD);
  and and_9 (and_9_out, Q2, Q1, and_1_out);
  and and_10 (and_10_out, D4, not_2_out);
  and and_11 (and_11_out, Q4, nLD);
  and and_12 (and_12_out, Q3, Q2, Q1, and_1_out);
  xor xor_1 (xor_1_out, and_3_out, and_1_out);
  xor xor_2 (xor_2_out, and_5_out, and_6_out);
  xor xor_3 (xor_3_out, and_8_out, and_9_out);
  xor xor_4 (xor_4_out, and_11_out, and_12_out);
  or or_1 (or_1_out, and_2_out, xor_1_out);
  or or_2 (or_2_out, and_4_out, xor_2_out);
  or or_3 (or_3_out, and_7_out, xor_3_out);
  or or_4 (or_4_out, and_10_out, xor_4_out);
  D_Flip_Flop d_flip_flop_1 (.Q(Q1), .CLR(not_1_out), .D(or_1_out), .CLK(CLK));  // open: R, SET
  D_Flip_Flop d_flip_flop_2 (.Q(Q2), .CLR(not_1_out), .D(or_2_out), .CLK(CLK));  // open: R, SET
  D_Flip_Flop d_flip_flop_3 (.Q(Q3), .CLR(not_1_out), .D(or_3_out), .CLK(CLK));  // open: R, SET
  D_Flip_Flop d_flip_flop_4 (.Q(Q4), .CLR(not_1_out), .D(or_4_out), .CLK(CLK));  // open: R, SET
  and and_13 (TC, Q4, Q3, Q2, Q1, CET);
endmodule

module IC_74163 (
  input  CLK,
  input  nSR,
  input  nPE,
  input  CEP,
  input  CET,
  input  D1,
  input  D2,
  input  D3,
  input  D4,
  output Q1,
  output Q2,
  output Q3,
  output Q4,
  output TC
);

  wire and_1_out, and_2_out, and_3_out, and_4_out, and_5_out, and_6_out, and_7_out, and_8_out, and_9_out,
       and_10_out, and_11_out, and_12_out, and_13_out, not_3_out, or_1_out, or_2_out, or_3_out, or_4_out,
       xor_1_out, xor_2_out, xor_3_out, xor_4_out;

  // NOT_Gate not_1 is placed but not wired
  // NOT_Gate not_2 is placed but not wired
  and and_1 (and_1_out, nPE, CEP, CET);
  not not_3 (not_3_out, nPE);
  and and_2 (and_2_out, D1, nSR, not_3_out);
  and and_3 (and_3_out, Q1, nSR, nPE);
  and and_4 (and_4_out, nSR, and_1_out);
  and and_5 (and_5_out, D2, nSR, not_3_out);
  and and_6 (and_6_out, Q2, nSR, nPE);
  and and_7 (and_7_out, Q1, nSR, and_1_out);
  and and_8 (and_8_out, D3, nSR, not_3_out);
  and and_9 (and_9_out, Q3, nSR, nPE);
  and and_10 (and_10_out, Q2, Q1, and_1_out, nSR);
  and and_11 (and_11_out, D4, nSR, not_3_out);
  and and_12 (and_12_out, Q4, nSR, nPE);
  and and_13 (and_13_out, Q3, Q2, nSR, Q1, and_1_out);
  xor xor_1 (xor_1_out, and_3_out, and_4_out);
  xor xor_2 (xor_2_out, and_6_out, and_7_out);
  xor xor_3 (xor_3_out, and_9_out, and_10_out);
  xor xor_4 (xor_4_out, and_12_out, and_13_out);
  or or_1 (or_1_out, and_2_out, xor_1_out);
  or or_2 (or_2_out, and_5_out, xor_2_out);
  or or_3 (or_3_out, and_8_out, xor_3_out);
  or or_4 (or_4_out, and_11_out, xor_4_out);
  D_Flip_Flop d_flip_flop_1 (.Q(Q1), .D(or_1_out), .CLK(CLK));  // open: R, SET, CLR
  D_Flip_Flop d_flip_flop_2 (.Q(Q2), .D(or_2_out), .CLK(CLK));  // open: R, SET, CLR
  D_Flip_Flop d_flip_flop_3 (.Q(Q3), .D(or_3_out), .CLK(CLK));  // open: R, SET, CLR
  D_Flip_Flop d_flip_flop_4 (.Q(Q4), .D(or_4_out), .CLK(CLK));  // open: R, SET, CLR
  and and_14 (TC, Q4, Q3, Q2, Q1, CET);
endmodule

// 74x163 CONT
module IC_74x163 (
  input  CLK,
  input  nCLR,
  input  nLD,
  input  CEP,
  input  CET,
  input  D1,
  input  D2,
  input  D3,
  input  D4,
  output Q1,
  output Q2,
  output Q3,
  output Q4,
  output TC
);

  wire and_1_out, and_2_out, and_3_out, and_4_out, and_5_out, and_6_out, and_7_out, and_8_out, and_9_out,
       and_10_out, and_11_out, and_12_out, and_13_out, not_1_out, or_1_out, or_2_out, or_3_out, or_4_out,
       xor_1_out, xor_2_out, xor_3_out, xor_4_out;

  and and_1 (and_1_out, nLD, CEP, CET);
  not not_1 (not_1_out, nLD);
  and and_2 (and_2_out, D1, nCLR, not_1_out);
  and and_3 (and_3_out, Q1, nCLR, nLD);
  and and_4 (and_4_out, nCLR, and_1_out);
  and and_5 (and_5_out, D2, nCLR, not_1_out);
  and and_6 (and_6_out, Q2, nCLR, nLD);
  and and_7 (and_7_out, Q1, nCLR, and_1_out);
  and and_8 (and_8_out, D3, nCLR, not_1_out);
  and and_9 (and_9_out, Q3, nCLR, nLD);
  and and_10 (and_10_out, Q2, Q1, and_1_out, nCLR);
  and and_11 (and_11_out, D4, nCLR, not_1_out);
  and and_12 (and_12_out, Q4, nCLR, nLD);
  and and_13 (and_13_out, Q3, Q2, nCLR, Q1, and_1_out);
  xor xor_1 (xor_1_out, and_3_out, and_4_out);
  xor xor_2 (xor_2_out, and_6_out, and_7_out);
  xor xor_3 (xor_3_out, and_9_out, and_10_out);
  xor xor_4 (xor_4_out, and_12_out, and_13_out);
  or or_1 (or_1_out, and_2_out, xor_1_out);
  or or_2 (or_2_out, and_5_out, xor_2_out);
  or or_3 (or_3_out, and_8_out, xor_3_out);
  or or_4 (or_4_out, and_11_out, xor_4_out);
  D_Flip_Flop d_flip_flop_1 (.Q(Q1), .D(or_1_out), .CLK(CLK));  // open: R, SET, CLR
  D_Flip_Flop d_flip_flop_2 (.Q(Q2), .D(or_2_out), .CLK(CLK));  // open: R, SET, CLR
  D_Flip_Flop d_flip_flop_3 (.Q(Q3), .D(or_3_out), .CLK(CLK));  // open: R, SET, CLR
  D_Flip_Flop d_flip_flop_4 (.Q(Q4), .D(or_4_out), .CLK(CLK));  // open: R, SET, CLR
  and and_14 (TC, Q4, Q3, Q2, Q1, CET);
endmodule

module IC_74173 (
  input  D1,
  input  D2,
  input  D3,
  input  D4,
  input  CLK,
  input  CE1,
  input  CE2,
  input  CLR,
  input  OE1,
  input  OE2,
  output Q1,
  output Q2,
  output Q3,
  output Q4
);

  wire and_1_out, d_flip_flop_1_q, d_flip_flop_2_q, d_flip_flop_3_q, d_flip_flop_4_q, nor_1_out, nor_2_out;

  nor nor_1 (nor_1_out, CE1, CE2);
  nor nor_2 (nor_2_out, OE1, OE2);
  and and_1 (and_1_out, CLK, nor_1_out);
  D_Flip_Flop d_flip_flop_1 (.Q(d_flip_flop_1_q), .CLR(CLR), .D(D1), .CLK(and_1_out));  // open: R, SET
  D_Flip_Flop d_flip_flop_2 (.Q(d_flip_flop_2_q), .CLR(CLR), .D(D2), .CLK(and_1_out));  // open: R, SET
  D_Flip_Flop d_flip_flop_3 (.Q(d_flip_flop_3_q), .CLR(CLR), .D(D3), .CLK(and_1_out));  // open: R, SET
  D_Flip_Flop d_flip_flop_4 (.Q(d_flip_flop_4_q), .CLR(CLR), .D(D4), .CLK(and_1_out));  // open: R, SET
  assign Q1 = nor_2_out ? d_flip_flop_1_q : 1'bz;  // Controlled_Buffer controlled_buffer_1
  assign Q2 = nor_2_out ? d_flip_flop_2_q : 1'bz;  // Controlled_Buffer controlled_buffer_2
  assign Q3 = nor_2_out ? d_flip_flop_3_q : 1'bz;  // Controlled_Buffer controlled_buffer_3
  assign Q4 = nor_2_out ? d_flip_flop_4_q : 1'bz;  // Controlled_Buffer controlled_buffer_4
endmodule

module IC_74175 (
  input  D1,
  input  D2,
  input  D3,
  input  D4,
  input  CLK,
  input  CLR,
  output Q1,
  output R1,
  output Q2,
  output R2,
  output Q3,
  output R3,
  output Q4,
  output R4
);

  wire not_1_out;

  not not_1 (not_1_out, CLR);
  D_Flip_Flop d_flip_flop_1 (.Q(Q1), .R(R1), .CLR(not_1_out), .D(D1), .CLK(CLK));  // open: SET
  D_Flip_Flop d_flip_flop_2 (.Q(Q2), .R(R2), .CLR(not_1_out), .D(D2), .CLK(CLK));  // open: SET
  D_Flip_Flop d_flip_flop_3 (.Q(Q3), .R(R3), .CLR(not_1_out), .D(D3), .CLK(CLK));  // open: SET
  D_Flip_Flop d_flip_flop_4 (.Q(Q4), .R(R4), .CLR(not_1_out), .D(D4), .CLK(CLK));  // open: SET
endmodule

module IC_74238 (
  input  A0,
  input  A1,
  input  A2,
  input  OE1,
  input  OE2,
  input  OE3,
  output Y0,
  output Y1,
  output Y2,
  output Y3,
  output Y4,
  output Y5,
  output Y6,
  output Y7
);

  wire and_1_out, not_1_out, not_2_out, not_3_out, not_4_out, not_5_out;

  not not_1 (not_1_out, A0);
  not not_2 (not_2_out, A1);
  not not_3 (not_3_out, A2);
  not not_4 (not_4_out, OE1);
  not not_5 (not_5_out, OE2);
  and and_1 (and_1_out, not_4_out, not_5_out, OE3);
  and and_2 (Y0, not_1_out, not_2_out, not_3_out, and_1_out);
  and and_3 (Y1, A0, not_2_out, not_3_out, and_1_out);
  and and_4 (Y2, not_1_out, A1, not_3_out, and_1_out);
  and and_5 (Y3, A0, A1, not_3_out, and_1_out);
  and and_6 (Y4, not_1_out, not_2_out, A2, and_1_out);
  and and_7 (Y5, A0, not_2_out, A2, and_1_out);
  and and_8 (Y6, not_1_out, A1, A2, and_1_out);
  and and_9 (Y7, A0, A1, A2, and_1_out);
endmodule

// 74x238 3:8
module IC_74x238 (
  input  A,
  input  B,
  input  C,
  input  nG2A,
  input  nG2B,
  input  G1,
  output Y0,
  output Y1,
  output Y2,
  output Y3,
  output Y4,
  output Y5,
  output Y6,
  output Y7
);

  wire and_1_out;

  and and_1 (and_1_out, ~nG2A, ~nG2B, G1);  // AND_Gate
  Decoder #(.select(3)) decoder_1 (
    .out0(Y0), .out1(Y1), .out2(Y2), .out3(Y3), .out4(Y4), .out5(Y5), .out6(Y6), .out7(Y7), .sel({C, B, A}),
    .en(and_1_out));
endmodule

module IC_74244 (
  input  A1,
  input  A2,
  input  A3,
  input  A4,
  input  OEA,
  input  B1,
  input  B2,
  input  B3,
  input  B4,
  input  OEB,
  output Y1,
  output Y2,
  output Y3,
  output Y4,
  output Z1,
  output Z2,
  output Z3,
  output Z4
);

  wire not_1_out, not_2_out;

  not not_1 (not_1_out, OEA);
  not not_2 (not_2_out, OEB);
  assign Y1 = not_1_out ? A1 : 1'bz;  // Controlled_Buffer controlled_buffer_1
  assign Y2 = not_1_out ? A2 : 1'bz;  // Controlled_Buffer controlled_buffer_2
  assign Y3 = not_1_out ? A3 : 1'bz;  // Controlled_Buffer controlled_buffer_3
  assign Y4 = not_1_out ? A4 : 1'bz;  // Controlled_Buffer controlled_buffer_4
  assign Z1 = not_2_out ? B1 : 1'bz;  // Controlled_Buffer controlled_buffer_5
  assign Z2 = not_2_out ? B2 : 1'bz;  // Controlled_Buffer controlled_buffer_6
  assign Z3 = not_2_out ? B3 : 1'bz;  // Controlled_Buffer controlled_buffer_7
  assign Z4 = not_2_out ? B4 : 1'bz;  // Controlled_Buffer controlled_buffer_8
endmodule

// 74x11244 1:1
module IC_74x11244 (
  input  A1_1,
  input  A1_2,
  input  A1_3,
  input  A1_4,
  input  nOE1,
  input  A2_1,
  input  A2_2,
  input  A2_3,
  input  A2_4,
  input  nOE2,
  output Y1_1,
  output Y1_2,
  output Y1_3,
  output Y1_4,
  output Y2_1,
  output Y2_2,
  output Y2_3,
  output Y2_4
);

  wire not_1_out, not_2_out;

  not not_1 (not_1_out, nOE1);
  not not_2 (not_2_out, nOE2);
  assign {Y1_4, Y1_3, Y1_2, Y1_1} = not_1_out ? {A1_4, A1_3, A1_2, A1_1} : 4'bz;  // Controlled_Buffer controlled_buffer_1
  assign {Y2_4, Y2_3, Y2_2, Y2_1} = not_2_out ? {A2_4, A2_3, A2_2, A2_1} : 4'bz;  // Controlled_Buffer controlled_buffer_2
endmodule

// 74x241 1:1
module IC_74x241 (
  input  A1,
  input  A2,
  input  A3,
  input  A4,
  input  nOEA,
  input  B1,
  input  B2,
  input  B3,
  input  B4,
  input  OEB,
  output Y1,
  output Y2,
  output Y3,
  output Y4,
  output Z1,
  output Z2,
  output Z3,
  output Z4
);

  wire not_1_out;

  not not_1 (not_1_out, nOEA);
  assign {Y4, Y3, Y2, Y1} = not_1_out ? {A4, A3, A2, A1} : 4'bz;  // Controlled_Buffer controlled_buffer_1
  assign {Z4, Z3, Z2, Z1} = OEB ? {B4, B3, B2, B1} : 4'bz;  // Controlled_Buffer controlled_buffer_2
endmodule

// 74x251 8:1
module IC_74x251 (
  input  I0,
  input  I1,
  input  I2,
  input  I3,
  input  I4,
  input  I5,
  input  I6,
  input  I7,
  input  S0,
  input  S1,
  input  S2,
  input  nOE,
  output Y,
  output W
);

  wire multiplexer_1_out, not_1_out;

  not not_1 (not_1_out, nOE);
  Multiplexer #(.disabled("Z"), .enable("false"), .select(3)) multiplexer_1 (
    .in0(I0), .in1(I1), .in2(I2), .in3(I3), .in4(I4), .in5(I5), .in6(I6), .in7(I7), .out(multiplexer_1_out),
    .sel({S2, S1, S0}));
  assign Y = not_1_out ? multiplexer_1_out : 1'bz;  // Controlled_Buffer controlled_buffer_1
  assign W = not_1_out ? ~multiplexer_1_out : 1'bz;  // Controlled_Inverter controlled_inverter_1
endmodule

// 74x253 4:1
module IC_74x253 (
  input  I_n_0,
  input  I1_1,
  input  I1_2,
  input  I1_3,
  input  I2_0,
  input  I2_1,
  input  I2_2,
  input  I2_3,
  input  S0,
  input  S1,
  input  nOE1,
  input  nOE2,
  output Y1,
  output Y2
);

  wire not_1_out, not_2_out;

  not not_1 (not_1_out, nOE1);
  not not_2 (not_2_out, nOE2);
  Multiplexer #(.disabled("Z"), .select(2)) multiplexer_1 (
    .in0(I_n_0), .in1(I1_1), .in2(I1_2), .in3(I1_3), .out(Y1), .sel({S1, S0}), .en(not_1_out));
  Multiplexer #(.disabled("Z"), .select(2)) multiplexer_2 (
    .in0(I2_0), .in1(I2_1), .in2(I2_2), .in3(I2_3), .out(Y2), .sel({S1, S0}), .en(not_2_out));
endmodule

// 74x257 2:1
module IC_74x257 (
  input  I1_0,
  input  I2_0,
  input  I1_1,
  input  I2_1,
  input  I1_2,
  input  I2_2,
  input  I1_3,
  input  I2_3,
  input  nA_B,
  input  nOE,
  output Y1,
  output Y2,
  output Y3,
  output Y4
);

  wire not_1_out;

  not not_1 (not_1_out, nOE);
  Multiplexer #(.disabled("Z")) multiplexer_1 (.in0(I1_0), .in1(I2_0), .out(Y1), .sel(nA_B), .en(not_1_out));
  Multiplexer #(.disabled("Z")) multiplexer_2 (.in0(I1_1), .in1(I2_1), .out(Y2), .sel(nA_B), .en(not_1_out));
  Multiplexer #(.disabled("Z")) multiplexer_3 (.in0(I1_2), .in1(I2_2), .out(Y3), .sel(nA_B), .en(not_1_out));
  Multiplexer #(.disabled("Z")) multiplexer_4 (.in0(I1_3), .in1(I2_3), .out(Y4), .sel(nA_B), .en(not_1_out));
endmodule

module IC_74273 (
  input  D1,
  input  D2,
  input  D3,
  input  D4,
  input  D5,
  input  D6,
  input  D7,
  input  D8,
  input  CLK,
  input  CLR,
  output Y1,
  output Y2,
  output Y3,
  output Y4,
  output Y5,
  output Y6,
  output Y7,
  output Y8
);

  wire not_1_out;

  not not_1 (not_1_out, CLR);
  D_Flip_Flop d_flip_flop_1 (.Q(Y1), .CLR(not_1_out), .D(D1), .CLK(CLK));  // open: R, SET
  D_Flip_Flop d_flip_flop_2 (.Q(Y2), .CLR(not_1_out), .D(D2), .CLK(CLK));  // open: R, SET
  D_Flip_Flop d_flip_flop_3 (.Q(Y3), .CLR(not_1_out), .D(D3), .CLK(CLK));  // open: R, SET
  D_Flip_Flop d_flip_flop_4 (.Q(Y4), .CLR(not_1_out), .D(D4), .CLK(CLK));  // open: R, SET
  D_Flip_Flop d_flip_flop_5 (.Q(Y5), .CLR(not_1_out), .D(D5), .CLK(CLK));  // open: R, SET
  D_Flip_Flop d_flip_flop_6 (.Q(Y6), .CLR(not_1_out), .D(D6), .CLK(CLK));  // open: R, SET
  D_Flip_Flop d_flip_flop_7 (.Q(Y7), .CLR(not_1_out), .D(D7), .CLK(CLK));  // open: R, SET
  D_Flip_Flop d_flip_flop_8 (.Q(Y8), .CLR(not_1_out), .D(D8), .CLK(CLK));  // open: R, SET
endmodule

// 74x273 DFF
module IC_74x273 (
  input  D1,
  input  D2,
  input  D3,
  input  D4,
  input  D5,
  input  D6,
  input  D7,
  input  D8,
  input  CLK,
  input  nMR,
  output Q1,
  output Q2,
  output Q3,
  output Q4,
  output Q5,
  output Q6,
  output Q7,
  output Q8,
  output [7:0] Probe
);

  wire not_1_out;

  not not_1 (not_1_out, nMR);
  Register register_1 (.D({D8, D7, D6, D5, D4, D3, D2, D1}), .en(1'b1), .Q(Probe), .clk(CLK), .clr(not_1_out));

  assign Q1 = Probe[0];
  assign Q2 = Probe[1];
  assign Q3 = Probe[2];
  assign Q4 = Probe[3];
  assign Q5 = Probe[4];
  assign Q6 = Probe[5];
  assign Q7 = Probe[6];
  assign Q8 = Probe[7];
endmodule

module IC_74283 (
  input  A1,
  input  A2,
  input  A3,
  input  A4,
  input  B1,
  input  B2,
  input  B3,
  input  B4,
  input  CIN,
  output Y1,
  output Y2,
  output Y3,
  output Y4,
  output COUT
);

  wire and_1_out, and_2_out, and_3_out, and_4_out, and_5_out, and_6_out, and_7_out, and_8_out, and_9_out,
       and_10_out, and_11_out, and_12_out, and_13_out, and_14_out, nand_1_out, nand_2_out, nand_3_out,
       nand_4_out, nor_1_out, nor_2_out, nor_3_out, nor_4_out, nor_5_out, nor_6_out, nor_7_out, not_1_out,
       not_2_out, not_3_out, not_4_out, not_5_out, not_6_out;

  not not_1 (not_1_out, CIN);
  nor nor_1 (nor_1_out, A1, B1);
  nand nand_1 (nand_1_out, A1, B1);
  nor nor_2 (nor_2_out, A2, B2);
  nand nand_2 (nand_2_out, A2, B2);
  nor nor_3 (nor_3_out, A3, B3);
  nand nand_3 (nand_3_out, A3, B3);
  nor nor_4 (nor_4_out, A4, B4);
  nand nand_4 (nand_4_out, A4, B4);
  not not_2 (not_2_out, not_1_out);
  not not_3 (not_3_out, nor_1_out);
  and and_1 (and_1_out, not_1_out, nand_1_out);
  not not_4 (not_4_out, nor_2_out);
  and and_2 (and_2_out, not_1_out, nand_1_out, nand_2_out);
  and and_3 (and_3_out, nand_2_out, nor_1_out);
  not not_5 (not_5_out, nor_3_out);
  and and_4 (and_4_out, not_1_out, nand_1_out, nand_2_out, nand_3_out);
  and and_5 (and_5_out, nand_2_out, nand_3_out, nor_1_out);
  and and_6 (and_6_out, nand_3_out, nor_2_out);
  not not_6 (not_6_out, nor_4_out);
  and and_7 (and_7_out, not_1_out, nand_1_out, nand_2_out, nand_3_out, nand_4_out);
  and and_8 (and_8_out, nand_2_out, nand_3_out, nand_4_out, nor_1_out);
  and and_9 (and_9_out, nand_3_out, nand_4_out, nor_2_out);
  and and_10 (and_10_out, nand_4_out, nor_3_out);
  and and_11 (and_11_out, not_3_out, nand_1_out);
  nor nor_5 (nor_5_out, and_1_out, nor_1_out);
  and and_12 (and_12_out, not_4_out, nand_2_out);
  nor nor_6 (nor_6_out, and_2_out, and_3_out, nor_2_out);
  and and_13 (and_13_out, not_5_out, nand_3_out);
  nor nor_7 (nor_7_out, and_4_out, and_5_out, and_6_out, nor_3_out);
  and and_14 (and_14_out, not_6_out, nand_4_out);
  nor nor_8 (COUT, and_7_out, and_8_out, and_9_out, and_10_out, nor_4_out);
  xor xor_1 (Y1, not_2_out, and_11_out);
  xor xor_2 (Y2, nor_5_out, and_12_out);
  xor xor_3 (Y3, nor_6_out, and_13_out);
  xor xor_4 (Y4, nor_7_out, and_14_out);
endmodule

// 74x283 ADD
module IC_74x283 (
  input  CIN,
  input  A1,
  input  A2,
  input  A3,
  input  A4,
  input  B1,
  input  B2,
  input  B3,
  input  B4,
  output Y1,
  output Y2,
  output Y3,
  output Y4,
  output COUT
);

  Adder #(.width(4)) adder_1 (
    .a({A4, A3, A2, A1}), .b({B4, B3, B2, B1}), .out({Y4, Y3, Y2, Y1}), .cin(CIN), .cout(COUT));
endmodule

module IC_74374 (
  input  D1,
  input  D2,
  input  D3,
  input  D4,
  input  D5,
  input  D6,
  input  D7,
  input  D8,
  input  CLK,
  input  OE,
  output Y1,
  output Y2,
  output Y3,
  output Y4,
  output Y5,
  output Y6,
  output Y7,
  output Y8
);

  wire d_flip_flop_1_q, d_flip_flop_2_q, d_flip_flop_3_q, d_flip_flop_4_q, d_flip_flop_5_q, d_flip_flop_6_q,
       d_flip_flop_7_q, d_flip_flop_8_q, not_1_out;

  D_Flip_Flop d_flip_flop_1 (.Q(d_flip_flop_1_q), .D(D1), .CLK(CLK));  // open: R, SET, CLR
  D_Flip_Flop d_flip_flop_2 (.Q(d_flip_flop_2_q), .D(D2), .CLK(CLK));  // open: R, SET, CLR
  D_Flip_Flop d_flip_flop_3 (.Q(d_flip_flop_3_q), .D(D3), .CLK(CLK));  // open: R, SET, CLR
  D_Flip_Flop d_flip_flop_4 (.Q(d_flip_flop_4_q), .D(D4), .CLK(CLK));  // open: R, SET, CLR
  D_Flip_Flop d_flip_flop_5 (.Q(d_flip_flop_5_q), .D(D5), .CLK(CLK));  // open: R, SET, CLR
  D_Flip_Flop d_flip_flop_6 (.Q(d_flip_flop_6_q), .D(D6), .CLK(CLK));  // open: R, SET, CLR
  D_Flip_Flop d_flip_flop_7 (.Q(d_flip_flop_7_q), .D(D7), .CLK(CLK));  // open: R, SET, CLR
  D_Flip_Flop d_flip_flop_8 (.Q(d_flip_flop_8_q), .D(D8), .CLK(CLK));  // open: R, SET, CLR
  not not_1 (not_1_out, OE);
  assign Y1 = not_1_out ? d_flip_flop_1_q : 1'bz;  // Controlled_Buffer controlled_buffer_1
  assign Y2 = not_1_out ? d_flip_flop_2_q : 1'bz;  // Controlled_Buffer controlled_buffer_2
  assign Y3 = not_1_out ? d_flip_flop_3_q : 1'bz;  // Controlled_Buffer controlled_buffer_3
  assign Y4 = not_1_out ? d_flip_flop_4_q : 1'bz;  // Controlled_Buffer controlled_buffer_4
  assign Y5 = not_1_out ? d_flip_flop_5_q : 1'bz;  // Controlled_Buffer controlled_buffer_5
  assign Y6 = not_1_out ? d_flip_flop_6_q : 1'bz;  // Controlled_Buffer controlled_buffer_6
  assign Y7 = not_1_out ? d_flip_flop_7_q : 1'bz;  // Controlled_Buffer controlled_buffer_7
  assign Y8 = not_1_out ? d_flip_flop_8_q : 1'bz;  // Controlled_Buffer controlled_buffer_8
endmodule

module IC_74377 (
  input  D1,
  input  D2,
  input  D3,
  input  D4,
  input  D5,
  input  D6,
  input  D7,
  input  D8,
  input  CLK,
  input  CE,
  output Y1,
  output Y2,
  output Y3,
  output Y4,
  output Y5,
  output Y6,
  output Y7,
  output Y8
);

  wire and_1_out, not_1_out;

  not not_1 (not_1_out, CE);
  and and_1 (and_1_out, CLK, not_1_out);
  D_Flip_Flop d_flip_flop_1 (.Q(Y1), .D(D1), .CLK(and_1_out));  // open: R, SET, CLR
  D_Flip_Flop d_flip_flop_2 (.Q(Y2), .D(D2), .CLK(and_1_out));  // open: R, SET, CLR
  D_Flip_Flop d_flip_flop_3 (.Q(Y3), .D(D3), .CLK(and_1_out));  // open: R, SET, CLR
  D_Flip_Flop d_flip_flop_4 (.Q(Y4), .D(D4), .CLK(and_1_out));  // open: R, SET, CLR
  D_Flip_Flop d_flip_flop_5 (.Q(Y5), .D(D5), .CLK(and_1_out));  // open: R, SET, CLR
  D_Flip_Flop d_flip_flop_6 (.Q(Y6), .D(D6), .CLK(and_1_out));  // open: R, SET, CLR
  D_Flip_Flop d_flip_flop_7 (.Q(Y7), .D(D7), .CLK(and_1_out));  // open: R, SET, CLR
  D_Flip_Flop d_flip_flop_8 (.Q(Y8), .D(D8), .CLK(and_1_out));  // open: R, SET, CLR
endmodule

// 74x541 1:1
module IC_74x541 (
  input  I1,
  input  I2,
  input  I3,
  input  I4,
  input  I5,
  input  I6,
  input  I7,
  input  I8,
  input  nOE1,
  input  nOE2,
  output Q1,
  output Q2,
  output Q3,
  output Q4,
  output Q5,
  output Q6,
  output Q7,
  output Q8
);

  wire and_1_out;

  and and_1 (and_1_out, ~nOE1, ~nOE2);  // AND_Gate
  assign {Q8, Q7, Q6, Q5, Q4, Q3, Q2, Q1} = and_1_out ? {I8, I7, I6, I5, I4, I3, I2, I1} : 8'bz;  // Controlled_Buffer controlled_buffer_1
endmodule

// 74x563 D_L
module IC_74x563 (
  input  D1,
  input  D2,
  input  D3,
  input  D4,
  input  D5,
  input  D6,
  input  D7,
  input  D8,
  input  LE,
  input  nOE,
  output Q1,
  output Q2,
  output Q3,
  output Q4,
  output Q5,
  output Q6,
  output Q7,
  output Q8,
  output [7:0] Probe
);

  wire not_1_out;
  wire [7:0] register_1_q;

  not not_1 (not_1_out, nOE);
  Register #(.trigger("high")) register_1 (
    .D({D8, D7, D6, D5, D4, D3, D2, D1}), .en(1'b1), .Q(register_1_q), .clk(LE));  // open: clr
  assign {Q8, Q7, Q6, Q5, Q4, Q3, Q2, Q1} = not_1_out ? ~register_1_q : 8'bz;  // Controlled_Inverter controlled_inverter_1
  assign Probe = ~register_1_q;  // NOT_Gate not_2, 8 bits wide
endmodule

// 74x573 D-L
module IC_74x573 (
  input  D1,
  input  D2,
  input  D3,
  input  D4,
  input  D5,
  input  D6,
  input  D7,
  input  D8,
  input  LE,
  input  nOE,
  output Q1,
  output Q2,
  output Q3,
  output Q4,
  output Q5,
  output Q6,
  output Q7,
  output Q8,
  output [7:0] Probe
);

  wire not_1_out;

  not not_1 (not_1_out, nOE);
  Register #(.trigger("high")) register_1 (
    .D({D8, D7, D6, D5, D4, D3, D2, D1}), .en(1'b1), .Q(Probe), .clk(LE));  // open: clr
  assign {Q8, Q7, Q6, Q5, Q4, Q3, Q2, Q1} = not_1_out ? Probe : 8'bz;  // Controlled_Buffer controlled_buffer_1
endmodule

// 74x574 DFF
module IC_74x574 (
  input  D1,
  input  D2,
  input  D3,
  input  D4,
  input  D5,
  input  D6,
  input  D7,
  input  D8,
  input  CLK,
  input  nOE,
  output Q1,
  output Q2,
  output Q3,
  output Q4,
  output Q5,
  output Q6,
  output Q7,
  output Q8,
  output [7:0] Probe
);

  wire not_1_out;

  not not_1 (not_1_out, nOE);
  Register register_1 (.D({D8, D7, D6, D5, D4, D3, D2, D1}), .en(1'b1), .Q(Probe), .clk(CLK));  // open: clr
  assign {Q8, Q7, Q6, Q5, Q4, Q3, Q2, Q1} = not_1_out ? Probe : 8'bz;  // Controlled_Buffer controlled_buffer_1
endmodule

// 74x3251 8:1
module IC_74x3251 (
  input  B1,
  input  B2,
  input  B3,
  input  B4,
  input  B5,
  input  B6,
  input  B7,
  input  B8,
  input  S0,
  input  S1,
  input  S2,
  input  nOE,
  output A
);

  wire not_1_out;

  not not_1 (not_1_out, nOE);
  Multiplexer #(.disabled("Z"), .select(3)) multiplexer_1 (
    .in0(B1), .in1(B2), .in2(B3), .in3(B4), .in4(B5), .in5(B6), .in6(B7), .in7(B8), .out(A),
    .sel({S2, S1, S0}), .en(not_1_out));
endmodule

// 74x3253 4:1
module IC_74x3253 (
  input  B1_1,
  input  B1_2,
  input  B1_3,
  input  B1_4,
  input  B2_1,
  input  B2_2,
  input  B2_3,
  input  B2_4,
  input  S0,
  input  S1,
  input  nOE1,
  input  nOE2,
  output A1,
  output A2
);

  wire and_1_out;

  and and_1 (and_1_out, ~nOE1, ~nOE2);  // AND_Gate
  Multiplexer #(.disabled("Z"), .select(2)) multiplexer_1 (
    .in0(B1_1), .in1(B1_2), .in2(B1_3), .in3(B1_4), .out(A1), .sel({S1, S0}), .en(and_1_out));
  Multiplexer #(.disabled("Z"), .select(2)) multiplexer_2 (
    .in0(B2_1), .in1(B2_2), .in2(B2_3), .in3(B2_4), .out(A2), .sel({S1, S0}), .en(and_1_out));
endmodule

// 74x3257 2:1
module IC_74x3257 (
  input  B1_1,
  input  B2_1,
  input  B1_2,
  input  B2_2,
  input  B1_3,
  input  B2_3,
  input  B1_4,
  input  B2_4,
  input  S,
  input  nOE,
  output A1,
  output A2,
  output A3,
  output A4
);

  wire not_1_out;

  not not_1 (not_1_out, nOE);
  Multiplexer #(.disabled("Z")) multiplexer_1 (.in0(B1_1), .in1(B2_1), .out(A1), .sel(S), .en(not_1_out));
  Multiplexer #(.disabled("Z")) multiplexer_2 (.in0(B1_2), .in1(B2_2), .out(A2), .sel(S), .en(not_1_out));
  Multiplexer #(.disabled("Z")) multiplexer_3 (.in0(B1_3), .in1(B2_3), .out(A3), .sel(S), .en(not_1_out));
  Multiplexer #(.disabled("Z")) multiplexer_4 (.in0(B1_4), .in1(B2_4), .out(A4), .sel(S), .en(not_1_out));
endmodule

// 74x3345 1:1
module IC_74x3345 (
  input  B1,
  input  B2,
  input  B3,
  input  B4,
  input  B5,
  input  B6,
  input  B7,
  input  B8,
  input  OE,
  input  nOE,
  output A1,
  output A2,
  output A3,
  output A4,
  output A5,
  output A6,
  output A7,
  output A8
);

  wire or_1_out;

  or or_1 (or_1_out, OE, ~nOE);  // OR_Gate
  assign {A8, A7, A6, A5, A4, A3, A2, A1} = or_1_out ? {B8, B7, B6, B5, B4, B3, B2, B1} : 8'bz;  // Controlled_Buffer controlled_buffer_1
endmodule

// 1G3157
module IC_74x1G3157 (
  input  B1,
  input  B2,
  input  S,
  output A
);

  Multiplexer #(.disabled("Z"), .enable("false")) multiplexer_1 (.in0(B1), .in1(B2), .out(A), .sel(S));
endmodule

// 74x3257 1:2
module IC_74x32571 (
  input  A1,
  input  A2,
  input  A3,
  input  A4,
  input  S,
  input  nOE,
  output B1_1,
  output B1_2,
  output B1_3,
  output B1_4,
  output B2_1,
  output B2_2,
  output B2_3,
  output B2_4
);

  wire and_1_out, and_2_out, not_1_out, not_2_out;

  assign B1_1 = and_1_out ? A1 : 1'bz;  // Controlled_Buffer controlled_buffer_1
  assign B1_2 = and_1_out ? A2 : 1'bz;  // Controlled_Buffer controlled_buffer_2
  assign B1_3 = and_1_out ? A3 : 1'bz;  // Controlled_Buffer controlled_buffer_3
  assign B1_4 = and_1_out ? A4 : 1'bz;  // Controlled_Buffer controlled_buffer_4
  assign B2_1 = and_2_out ? A1 : 1'bz;  // Controlled_Buffer controlled_buffer_5
  assign B2_2 = and_2_out ? A2 : 1'bz;  // Controlled_Buffer controlled_buffer_6
  assign B2_3 = and_2_out ? A3 : 1'bz;  // Controlled_Buffer controlled_buffer_7
  assign B2_4 = and_2_out ? A4 : 1'bz;  // Controlled_Buffer controlled_buffer_8
  and and_1 (and_1_out, not_1_out, not_2_out);
  not not_1 (not_1_out, S);
  not not_2 (not_2_out, nOE);
  and and_2 (and_2_out, S, not_2_out);
endmodule

// 3G34 1:1
module IC_74x3G34 (
  input  A1,
  input  A2,
  input  A3,
  output Y1,
  output Y2,
  output Y3
);

  buf buffer_1 (Y1, A1);
  buf buffer_2 (Y2, A2);
  buf buffer_3 (Y3, A3);
endmodule

module D_Flip_Flop (
  input  SET,
  input  D,
  input  CLK,
  input  CLR,
  output Q,
  output R
);

  D_Flip_Flop_part #(.enable("true")) d_ff_1 (.clk(CLK), .D(D), .Q(Q), .Qn(R), .preset(SET), .reset(CLR));  // open: en
endmodule

module D_Latch (
  input  SET,
  input  D,
  input  LE,
  input  CLR,
  output Q,
  output R
);

  D_Flip_Flop_part #(.enable("true"), .trigger("high")) d_ff_1 (
    .clk(LE), .D(D), .Q(Q), .Qn(R), .preset(SET), .reset(CLR));  // open: en
endmodule

module JK_Flip_Flop (
  input  SET,
  input  J,
  input  CLK,
  input  K,
  input  CLR,
  output Q,
  output R
);

  J_K_Flip_Flop #(.enable("true")) j_k_ff_1 (
    .J(J), .clk(CLK), .K(K), .Q(Q), .Qn(R), .preset(SET), .reset(CLR));  // open: en
endmodule
